// Logisim project ALU_modular_design.circ as structural Verilog
module ALU_1bit (
  input  A,
  input  B,
  input  SUB,
  input  Cin,
  input  SEL0,
  input  SEL1,
  output Cout_output,
  output out_8
);

  wire AND_out_out, Beff_out, OR_out_out, SUM_out, t1_out, t2_out, X_out, XOR_out_out;

  and AND_out (AND_out_out, A, B);
  or OR_out (OR_out_out, A, B);
  xor XOR_out (XOR_out_out, A, B);
  xor Beff (Beff_out, B, SUB);
  xor X (X_out, A, Beff_out);
  and t1 (t1_out, A, Beff_out);
  and t2 (t2_out, X_out, Cin);
  xor SUM (SUM_out, X_out, Cin);
  or Cout (Cout_output, t1_out, t2_out);
  mux_4_to_1 mux_4_to_1_1 (
    .A(AND_out_out), .B(OR_out_out), .C(SUM_out), .D(XOR_out_out), .SEL_0(SEL0), .SEL_1(SEL1), .Q(out_8));
endmodule

module main (
  input  in_1,
  input  [19:0] in_2,
  output [31:0] out_3,
  output [31:0] out_4,
  output [31:0] out_5,
  output [3:0] out_6,
  output [31:0] out_7,
  output [31:0] out_8,
  output [31:0] out_9,
  output [31:0] out_10,
  output out_11,
  output [31:0] out_12,
  output [31:0] out_13,
  output [31:0] out_14,
  output [31:0] out_15,
  output out_16,
  output [31:0] out_17,
  output [31:0] out_18,
  output [31:0] out_19,
  output [31:0] out_20,
  output [31:0] out_21,
  output [31:0] out_22,
  output [31:0] out_23,
  output out_24
);

  wire alu_32bit_1_carry, alu_32bit_1_negative, alu_32bit_1_overflow, alu_32bit_1_zero, and_1_out, and_2_out,
       clock_1_out, or_1_out, or_2_out, register_1_q;
  wire [3:0] alu_32bit_1_result_2, alu_32bit_1_result_3, alu_32bit_1_result_4, alu_32bit_1_result_5,
       alu_32bit_1_result_6, alu_32bit_1_result_7, pc_fetch_1_out_5;
  wire [7:0] alu_32bit_1_result;
  wire [31:0] multiplexer_1_out, ram_1_dout, reg16x32_1_rd_a, reg16x32_1_rd_b;

  Clock clock_1 (.out(clock_1_out));
  PC_fetch pc_fetch_1 (
    .BRANCH(or_2_out), .IMM({in_2, out_3[11:0]}), .CLK(clock_1_out), .RST(in_1), .out_5(pc_fetch_1_out_5));
  ROM #(.addrWidth(4), .dataWidth(32)) rom_1 (.addr(pc_fetch_1_out_5), .data(out_3));
  reg16x32 reg16x32_1 (
    .CLK(clock_1_out), .WA(out_3[27:24]), .WD(out_5), .WE(out_3[28]), .RST(in_1), .RA(out_3[23:20]),
    .RB(out_3[19:16]), .R0_OUTPUT(out_7), .R1_OUTPUT(out_8), .R3_OUTPUT(out_9), .R2_OUPUT(out_10),
    .R5_OUTPUT(out_12), .R4_OUTPUT(out_13), .RD_A(reg16x32_1_rd_a), .R6_OUTPUT(out_14),
    .RD_B(reg16x32_1_rd_b), .R8_OUTPUT(out_15), .R9_OUTPUT(out_17), .R11_OUTPUT(out_18), .R10_OUTPUT(out_19),
    .R13_OUTPUT(out_20), .R12_OUTPUT(out_21), .R15_OUTPUT(out_22), .R14_OUTPUT(out_23));
  // Probe on reg16x32_1_rd_a
  // Probe on reg16x32_1_rd_b
  Multiplexer #(.width(32)) multiplexer_1 (
    .in0(reg16x32_1_rd_b), .in1({in_2, out_3[11:0]}), .out(multiplexer_1_out), .sel(or_1_out));
  // Probe on out_3[19:16]
  // Probe on out_3[23:20]
  // Probe on out_3[27:24]
  // Probe on out_3[29]
  // Probe on out_3[30]
  // Probe on out_3[31]
  // Probe on reg16x32_1_rd_a
  // Probe on multiplexer_1_out
  // Probe on {in_2, out_3[11:0]}
  and and_1 (and_1_out, out_3[19], out_3[18], out_3[17], out_3[16]);
  or or_1 (or_1_out, and_1_out, out_3[13], out_3[12]);
  or or_2 (or_2_out, out_3[15], and_2_out);
  ALU_32bit alu_32bit_1 (
    .SUB(out_3[29]), .SEL0(out_3[31]), .SEL1(out_3[30]), .A(reg16x32_1_rd_a), .B(multiplexer_1_out),
    .result({alu_32bit_1_result_7, alu_32bit_1_result_6, alu_32bit_1_result_5, alu_32bit_1_result_4, alu_32bit_1_result_3, alu_32bit_1_result_2, alu_32bit_1_result[7:6], out_6, alu_32bit_1_result[1:0]}),
    .zero(alu_32bit_1_zero), .negative(alu_32bit_1_negative), .overflow(alu_32bit_1_overflow),
    .carry(alu_32bit_1_carry));
  and and_2 (and_2_out, out_3[14], register_1_q);
  // Probe on {alu_32bit_1_result_7, alu_32bit_1_result_6, alu_32bit_1_result_5, alu_32bit_1_result_4, alu_32bit_1_result_3, alu_32bit_1_result_2, alu_32bit_1_result[7:6], out_6, alu_32bit_1_result[1:0]}
  Register #(.width(1)) register_1 (
    .D(alu_32bit_1_zero), .en(out_3[28]), .clk(clock_1_out), .Q(register_1_q), .clr(in_1));
  Register #(.width(1)) register_2 (
    .D(alu_32bit_1_negative), .en(out_3[28]), .clk(clock_1_out), .Q(out_11), .clr(in_1));
  Register #(.width(1)) register_3 (
    .D(alu_32bit_1_overflow), .en(out_3[28]), .clk(clock_1_out), .Q(out_16), .clr(in_1));
  Register #(.width(1)) register_4 (.D(alu_32bit_1_carry), .en(out_3[28]), .clk(clock_1_out), .Q(out_24), .clr(in_1));
  // Probe on out_3[12]
  RAM #(.addrWidth(4), .dataWidth(32)) ram_1 (
    .addr(out_6), .we(out_3[12]), .oe(out_3[13]), .clk(clock_1_out), .din(reg16x32_1_rd_b), .dout(ram_1_dout));
  // Probe on ram_1_dout
  Multiplexer #(.width(32)) multiplexer_2 (
    .in0({alu_32bit_1_result_7, alu_32bit_1_result_6, alu_32bit_1_result_5, alu_32bit_1_result_4, alu_32bit_1_result_3, alu_32bit_1_result_2, alu_32bit_1_result[7:6], out_6, alu_32bit_1_result[1:0]}),
    .in1(ram_1_dout), .out(out_5), .sel(out_3[13]));

  assign out_4 = {in_2, out_3[11:0]};

  // Notes on the sheet:
  //   contents of rom_1 (hex, n*v repeats v):
  //   d0000000 d1110000 d2220000 d3330000 d4440000 d5550000 911f0004 922f0006 80011800 80021804 940f2804
  //   950f2800 93340000 93340000 93350000 80031808
endmodule

module mux_4_to_1 (
  input  A,
  input  B,
  input  C,
  input  D,
  input  SEL_0,
  input  SEL_1,
  output Q
);

  wire nand_1_out, nand_2_out, nand_3_out, nand_4_out, nand_5_out, nand_6_out;

  nand nand_1 (nand_1_out, SEL_0, SEL_0);
  nand nand_2 (nand_2_out, SEL_1, SEL_1);
  nand nand_3 (nand_3_out, A, nand_1_out, nand_2_out);
  nand nand_4 (nand_4_out, B, nand_1_out, SEL_1);
  nand nand_5 (nand_5_out, C, nand_2_out, SEL_0);
  nand nand_6 (nand_6_out, D, SEL_0, SEL_1);
  nand nand_7 (Q, nand_3_out, nand_4_out, nand_5_out, nand_6_out);
endmodule

module reg32bit (
  input  A0,
  input  A1,
  input  A2,
  input  A3,
  input  B0,
  input  B1,
  input  B2,
  input  B3,
  input  SEL,
  input  CLK,
  input  in_11,
  input  in_12,
  input  in_13,
  input  in_14,
  input  in_15,
  input  in_16,
  input  in_17,
  input  in_18,
  input  in_19,
  input  in_20,
  input  in_21,
  input  in_22,
  input  in_23,
  input  in_24,
  input  in_25,
  input  in_26,
  input  in_27,
  input  in_28,
  input  in_29,
  input  in_30,
  input  in_31,
  input  in_32,
  input  in_33,
  input  in_34,
  input  in_35,
  input  in_36,
  input  in_37,
  input  in_38,
  input  in_39,
  input  in_40,
  input  in_41,
  input  in_42,
  input  in_43,
  input  in_44,
  input  in_45,
  input  in_46,
  input  in_47,
  input  in_48,
  input  in_49,
  input  in_50,
  input  in_51,
  input  in_52,
  input  in_53,
  input  in_54,
  input  in_55,
  input  in_56,
  input  in_57,
  input  in_58,
  input  in_59,
  input  in_60,
  input  in_61,
  input  in_62,
  input  in_63,
  input  in_64,
  input  in_65,
  input  in_66,
  output Q_0,
  output Q_1,
  output Q_2,
  output Q_3,
  output Q_0_not,
  output Q_1_not,
  output Q_2_not,
  output Q_3_not,
  output out_75,
  output out_76,
  output out_77,
  output out_78,
  output out_79,
  output out_80,
  output out_81,
  output out_82,
  output out_83,
  output out_84,
  output out_85,
  output out_86,
  output out_87,
  output out_88,
  output out_89,
  output out_90,
  output out_91,
  output out_92,
  output out_93,
  output out_94,
  output out_95,
  output out_96,
  output out_97,
  output out_98,
  output out_99,
  output out_100,
  output out_101,
  output out_102,
  output out_103,
  output out_104,
  output out_105,
  output out_106,
  output out_107,
  output out_108,
  output out_109,
  output out_110,
  output out_111,
  output out_112,
  output out_113,
  output out_114,
  output out_115,
  output out_116,
  output out_117,
  output out_118,
  output out_119,
  output out_120,
  output out_121,
  output out_122,
  output out_123,
  output out_124,
  output out_125,
  output out_126,
  output out_127,
  output out_128,
  output out_129,
  output out_130
);

  d_flip_flop d_flip_flop_1 (.A(A0), .B(B0), .SEL(SEL), .CLK(CLK), .Q(Q_0), .Q_not(Q_0_not));
  d_flip_flop d_flip_flop_2 (.A(in_11), .B(in_15), .SEL(SEL), .CLK(CLK), .Q(out_75), .Q_not(out_79));
  d_flip_flop d_flip_flop_3 (.A(in_19), .B(in_23), .SEL(SEL), .CLK(CLK), .Q(out_83), .Q_not(out_87));
  d_flip_flop d_flip_flop_4 (.A(in_27), .B(in_31), .SEL(SEL), .CLK(CLK), .Q(out_91), .Q_not(out_95));
  d_flip_flop d_flip_flop_5 (.A(in_35), .B(in_39), .SEL(SEL), .CLK(CLK), .Q(out_99), .Q_not(out_103));
  d_flip_flop d_flip_flop_6 (.A(in_43), .B(in_47), .SEL(SEL), .CLK(CLK), .Q(out_107), .Q_not(out_111));
  d_flip_flop d_flip_flop_7 (.A(in_51), .B(in_55), .SEL(SEL), .CLK(CLK), .Q(out_115), .Q_not(out_119));
  d_flip_flop d_flip_flop_8 (.A(in_59), .B(in_63), .SEL(SEL), .CLK(CLK), .Q(out_123), .Q_not(out_127));
  d_flip_flop d_flip_flop_9 (.A(A1), .B(B1), .SEL(SEL), .CLK(CLK), .Q(Q_1), .Q_not(Q_1_not));
  d_flip_flop d_flip_flop_10 (.A(in_12), .B(in_16), .SEL(SEL), .CLK(CLK), .Q(out_76), .Q_not(out_80));
  d_flip_flop d_flip_flop_11 (.A(in_20), .B(in_24), .SEL(SEL), .CLK(CLK), .Q(out_84), .Q_not(out_88));
  d_flip_flop d_flip_flop_12 (.A(in_28), .B(in_32), .SEL(SEL), .CLK(CLK), .Q(out_92), .Q_not(out_96));
  d_flip_flop d_flip_flop_13 (.A(in_36), .B(in_40), .SEL(SEL), .CLK(CLK), .Q(out_100), .Q_not(out_104));
  d_flip_flop d_flip_flop_14 (.A(in_44), .B(in_48), .SEL(SEL), .CLK(CLK), .Q(out_108), .Q_not(out_112));
  d_flip_flop d_flip_flop_15 (.A(in_52), .B(in_56), .SEL(SEL), .CLK(CLK), .Q(out_116), .Q_not(out_120));
  d_flip_flop d_flip_flop_16 (.A(in_60), .B(in_64), .SEL(SEL), .CLK(CLK), .Q(out_124), .Q_not(out_128));
  d_flip_flop d_flip_flop_17 (.A(A2), .B(B2), .SEL(SEL), .CLK(CLK), .Q(Q_2), .Q_not(Q_2_not));
  d_flip_flop d_flip_flop_18 (.A(in_13), .B(in_17), .SEL(SEL), .CLK(CLK), .Q(out_77), .Q_not(out_81));
  d_flip_flop d_flip_flop_19 (.A(in_21), .B(in_25), .SEL(SEL), .CLK(CLK), .Q(out_85), .Q_not(out_89));
  d_flip_flop d_flip_flop_20 (.A(in_29), .B(in_33), .SEL(SEL), .CLK(CLK), .Q(out_93), .Q_not(out_97));
  d_flip_flop d_flip_flop_21 (.A(in_37), .B(in_41), .SEL(SEL), .CLK(CLK), .Q(out_101), .Q_not(out_105));
  d_flip_flop d_flip_flop_22 (.A(in_45), .B(in_49), .SEL(SEL), .CLK(CLK), .Q(out_109), .Q_not(out_113));
  d_flip_flop d_flip_flop_23 (.A(in_53), .B(in_57), .SEL(SEL), .CLK(CLK), .Q(out_117), .Q_not(out_121));
  d_flip_flop d_flip_flop_24 (.A(in_61), .B(in_65), .SEL(SEL), .CLK(CLK), .Q(out_125), .Q_not(out_129));
  d_flip_flop d_flip_flop_25 (.A(A3), .B(B3), .SEL(SEL), .CLK(CLK), .Q(Q_3), .Q_not(Q_3_not));
  d_flip_flop d_flip_flop_26 (.A(in_14), .B(in_18), .SEL(SEL), .CLK(CLK), .Q(out_78), .Q_not(out_82));
  d_flip_flop d_flip_flop_27 (.A(in_22), .B(in_26), .SEL(SEL), .CLK(CLK), .Q(out_86), .Q_not(out_90));
  d_flip_flop d_flip_flop_28 (.A(in_30), .B(in_34), .SEL(SEL), .CLK(CLK), .Q(out_94), .Q_not(out_98));
  d_flip_flop d_flip_flop_29 (.A(in_38), .B(in_42), .SEL(SEL), .CLK(CLK), .Q(out_102), .Q_not(out_106));
  d_flip_flop d_flip_flop_30 (.A(in_46), .B(in_50), .SEL(SEL), .CLK(CLK), .Q(out_110), .Q_not(out_114));
  d_flip_flop d_flip_flop_31 (.A(in_54), .B(in_58), .SEL(SEL), .CLK(CLK), .Q(out_118), .Q_not(out_122));
  d_flip_flop d_flip_flop_32 (.A(in_62), .B(in_66), .SEL(SEL), .CLK(CLK), .Q(out_126), .Q_not(out_130));
endmodule

module sr_latch (
  input  R,
  input  S,
  output out_3,
  output out_4
);

  nand nand_1 (out_3, R, out_4);
  nand nand_2 (out_4, out_3, S);
endmodule

module d_latch (
  input  in_1,
  input  in_2,
  output out_3,
  output out_4
);

  wire nand_1_out, nand_2_out, not_1_out;

  not not_1 (not_1_out, in_1);
  nand nand_1 (nand_1_out, in_1, in_2);
  nand nand_2 (nand_2_out, not_1_out, in_2);
  sr_latch sr_latch_1 (.R(nand_1_out), .S(nand_2_out), .out_3(out_3), .out_4(out_4));
endmodule

module d_flip_flop (
  input  A,
  input  B,
  input  SEL,
  input  CLK,
  output Q,
  output Q_not
);

  wire MASTER_out_3, mux_2_to_1_1_out_4, not_1_out;

  mux_2_to_1 mux_2_to_1_1 (.A(A), .B(B), .SEL(SEL), .out_4(mux_2_to_1_1_out_4));
  not not_1 (not_1_out, CLK);
  d_latch MASTER (.in_1(mux_2_to_1_1_out_4), .in_2(not_1_out), .out_3(MASTER_out_3));  // open: out_4
  d_latch SLAVE (.in_1(MASTER_out_3), .in_2(CLK), .out_3(Q), .out_4(Q_not));
endmodule

module mux_2_to_1 (
  input  A,
  input  B,
  input  SEL,
  output out_4
);

  wire a_and_selnot_out, b_and_sel_out, not_1_out;

  not not_1 (not_1_out, SEL);
  nand a_and_selnot (a_and_selnot_out, A, not_1_out);
  nand b_and_sel (b_and_sel_out, B, SEL);
  nand Y (out_4, a_and_selnot_out, b_and_sel_out);
endmodule

module overflow_flag (
  input  B_MSB,
  input  A_MSB,
  input  R_MSB,
  input  OP,
  output out_5
);

  wire A_XNOR_B_out, A_XOR_B_out, A_XOR_R_out, ADDITION_out, R_XOR_A_out, SUBTRACTION_out;

  xnor A_XNOR_B (A_XNOR_B_out, B_MSB, A_MSB);
  xor R_XOR_A (R_XOR_A_out, A_MSB, R_MSB);
  xor A_XOR_B (A_XOR_B_out, A_MSB, B_MSB);
  xor A_XOR_R (A_XOR_R_out, A_MSB, R_MSB);
  and ADDITION (ADDITION_out, A_XNOR_B_out, R_XOR_A_out);
  and SUBTRACTION (SUBTRACTION_out, A_XOR_B_out, A_XOR_R_out);
  mux_2_to_1 mux_2_to_1_1 (.A(ADDITION_out), .B(SUBTRACTION_out), .SEL(OP), .out_4(out_5));
endmodule

module PC_fetch (
  input  BRANCH,
  input  [31:0] IMM,
  input  CLK,
  input  RST,
  output [3:0] out_5
);

  wire [31:0] adder_1_out, adder_2_out, multiplexer_1_out, PC_q;

  Register #(.width(32)) PC (
    .D(multiplexer_1_out), .en(1'b1), .clk(CLK), .Q({PC_q[31:6], out_5, PC_q[1:0]}), .clr(RST));
  Adder #(.width(32)) adder_1 (
    .a({PC_q[31:6], out_5, PC_q[1:0]}), .b(32'h4), .out(adder_1_out), .cin(1'b0));  // open: cout
  Adder #(.width(32)) adder_2 (
    .a({PC_q[31:6], out_5, PC_q[1:0]}), .b(IMM), .out(adder_2_out), .cin(1'b0));  // open: cout
  Multiplexer #(.width(32)) multiplexer_1 (.in0(adder_1_out), .in1(adder_2_out), .out(multiplexer_1_out), .sel(BRANCH));
endmodule

module reg4x32file (
  input  CLK,
  input  [1:0] WA,
  input  [31:0] WD,
  input  WE,
  input  [1:0] RA,
  input  [1:0] RB,
  input  RST,
  output [31:0] RD_A,
  output [31:0] RD_B
);

  wire and_1_out, and_2_out, and_3_out, and_4_out, decoder2x4_1_d0, decoder2x4_1_d1, decoder2x4_1_d2,
       decoder2x4_1_d3;
  wire [31:0] R0_q, R1_q, R2_q, R3_q;

  decoder2x4 decoder2x4_1 (
    .in_1(WA), .D0(decoder2x4_1_d0), .D1(decoder2x4_1_d1), .D2(decoder2x4_1_d2), .D3(decoder2x4_1_d3));
  and and_1 (and_1_out, decoder2x4_1_d0, WE);
  and and_2 (and_2_out, decoder2x4_1_d1, WE);
  and and_3 (and_3_out, decoder2x4_1_d2, WE);
  and and_4 (and_4_out, decoder2x4_1_d3, WE);
  Register #(.width(32)) R0 (.D(WD), .en(and_1_out), .clk(CLK), .Q(R0_q), .clr(RST));
  Register #(.width(32)) R2 (.D(WD), .en(and_3_out), .clk(CLK), .Q(R2_q), .clr(RST));
  Register #(.width(32)) R1 (.D(WD), .en(and_2_out), .clk(CLK), .Q(R1_q), .clr(RST));
  Register #(.width(32)) R3 (.D(WD), .en(and_4_out), .clk(CLK), .Q(R3_q), .clr(RST));
  Multiplexer #(.select(2), .width(32)) multiplexer_1 (
    .in0(R0_q), .in1(R1_q), .in2(R2_q), .in3(R3_q), .out(RD_A), .sel(RA));
  Multiplexer #(.select(2), .width(32)) multiplexer_2 (
    .in0(R0_q), .in1(R1_q), .in2(R2_q), .in3(R3_q), .out(RD_B), .sel(RB));
endmodule

module decoder2x4 (
  input  [1:0] in_1,
  output D0,
  output D1,
  output D2,
  output D3
);

  wire NOT_A0_out, NOT_A1_out;

  not NOT_A0 (NOT_A0_out, in_1[0]);
  not NOT_A1 (NOT_A1_out, in_1[1]);
  and and_1 (D0, NOT_A0_out, NOT_A1_out);
  and and_2 (D1, NOT_A1_out, in_1[0]);
  and and_3 (D2, in_1[1], NOT_A0_out);
  and and_4 (D3, in_1[1], in_1[0]);
endmodule

module ALU_32bit (
  input  SUB,
  input  SEL0,
  input  SEL1,
  input  [31:0] A,
  input  [31:0] B,
  output [31:0] result,
  output zero,
  output negative,
  output overflow,
  output carry
);

  wire alu_1bit_1_cout_output, alu_1bit_2_cout_output, alu_1bit_3_cout_output, alu_1bit_4_cout_output,
       alu_1bit_5_cout_output, alu_1bit_6_cout_output, alu_1bit_7_cout_output, alu_1bit_8_cout_output,
       alu_1bit_9_cout_output, alu_1bit_10_cout_output, alu_1bit_11_cout_output, alu_1bit_12_cout_output,
       alu_1bit_13_cout_output, alu_1bit_14_cout_output, alu_1bit_15_cout_output, alu_1bit_16_cout_output,
       alu_1bit_17_cout_output, alu_1bit_18_cout_output, alu_1bit_19_cout_output, alu_1bit_20_cout_output,
       alu_1bit_21_cout_output, alu_1bit_22_cout_output, alu_1bit_23_cout_output, alu_1bit_24_cout_output,
       alu_1bit_25_cout_output, alu_1bit_26_cout_output, alu_1bit_27_cout_output, alu_1bit_28_cout_output,
       alu_1bit_29_cout_output, alu_1bit_30_cout_output, alu_1bit_31_cout_output;
  wire [3:0] or_1_out;

  Hex_Digit_Display hex_digit_display_1 (.value(A[31:28]));  // open: dp
  Hex_Digit_Display hex_digit_display_2 (.value(B[31:28]));  // open: dp
  Hex_Digit_Display hex_digit_display_3 (.value({negative, result[30:28]}));  // open: dp
  Hex_Digit_Display hex_digit_display_4 (.value(A[27:24]));  // open: dp
  Hex_Digit_Display hex_digit_display_5 (.value(A[23:20]));  // open: dp
  Hex_Digit_Display hex_digit_display_6 (.value(B[27:24]));  // open: dp
  Hex_Digit_Display hex_digit_display_7 (.value(B[23:20]));  // open: dp
  Hex_Digit_Display hex_digit_display_8 (.value(result[27:24]));  // open: dp
  Hex_Digit_Display hex_digit_display_9 (.value(result[23:20]));  // open: dp
  Hex_Digit_Display hex_digit_display_10 (.value(A[19:16]));  // open: dp
  Hex_Digit_Display hex_digit_display_11 (.value(A[15:12]));  // open: dp
  Hex_Digit_Display hex_digit_display_12 (.value(B[19:16]));  // open: dp
  Hex_Digit_Display hex_digit_display_13 (.value(B[15:12]));  // open: dp
  Hex_Digit_Display hex_digit_display_14 (.value(result[19:16]));  // open: dp
  Hex_Digit_Display hex_digit_display_15 (.value(result[15:12]));  // open: dp
  Hex_Digit_Display hex_digit_display_16 (.value(A[11:8]));  // open: dp
  Hex_Digit_Display hex_digit_display_17 (.value(A[7:4]));  // open: dp
  Hex_Digit_Display hex_digit_display_18 (.value(B[11:8]));  // open: dp
  Hex_Digit_Display hex_digit_display_19 (.value(B[7:4]));  // open: dp
  Hex_Digit_Display hex_digit_display_20 (.value(result[11:8]));  // open: dp
  Hex_Digit_Display hex_digit_display_21 (.value(result[7:4]));  // open: dp
  Hex_Digit_Display hex_digit_display_22 (.value(A[3:0]));  // open: dp
  Hex_Digit_Display hex_digit_display_23 (.value(B[3:0]));  // open: dp
  Hex_Digit_Display hex_digit_display_24 (.value(result[3:0]));  // open: dp
  LED led_1 (.in(negative));
  LED led_2 (.in(result[30]));
  LED led_3 (.in(A[31]));
  LED led_4 (.in(result[29]));
  LED led_5 (.in(result[28]));
  LED led_6 (.in(A[30]));
  LED led_7 (.in(A[29]));
  LED led_8 (.in(B[31]));
  LED led_9 (.in(A[28]));
  overflow_flag overflow_flag_1 (.B_MSB(B[31]), .A_MSB(A[31]), .R_MSB(negative), .OP(SUB), .out_5(overflow));
  LED led_10 (.in(B[30]));
  LED led_11 (.in(B[29]));
  LED led_12 (.in(B[28]));
  assign or_1_out = {negative, result[30:28]} | result[27:24] | result[23:20] | result[19:16] | result[15:12] | result[11:8] | result[7:4] | result[3:0];  // OR_Gate or_1, 4 bits wide
  _7_Segment_Display u_7_segment_display_1 (
    .f(overflow), .b(overflow), .e(overflow), .d(overflow), .c(overflow));  // open: g, a, dp
  nor nor_1 (zero, or_1_out[3], or_1_out[2], or_1_out[1], or_1_out[0]);
  _7_Segment_Display u_7_segment_display_2 (
    .f(zero), .a(zero), .b(zero), .e(zero), .d(zero), .c(zero), .dp(zero));  // open: g
  _7_Segment_Display u_7_segment_display_3 (.g(negative));  // open: f, a, b, e, d, c, dp
  _7_Segment_Display u_7_segment_display_4 (.f(carry), .a(carry), .e(carry), .d(carry));  // open: g, b, c, dp
  ALU_1bit alu_1bit_1 (
    .A(A[0]), .B(B[0]), .SUB(SUB), .Cin(SUB), .SEL0(SEL0), .SEL1(SEL1), .Cout_output(alu_1bit_1_cout_output),
    .out_8(result[0]));
  ALU_1bit alu_1bit_2 (
    .A(A[4]), .B(B[4]), .SUB(SUB), .Cin(alu_1bit_25_cout_output), .SEL0(SEL0), .SEL1(SEL1),
    .Cout_output(alu_1bit_2_cout_output), .out_8(result[4]));
  ALU_1bit alu_1bit_3 (
    .A(A[8]), .B(B[8]), .SUB(SUB), .Cin(alu_1bit_26_cout_output), .SEL0(SEL0), .SEL1(SEL1),
    .Cout_output(alu_1bit_3_cout_output), .out_8(result[8]));
  ALU_1bit alu_1bit_4 (
    .A(A[12]), .B(B[12]), .SUB(SUB), .Cin(alu_1bit_27_cout_output), .SEL0(SEL0), .SEL1(SEL1),
    .Cout_output(alu_1bit_4_cout_output), .out_8(result[12]));
  ALU_1bit alu_1bit_5 (
    .A(A[16]), .B(B[16]), .SUB(SUB), .Cin(alu_1bit_28_cout_output), .SEL0(SEL0), .SEL1(SEL1),
    .Cout_output(alu_1bit_5_cout_output), .out_8(result[16]));
  ALU_1bit alu_1bit_6 (
    .A(A[20]), .B(B[20]), .SUB(SUB), .Cin(alu_1bit_29_cout_output), .SEL0(SEL0), .SEL1(SEL1),
    .Cout_output(alu_1bit_6_cout_output), .out_8(result[20]));
  ALU_1bit alu_1bit_7 (
    .A(A[24]), .B(B[24]), .SUB(SUB), .Cin(alu_1bit_30_cout_output), .SEL0(SEL0), .SEL1(SEL1),
    .Cout_output(alu_1bit_7_cout_output), .out_8(result[24]));
  ALU_1bit alu_1bit_8 (
    .A(A[28]), .B(B[28]), .SUB(SUB), .Cin(alu_1bit_31_cout_output), .SEL0(SEL0), .SEL1(SEL1),
    .Cout_output(alu_1bit_8_cout_output), .out_8(result[28]));
  ALU_1bit alu_1bit_9 (
    .A(A[1]), .B(B[1]), .SUB(SUB), .Cin(alu_1bit_1_cout_output), .SEL0(SEL0), .SEL1(SEL1),
    .Cout_output(alu_1bit_9_cout_output), .out_8(result[1]));
  ALU_1bit alu_1bit_10 (
    .A(A[5]), .B(B[5]), .SUB(SUB), .Cin(alu_1bit_2_cout_output), .SEL0(SEL0), .SEL1(SEL1),
    .Cout_output(alu_1bit_10_cout_output), .out_8(result[5]));
  ALU_1bit alu_1bit_11 (
    .A(A[9]), .B(B[9]), .SUB(SUB), .Cin(alu_1bit_3_cout_output), .SEL0(SEL0), .SEL1(SEL1),
    .Cout_output(alu_1bit_11_cout_output), .out_8(result[9]));
  ALU_1bit alu_1bit_12 (
    .A(A[13]), .B(B[13]), .SUB(SUB), .Cin(alu_1bit_4_cout_output), .SEL0(SEL0), .SEL1(SEL1),
    .Cout_output(alu_1bit_12_cout_output), .out_8(result[13]));
  ALU_1bit alu_1bit_13 (
    .A(A[17]), .B(B[17]), .SUB(SUB), .Cin(alu_1bit_5_cout_output), .SEL0(SEL0), .SEL1(SEL1),
    .Cout_output(alu_1bit_13_cout_output), .out_8(result[17]));
  ALU_1bit alu_1bit_14 (
    .A(A[21]), .B(B[21]), .SUB(SUB), .Cin(alu_1bit_6_cout_output), .SEL0(SEL0), .SEL1(SEL1),
    .Cout_output(alu_1bit_14_cout_output), .out_8(result[21]));
  ALU_1bit alu_1bit_15 (
    .A(A[25]), .B(B[25]), .SUB(SUB), .Cin(alu_1bit_7_cout_output), .SEL0(SEL0), .SEL1(SEL1),
    .Cout_output(alu_1bit_15_cout_output), .out_8(result[25]));
  ALU_1bit alu_1bit_16 (
    .A(A[29]), .B(B[29]), .SUB(SUB), .Cin(alu_1bit_8_cout_output), .SEL0(SEL0), .SEL1(SEL1),
    .Cout_output(alu_1bit_16_cout_output), .out_8(result[29]));
  ALU_1bit alu_1bit_17 (
    .A(A[2]), .B(B[2]), .SUB(SUB), .Cin(alu_1bit_9_cout_output), .SEL0(SEL0), .SEL1(SEL1),
    .Cout_output(alu_1bit_17_cout_output), .out_8(result[2]));
  ALU_1bit alu_1bit_18 (
    .A(A[6]), .B(B[6]), .SUB(SUB), .Cin(alu_1bit_10_cout_output), .SEL0(SEL0), .SEL1(SEL1),
    .Cout_output(alu_1bit_18_cout_output), .out_8(result[6]));
  ALU_1bit alu_1bit_19 (
    .A(A[10]), .B(B[10]), .SUB(SUB), .Cin(alu_1bit_11_cout_output), .SEL0(SEL0), .SEL1(SEL1),
    .Cout_output(alu_1bit_19_cout_output), .out_8(result[10]));
  ALU_1bit alu_1bit_20 (
    .A(A[14]), .B(B[14]), .SUB(SUB), .Cin(alu_1bit_12_cout_output), .SEL0(SEL0), .SEL1(SEL1),
    .Cout_output(alu_1bit_20_cout_output), .out_8(result[14]));
  ALU_1bit alu_1bit_21 (
    .A(A[18]), .B(B[18]), .SUB(SUB), .Cin(alu_1bit_13_cout_output), .SEL0(SEL0), .SEL1(SEL1),
    .Cout_output(alu_1bit_21_cout_output), .out_8(result[18]));
  ALU_1bit alu_1bit_22 (
    .A(A[22]), .B(B[22]), .SUB(SUB), .Cin(alu_1bit_14_cout_output), .SEL0(SEL0), .SEL1(SEL1),
    .Cout_output(alu_1bit_22_cout_output), .out_8(result[22]));
  ALU_1bit alu_1bit_23 (
    .A(A[26]), .B(B[26]), .SUB(SUB), .Cin(alu_1bit_15_cout_output), .SEL0(SEL0), .SEL1(SEL1),
    .Cout_output(alu_1bit_23_cout_output), .out_8(result[26]));
  ALU_1bit alu_1bit_24 (
    .A(A[30]), .B(B[30]), .SUB(SUB), .Cin(alu_1bit_16_cout_output), .SEL0(SEL0), .SEL1(SEL1),
    .Cout_output(alu_1bit_24_cout_output), .out_8(result[30]));
  ALU_1bit alu_1bit_25 (
    .A(A[3]), .B(B[3]), .SUB(SUB), .Cin(alu_1bit_17_cout_output), .SEL0(SEL0), .SEL1(SEL1),
    .Cout_output(alu_1bit_25_cout_output), .out_8(result[3]));
  ALU_1bit alu_1bit_26 (
    .A(A[7]), .B(B[7]), .SUB(SUB), .Cin(alu_1bit_18_cout_output), .SEL0(SEL0), .SEL1(SEL1),
    .Cout_output(alu_1bit_26_cout_output), .out_8(result[7]));
  ALU_1bit alu_1bit_27 (
    .A(A[11]), .B(B[11]), .SUB(SUB), .Cin(alu_1bit_19_cout_output), .SEL0(SEL0), .SEL1(SEL1),
    .Cout_output(alu_1bit_27_cout_output), .out_8(result[11]));
  ALU_1bit alu_1bit_28 (
    .A(A[15]), .B(B[15]), .SUB(SUB), .Cin(alu_1bit_20_cout_output), .SEL0(SEL0), .SEL1(SEL1),
    .Cout_output(alu_1bit_28_cout_output), .out_8(result[15]));
  ALU_1bit alu_1bit_29 (
    .A(A[19]), .B(B[19]), .SUB(SUB), .Cin(alu_1bit_21_cout_output), .SEL0(SEL0), .SEL1(SEL1),
    .Cout_output(alu_1bit_29_cout_output), .out_8(result[19]));
  ALU_1bit alu_1bit_30 (
    .A(A[23]), .B(B[23]), .SUB(SUB), .Cin(alu_1bit_22_cout_output), .SEL0(SEL0), .SEL1(SEL1),
    .Cout_output(alu_1bit_30_cout_output), .out_8(result[23]));
  ALU_1bit alu_1bit_31 (
    .A(A[27]), .B(B[27]), .SUB(SUB), .Cin(alu_1bit_23_cout_output), .SEL0(SEL0), .SEL1(SEL1),
    .Cout_output(alu_1bit_31_cout_output), .out_8(result[27]));
  ALU_1bit alu_1bit_32 (
    .A(A[31]), .B(B[31]), .SUB(SUB), .Cin(alu_1bit_24_cout_output), .SEL0(SEL0), .SEL1(SEL1),
    .Cout_output(carry), .out_8(negative));

  assign result[31] = negative;
endmodule

module reg16x32 (
  input  CLK,
  input  [3:0] WA,
  input  [31:0] WD,
  input  WE,
  input  RST,
  input  [3:0] RA,
  input  [3:0] RB,
  output [31:0] R0_OUTPUT,
  output [31:0] R1_OUTPUT,
  output [31:0] R3_OUTPUT,
  output [31:0] R2_OUPUT,
  output [31:0] R5_OUTPUT,
  output [31:0] R4_OUTPUT,
  output [31:0] RD_A,
  output [31:0] R6_OUTPUT,
  output [31:0] RD_B,
  output [31:0] R8_OUTPUT,
  output [31:0] R9_OUTPUT,
  output [31:0] R11_OUTPUT,
  output [31:0] R10_OUTPUT,
  output [31:0] R13_OUTPUT,
  output [31:0] R12_OUTPUT,
  output [31:0] R15_OUTPUT,
  output [31:0] R14_OUTPUT
);

  wire and_1_out, and_2_out, and_3_out, and_4_out, and_5_out, and_6_out, and_7_out, and_8_out, and_9_out,
       and_10_out, and_11_out, and_12_out, and_13_out, and_14_out, and_15_out, and_16_out, decoder_1_out0,
       decoder_1_out1, decoder_1_out2, decoder_1_out3, decoder_1_out4, decoder_1_out5, decoder_1_out6,
       decoder_1_out7, decoder_1_out8, decoder_1_out9, decoder_1_out10, decoder_1_out11, decoder_1_out12,
       decoder_1_out13, decoder_1_out14, decoder_1_out15;
  wire [31:0] R7_q;

  Decoder #(.select(4)) decoder_1 (
    .out0(decoder_1_out0), .out1(decoder_1_out1), .out2(decoder_1_out2), .out3(decoder_1_out3),
    .out4(decoder_1_out4), .out5(decoder_1_out5), .out6(decoder_1_out6), .out7(decoder_1_out7),
    .out8(decoder_1_out8), .out9(decoder_1_out9), .out10(decoder_1_out10), .out11(decoder_1_out11),
    .out12(decoder_1_out12), .out13(decoder_1_out13), .out14(decoder_1_out14), .out15(decoder_1_out15),
    .sel(WA), .en(WE));
  and and_1 (and_1_out, decoder_1_out0, WE);
  and and_2 (and_2_out, decoder_1_out1, WE);
  and and_3 (and_3_out, decoder_1_out2, WE);
  and and_4 (and_4_out, decoder_1_out3, WE);
  and and_5 (and_5_out, decoder_1_out4, WE);
  and and_6 (and_6_out, decoder_1_out5, WE);
  and and_7 (and_7_out, decoder_1_out6, WE);
  and and_8 (and_8_out, decoder_1_out7, WE);
  and and_9 (and_9_out, decoder_1_out8, WE);
  and and_10 (and_10_out, decoder_1_out9, WE);
  and and_11 (and_11_out, decoder_1_out10, WE);
  and and_12 (and_12_out, decoder_1_out11, WE);
  and and_13 (and_13_out, decoder_1_out12, WE);
  and and_14 (and_14_out, decoder_1_out13, WE);
  and and_15 (and_15_out, decoder_1_out14, WE);
  and and_16 (and_16_out, decoder_1_out15, WE);
  Register #(.width(32)) R0 (.D(WD), .en(and_1_out), .clk(CLK), .Q(R0_OUTPUT), .clr(RST));
  Register #(.width(32)) R2 (.D(WD), .en(and_3_out), .clk(CLK), .Q(R2_OUPUT), .clr(RST));
  Register #(.width(32)) R4 (.D(WD), .en(and_5_out), .clk(CLK), .Q(R4_OUTPUT), .clr(RST));
  Register #(.width(32)) R6 (.D(WD), .en(and_7_out), .clk(CLK), .Q(R6_OUTPUT), .clr(RST));
  Register #(.width(32)) R8 (.D(WD), .en(and_9_out), .clk(CLK), .Q(R8_OUTPUT), .clr(RST));
  Register #(.width(32)) R10 (.D(WD), .en(and_11_out), .clk(CLK), .Q(R10_OUTPUT), .clr(RST));
  Register #(.width(32)) R12 (.D(WD), .en(and_13_out), .clk(CLK), .Q(R12_OUTPUT), .clr(RST));
  Register #(.width(32)) R14 (.D(WD), .en(and_15_out), .clk(CLK), .Q(R14_OUTPUT), .clr(RST));
  Register #(.width(32)) R1 (.D(WD), .en(and_2_out), .clk(CLK), .Q(R1_OUTPUT), .clr(RST));
  Register #(.width(32)) R3 (.D(WD), .en(and_4_out), .clk(CLK), .Q(R3_OUTPUT), .clr(RST));
  Register #(.width(32)) R5 (.D(WD), .en(and_6_out), .clk(CLK), .Q(R5_OUTPUT), .clr(RST));
  Register #(.width(32)) R7 (.D(WD), .en(and_8_out), .clk(CLK), .Q(R7_q), .clr(RST));
  Register #(.width(32)) R9 (.D(WD), .en(and_10_out), .clk(CLK), .Q(R9_OUTPUT), .clr(RST));
  Register #(.width(32)) R11 (.D(WD), .en(and_12_out), .clk(CLK), .Q(R11_OUTPUT), .clr(RST));
  Register #(.width(32)) R13 (.D(WD), .en(and_14_out), .clk(CLK), .Q(R13_OUTPUT), .clr(RST));
  Register #(.width(32)) R15 (.D(WD), .en(and_16_out), .clk(CLK), .Q(R15_OUTPUT), .clr(RST));
  Multiplexer #(.select(4), .width(32)) multiplexer_1 (
    .in0(R0_OUTPUT), .in1(R1_OUTPUT), .in2(R2_OUPUT), .in3(R3_OUTPUT), .in4(R4_OUTPUT), .in5(R5_OUTPUT),
    .in6(R6_OUTPUT), .in7(R7_q), .in8(R8_OUTPUT), .in9(R9_OUTPUT), .in10(R10_OUTPUT), .in11(R11_OUTPUT),
    .in12(R12_OUTPUT), .in13(R13_OUTPUT), .in14(R14_OUTPUT), .in15(R15_OUTPUT), .out(RD_A), .sel(RA));
  Multiplexer #(.select(4), .width(32)) multiplexer_2 (
    .in0(R0_OUTPUT), .in1(R1_OUTPUT), .in2(R2_OUPUT), .in3(R3_OUTPUT), .in4(R4_OUTPUT), .in5(R5_OUTPUT),
    .in6(R6_OUTPUT), .in7(R7_q), .in8(R8_OUTPUT), .in9(R9_OUTPUT), .in10(R10_OUTPUT), .in11(R11_OUTPUT),
    .in12(R12_OUTPUT), .in13(R13_OUTPUT), .in14(R14_OUTPUT), .in15(R15_OUTPUT), .out(RD_B), .sel(RB));
endmodule

module main_v2 (
  input  in_1,
  input  [19:0] in_2,
  output [31:0] out_3,
  output [31:0] out_4,
  output [31:0] out_5,
  output [3:0] out_6,
  output [31:0] out_7,
  output [31:0] out_8,
  output [31:0] out_9,
  output [31:0] out_10,
  output out_11,
  output [31:0] out_12,
  output [31:0] out_13,
  output [31:0] out_14,
  output out_15,
  output out_16
);

  wire alu_32bit_1_carry, alu_32bit_1_negative, alu_32bit_1_overflow, alu_32bit_1_zero, and_1_out, and_2_out,
       clock_1_out, or_1_out, or_2_out, register_1_q;
  wire [3:0] alu_32bit_1_result_2, alu_32bit_1_result_3, alu_32bit_1_result_4, alu_32bit_1_result_5,
       alu_32bit_1_result_6, alu_32bit_1_result_7, pc_fetch_1_out_5;
  wire [7:0] alu_32bit_1_result;
  wire [31:0] multiplexer_1_out, ram_1_dout, reg16x32_1_rd_a, reg16x32_1_rd_b;

  Clock clock_1 (.out(clock_1_out));
  PC_fetch pc_fetch_1 (
    .BRANCH(or_2_out), .IMM({in_2, out_3[11:0]}), .CLK(clock_1_out), .RST(in_1), .out_5(pc_fetch_1_out_5));
  ROM #(.addrWidth(4), .dataWidth(32)) rom_1 (.addr(pc_fetch_1_out_5), .data(out_3));
  reg16x32 reg16x32_1 (
    .CLK(clock_1_out), .WA(out_3[27:24]), .WD(out_5), .WE(out_3[28]), .RST(in_1), .RA(out_3[23:20]),
    .RB(out_3[19:16]), .R0_OUTPUT(out_7), .R1_OUTPUT(out_8), .R3_OUTPUT(out_9), .R2_OUPUT(out_10),
    .R5_OUTPUT(out_12), .R4_OUTPUT(out_13), .RD_A(reg16x32_1_rd_a), .R6_OUTPUT(out_14), .RD_B(reg16x32_1_rd_b));  // open: R8_OUTPUT, R9_OUTPUT, R11_OUTPUT, R10_OUTPUT, R13_OUTPUT, R12_OUTPUT, R15_OUTPUT, R14_OUTPUT
  // Probe on reg16x32_1_rd_a
  // Probe on reg16x32_1_rd_b
  Multiplexer #(.width(32)) multiplexer_1 (
    .in0(reg16x32_1_rd_b), .in1({in_2, out_3[11:0]}), .out(multiplexer_1_out), .sel(or_1_out));
  // Probe on out_3[19:16]
  // Probe on out_3[23:20]
  // Probe on out_3[27:24]
  // Probe on out_3[29]
  // Probe on out_3[30]
  // Probe on out_3[31]
  // Probe on reg16x32_1_rd_a
  // Probe on multiplexer_1_out
  // Probe on {in_2, out_3[11:0]}
  and and_1 (and_1_out, out_3[19], out_3[18], out_3[17], out_3[16]);
  or or_1 (or_1_out, and_1_out, out_3[13], out_3[12]);
  or or_2 (or_2_out, out_3[15], and_2_out);
  ALU_32bit alu_32bit_1 (
    .SUB(out_3[29]), .SEL0(out_3[31]), .SEL1(out_3[30]), .A(reg16x32_1_rd_a), .B(multiplexer_1_out),
    .result({alu_32bit_1_result_7, alu_32bit_1_result_6, alu_32bit_1_result_5, alu_32bit_1_result_4, alu_32bit_1_result_3, alu_32bit_1_result_2, alu_32bit_1_result[7:6], out_6, alu_32bit_1_result[1:0]}),
    .zero(alu_32bit_1_zero), .negative(alu_32bit_1_negative), .overflow(alu_32bit_1_overflow),
    .carry(alu_32bit_1_carry));
  and and_2 (and_2_out, out_3[14], register_1_q);
  // Probe on {alu_32bit_1_result_7, alu_32bit_1_result_6, alu_32bit_1_result_5, alu_32bit_1_result_4, alu_32bit_1_result_3, alu_32bit_1_result_2, alu_32bit_1_result[7:6], out_6, alu_32bit_1_result[1:0]}
  Register #(.width(1)) register_1 (
    .D(alu_32bit_1_zero), .en(out_3[28]), .clk(clock_1_out), .Q(register_1_q), .clr(in_1));
  Register #(.width(1)) register_2 (
    .D(alu_32bit_1_negative), .en(out_3[28]), .clk(clock_1_out), .Q(out_11), .clr(in_1));
  Register #(.width(1)) register_3 (
    .D(alu_32bit_1_overflow), .en(out_3[28]), .clk(clock_1_out), .Q(out_15), .clr(in_1));
  Register #(.width(1)) register_4 (.D(alu_32bit_1_carry), .en(out_3[28]), .clk(clock_1_out), .Q(out_16), .clr(in_1));
  // Probe on out_3[12]
  RAM #(.addrWidth(4), .dataWidth(32)) ram_1 (
    .addr(out_6), .we(out_3[12]), .oe(out_3[13]), .clk(clock_1_out), .din(reg16x32_1_rd_b), .dout(ram_1_dout));
  // Probe on ram_1_dout
  Multiplexer #(.width(32)) multiplexer_2 (
    .in0({alu_32bit_1_result_7, alu_32bit_1_result_6, alu_32bit_1_result_5, alu_32bit_1_result_4, alu_32bit_1_result_3, alu_32bit_1_result_2, alu_32bit_1_result[7:6], out_6, alu_32bit_1_result[1:0]}),
    .in1(ram_1_dout), .out(out_5), .sel(out_3[13]));

  assign out_4 = {in_2, out_3[11:0]};

  // Notes on the sheet:
  //   contents of rom_1 (hex, n*v repeats v):
  //   d0000000 d1110000 d2220000 d3330000 d4440000 d5550000 911f0004 922f0006 80011800 80021804 940f2804
  //   950f2800 93340000 93340000 93350000 80031808
endmodule

module PE_cell (
  input  [31:0] w_in,
  input  w_load,
  input  CLK,
  input  [31:0] psum_in,
  input  [31:0] a_in,
  output [31:0] psum_out,
  output [31:0] a_out
);

  wire [31:0] adder_1_out, multiplier_1_out, W_reg_q;

  Register #(.width(32)) W_reg (.D(w_in), .en(w_load), .clk(CLK), .Q(W_reg_q));  // open: clr
  Multiplier #(.width(32)) multiplier_1 (.a(a_in), .b(W_reg_q), .out(multiplier_1_out));  // open: cin, cout
  Register #(.width(32)) a_reg (.D(a_in), .clk(CLK), .Q(a_out));  // open: en, clr
  Register #(.width(32)) psum_reg (.D(adder_1_out), .clk(CLK), .Q(psum_out));  // open: en, clr
  Adder #(.width(32)) adder_1 (.a(psum_in), .b(multiplier_1_out), .out(adder_1_out));  // open: cin, cout
endmodule

module Systollic_2x2 (
  input  [31:0] in_1,
  input  [31:0] in_2,
  input  in_3,
  input  [31:0] in_4,
  input  [31:0] in_5,
  input  [31:0] in_6,
  input  [31:0] in_7,
  output [31:0] out_8,
  output [31:0] out_9,
  output [31:0] out_10,
  output [31:0] out_11
);

  wire clock_1_out;
  wire [31:0] pe_cell_1_a_out, pe_cell_1_psum_out, pe_cell_2_a_out, pe_cell_3_psum_out;

  Clock clock_1 (.out(clock_1_out));
  PE_cell pe_cell_1 (
    .w_in(in_1), .w_load(in_3), .CLK(clock_1_out), .psum_in({32{1'b0}}), .a_in(in_4),
    .psum_out(pe_cell_1_psum_out), .a_out(pe_cell_1_a_out));
  PE_cell pe_cell_2 (
    .w_in(in_5), .w_load(in_3), .CLK(clock_1_out), .psum_in(pe_cell_1_psum_out), .a_in(in_7),
    .psum_out(out_9), .a_out(pe_cell_2_a_out));
  // Probe on pe_cell_1_psum_out
  PE_cell pe_cell_3 (
    .w_in(in_2), .w_load(in_3), .CLK(clock_1_out), .psum_in({32{1'b0}}), .a_in(pe_cell_1_a_out),
    .psum_out(pe_cell_3_psum_out), .a_out(out_8));
  PE_cell pe_cell_4 (
    .w_in(in_6), .w_load(in_3), .CLK(clock_1_out), .psum_in(pe_cell_3_psum_out), .a_in(pe_cell_2_a_out),
    .psum_out(out_10), .a_out(out_11));
  // Probe on pe_cell_3_psum_out
endmodule

module systolic_4x4 (
  input  CLK,
  input  [31:0] w00,
  input  [31:0] w01,
  input  [31:0] w02,
  input  [31:0] w03,
  input  w_load,
  input  [31:0] row0,
  input  [31:0] w10,
  input  [31:0] w11,
  input  [31:0] w12,
  input  [31:0] w13,
  input  [31:0] row1,
  input  [31:0] w20,
  input  [31:0] w21,
  input  [31:0] w22,
  input  [31:0] w23,
  input  [31:0] row2,
  input  [31:0] w30,
  input  [31:0] w31,
  input  [31:0] w32,
  input  [31:0] w33,
  input  [31:0] row3,
  output [31:0] c_col0,
  output [31:0] c_col1,
  output [31:0] c_col2,
  output [31:0] c_col3
);

  wire [31:0] pe_cell_1_a_out, pe_cell_1_psum_out, pe_cell_2_a_out, pe_cell_2_psum_out, pe_cell_3_a_out,
       pe_cell_3_psum_out, pe_cell_4_a_out, pe_cell_5_a_out, pe_cell_5_psum_out, pe_cell_6_a_out,
       pe_cell_6_psum_out, pe_cell_7_a_out, pe_cell_7_psum_out, pe_cell_8_a_out, pe_cell_9_a_out,
       pe_cell_9_psum_out, pe_cell_10_a_out, pe_cell_10_psum_out, pe_cell_11_a_out, pe_cell_11_psum_out,
       pe_cell_12_a_out, pe_cell_13_a_out, pe_cell_13_psum_out, pe_cell_14_a_out, pe_cell_14_psum_out,
       pe_cell_15_a_out, pe_cell_15_psum_out, pe_cell_16_a_out;

  PE_cell pe_cell_1 (
    .w_in(w00), .w_load(w_load), .CLK(CLK), .psum_in({32{1'b0}}), .a_in(row0), .psum_out(pe_cell_1_psum_out),
    .a_out(pe_cell_1_a_out));
  PE_cell pe_cell_2 (
    .w_in(w10), .w_load(w_load), .CLK(CLK), .psum_in(pe_cell_1_psum_out), .a_in(row1),
    .psum_out(pe_cell_2_psum_out), .a_out(pe_cell_2_a_out));
  PE_cell pe_cell_3 (
    .w_in(w20), .w_load(w_load), .CLK(CLK), .psum_in(pe_cell_2_psum_out), .a_in(row2),
    .psum_out(pe_cell_3_psum_out), .a_out(pe_cell_3_a_out));
  PE_cell pe_cell_4 (
    .w_in(w30), .w_load(w_load), .CLK(CLK), .psum_in(pe_cell_3_psum_out), .a_in(row3), .psum_out(c_col0),
    .a_out(pe_cell_4_a_out));
  // Probe on pe_cell_1_psum_out
  // Probe on pe_cell_2_psum_out
  // Probe on pe_cell_3_psum_out
  PE_cell pe_cell_5 (
    .w_in(w01), .w_load(w_load), .CLK(CLK), .psum_in({32{1'b0}}), .a_in(pe_cell_1_a_out),
    .psum_out(pe_cell_5_psum_out), .a_out(pe_cell_5_a_out));
  PE_cell pe_cell_6 (
    .w_in(w11), .w_load(w_load), .CLK(CLK), .psum_in(pe_cell_5_psum_out), .a_in(pe_cell_2_a_out),
    .psum_out(pe_cell_6_psum_out), .a_out(pe_cell_6_a_out));
  PE_cell pe_cell_7 (
    .w_in(w21), .w_load(w_load), .CLK(CLK), .psum_in(pe_cell_6_psum_out), .a_in(pe_cell_3_a_out),
    .psum_out(pe_cell_7_psum_out), .a_out(pe_cell_7_a_out));
  PE_cell pe_cell_8 (
    .w_in(w31), .w_load(w_load), .CLK(CLK), .psum_in(pe_cell_7_psum_out), .a_in(pe_cell_4_a_out),
    .psum_out(c_col1), .a_out(pe_cell_8_a_out));
  // Probe on pe_cell_5_psum_out
  // Probe on pe_cell_6_psum_out
  // Probe on pe_cell_7_psum_out
  PE_cell pe_cell_9 (
    .w_in(w02), .w_load(w_load), .CLK(CLK), .psum_in({32{1'b0}}), .a_in(pe_cell_5_a_out),
    .psum_out(pe_cell_9_psum_out), .a_out(pe_cell_9_a_out));
  PE_cell pe_cell_10 (
    .w_in(w12), .w_load(w_load), .CLK(CLK), .psum_in(pe_cell_9_psum_out), .a_in(pe_cell_6_a_out),
    .psum_out(pe_cell_10_psum_out), .a_out(pe_cell_10_a_out));
  PE_cell pe_cell_11 (
    .w_in(w22), .w_load(w_load), .CLK(CLK), .psum_in(pe_cell_10_psum_out), .a_in(pe_cell_7_a_out),
    .psum_out(pe_cell_11_psum_out), .a_out(pe_cell_11_a_out));
  PE_cell pe_cell_12 (
    .w_in(w32), .w_load(w_load), .CLK(CLK), .psum_in(pe_cell_11_psum_out), .a_in(pe_cell_8_a_out),
    .psum_out(c_col2), .a_out(pe_cell_12_a_out));
  // Probe on pe_cell_9_psum_out
  // Probe on pe_cell_10_psum_out
  // Probe on pe_cell_11_psum_out
  PE_cell pe_cell_13 (
    .w_in(w03), .w_load(w_load), .CLK(CLK), .psum_in({32{1'b0}}), .a_in(pe_cell_9_a_out),
    .psum_out(pe_cell_13_psum_out), .a_out(pe_cell_13_a_out));
  PE_cell pe_cell_14 (
    .w_in(w13), .w_load(w_load), .CLK(CLK), .psum_in(pe_cell_13_psum_out), .a_in(pe_cell_10_a_out),
    .psum_out(pe_cell_14_psum_out), .a_out(pe_cell_14_a_out));
  PE_cell pe_cell_15 (
    .w_in(w23), .w_load(w_load), .CLK(CLK), .psum_in(pe_cell_14_psum_out), .a_in(pe_cell_11_a_out),
    .psum_out(pe_cell_15_psum_out), .a_out(pe_cell_15_a_out));
  PE_cell pe_cell_16 (
    .w_in(w33), .w_load(w_load), .CLK(CLK), .psum_in(pe_cell_15_psum_out), .a_in(pe_cell_12_a_out),
    .psum_out(c_col3), .a_out(pe_cell_16_a_out));
  // Probe on pe_cell_13_psum_out
  // Probe on pe_cell_14_psum_out
  // Probe on pe_cell_15_psum_out
endmodule

module matmul4x4 (
  input  in_1,
  input  [31:0] in_2,
  input  [31:0] in_3,
  input  [31:0] in_4,
  input  [31:0] in_5,
  output [31:0] out_6,
  output [31:0] out_7,
  output [31:0] out_8,
  output [31:0] out_9
);

  wire clock_1_out;
  wire [31:0] register_1_q, register_2_q, register_3_q, register_4_q, register_5_q, register_6_q,
       register_7_q, register_8_q, register_10_q, systolic_4x4_1_c_col0, systolic_4x4_1_c_col1,
       systolic_4x4_1_c_col2;

  Clock clock_1 (.out(clock_1_out));
  Register #(.width(32)) register_1 (.D(in_4), .clk(clock_1_out), .Q(register_1_q));  // open: en, clr
  Register #(.width(32)) register_2 (.D(in_3), .clk(clock_1_out), .Q(register_2_q));  // open: en, clr
  Register #(.width(32)) register_3 (.D(in_5), .clk(clock_1_out), .Q(register_3_q));  // open: en, clr
  Register #(.width(32)) register_4 (.D(register_1_q), .clk(clock_1_out), .Q(register_4_q));  // open: en, clr
  Register #(.width(32)) register_5 (.D(register_3_q), .clk(clock_1_out), .Q(register_5_q));  // open: en, clr
  Register #(.width(32)) register_6 (.D(register_5_q), .clk(clock_1_out), .Q(register_6_q));  // open: en, clr
  systolic_4x4 systolic_4x4_1 (
    .CLK(clock_1_out), .w00(32'hf), .w01(32'hf), .w02(32'hf), .w03(32'hf), .w_load(in_1), .row0(in_2),
    .w10(32'hf), .w11(32'hf), .w12(32'hf), .w13(32'hf), .row1(register_2_q), .w20(32'hf), .w21(32'hf),
    .w22(32'hf), .w23(32'hf), .row2(register_4_q), .w30(32'hf), .w31(32'hf), .w32(32'hf), .w33(32'hf),
    .row3(register_6_q), .c_col0(systolic_4x4_1_c_col0), .c_col1(systolic_4x4_1_c_col1),
    .c_col2(systolic_4x4_1_c_col2), .c_col3(out_7));
  Register #(.width(32)) register_7 (.D(systolic_4x4_1_c_col0), .clk(clock_1_out), .Q(register_7_q));  // open: en, clr
  Register #(.width(32)) register_8 (.D(systolic_4x4_1_c_col1), .clk(clock_1_out), .Q(register_8_q));  // open: en, clr
  Register #(.width(32)) register_9 (.D(systolic_4x4_1_c_col2), .clk(clock_1_out), .Q(out_9));  // open: en, clr
  Register #(.width(32)) register_10 (.D(register_7_q), .clk(clock_1_out), .Q(register_10_q));  // open: en, clr
  Register #(.width(32)) register_11 (.D(register_8_q), .clk(clock_1_out), .Q(out_8));  // open: en, clr
  Register #(.width(32)) register_12 (.D(register_10_q), .clk(clock_1_out), .Q(out_6));  // open: en, clr
endmodule

module Systolic_2x1 (
  input  CLK,
  input  [31:0] w0,
  input  w_load,
  input  [31:0] a0,
  input  [31:0] w1,
  input  [31:0] a1,
  output [31:0] psum_out
);

  wire [31:0] pe_cell_1_psum_out;

  PE_cell pe_cell_1 (
    .w_in(w0), .w_load(w_load), .CLK(CLK), .psum_in({32{1'b0}}), .a_in(a0), .psum_out(pe_cell_1_psum_out));  // open: a_out
  PE_cell pe_cell_2 (
    .w_in(w1), .w_load(w_load), .CLK(CLK), .psum_in(pe_cell_1_psum_out), .a_in(a1), .psum_out(psum_out));  // open: a_out
endmodule

// VHDL entity CustomISA, as the project stores it:
--------------------------------------------------------------------------------
-- Project :
-- File    :
-- Autor   :
-- Date    :
--
--------------------------------------------------------------------------------
-- Description :
--
--------------------------------------------------------------------------------

LIBRARY ieee;
USE ieee.std_logic_1164.all;

ENTITY CustomISA IS
  PORT (
  ------------------------------------------------------------------------------
  --Insert input ports below
    clock      : IN  std_logic;                    -- input bit example
    val        : IN  std_logic_vector(3 DOWNTO 0); -- input vector example
  ------------------------------------------------------------------------------
  --Insert output ports below
    max        : OUT std_logic;                    -- output bit example
    cpt        : OUT std_logic_vector(3 DOWNTO 0)  -- output vector example
    );
END CustomISA;

--------------------------------------------------------------------------------
--Complete your VHDL description below
--------------------------------------------------------------------------------

ARCHITECTURE TypeArchitecture OF CustomISA IS

BEGIN


END TypeArchitecture;

// VHDL entity regfile, as the project stores it:
--------------------------------------------------------------------------------
-- Project :
-- File    :
-- Autor   :
-- Date    :
--
--------------------------------------------------------------------------------
-- Description :
--
--------------------------------------------------------------------------------

LIBRARY ieee;
USE ieee.std_logic_1164.all;

ENTITY regfile IS
  PORT (
  ------------------------------------------------------------------------------
  --Insert input ports below
    clock      : IN  std_logic;                    -- input bit example
    val        : IN  std_logic_vector(3 DOWNTO 0); -- input vector example
  ------------------------------------------------------------------------------
  --Insert output ports below
    max        : OUT std_logic;                    -- output bit example
    cpt        : OUT std_logic_vector(3 DOWNTO 0)  -- output vector example
    );
END regfile;

--------------------------------------------------------------------------------
--Complete your VHDL description below
--------------------------------------------------------------------------------

ARCHITECTURE TypeArchitecture OF regfile IS

BEGIN


END TypeArchitecture;
