// Logisim project ALU_modular_design.circ as structural Verilog: 9 circuits, main circuit main
module ALU_1bit (
  input  A,
  input  B,
  input  SUB,
  input  Cin,
  input  SEL0,
  input  SEL1,
  output Cout_output,
  output out_8
);

  wire AND_out_out, Beff_out, OR_out_out, SUM_out, t1_out, t2_out, X_out, XOR_out_out;

  and AND_out (AND_out_out, A, B);
  or OR_out (OR_out_out, A, B);
  xor XOR_out (XOR_out_out, A, B);
  xor Beff (Beff_out, B, SUB);
  xor X (X_out, A, Beff_out);
  and t1 (t1_out, A, Beff_out);
  and t2 (t2_out, X_out, Cin);
  xor SUM (SUM_out, X_out, Cin);
  or Cout (Cout_output, t1_out, t2_out);
  mux_4_to_1 mux_4_to_1_1 (
    .A(AND_out_out), .B(OR_out_out), .C(SUM_out), .D(XOR_out_out), .SEL_0(SEL0), .SEL_1(SEL1), .Q(out_8));
endmodule

module main (
  input  A_0,
  input  A_1,
  input  A_2,
  input  A_3,
  input  B_0,
  input  B_1,
  input  B_2,
  input  B_3,
  input  SUB,
  input  SEL0,
  input  SEL1,
  input  in_12,
  input  in_13,
  input  in_14,
  input  in_15,
  input  in_16,
  input  in_17,
  input  in_18,
  input  in_19,
  input  in_20,
  input  in_21,
  input  in_22,
  input  in_23,
  input  in_24,
  input  in_25,
  input  in_26,
  input  in_27,
  input  in_28,
  input  in_29,
  input  in_30,
  input  in_31,
  input  in_32,
  input  in_33,
  input  in_34,
  input  in_35,
  input  in_36,
  input  in_37,
  input  in_38,
  input  in_39,
  input  in_40,
  input  in_41,
  input  in_42,
  input  in_43,
  input  in_44,
  input  in_45,
  input  in_46,
  input  in_47,
  input  in_48,
  input  in_49,
  input  in_50,
  input  in_51,
  input  in_52,
  input  in_53,
  input  in_54,
  input  in_55,
  input  in_56,
  input  in_57,
  input  in_58,
  input  in_59,
  input  in_60,
  input  in_61,
  input  in_62,
  input  in_63,
  input  in_64,
  input  in_65,
  input  in_66,
  input  in_67,
  output out_68,
  output out_69,
  output out_70,
  output out_71,
  output out_72,
  output out_73,
  output out_74,
  output out_75,
  output out_76,
  output out_77,
  output out_78,
  output out_79,
  output out_80,
  output out_81,
  output out_82,
  output out_83,
  output out_84,
  output out_85,
  output out_86,
  output out_87,
  output out_88,
  output out_89,
  output out_90,
  output out_91,
  output out_92,
  output out_93,
  output out_94,
  output out_95,
  output out_96,
  output out_97,
  output out_98,
  output out_99,
  output out_100
);

  wire alu_1bit_1_cout_output, alu_1bit_2_cout_output, alu_1bit_3_cout_output, alu_1bit_4_cout_output,
       alu_1bit_5_cout_output, alu_1bit_6_cout_output, alu_1bit_7_cout_output, alu_1bit_8_cout_output,
       alu_1bit_9_cout_output, alu_1bit_10_cout_output, alu_1bit_11_cout_output, alu_1bit_12_cout_output,
       alu_1bit_13_cout_output, alu_1bit_14_cout_output, alu_1bit_15_cout_output, alu_1bit_16_cout_output,
       alu_1bit_17_cout_output, alu_1bit_18_cout_output, alu_1bit_19_cout_output, alu_1bit_20_cout_output,
       alu_1bit_21_cout_output, alu_1bit_22_cout_output, alu_1bit_23_cout_output, alu_1bit_24_cout_output,
       alu_1bit_25_cout_output, alu_1bit_26_cout_output, alu_1bit_27_cout_output, alu_1bit_28_cout_output,
       alu_1bit_29_cout_output, alu_1bit_30_cout_output, alu_1bit_31_cout_output, CLK_out, nor_1_out,
       overflow_flag_1_out_5, register_3_q, register_4_q, register_6_q;
  wire [3:0] or_1_out, register_1_q, register_1_q_2, register_1_q_3, register_1_q_4, register_1_q_5,
       register_1_q_6, register_1_q_7, register_1_q_8, register_2_q, register_2_q_2, register_2_q_3,
       register_2_q_4, register_2_q_5, register_2_q_6, register_2_q_7, register_2_q_8;
  wire [31:0] register_5_q;

  Hex_Digit_Display hex_digit_display_1 (.value(register_1_q_8));  // open: dp
  Hex_Digit_Display hex_digit_display_2 (.value(register_2_q_8));  // open: dp
  Hex_Digit_Display hex_digit_display_3 (.value(register_5_q[31:28]));  // open: dp
  Hex_Digit_Display hex_digit_display_4 (.value(register_1_q_7));  // open: dp
  Hex_Digit_Display hex_digit_display_5 (.value(register_1_q_6));  // open: dp
  Hex_Digit_Display hex_digit_display_6 (.value(register_2_q_7));  // open: dp
  Hex_Digit_Display hex_digit_display_7 (.value(register_2_q_6));  // open: dp
  Hex_Digit_Display hex_digit_display_8 (.value(register_5_q[27:24]));  // open: dp
  Hex_Digit_Display hex_digit_display_9 (.value(register_5_q[23:20]));  // open: dp
  Hex_Digit_Display hex_digit_display_10 (.value(register_1_q_5));  // open: dp
  Hex_Digit_Display hex_digit_display_11 (.value(register_1_q_4));  // open: dp
  Hex_Digit_Display hex_digit_display_12 (.value(register_2_q_5));  // open: dp
  Hex_Digit_Display hex_digit_display_13 (.value(register_2_q_4));  // open: dp
  Hex_Digit_Display hex_digit_display_14 (.value(register_5_q[19:16]));  // open: dp
  Hex_Digit_Display hex_digit_display_15 (.value(register_5_q[15:12]));  // open: dp
  Hex_Digit_Display hex_digit_display_16 (.value(register_1_q_3));  // open: dp
  Hex_Digit_Display hex_digit_display_17 (.value(register_1_q_2));  // open: dp
  Hex_Digit_Display hex_digit_display_18 (.value(register_2_q_3));  // open: dp
  Hex_Digit_Display hex_digit_display_19 (.value(register_2_q_2));  // open: dp
  Hex_Digit_Display hex_digit_display_20 (.value(register_5_q[11:8]));  // open: dp
  Hex_Digit_Display hex_digit_display_21 (.value(register_5_q[7:4]));  // open: dp
  Hex_Digit_Display hex_digit_display_22 (.value(register_1_q));  // open: dp
  Hex_Digit_Display hex_digit_display_23 (.value(register_2_q));  // open: dp
  Hex_Digit_Display hex_digit_display_24 (.value(register_5_q[3:0]));  // open: dp
  Register #(.width(32)) register_1 (
    .D({in_63, in_62, in_61, in_60, in_55, in_54, in_53, in_52, in_47, in_46, in_45, in_44, in_39, in_38, in_37, in_36, in_31, in_30, in_29, in_28, in_23, in_22, in_21, in_20, in_15, in_14, in_13, in_12, A_3, A_2, A_1, A_0}),
    .clk(CLK_out),
    .Q({register_1_q_8, register_1_q_7, register_1_q_6, register_1_q_5, register_1_q_4, register_1_q_3, register_1_q_2, register_1_q}));  // open: en, clr
  Register #(.width(32)) register_2 (
    .D({in_67, in_66, in_65, in_64, in_59, in_58, in_57, in_56, in_51, in_50, in_49, in_48, in_43, in_42, in_41, in_40, in_35, in_34, in_33, in_32, in_27, in_26, in_25, in_24, in_19, in_18, in_17, in_16, B_3, B_2, B_1, B_0}),
    .clk(CLK_out),
    .Q({register_2_q_8, register_2_q_7, register_2_q_6, register_2_q_5, register_2_q_4, register_2_q_3, register_2_q_2, register_2_q}));  // open: en, clr
  LED led_1 (.in(register_5_q[31]));
  LED led_2 (.in(register_5_q[30]));
  LED led_3 (.in(register_1_q_8[3]));
  LED led_4 (.in(register_5_q[29]));
  LED led_5 (.in(register_5_q[28]));
  LED led_6 (.in(register_1_q_8[2]));
  LED led_7 (.in(register_1_q_8[1]));
  LED led_8 (.in(register_2_q_8[3]));
  LED led_9 (.in(register_1_q_8[0]));
  overflow_flag overflow_flag_1 (
    .B_MSB(register_2_q_8[3]), .A_MSB(register_1_q_8[3]), .R_MSB(register_5_q[31]), .OP(SUB),
    .out_5(overflow_flag_1_out_5));
  Clock CLK (.out(CLK_out));
  LED led_10 (.in(register_2_q_8[2]));
  LED led_11 (.in(register_2_q_8[1]));
  Register #(.width(1)) register_3 (.D(overflow_flag_1_out_5), .clk(CLK_out), .Q(register_3_q));  // open: en, clr
  LED led_12 (.in(register_2_q_8[0]));
  assign or_1_out = register_5_q[31:28] | register_5_q[27:24] | register_5_q[23:20] | register_5_q[19:16] | register_5_q[15:12] | register_5_q[11:8] | register_5_q[7:4] | register_5_q[3:0];  // OR_Gate or_1, 4 bits wide
  _7_Segment_Display u_7_segment_display_1 (
    .f(register_3_q), .b(register_3_q), .e(register_3_q), .d(register_3_q), .c(register_3_q));  // open: g, a, dp
  nor nor_1 (nor_1_out, or_1_out[3], or_1_out[2], or_1_out[1], or_1_out[0]);
  _7_Segment_Display u_7_segment_display_2 (
    .f(nor_1_out), .a(nor_1_out), .b(nor_1_out), .e(nor_1_out), .d(nor_1_out), .c(nor_1_out), .dp(nor_1_out));  // open: g
  _7_Segment_Display u_7_segment_display_3 (.g(register_6_q));  // open: f, a, b, e, d, c, dp
  Register #(.width(1)) register_4 (.D(out_96), .clk(CLK_out), .Q(register_4_q));  // open: en, clr
  _7_Segment_Display u_7_segment_display_4 (
    .f(register_4_q), .a(register_4_q), .e(register_4_q), .d(register_4_q));  // open: g, b, c, dp
  Register #(.width(32)) register_5 (
    .D({out_100, out_99, out_98, out_97, out_95, out_94, out_93, out_92, out_91, out_90, out_89, out_88, out_87, out_86, out_85, out_84, out_83, out_82, out_81, out_80, out_79, out_78, out_77, out_76, out_75, out_74, out_73, out_72, out_71, out_70, out_69, out_68}),
    .clk(CLK_out), .Q(register_5_q));  // open: en, clr
  Register #(.width(1)) register_6 (.D(out_100), .clk(CLK_out), .Q(register_6_q));  // open: en, clr
  ALU_1bit alu_1bit_1 (
    .A(A_0), .B(B_0), .SUB(SUB), .Cin(SUB), .SEL0(SEL0), .SEL1(SEL1), .Cout_output(alu_1bit_1_cout_output),
    .out_8(out_68));
  ALU_1bit alu_1bit_2 (
    .A(in_12), .B(in_16), .SUB(SUB), .Cin(alu_1bit_25_cout_output), .SEL0(SEL0), .SEL1(SEL1),
    .Cout_output(alu_1bit_2_cout_output), .out_8(out_72));
  ALU_1bit alu_1bit_3 (
    .A(in_20), .B(in_24), .SUB(SUB), .Cin(alu_1bit_26_cout_output), .SEL0(SEL0), .SEL1(SEL1),
    .Cout_output(alu_1bit_3_cout_output), .out_8(out_76));
  ALU_1bit alu_1bit_4 (
    .A(in_28), .B(in_32), .SUB(SUB), .Cin(alu_1bit_27_cout_output), .SEL0(SEL0), .SEL1(SEL1),
    .Cout_output(alu_1bit_4_cout_output), .out_8(out_80));
  ALU_1bit alu_1bit_5 (
    .A(in_36), .B(in_40), .SUB(SUB), .Cin(alu_1bit_28_cout_output), .SEL0(SEL0), .SEL1(SEL1),
    .Cout_output(alu_1bit_5_cout_output), .out_8(out_84));
  ALU_1bit alu_1bit_6 (
    .A(in_44), .B(in_48), .SUB(SUB), .Cin(alu_1bit_29_cout_output), .SEL0(SEL0), .SEL1(SEL1),
    .Cout_output(alu_1bit_6_cout_output), .out_8(out_88));
  ALU_1bit alu_1bit_7 (
    .A(in_52), .B(in_56), .SUB(SUB), .Cin(alu_1bit_30_cout_output), .SEL0(SEL0),
    .Cout_output(alu_1bit_7_cout_output), .out_8(out_92));  // open: SEL1
  ALU_1bit alu_1bit_8 (
    .A(in_60), .B(in_64), .SUB(SUB), .Cin(alu_1bit_31_cout_output), .SEL0(SEL0), .SEL1(SEL1),
    .Cout_output(alu_1bit_8_cout_output), .out_8(out_97));
  ALU_1bit alu_1bit_9 (
    .A(A_1), .B(B_1), .SUB(SUB), .Cin(alu_1bit_1_cout_output), .SEL0(SEL0), .SEL1(SEL1),
    .Cout_output(alu_1bit_9_cout_output), .out_8(out_69));
  ALU_1bit alu_1bit_10 (
    .A(in_13), .B(in_17), .SUB(SUB), .Cin(alu_1bit_2_cout_output), .SEL0(SEL0), .SEL1(SEL1),
    .Cout_output(alu_1bit_10_cout_output), .out_8(out_73));
  ALU_1bit alu_1bit_11 (
    .A(in_21), .B(in_25), .SUB(SUB), .Cin(alu_1bit_3_cout_output), .SEL0(SEL0), .SEL1(SEL1),
    .Cout_output(alu_1bit_11_cout_output), .out_8(out_77));
  ALU_1bit alu_1bit_12 (
    .A(in_29), .B(in_33), .SUB(SUB), .Cin(alu_1bit_4_cout_output), .SEL0(SEL0), .SEL1(SEL1),
    .Cout_output(alu_1bit_12_cout_output), .out_8(out_81));
  ALU_1bit alu_1bit_13 (
    .A(in_37), .B(in_41), .SUB(SUB), .Cin(alu_1bit_5_cout_output), .SEL0(SEL0), .SEL1(SEL1),
    .Cout_output(alu_1bit_13_cout_output), .out_8(out_85));
  ALU_1bit alu_1bit_14 (
    .A(in_45), .B(in_49), .SUB(SUB), .Cin(alu_1bit_6_cout_output), .SEL0(SEL0), .SEL1(SEL1),
    .Cout_output(alu_1bit_14_cout_output), .out_8(out_89));
  ALU_1bit alu_1bit_15 (
    .A(in_53), .B(in_57), .SUB(SUB), .Cin(alu_1bit_7_cout_output), .SEL0(SEL0),
    .Cout_output(alu_1bit_15_cout_output), .out_8(out_93));  // open: SEL1
  ALU_1bit alu_1bit_16 (
    .A(in_61), .B(in_65), .SUB(SUB), .Cin(alu_1bit_8_cout_output), .SEL0(SEL0), .SEL1(SEL1),
    .Cout_output(alu_1bit_16_cout_output), .out_8(out_98));
  ALU_1bit alu_1bit_17 (
    .A(A_2), .B(B_2), .SUB(SUB), .Cin(alu_1bit_9_cout_output), .SEL0(SEL0), .SEL1(SEL1),
    .Cout_output(alu_1bit_17_cout_output), .out_8(out_70));
  ALU_1bit alu_1bit_18 (
    .A(in_14), .B(in_18), .SUB(SUB), .Cin(alu_1bit_10_cout_output), .SEL0(SEL0), .SEL1(SEL1),
    .Cout_output(alu_1bit_18_cout_output), .out_8(out_74));
  ALU_1bit alu_1bit_19 (
    .A(in_22), .B(in_26), .SUB(SUB), .Cin(alu_1bit_11_cout_output), .SEL0(SEL0), .SEL1(SEL1),
    .Cout_output(alu_1bit_19_cout_output), .out_8(out_78));
  ALU_1bit alu_1bit_20 (
    .A(in_30), .B(in_34), .SUB(SUB), .Cin(alu_1bit_12_cout_output), .SEL0(SEL0), .SEL1(SEL1),
    .Cout_output(alu_1bit_20_cout_output), .out_8(out_82));
  ALU_1bit alu_1bit_21 (
    .A(in_38), .B(in_42), .SUB(SUB), .Cin(alu_1bit_13_cout_output), .SEL0(SEL0), .SEL1(SEL1),
    .Cout_output(alu_1bit_21_cout_output), .out_8(out_86));
  ALU_1bit alu_1bit_22 (
    .A(in_46), .B(in_50), .SUB(SUB), .Cin(alu_1bit_14_cout_output), .SEL0(SEL0), .SEL1(SEL1),
    .Cout_output(alu_1bit_22_cout_output), .out_8(out_90));
  ALU_1bit alu_1bit_23 (
    .A(in_54), .B(in_58), .SUB(SUB), .Cin(alu_1bit_15_cout_output), .SEL0(SEL0), .SEL1(SEL1),
    .Cout_output(alu_1bit_23_cout_output), .out_8(out_94));
  ALU_1bit alu_1bit_24 (
    .A(in_62), .B(in_66), .SUB(SUB), .Cin(alu_1bit_16_cout_output), .SEL0(SEL0), .SEL1(SEL1),
    .Cout_output(alu_1bit_24_cout_output), .out_8(out_99));
  ALU_1bit alu_1bit_25 (
    .A(A_3), .B(B_3), .SUB(SUB), .Cin(alu_1bit_17_cout_output), .SEL0(SEL0), .SEL1(SEL1),
    .Cout_output(alu_1bit_25_cout_output), .out_8(out_71));
  ALU_1bit alu_1bit_26 (
    .A(in_15), .B(in_19), .SUB(SUB), .Cin(alu_1bit_18_cout_output), .SEL0(SEL0), .SEL1(SEL1),
    .Cout_output(alu_1bit_26_cout_output), .out_8(out_75));
  ALU_1bit alu_1bit_27 (
    .A(in_23), .B(in_27), .SUB(SUB), .Cin(alu_1bit_19_cout_output), .SEL0(SEL0), .SEL1(SEL1),
    .Cout_output(alu_1bit_27_cout_output), .out_8(out_79));
  ALU_1bit alu_1bit_28 (
    .A(in_31), .B(in_35), .SUB(SUB), .Cin(alu_1bit_20_cout_output), .SEL0(SEL0), .SEL1(SEL1),
    .Cout_output(alu_1bit_28_cout_output), .out_8(out_83));
  ALU_1bit alu_1bit_29 (
    .A(in_39), .B(in_43), .SUB(SUB), .Cin(alu_1bit_21_cout_output), .SEL0(SEL0), .SEL1(SEL1),
    .Cout_output(alu_1bit_29_cout_output), .out_8(out_87));
  ALU_1bit alu_1bit_30 (
    .A(in_47), .B(in_51), .SUB(SUB), .Cin(alu_1bit_22_cout_output), .SEL0(SEL0), .SEL1(SEL1),
    .Cout_output(alu_1bit_30_cout_output), .out_8(out_91));
  ALU_1bit alu_1bit_31 (
    .A(in_55), .B(in_59), .SUB(SUB), .Cin(alu_1bit_23_cout_output), .SEL0(SEL0), .SEL1(SEL1),
    .Cout_output(alu_1bit_31_cout_output), .out_8(out_95));
  ALU_1bit alu_1bit_32 (
    .A(in_63), .B(in_67), .SUB(SUB), .Cin(alu_1bit_24_cout_output), .SEL0(SEL0), .SEL1(SEL1),
    .Cout_output(out_96), .out_8(out_100));
endmodule

module mux_4_to_1 (
  input  A,
  input  B,
  input  C,
  input  D,
  input  SEL_0,
  input  SEL_1,
  output Q
);

  wire nand_1_out, nand_2_out, nand_3_out, nand_4_out, nand_5_out, nand_6_out;

  nand nand_1 (nand_1_out, SEL_0, SEL_0);
  nand nand_2 (nand_2_out, SEL_1, SEL_1);
  nand nand_3 (nand_3_out, A, nand_1_out, nand_2_out);
  nand nand_4 (nand_4_out, B, nand_1_out, SEL_1);
  nand nand_5 (nand_5_out, C, nand_2_out, SEL_0);
  nand nand_6 (nand_6_out, D, SEL_0, SEL_1);
  nand nand_7 (Q, nand_3_out, nand_4_out, nand_5_out, nand_6_out);
endmodule

module reg32bit (
  input  A0,
  input  A1,
  input  A2,
  input  A3,
  input  B0,
  input  B1,
  input  B2,
  input  B3,
  input  SEL,
  input  CLK,
  input  in_11,
  input  in_12,
  input  in_13,
  input  in_14,
  input  in_15,
  input  in_16,
  input  in_17,
  input  in_18,
  input  in_19,
  input  in_20,
  input  in_21,
  input  in_22,
  input  in_23,
  input  in_24,
  input  in_25,
  input  in_26,
  input  in_27,
  input  in_28,
  input  in_29,
  input  in_30,
  input  in_31,
  input  in_32,
  input  in_33,
  input  in_34,
  input  in_35,
  input  in_36,
  input  in_37,
  input  in_38,
  input  in_39,
  input  in_40,
  input  in_41,
  input  in_42,
  input  in_43,
  input  in_44,
  input  in_45,
  input  in_46,
  input  in_47,
  input  in_48,
  input  in_49,
  input  in_50,
  input  in_51,
  input  in_52,
  input  in_53,
  input  in_54,
  input  in_55,
  input  in_56,
  input  in_57,
  input  in_58,
  input  in_59,
  input  in_60,
  input  in_61,
  input  in_62,
  input  in_63,
  input  in_64,
  input  in_65,
  input  in_66,
  output Q_0,
  output Q_1,
  output Q_2,
  output Q_3,
  output Q_0_not,
  output Q_1_not,
  output Q_2_not,
  output Q_3_not,
  output out_75,
  output out_76,
  output out_77,
  output out_78,
  output out_79,
  output out_80,
  output out_81,
  output out_82,
  output out_83,
  output out_84,
  output out_85,
  output out_86,
  output out_87,
  output out_88,
  output out_89,
  output out_90,
  output out_91,
  output out_92,
  output out_93,
  output out_94,
  output out_95,
  output out_96,
  output out_97,
  output out_98,
  output out_99,
  output out_100,
  output out_101,
  output out_102,
  output out_103,
  output out_104,
  output out_105,
  output out_106,
  output out_107,
  output out_108,
  output out_109,
  output out_110,
  output out_111,
  output out_112,
  output out_113,
  output out_114,
  output out_115,
  output out_116,
  output out_117,
  output out_118,
  output out_119,
  output out_120,
  output out_121,
  output out_122,
  output out_123,
  output out_124,
  output out_125,
  output out_126,
  output out_127,
  output out_128,
  output out_129,
  output out_130
);

  d_flip_flop d_flip_flop_1 (.A(A0), .B(B0), .SEL(SEL), .CLK(CLK), .Q(Q_0), .Q_not(Q_0_not));
  d_flip_flop d_flip_flop_2 (.A(in_11), .B(in_15), .SEL(SEL), .CLK(CLK), .Q(out_75), .Q_not(out_79));
  d_flip_flop d_flip_flop_3 (.A(in_19), .B(in_23), .SEL(SEL), .CLK(CLK), .Q(out_83), .Q_not(out_87));
  d_flip_flop d_flip_flop_4 (.A(in_27), .B(in_31), .SEL(SEL), .CLK(CLK), .Q(out_91), .Q_not(out_95));
  d_flip_flop d_flip_flop_5 (.A(in_35), .B(in_39), .SEL(SEL), .CLK(CLK), .Q(out_99), .Q_not(out_103));
  d_flip_flop d_flip_flop_6 (.A(in_43), .B(in_47), .SEL(SEL), .CLK(CLK), .Q(out_107), .Q_not(out_111));
  d_flip_flop d_flip_flop_7 (.A(in_51), .B(in_55), .SEL(SEL), .CLK(CLK), .Q(out_115), .Q_not(out_119));
  d_flip_flop d_flip_flop_8 (.A(in_59), .B(in_63), .SEL(SEL), .CLK(CLK), .Q(out_123), .Q_not(out_127));
  d_flip_flop d_flip_flop_9 (.A(A1), .B(B1), .SEL(SEL), .CLK(CLK), .Q(Q_1), .Q_not(Q_1_not));
  d_flip_flop d_flip_flop_10 (.A(in_12), .B(in_16), .SEL(SEL), .CLK(CLK), .Q(out_76), .Q_not(out_80));
  d_flip_flop d_flip_flop_11 (.A(in_20), .B(in_24), .SEL(SEL), .CLK(CLK), .Q(out_84), .Q_not(out_88));
  d_flip_flop d_flip_flop_12 (.A(in_28), .B(in_32), .SEL(SEL), .CLK(CLK), .Q(out_92), .Q_not(out_96));
  d_flip_flop d_flip_flop_13 (.A(in_36), .B(in_40), .SEL(SEL), .CLK(CLK), .Q(out_100), .Q_not(out_104));
  d_flip_flop d_flip_flop_14 (.A(in_44), .B(in_48), .SEL(SEL), .CLK(CLK), .Q(out_108), .Q_not(out_112));
  d_flip_flop d_flip_flop_15 (.A(in_52), .B(in_56), .SEL(SEL), .CLK(CLK), .Q(out_116), .Q_not(out_120));
  d_flip_flop d_flip_flop_16 (.A(in_60), .B(in_64), .SEL(SEL), .CLK(CLK), .Q(out_124), .Q_not(out_128));
  d_flip_flop d_flip_flop_17 (.A(A2), .B(B2), .SEL(SEL), .CLK(CLK), .Q(Q_2), .Q_not(Q_2_not));
  d_flip_flop d_flip_flop_18 (.A(in_13), .B(in_17), .SEL(SEL), .CLK(CLK), .Q(out_77), .Q_not(out_81));
  d_flip_flop d_flip_flop_19 (.A(in_21), .B(in_25), .SEL(SEL), .CLK(CLK), .Q(out_85), .Q_not(out_89));
  d_flip_flop d_flip_flop_20 (.A(in_29), .B(in_33), .SEL(SEL), .CLK(CLK), .Q(out_93), .Q_not(out_97));
  d_flip_flop d_flip_flop_21 (.A(in_37), .B(in_41), .SEL(SEL), .CLK(CLK), .Q(out_101), .Q_not(out_105));
  d_flip_flop d_flip_flop_22 (.A(in_45), .B(in_49), .SEL(SEL), .CLK(CLK), .Q(out_109), .Q_not(out_113));
  d_flip_flop d_flip_flop_23 (.A(in_53), .B(in_57), .SEL(SEL), .CLK(CLK), .Q(out_117), .Q_not(out_121));
  d_flip_flop d_flip_flop_24 (.A(in_61), .B(in_65), .SEL(SEL), .CLK(CLK), .Q(out_125), .Q_not(out_129));
  d_flip_flop d_flip_flop_25 (.A(A3), .B(B3), .SEL(SEL), .CLK(CLK), .Q(Q_3), .Q_not(Q_3_not));
  d_flip_flop d_flip_flop_26 (.A(in_14), .B(in_18), .SEL(SEL), .CLK(CLK), .Q(out_78), .Q_not(out_82));
  d_flip_flop d_flip_flop_27 (.A(in_22), .B(in_26), .SEL(SEL), .CLK(CLK), .Q(out_86), .Q_not(out_90));
  d_flip_flop d_flip_flop_28 (.A(in_30), .B(in_34), .SEL(SEL), .CLK(CLK), .Q(out_94), .Q_not(out_98));
  d_flip_flop d_flip_flop_29 (.A(in_38), .B(in_42), .SEL(SEL), .CLK(CLK), .Q(out_102), .Q_not(out_106));
  d_flip_flop d_flip_flop_30 (.A(in_46), .B(in_50), .SEL(SEL), .CLK(CLK), .Q(out_110), .Q_not(out_114));
  d_flip_flop d_flip_flop_31 (.A(in_54), .B(in_58), .SEL(SEL), .CLK(CLK), .Q(out_118), .Q_not(out_122));
  d_flip_flop d_flip_flop_32 (.A(in_62), .B(in_66), .SEL(SEL), .CLK(CLK), .Q(out_126), .Q_not(out_130));
endmodule

module sr_latch (
  input  R,
  input  S,
  output out_3,
  output out_4
);

  nand nand_1 (out_3, R, out_4);
  nand nand_2 (out_4, out_3, S);
endmodule

module d_latch (
  input  in_1,
  input  in_2,
  output out_3,
  output out_4
);

  wire nand_1_out, nand_2_out, not_1_out;

  not not_1 (not_1_out, in_1);
  nand nand_1 (nand_1_out, in_1, in_2);
  nand nand_2 (nand_2_out, not_1_out, in_2);
  sr_latch sr_latch_1 (.R(nand_1_out), .S(nand_2_out), .out_3(out_3), .out_4(out_4));
endmodule

module d_flip_flop (
  input  A,
  input  B,
  input  SEL,
  input  CLK,
  output Q,
  output Q_not
);

  wire MASTER_out_3, mux_2_to_1_1_out_4, not_1_out;

  mux_2_to_1 mux_2_to_1_1 (.A(A), .B(B), .SEL(SEL), .out_4(mux_2_to_1_1_out_4));
  not not_1 (not_1_out, CLK);
  d_latch MASTER (.in_1(mux_2_to_1_1_out_4), .in_2(not_1_out), .out_3(MASTER_out_3));  // open: out_4
  d_latch SLAVE (.in_1(MASTER_out_3), .in_2(CLK), .out_3(Q), .out_4(Q_not));
endmodule

module mux_2_to_1 (
  input  A,
  input  B,
  input  SEL,
  output out_4
);

  wire a_and_selnot_out, b_and_sel_out, not_1_out;

  not not_1 (not_1_out, SEL);
  nand a_and_selnot (a_and_selnot_out, A, not_1_out);
  nand b_and_sel (b_and_sel_out, B, SEL);
  nand Y (out_4, a_and_selnot_out, b_and_sel_out);
endmodule

module overflow_flag (
  input  B_MSB,
  input  A_MSB,
  input  R_MSB,
  input  OP,
  output out_5
);

  wire A_XNOR_B_out, A_XOR_B_out, A_XOR_R_out, ADDITION_out, R_XOR_A_out, SUBTRACTION_out;

  xnor A_XNOR_B (A_XNOR_B_out, B_MSB, A_MSB);
  xor R_XOR_A (R_XOR_A_out, A_MSB, R_MSB);
  xor A_XOR_B (A_XOR_B_out, A_MSB, B_MSB);
  xor A_XOR_R (A_XOR_R_out, A_MSB, R_MSB);
  and ADDITION (ADDITION_out, A_XNOR_B_out, R_XOR_A_out);
  and SUBTRACTION (SUBTRACTION_out, A_XOR_B_out, A_XOR_R_out);
  mux_2_to_1 mux_2_to_1_1 (.A(ADDITION_out), .B(SUBTRACTION_out), .SEL(OP), .out_4(out_5));
endmodule
