// Logisim project Subtractor4Bit.circ as structural Verilog: 1 circuit, main circuit main
module main (
  input  in_1,
  input  in_2,
  input  in_3,
  input  in_4,
  input  in_5,
  input  in_6,
  input  in_7,
  input  in_8,
  input  in_9,
  output out_10
);

  wire and_1_out, and_2_out, and_3_out, and_4_out, and_5_out, and_6_out, and_7_out, and_8_out, or_1_out,
       or_2_out, or_3_out, xor_1_out, xor_2_out, xor_4_out, xor_5_out, xor_7_out, xor_8_out, xor_10_out,
       xor_11_out;
  wire [3:0] xor_3_out;

  xor xor_1 (xor_1_out, in_7, in_9);
  xor xor_2 (xor_2_out, in_3, xor_1_out);
  and and_1 (and_1_out, in_3, xor_1_out);
  and and_2 (and_2_out, xor_2_out, in_9);
  xor xor_3 (xor_3_out[0], xor_2_out, in_9);
  or or_1 (or_1_out, and_1_out, and_2_out);
  xor xor_4 (xor_4_out, in_8, in_9);
  Hex_Digit_Display hex_digit_display_1 (.value(xor_3_out));  // open: dp
  xor xor_5 (xor_5_out, in_4, xor_4_out);
  and and_3 (and_3_out, in_4, xor_4_out);
  and and_4 (and_4_out, xor_5_out, or_1_out);
  xor xor_6 (xor_3_out[1], xor_5_out, or_1_out);
  or or_2 (or_2_out, and_3_out, and_4_out);
  xor xor_7 (xor_7_out, in_5, in_9);
  xor xor_8 (xor_8_out, in_1, xor_7_out);
  and and_5 (and_5_out, in_1, xor_7_out);
  and and_6 (and_6_out, xor_8_out, or_2_out);
  xor xor_9 (xor_3_out[2], xor_8_out, or_2_out);
  or or_3 (or_3_out, and_5_out, and_6_out);
  xor xor_10 (xor_10_out, in_6, in_9);
  xor xor_11 (xor_11_out, in_2, xor_10_out);
  and and_7 (and_7_out, in_2, xor_10_out);
  and and_8 (and_8_out, xor_11_out, or_3_out);
  xor xor_12 (xor_3_out[3], xor_11_out, or_3_out);
  or or_4 (out_10, and_7_out, and_8_out);
endmodule
