// Logisim project Subtractor8Bit.circ as structural Verilog: 1 circuit, main circuit main
module main (
  input  in_1,
  input  in_2,
  input  in_3,
  input  in_4,
  input  in_5,
  input  in_6,
  input  in_7,
  input  in_8,
  input  in_9,
  input  in_10,
  input  in_11,
  input  in_12,
  input  in_13,
  input  in_14,
  input  in_15,
  input  in_16,
  input  in_17
);

  wire and_1_out, and_2_out, and_3_out, and_4_out, and_5_out, and_6_out, and_7_out, and_8_out, and_9_out,
       and_10_out, and_11_out, and_12_out, and_13_out, and_14_out, and_15_out, and_16_out, or_1_out,
       or_2_out, or_3_out, or_4_out, or_5_out, or_6_out, or_7_out, xor_1_out, xor_2_out, xor_4_out,
       xor_5_out, xor_7_out, xor_8_out, xor_10_out, xor_11_out, xor_13_out, xor_14_out, xor_16_out,
       xor_17_out, xor_19_out, xor_20_out, xor_22_out, xor_23_out;
  wire [7:0] xor_3_out;

  xor xor_1 (xor_1_out, in_15, in_17);
  xor xor_2 (xor_2_out, in_7, xor_1_out);
  and and_1 (and_1_out, in_7, xor_1_out);
  and and_2 (and_2_out, xor_2_out, in_17);
  Hex_Digit_Display hex_digit_display_1 (.value(xor_3_out[7:4]));  // open: dp
  xor xor_3 (xor_3_out[0], xor_2_out, in_17);
  or or_1 (or_1_out, and_1_out, and_2_out);
  Hex_Digit_Display hex_digit_display_2 (.value(xor_3_out[3:0]));  // open: dp
  xor xor_4 (xor_4_out, in_16, in_17);
  xor xor_5 (xor_5_out, in_8, xor_4_out);
  and and_3 (and_3_out, in_8, xor_4_out);
  and and_4 (and_4_out, xor_5_out, or_1_out);
  xor xor_6 (xor_3_out[1], xor_5_out, or_1_out);
  or or_2 (or_2_out, and_3_out, and_4_out);
  xor xor_7 (xor_7_out, in_10, in_17);
  xor xor_8 (xor_8_out, in_2, xor_7_out);
  and and_5 (and_5_out, in_2, xor_7_out);
  and and_6 (and_6_out, xor_8_out, or_2_out);
  xor xor_9 (xor_3_out[2], xor_8_out, or_2_out);
  or or_3 (or_3_out, and_5_out, and_6_out);
  xor xor_10 (xor_10_out, in_11, in_17);
  xor xor_11 (xor_11_out, in_3, xor_10_out);
  and and_7 (and_7_out, in_3, xor_10_out);
  and and_8 (and_8_out, xor_11_out, or_3_out);
  xor xor_12 (xor_3_out[3], xor_11_out, or_3_out);
  or or_4 (or_4_out, and_7_out, and_8_out);
  xor xor_13 (xor_13_out, in_9, in_17);
  xor xor_14 (xor_14_out, in_1, xor_13_out);
  and and_9 (and_9_out, in_1, xor_13_out);
  and and_10 (and_10_out, xor_14_out, or_4_out);
  xor xor_15 (xor_3_out[4], xor_14_out, or_4_out);
  or or_5 (or_5_out, and_9_out, and_10_out);
  xor xor_16 (xor_16_out, in_12, in_17);
  xor xor_17 (xor_17_out, in_4, xor_16_out);
  and and_11 (and_11_out, in_4, xor_16_out);
  and and_12 (and_12_out, xor_17_out, or_5_out);
  xor xor_18 (xor_3_out[5], xor_17_out, or_5_out);
  or or_6 (or_6_out, and_11_out, and_12_out);
  xor xor_19 (xor_19_out, in_13, in_17);
  xor xor_20 (xor_20_out, in_5, xor_19_out);
  and and_13 (and_13_out, in_5, xor_19_out);
  and and_14 (and_14_out, xor_20_out, or_6_out);
  xor xor_21 (xor_3_out[6], xor_20_out, or_6_out);
  or or_7 (or_7_out, and_13_out, and_14_out);
  xor xor_22 (xor_22_out, in_14, in_17);
  xor xor_23 (xor_23_out, in_6, xor_22_out);
  and and_15 (and_15_out, in_6, xor_22_out);
  and and_16 (and_16_out, xor_23_out, or_7_out);
  xor xor_24 (xor_3_out[7], xor_23_out, or_7_out);
  // OR_Gate or_8 has open pins: in0=and_15_out, in1=and_16_out, out=open
endmodule
