// Logisim project adder_32bit.circ as structural Verilog: 1 circuit, main circuit adder_32
module adder_32 (
  input  A,
  input  in_2,
  input  in_3,
  input  in_4,
  input  in_5,
  input  in_6,
  input  in_7,
  input  in_8,
  input  B,
  input  in_10,
  input  in_11,
  input  in_12,
  input  in_13,
  input  in_14,
  input  in_15,
  input  in_16,
  input  Cin,
  input  in_18,
  input  in_19,
  input  in_20,
  input  in_21,
  input  in_22,
  input  in_23,
  input  in_24,
  input  in_25,
  input  in_26,
  input  in_27,
  input  in_28,
  input  in_29,
  input  in_30,
  input  in_31,
  input  in_32,
  input  in_33,
  input  in_34,
  input  in_35,
  input  in_36,
  input  in_37,
  input  in_38,
  input  in_39,
  input  in_40,
  input  in_41,
  input  in_42,
  input  in_43,
  input  in_44,
  input  in_45,
  input  in_46,
  input  in_47,
  input  in_48,
  input  in_49,
  input  in_50,
  input  in_51,
  input  in_52,
  input  in_53,
  input  in_54,
  input  in_55,
  input  in_56,
  input  in_57,
  input  in_58,
  input  in_59,
  input  in_60,
  input  in_61,
  input  in_62,
  input  in_63,
  input  in_64,
  input  in_65
);

  wire and_1_out, and_2_out, and_3_out, and_4_out, and_5_out, and_6_out, and_7_out, and_8_out, and_9_out,
       and_10_out, and_11_out, and_12_out, and_13_out, and_14_out, and_15_out, and_16_out, and_17_out,
       and_18_out, and_19_out, and_20_out, and_21_out, and_22_out, and_23_out, and_24_out, and_25_out,
       and_26_out, and_27_out, and_28_out, and_29_out, and_30_out, and_31_out, and_32_out, and_33_out,
       and_34_out, and_35_out, and_36_out, and_37_out, and_38_out, and_39_out, and_40_out, and_41_out,
       and_42_out, and_43_out, and_44_out, and_45_out, and_46_out, and_47_out, and_48_out, and_49_out,
       and_50_out, and_51_out, and_52_out, and_53_out, and_54_out, and_55_out, and_56_out, and_57_out,
       and_58_out, and_59_out, and_60_out, and_61_out, and_62_out, and_a_beff_out, and_Cin_xorabeff_out,
       b_eff_out, or_1_out, or_2_out, or_3_out, or_4_out, or_5_out, or_6_out, or_7_out, or_8_out, or_9_out,
       or_10_out, or_11_out, or_12_out, or_13_out, or_14_out, or_15_out, or_16_out, or_17_out, or_18_out,
       or_19_out, or_20_out, or_21_out, or_22_out, or_23_out, or_24_out, or_25_out, or_26_out, or_27_out,
       or_28_out, or_29_out, or_30_out, or_andab_andCinxorab_out, xor_1_out, xor_2_out, xor_3_out, xor_4_out,
       xor_5_out, xor_6_out, xor_10_out, xor_11_out, xor_12_out, xor_13_out, xor_14_out, xor_15_out,
       xor_16_out, xor_17_out, xor_22_out, xor_23_out, xor_24_out, xor_25_out, xor_26_out, xor_27_out,
       xor_28_out, xor_29_out, xor_34_out, xor_35_out, xor_36_out, xor_37_out, xor_38_out, xor_39_out,
       xor_40_out, xor_41_out, xor_46_out, xor_47_out, xor_48_out, xor_49_out, xor_50_out, xor_51_out,
       xor_52_out, xor_53_out, xor_58_out, xor_59_out, xor_60_out, xor_61_out, xor_62_out, xor_63_out,
       xor_64_out, xor_65_out, xor_70_out, xor_71_out, xor_72_out, xor_73_out, xor_74_out, xor_75_out,
       xor_76_out, xor_77_out, xor_82_out, xor_83_out, xor_84_out, xor_85_out, xor_86_out, xor_87_out,
       xor_88_out, xor_89_out, xor_a_beff_out;
  wire [3:0] xor_7_out, xor_8_out, xor_9_out, xor_54_out, xor_55_out, xor_56_out, xor_57_out,
       xor_abeff_Cin_out;

  Hex_Digit_Display hex_digit_display_1 (.value(xor_57_out));  // open: dp
  Hex_Digit_Display hex_digit_display_2 (.value(xor_9_out));  // open: dp
  Hex_Digit_Display hex_digit_display_3 (.value(xor_56_out));  // open: dp
  Hex_Digit_Display hex_digit_display_4 (.value(xor_8_out));  // open: dp
  Hex_Digit_Display hex_digit_display_5 (.value(xor_55_out));  // open: dp
  Hex_Digit_Display hex_digit_display_6 (.value(xor_7_out));  // open: dp
  Hex_Digit_Display hex_digit_display_7 (.value(xor_54_out));  // open: dp
  Hex_Digit_Display hex_digit_display_8 (.value(xor_abeff_Cin_out));  // open: dp
  xor b_eff (b_eff_out, B, Cin);
  xor xor_1 (xor_1_out, in_26, Cin);
  xor xor_2 (xor_2_out, in_42, or_29_out);
  xor xor_3 (xor_3_out, in_58, or_29_out);
  xor xor_a_beff (xor_a_beff_out, A, b_eff_out);
  xor xor_4 (xor_4_out, in_18, xor_1_out);
  xor xor_5 (xor_5_out, in_34, xor_2_out);
  xor xor_6 (xor_6_out, in_50, xor_3_out);
  and and_a_beff (and_a_beff_out, A, b_eff_out);
  and and_Cin_xorabeff (and_Cin_xorabeff_out, xor_a_beff_out, Cin);
  and and_1 (and_1_out, in_18, xor_1_out);
  and and_2 (and_2_out, xor_4_out, or_28_out);
  and and_3 (and_3_out, in_34, xor_2_out);
  and and_4 (and_4_out, xor_5_out, or_29_out);
  and and_5 (and_5_out, in_50, xor_3_out);
  and and_6 (and_6_out, xor_6_out, or_30_out);
  xor xor_abeff_Cin (xor_abeff_Cin_out[0], xor_a_beff_out, Cin);
  or or_andab_andCinxorab (or_andab_andCinxorab_out, and_a_beff_out, and_Cin_xorabeff_out);
  xor xor_7 (xor_7_out[0], xor_4_out, or_28_out);
  or or_1 (or_1_out, and_1_out, and_2_out);
  xor xor_8 (xor_8_out[0], xor_5_out, or_29_out);
  or or_2 (or_2_out, and_3_out, and_4_out);
  xor xor_9 (xor_9_out[0], xor_6_out, or_30_out);
  or or_3 (or_3_out, and_5_out, and_6_out);
  LED led_1 (.in(xor_abeff_Cin_out[0]));
  LED led_2 (.in(xor_7_out[0]));
  LED led_3 (.in(xor_8_out[0]));
  LED led_4 (.in(xor_9_out[0]));
  xor xor_10 (xor_10_out, in_10, Cin);
  xor xor_11 (xor_11_out, in_27, Cin);
  xor xor_12 (xor_12_out, in_43, or_29_out);
  xor xor_13 (xor_13_out, in_59, or_29_out);
  xor xor_14 (xor_14_out, in_2, xor_10_out);
  xor xor_15 (xor_15_out, in_19, xor_11_out);
  xor xor_16 (xor_16_out, in_35, xor_12_out);
  xor xor_17 (xor_17_out, in_51, xor_13_out);
  and and_7 (and_7_out, in_2, xor_10_out);
  and and_8 (and_8_out, xor_14_out, or_andab_andCinxorab_out);
  and and_9 (and_9_out, in_19, xor_11_out);
  and and_10 (and_10_out, xor_15_out, or_1_out);
  and and_11 (and_11_out, in_35, xor_12_out);
  and and_12 (and_12_out, xor_16_out, or_2_out);
  and and_13 (and_13_out, in_51, xor_13_out);
  and and_14 (and_14_out, xor_17_out, or_3_out);
  xor xor_18 (xor_abeff_Cin_out[1], xor_14_out, or_andab_andCinxorab_out);
  or or_4 (or_4_out, and_7_out, and_8_out);
  xor xor_19 (xor_7_out[1], xor_15_out, or_1_out);
  or or_5 (or_5_out, and_9_out, and_10_out);
  xor xor_20 (xor_8_out[1], xor_16_out, or_2_out);
  or or_6 (or_6_out, and_11_out, and_12_out);
  xor xor_21 (xor_9_out[1], xor_17_out, or_3_out);
  or or_7 (or_7_out, and_13_out, and_14_out);
  LED led_5 (.in(xor_abeff_Cin_out[1]));
  LED led_6 (.in(xor_7_out[1]));
  LED led_7 (.in(xor_8_out[1]));
  LED led_8 (.in(xor_9_out[1]));
  xor xor_22 (xor_22_out, in_11, Cin);
  xor xor_23 (xor_23_out, in_28, Cin);
  xor xor_24 (xor_24_out, in_44, or_29_out);
  xor xor_25 (xor_25_out, in_60, or_29_out);
  xor xor_26 (xor_26_out, in_3, xor_22_out);
  xor xor_27 (xor_27_out, in_20, xor_23_out);
  xor xor_28 (xor_28_out, in_36, xor_24_out);
  xor xor_29 (xor_29_out, in_52, xor_25_out);
  and and_15 (and_15_out, in_3, xor_22_out);
  and and_16 (and_16_out, xor_26_out, or_4_out);
  and and_17 (and_17_out, in_20, xor_23_out);
  and and_18 (and_18_out, xor_27_out, or_5_out);
  and and_19 (and_19_out, in_36, xor_24_out);
  and and_20 (and_20_out, xor_28_out, or_6_out);
  and and_21 (and_21_out, in_52, xor_25_out);
  and and_22 (and_22_out, xor_29_out, or_7_out);
  xor xor_30 (xor_abeff_Cin_out[2], xor_26_out, or_4_out);
  LED led_9 (.in(xor_abeff_Cin_out[2]));
  or or_8 (or_8_out, and_15_out, and_16_out);
  xor xor_31 (xor_7_out[2], xor_27_out, or_5_out);
  LED led_10 (.in(xor_7_out[2]));
  or or_9 (or_9_out, and_17_out, and_18_out);
  xor xor_32 (xor_8_out[2], xor_28_out, or_6_out);
  LED led_11 (.in(xor_8_out[2]));
  or or_10 (or_10_out, and_19_out, and_20_out);
  xor xor_33 (xor_9_out[2], xor_29_out, or_7_out);
  LED led_12 (.in(xor_9_out[2]));
  or or_11 (or_11_out, and_21_out, and_22_out);
  xor xor_34 (xor_34_out, in_12, Cin);
  xor xor_35 (xor_35_out, in_29, Cin);
  xor xor_36 (xor_36_out, in_45, or_29_out);
  xor xor_37 (xor_37_out, in_61, or_29_out);
  xor xor_38 (xor_38_out, in_4, xor_34_out);
  xor xor_39 (xor_39_out, in_21, xor_35_out);
  xor xor_40 (xor_40_out, in_37, xor_36_out);
  xor xor_41 (xor_41_out, in_53, xor_37_out);
  and and_23 (and_23_out, in_4, xor_34_out);
  and and_24 (and_24_out, xor_38_out, or_8_out);
  and and_25 (and_25_out, in_21, xor_35_out);
  and and_26 (and_26_out, xor_39_out, or_9_out);
  and and_27 (and_27_out, in_37, xor_36_out);
  and and_28 (and_28_out, xor_40_out, or_10_out);
  and and_29 (and_29_out, in_53, xor_37_out);
  and and_30 (and_30_out, xor_41_out, or_11_out);
  xor xor_42 (xor_abeff_Cin_out[3], xor_38_out, or_8_out);
  LED led_13 (.in(xor_abeff_Cin_out[3]));
  or or_12 (or_12_out, and_23_out, and_24_out);
  xor xor_43 (xor_7_out[3], xor_39_out, or_9_out);
  LED led_14 (.in(xor_7_out[3]));
  or or_13 (or_13_out, and_25_out, and_26_out);
  xor xor_44 (xor_8_out[3], xor_40_out, or_10_out);
  LED led_15 (.in(xor_8_out[3]));
  or or_14 (or_14_out, and_27_out, and_28_out);
  xor xor_45 (xor_9_out[3], xor_41_out, or_11_out);
  LED led_16 (.in(xor_9_out[3]));
  or or_15 (or_15_out, and_29_out, and_30_out);
  xor xor_46 (xor_46_out, in_13, Cin);
  xor xor_47 (xor_47_out, in_30, Cin);
  xor xor_48 (xor_48_out, in_46, or_29_out);
  xor xor_49 (xor_49_out, in_62, or_29_out);
  xor xor_50 (xor_50_out, in_5, xor_46_out);
  xor xor_51 (xor_51_out, in_22, xor_47_out);
  xor xor_52 (xor_52_out, in_38, xor_48_out);
  xor xor_53 (xor_53_out, in_54, xor_49_out);
  and and_31 (and_31_out, in_5, xor_46_out);
  and and_32 (and_32_out, xor_50_out, or_12_out);
  and and_33 (and_33_out, in_22, xor_47_out);
  and and_34 (and_34_out, xor_51_out, or_13_out);
  and and_35 (and_35_out, in_38, xor_48_out);
  and and_36 (and_36_out, xor_52_out, or_14_out);
  and and_37 (and_37_out, in_54, xor_49_out);
  and and_38 (and_38_out, xor_53_out, or_15_out);
  xor xor_54 (xor_54_out[0], xor_50_out, or_12_out);
  or or_16 (or_16_out, and_31_out, and_32_out);
  xor xor_55 (xor_55_out[0], xor_51_out, or_13_out);
  or or_17 (or_17_out, and_33_out, and_34_out);
  xor xor_56 (xor_56_out[0], xor_52_out, or_14_out);
  or or_18 (or_18_out, and_35_out, and_36_out);
  xor xor_57 (xor_57_out[0], xor_53_out, or_15_out);
  or or_19 (or_19_out, and_37_out, and_38_out);
  LED led_17 (.in(xor_54_out[0]));
  LED led_18 (.in(xor_55_out[0]));
  LED led_19 (.in(xor_56_out[0]));
  LED led_20 (.in(xor_57_out[0]));
  xor xor_58 (xor_58_out, in_14, Cin);
  xor xor_59 (xor_59_out, in_31, Cin);
  xor xor_60 (xor_60_out, in_47, or_29_out);
  xor xor_61 (xor_61_out, in_63, or_29_out);
  xor xor_62 (xor_62_out, in_6, xor_58_out);
  xor xor_63 (xor_63_out, in_23, xor_59_out);
  xor xor_64 (xor_64_out, in_39, xor_60_out);
  xor xor_65 (xor_65_out, in_55, xor_61_out);
  and and_39 (and_39_out, in_6, xor_58_out);
  and and_40 (and_40_out, xor_62_out, or_16_out);
  and and_41 (and_41_out, in_23, xor_59_out);
  and and_42 (and_42_out, xor_63_out, or_17_out);
  and and_43 (and_43_out, in_39, xor_60_out);
  and and_44 (and_44_out, xor_64_out, or_18_out);
  and and_45 (and_45_out, in_55, xor_61_out);
  and and_46 (and_46_out, xor_65_out, or_19_out);
  xor xor_66 (xor_54_out[1], xor_62_out, or_16_out);
  or or_20 (or_20_out, and_39_out, and_40_out);
  xor xor_67 (xor_55_out[1], xor_63_out, or_17_out);
  or or_21 (or_21_out, and_41_out, and_42_out);
  xor xor_68 (xor_56_out[1], xor_64_out, or_18_out);
  or or_22 (or_22_out, and_43_out, and_44_out);
  xor xor_69 (xor_57_out[1], xor_65_out, or_19_out);
  or or_23 (or_23_out, and_45_out, and_46_out);
  LED led_21 (.in(xor_54_out[1]));
  LED led_22 (.in(xor_55_out[1]));
  LED led_23 (.in(xor_56_out[1]));
  LED led_24 (.in(xor_57_out[1]));
  xor xor_70 (xor_70_out, in_15, Cin);
  xor xor_71 (xor_71_out, in_32, Cin);
  xor xor_72 (xor_72_out, in_48, or_29_out);
  xor xor_73 (xor_73_out, in_64, or_29_out);
  xor xor_74 (xor_74_out, in_7, xor_70_out);
  xor xor_75 (xor_75_out, in_24, xor_71_out);
  xor xor_76 (xor_76_out, in_40, xor_72_out);
  xor xor_77 (xor_77_out, in_56, xor_73_out);
  and and_47 (and_47_out, in_7, xor_70_out);
  and and_48 (and_48_out, xor_74_out, or_20_out);
  and and_49 (and_49_out, in_24, xor_71_out);
  and and_50 (and_50_out, xor_75_out, or_21_out);
  and and_51 (and_51_out, in_40, xor_72_out);
  and and_52 (and_52_out, xor_76_out, or_22_out);
  and and_53 (and_53_out, in_56, xor_73_out);
  and and_54 (and_54_out, xor_77_out, or_23_out);
  xor xor_78 (xor_54_out[2], xor_74_out, or_20_out);
  LED led_25 (.in(xor_54_out[2]));
  or or_24 (or_24_out, and_47_out, and_48_out);
  xor xor_79 (xor_55_out[2], xor_75_out, or_21_out);
  LED led_26 (.in(xor_55_out[2]));
  or or_25 (or_25_out, and_49_out, and_50_out);
  xor xor_80 (xor_56_out[2], xor_76_out, or_22_out);
  LED led_27 (.in(xor_56_out[2]));
  or or_26 (or_26_out, and_51_out, and_52_out);
  xor xor_81 (xor_57_out[2], xor_77_out, or_23_out);
  LED led_28 (.in(xor_57_out[2]));
  or or_27 (or_27_out, and_53_out, and_54_out);
  xor xor_82 (xor_82_out, in_16, Cin);
  xor xor_83 (xor_83_out, in_33, Cin);
  xor xor_84 (xor_84_out, in_49, or_29_out);
  xor xor_85 (xor_85_out, in_65, or_29_out);
  xor xor_86 (xor_86_out, in_8, xor_82_out);
  xor xor_87 (xor_87_out, in_25, xor_83_out);
  xor xor_88 (xor_88_out, in_41, xor_84_out);
  xor xor_89 (xor_89_out, in_57, xor_85_out);
  and and_55 (and_55_out, in_8, xor_82_out);
  and and_56 (and_56_out, xor_86_out, or_24_out);
  and and_57 (and_57_out, in_25, xor_83_out);
  and and_58 (and_58_out, xor_87_out, or_25_out);
  and and_59 (and_59_out, in_41, xor_84_out);
  and and_60 (and_60_out, xor_88_out, or_26_out);
  and and_61 (and_61_out, in_57, xor_85_out);
  and and_62 (and_62_out, xor_89_out, or_27_out);
  xor xor_90 (xor_54_out[3], xor_86_out, or_24_out);
  LED led_29 (.in(xor_54_out[3]));
  or or_28 (or_28_out, and_55_out, and_56_out);
  xor xor_91 (xor_55_out[3], xor_87_out, or_25_out);
  LED led_30 (.in(xor_55_out[3]));
  or or_29 (or_29_out, and_57_out, and_58_out);
  xor xor_92 (xor_56_out[3], xor_88_out, or_26_out);
  LED led_31 (.in(xor_56_out[3]));
  or or_30 (or_30_out, and_59_out, and_60_out);
  xor xor_93 (xor_57_out[3], xor_89_out, or_27_out);
  LED led_32 (.in(xor_57_out[3]));
  // OR_Gate or_31 has open pins: in0=and_61_out, in1=and_62_out, out=open
endmodule
