// Logisim project debug_armv4t.circ as structural Verilog: 33 circuits, main circuit main
// memory_updated_base
module main (
  input  in_1,
  output out_2,
  output [31:0] out_3,
  output branch_taken,
  output condition_pass,
  output [31:0] out_6,
  output [31:0] out_7,
  output [31:0] out_8,
  output [31:0] out_9,
  output [31:0] out_10,
  output [31:0] out_11,
  output [31:0] out_12,
  output [31:0] RD_A,
  output [31:0] out_14,
  output [31:0] out_15,
  output [31:0] out_16,
  output [31:0] out_17,
  output [31:0] out_18,
  output [31:0] out_19,
  output [31:0] out_20,
  output [31:0] out_21,
  output [31:0] out_22,
  output [31:0] out_23,
  output [31:0] out_24,
  output normal_reg_WE,
  output out_26,
  output is_BX,
  output is_BL,
  output bl_taken,
  output mem_class,
  output is_STR,
  output is_LDR,
  output [31:0] out_33,
  output [31:0] mem_offset,
  output [31:0] memory_address,
  output [31:0] memory_offset_effective,
  output ldr_reg_we
);

  wire alu_1_write_enable_out, and_1_out, and_2_out, and_3_out, and_5_out, and_6_out, and_9_out, and_10_out,
       and_12_out, block_transfer_control_1_active, block_transfer_control_1_done,
       block_transfer_control_1_hold_pc, block_transfer_control_1_load_enable,
       block_transfer_control_1_reg_selected, block_transfer_control_1_store_enable, branch_class_out,
       bx_taken_out, clock_1_out, comparator_2_eq, comparator_3_eq, comparator_4_eq, comparator_5_eq,
       comparator_6_eq, comparator_7_eq, comparator_8_eq, CSPR_enable_out, data_ram_we_out, final_reg_we_out,
       is_B_out, multiplexer_10_out, not_1_out, not_2_out, not_3_out, not_4_out, not_5_out, not_6_out,
       not_7_out, not_8_out, not_9_out, not_10_out, not_link_out, or_1_out, or_2_out, or_3_out, or_4_out,
       or_5_out, or_6_out, or_7_out, or_8_out, or_9_out, or_10_out, or_11_out, or_12_out, or_13_out,
       or_14_out, or_15_out, pc_apply_out, pc_defer_out, pc_pending_2_q, undriven, undriven_2;
  wire [1:0] multiplexer_16_out;
  wire [3:0] alu_1_v, block_transfer_control_1_reg_idx, CSPR_q, multiplexer_6_out, multiplexer_7_out,
       multiplexer_9_out, multiplexer_12_out, multiplexer_13_out, rom_2_data_2;
  wire [4:0] multiplexer_14_out;
  wire [9:0] pc_fetch_1_pc_out, rom_3_data;
  wire [15:0] rom_2_data_3;
  wire [23:12] rom_2_data;
  wire [31:0] adder_1_out, adder_2_out, adder_3_out, bit_extender_2_out, bit_extender_3_out,
       bit_extender_4_out, bit_extender_5_out, block_transfer_control_1_final_address,
       block_transfer_control_1_transfer_address, bx_arm_target_out, multiplexer_1_out, multiplexer_2_out,
       multiplexer_3_out, multiplexer_4_out, multiplexer_5_out, multiplexer_8_out, multiplexer_11_out,
       multiplexer_15_out, multiplexer_18_out, pc_fetch_1_pc_plus4, pc_target_q, reg16x32_1_1_rd_a,
       reg16x32_1_1_rd_b, rom_1_data, shifter_1_out, shifter_2_out;

  // Probe on and_6_out
  not not_1 (not_1_out, block_transfer_control_1_done);
  and pc_defer (pc_defer_out, and_6_out, block_transfer_control_1_hold_pc);
  and and_1 (and_1_out, not_1_out, pc_pending_2_q);
  // Probe to_or_in1_1: pin names not known
  // Probe on and_6_out
  // Probe pc_defer_2: pin names not known
  or or_1 (or_1_out, pc_defer_out, and_1_out);
  or or_2 (or_2_out, or_15_out, bx_taken_out);
  // Probe to_or_in0_2: pin names not known
  // Probe pc_apply_1: pin names not known
  or or_3 (or_3_out, or_2_out, pc_apply_out, and_6_out);
  Multiplexer #(.width(32)) multiplexer_1 (
    .in0(bx_arm_target_out), .in1(multiplexer_8_out), .out(multiplexer_1_out), .sel(and_6_out));
  // Probe pc_apply_2: pin names not known
  // Probe pc_pending: pin names not known
  // Probe pc_target_2: pin names not known
  Clock clock_1 (.out(clock_1_out));
  or or_4 (or_4_out, bx_taken_out, pc_apply_out, and_6_out);
  Register #(.width(32)) pc_target (
    .D(multiplexer_1_out), .en(and_6_out), .clk(clock_1_out), .Q(pc_target_q), .clr(in_1));
  // Probe on multiplexer_1_out
  Register #(.width(1)) pc_pending_2 (.D(or_1_out), .clk(clock_1_out), .Q(pc_pending_2_q), .clr(in_1));  // open: en
  // Probe pc_target_1: pin names not known
  and pc_apply (pc_apply_out, block_transfer_control_1_done, pc_pending_2_q);
  Multiplexer #(.width(32)) multiplexer_2 (
    .in0(multiplexer_1_out), .in1(pc_target_q), .out(multiplexer_2_out), .sel(pc_apply_out));
  // Probe bt_store_enable: pin names not known
  // Probe addr_bit12: pin names not known
  // Probe pc_defer_1: pin names not known
  // Probe pc_branch: pin names not known
  // Probe bt_transfer_address: pin names not known
  // Probe litpool_addr: pin names not known
  // Probe on rom_2_data_3
  // Probe pc_abs_select: pin names not known
  not not_2 (not_2_out, memory_address[12]);
  // Probe bx_arm_target_1: pin names not known
  // Probe bx_taken_1: pin names not known
  ROM #(.addrWidth(10), .dataWidth(32)) rom_1 (.addr(memory_address[11:2]), .data(rom_1_data));
  // Probe pc_abs_target: pin names not known
  // Probe instr_27_4: pin names not known
  // Probe to_not_in_1: pin names not known
  block_transfer_control block_transfer_control_1 (
    .clk(clock_1_out), .rst(in_1), .start(or_12_out), .is_pop(and_9_out), .reg_list_in(rom_2_data_3),
    .base_value(RD_A), .U(rom_2_data[19]), .P(out_26), .hold_pc(block_transfer_control_1_hold_pc),
    .active(block_transfer_control_1_active), .done(block_transfer_control_1_done),
    .reg_idx(block_transfer_control_1_reg_idx), .reg_selected(block_transfer_control_1_reg_selected),
    .transfer_address(block_transfer_control_1_transfer_address),
    .final_address(block_transfer_control_1_final_address),
    .store_enable(block_transfer_control_1_store_enable), .load_enable(block_transfer_control_1_load_enable),
    .phase_reg_q(out_2));
  pc_fetch pc_fetch_1 (
    .CLK(clock_1_out), .BRANCH(or_3_out), .hold(block_transfer_control_1_hold_pc), .IMM(adder_2_out),
    .abs_target(multiplexer_2_out), .abs_select(or_4_out), .RST(in_1), .pc_plus4(pc_fetch_1_pc_plus4),
    .pc_out(pc_fetch_1_pc_out));
  // Probe on pc_fetch_1_pc_plus4
  Comparator #(.width(24)) comparator_1 (
    .a({rom_2_data[23:21], out_26, rom_2_data[19:12], rom_2_data_3[15:4]}), .b(24'h12fff1), .eq(is_BX));  // open: gt, lt
  not not_3 (not_3_out, out_16[0]);
  // Probe is_program_addr: pin names not known
  // Probe bt_phase_reg_q: pin names not known
  ROM #(.addrWidth(10), .dataWidth(32)) rom_2 (
    .addr(pc_fetch_1_pc_out),
    .data({rom_2_data_2, rom_2_data[23:21], out_26, rom_2_data[19:12], rom_2_data_3}));
  // Probe litpool_data: pin names not known
  // Probe on block_transfer_control_1_active
  // Probe on block_transfer_control_1_done
  // Probe on block_transfer_control_1_reg_idx
  // Probe on block_transfer_control_1_reg_selected
  // Probe on block_transfer_control_1_load_enable
  // Probe on pc_fetch_1_pc_out
  // Probe bx_taken_2: pin names not known
  // Probe bx_arm_target_3: pin names not known
  or or_5 (or_5_out, block_transfer_control_1_done, block_transfer_control_1_hold_pc);
  // Probe bt_reg_list_in: pin names not known
  // Probe regfile_wd: pin names not known
  and bx_taken (bx_taken_out, is_BX, not_3_out, condition_pass);
  assign bx_arm_target_out = out_16 & 32'hfffffffc;  // AND_Gate bx_arm_target, 32 bits wide
  // Probe ram_data_out: pin names not known
  Multiplexer #(.width(32)) multiplexer_3 (.in0(out_33), .in1(rom_1_data), .out(multiplexer_3_out), .sel(not_2_out));
  // Probe on rom_2_data[23:21]
  // Probe opcode: pin names not known
  // Probe on rom_2_data_2
  // Probe pc_word_addr: pin names not known
  // Probe memory_address: pin names not known
  // Probe to_probe_p_1: pin names not known
  // Probe rst: pin names not known
  // Probe splitter_bit0_1: pin names not known
  // Probe splitter_bit1_1: pin names not known
  // Probe splitter_bit2_1: pin names not known
  // Probe splitter_bit3_1: pin names not known
  // Probe splitter_bit4_1: pin names not known
  // Probe splitter_bit5_1: pin names not known
  // Probe splitter_bit6_1: pin names not known
  // Probe rd_a: pin names not known
  // Probe instr_31_25: pin names not known
  // Probe to_and_in1_1: pin names not known
  // Probe pc_pc_plus4: pin names not known
  // Probe shift_field: pin names not known
  // Probe rd_b: pin names not known
  // Probe pc_imm: pin names not known
  // Probe splitter_bit0_2: pin names not known
  // Probe splitter_bit1_2: pin names not known
  // Probe splitter_bit2_2: pin names not known
  // Probe splitter_bit3_2: pin names not known
  // Probe splitter_bit4_2: pin names not known
  // Probe splitter_bit5_2: pin names not known
  // Probe splitter_bit6_2: pin names not known
  // Probe splitter_bit7: pin names not known
  // Probe splitter_bit8_1: pin names not known
  // Probe splitter_bit9_1: pin names not known
  // Probe splitter_bit10: pin names not known
  // Probe splitter_bit11: pin names not known
  // Probe splitter_bit12: pin names not known
  // Probe splitter_bit13: pin names not known
  // Probe splitter_bit14: pin names not known
  // Probe splitter_bit15: pin names not known
  // Probe splitter_bit16: pin names not known
  // Probe splitter_bit17: pin names not known
  // Probe splitter_bit18: pin names not known
  // Probe splitter_bit19: pin names not known
  // Probe rd: pin names not known
  // Probe bt_final_address: pin names not known
  // Probe is_bx: pin names not known
  // Probe clk: pin names not known
  // Probe on rom_2_data_3[15:12]
  Comparator #(.width(3)) comparator_2 (.a(rom_2_data[23:21]), .b(3'b100), .eq(comparator_2_eq));  // open: gt, lt
  // Probe rm: pin names not known
  and and_2 (and_2_out, comparator_2_eq, condition_pass);
  // Probe branch_offset: pin names not known
  // Probe to_bit_extender_in: pin names not known
  // Probe on rom_2_data[15:12]
  Multiplexer #(.width(32)) multiplexer_4 (
    .in0(out_3), .in1(pc_fetch_1_pc_plus4), .out(multiplexer_4_out), .sel(bl_taken));
  // Probe to_or_in0_1: pin names not known
  // Probe on rom_2_data[15:12]
  // Probe to_multiplexer_in0_1: pin names not known
  // Probe on rom_2_data[16]
  // Probe on rom_2_data[17]
  // Probe on rom_2_data[18]
  // Probe on rom_2_data[19]
  // Probe on out_26
  // Probe on comparator_2_eq
  // Probe on and_2_out
  // Probe on multiplexer_4_out
  Multiplexer #(.width(32)) multiplexer_5 (
    .in0(multiplexer_4_out), .in1(multiplexer_3_out), .out(multiplexer_5_out), .sel(or_6_out));
  // Probe to_multiplexer_sel: pin names not known
  or or_6 (or_6_out, block_transfer_control_1_load_enable, is_LDR);
  // Probe is_ldr: pin names not known
  assign mem_offset = {{20{1'b0}}, rom_2_data_3[11:0]};  // Bit_Extender bit_extender_1
  // Probe load_data: pin names not known
  not not_4 (not_4_out, rom_2_data[19]);
  // Probe on {out_26, rom_2_data[19:16]}
  // Probe to_multiplexer_in0_3: pin names not known
  Multiplexer #(.width(4)) multiplexer_6 (
    .in0(rom_2_data_3[15:12]), .in1(4'b1110), .out(multiplexer_6_out), .sel(bl_taken));
  // Probe to_multiplexer_in0_2: pin names not known
  // Probe instruction: pin names not known
  not not_5 (not_5_out, rom_2_data[16]);
  // Probe to_xor_in1: pin names not known
  assign bit_extender_2_out = {{31{not_4_out}}, not_4_out};  // Bit_Extender bit_extender_2
  // Probe to_multiplexer_in0_4: pin names not known
  Multiplexer #(.width(4)) multiplexer_7 (
    .in0(multiplexer_6_out), .in1(rom_2_data[15:12]), .out(multiplexer_7_out), .sel(and_10_out));
  Multiplexer #(.width(32)) multiplexer_8 (
    .in0(multiplexer_5_out), .in1(adder_1_out), .out(multiplexer_8_out), .sel(and_10_out));
  and and_3 (and_3_out, undriven_2, undriven);
  assign bit_extender_3_out = {{24{1'b0}}, rom_2_data_3[7:0]};  // Bit_Extender bit_extender_3
  // Probe rs: pin names not known
  // Probe on {rom_2_data[19:12], rom_2_data_3}
  // Probe mem_offset: pin names not known
  assign memory_offset_effective = mem_offset ^ bit_extender_2_out;  // XOR_Gate xor_1, 32 bits wide
  Comparator #(.width(5)) comparator_3 (
    .a(5'b10010), .b({out_26, rom_2_data[19:16]}), .eq(comparator_3_eq));  // open: gt, lt
  Comparator #(.width(5)) comparator_4 (
    .a(5'b01011), .b({out_26, rom_2_data[19:16]}), .eq(comparator_4_eq));  // open: gt, lt
  Multiplexer #(.width(4)) multiplexer_9 (
    .in0(multiplexer_7_out), .in1(block_transfer_control_1_reg_idx), .out(multiplexer_9_out),
    .sel(block_transfer_control_1_active));
  // Probe on multiplexer_9_out
  // Probe on rom_2_data[15:12]
  Multiplexer multiplexer_10 (
    .in0(or_7_out), .in1(block_transfer_control_1_load_enable), .out(multiplexer_10_out), .sel(or_5_out));
  or or_7 (or_7_out, and_10_out, or_8_out);
  or or_8 (or_8_out, final_reg_we_out, ldr_reg_we);
  or final_reg_we (final_reg_we_out, bl_taken, normal_reg_WE);
  // Probe base_writeback_en: pin names not known
  // Probe on rom_2_data_3[4]
  // Probe on rom_2_data_3[6:5]
  // Probe instr_2_0: pin names not known
  not not_6 (not_6_out, rom_2_data[23]);
  // Probe bl_taken: pin names not known
  // Probe to_and_in1_2: pin names not known
  // Probe on comparator_3_eq
  // Probe not_l: pin names not known
  // Probe on comparator_4_eq
  // Probe on multiplexer_8_out
  Multiplexer #(.width(32)) multiplexer_11 (
    .in0(adder_1_out), .in1(block_transfer_control_1_final_address), .out(multiplexer_11_out),
    .sel(block_transfer_control_1_done));
  // Probe on rom_2_data_3[11:7]
  // Probe branch_class_2: pin names not known
  // Probe to_and_in0_2: pin names not known
  // Probe to_and_in1_3: pin names not known
  // Probe to_adder_cin: pin names not known
  // Probe push_enable_tie: pin names not known
  not not_7 (not_7_out, rom_2_data[16]);
  // Probe rom_addr: pin names not known
  Multiplexer #(.width(4)) multiplexer_12 (
    .in0(rom_2_data_3[3:0]), .in1(rom_2_data_3[15:12]), .out(multiplexer_12_out), .sel(is_STR));
  // Probe to_multiplexer_in0_6: pin names not known
  Multiplexer #(.width(4)) multiplexer_13 (
    .in0(multiplexer_12_out), .in1(block_transfer_control_1_reg_idx), .out(multiplexer_13_out),
    .sel(block_transfer_control_1_active));
  // Probe regfile_wa: pin names not known
  // Probe is_str: pin names not known
  // Probe instr_7_3: pin names not known
  // Probe to_multiplexer_in1_2: pin names not known
  // Probe on rom_2_data[22]
  not not_8 (not_8_out, rom_2_data[22]);
  and and_4 (mem_class, rom_2_data[22], not_6_out);
  and and_5 (and_5_out, and_2_out, not_7_out, 1'b1);
  // Probe cspr_enable_2: pin names not known
  Comparator #(.width(4)) comparator_5 (.a(4'b1111), .b(multiplexer_9_out), .eq(comparator_5_eq));  // open: gt, lt
  // Probe to_and_in0_3: pin names not known
  // Probe on multiplexer_9_out
  // Probe regfile_we: pin names not known
  // Probe on multiplexer_11_out
  // Probe regfile_we2: pin names not known
  or or_9 (or_9_out, and_3_out, and_12_out);
  Multiplexer #(.width(5)) multiplexer_14 (
    .in0(rom_2_data_3[11:7]), .in1({rom_2_data_3[11:8], 1'b0}), .out(multiplexer_14_out), .sel(rom_2_data[21]));
  // Probe branch_class_1: pin names not known
  // Probe on rom_2_data[23]
  assign bit_extender_4_out = {{8{rom_2_data[19]}}, {rom_2_data[19:12], rom_2_data_3}};  // Bit_Extender bit_extender_4
  // Probe on and_5_out
  ROM #(.addrWidth(16), .dataWidth(10)) rom_3 (.addr({{12{1'b0}}, out_26, rom_2_data[19:17]}), .data(rom_3_data));
  and and_6 (and_6_out, comparator_5_eq, multiplexer_10_out);
  // Probe regfile_wd2: pin names not known
  // Probe instr_2_1: pin names not known
  // Probe branch_class_3: pin names not known
  and and_7 (is_STR, mem_class, not_5_out);
  and and_8 (is_LDR, mem_class, rom_2_data[16]);
  // Probe memory_offset_effective: pin names not known
  not not_9 (not_9_out, out_26);
  Comparator #(.width(4)) comparator_6 (.a(4'b1101), .b(rom_2_data[15:12]), .eq(comparator_6_eq));  // open: gt, lt
  // Probe to_multiplexer_in1_1: pin names not known
  // Probe to_shifter_in: pin names not known
  // Probe ldr_reg_we: pin names not known
  or or_10 (or_10_out, rom_2_data[17], not_9_out);
  and branch_class (branch_class_out, rom_2_data[21], not_8_out, rom_2_data[23]);
  // Probe mem_class: pin names not known
  // Probe on RD_A
  // Probe on or_10_out
  and and_9 (and_9_out, and_2_out, rom_2_data[16], 1'b1);
  // Probe pop_enable_tie: pin names not known; wires that end beside it: comparator_6_eq
  // Probe on comparator_6_eq
  // Probe on adder_1_out
  Adder #(.width(32)) adder_1 (
    .a(RD_A), .b(memory_offset_effective), .out(adder_1_out), .cin(not_4_out));  // open: cout
  // Probe on condition_pass
  and and_10 (and_10_out, condition_pass, is_STR, or_10_out);
  // Probe on and_9_out
  // Probe alu_ctrl_word: pin names not known
  reg16x32_1 reg16x32_1_1 (
    .CLK(clock_1_out), .WA(multiplexer_9_out), .WD(multiplexer_8_out), .WE(multiplexer_10_out), .RST(in_1),
    .WD2(multiplexer_11_out), .RA(rom_2_data[15:12]), .RB(multiplexer_13_out), .WE2(or_9_out),
    .WA2(rom_2_data[15:12]), .R0_OUTPUT(out_6), .R1_OUTPUT(out_7), .R3_OUTPUT(out_8), .R2_OUPUT(out_9),
    .R5_OUTPUT(out_10), .R4_OUTPUT(out_11), .RD_A(reg16x32_1_1_rd_a), .R7_OUTPUT(out_14), .R6_OUTPUT(out_15),
    .RD_B(reg16x32_1_1_rd_b), .R8_OUTPUT(out_17), .R9_OUTPUT(out_18), .R11_OUTPUT(out_19),
    .R10_OUTPUT(out_20), .R13_OUTPUT(out_21), .R12_OUTPUT(out_22), .R15_OUTPUT(out_23), .R14_OUTPUT(out_24));
  // Probe normal_reg_we: pin names not known
  // Probe alu_result: pin names not known
  // Probe cond_cond: pin names not known
  and and_11 (is_BL, branch_class_out, out_26);
  Shifter #(.width(32)) shifter_1 (.in(bit_extender_4_out), .\dist (5'b00010), .out(shifter_1_out));
  // Probe to_adder_a: pin names not known
  Multiplexer #(.width(32)) multiplexer_15 (.in0(RD_A), .in1(adder_1_out), .out(multiplexer_15_out), .sel(out_26));
  and and_12 (and_12_out, is_LDR, condition_pass, or_10_out);
  // Probe on and_10_out
  or or_11 (or_11_out, is_BX, branch_class_out);
  // Probe is_bl: pin names not known
  // Probe to_multiplexer_in0_7: pin names not known
  // Probe on and_12_out
  or or_12 (or_12_out, and_9_out, and_5_out);
  // Probe alu_write_enable: pin names not known
  // Probe alu_logic_sel: pin names not known
  // Probe alu_a_inv: pin names not known
  // Probe alu_engine_sel: pin names not known
  Multiplexer #(.width(2)) multiplexer_16 (
    .in0(rom_2_data_3[6:5]), .in1(2'b11), .out(multiplexer_16_out), .sel(rom_2_data[21]));
  // Probe to_or_in0_3: pin names not known
  // Probe branch_class_4: pin names not known
  Adder #(.width(32)) adder_2 (.a(shifter_1_out), .b(32'h8), .out(adder_2_out));  // open: cin, cout
  Multiplexer #(.width(32)) multiplexer_17 (
    .in0(multiplexer_15_out), .in1(block_transfer_control_1_transfer_address), .out(memory_address),
    .sel(block_transfer_control_1_active));
  // Probe on or_12_out
  // Probe alu_cin_sel: pin names not known
  // Probe alu_b_inv: pin names not known
  or or_13 (or_13_out, or_11_out, mem_class);
  // Probe to_not_in_2: pin names not known
  not not_link (not_link_out, is_BL);
  // Probe instr_1_0: pin names not known
  // Probe instr_31_10: pin names not known
  Multiplexer #(.width(32)) multiplexer_18 (
    .in0(out_16), .in1(bit_extender_3_out), .out(multiplexer_18_out), .sel(rom_2_data[21]));
  // Probe shift_input_32b: pin names not known
  // Probe imm_bit: pin names not known
  // Probe shift_typ: pin names not known
  // Probe shift_amnt: pin names not known
  // Probe not_link_2: pin names not known
  // Probe on memory_address[1:0]
  // Probe shift_outp: pin names not known
  // Probe on rom_3_data[9:8]
  not not_10 (not_10_out, or_13_out);
  and is_B (is_B_out, branch_class_out, not_link_out);
  and and_13 (bl_taken, condition_pass, is_BL);
  // Probe on memory_address[9:2]
  // Probe on memory_address[31:10]
  and data_ram_we (data_ram_we_out, condition_pass, is_STR);
  and and_14 (ldr_reg_we, is_LDR, condition_pass);
  assign bit_extender_5_out = {{22{1'b0}}, pc_fetch_1_pc_out};  // Bit_Extender bit_extender_5
  // Probe data_ram_we_2: pin names not known
  // Probe pc_zext32: pin names not known
  // Probe k2_shift_dist: pin names not known
  barrel_32b barrel_32b_1 (
    .input_32b(multiplexer_18_out), .amnt(multiplexer_14_out), .typ(multiplexer_16_out), .outp(out_12));
  or or_14 (or_14_out, data_ram_we_out, block_transfer_control_1_store_enable);
  Shifter #(.width(32)) shifter_2 (.in(bit_extender_5_out), .\dist (5'b00010), .out(shifter_2_out));
  // Probe k8_pc_offset: pin names not known
  // Probe k0_adder_cin: pin names not known
  // Probe k15_regnum: pin names not known
  ALU alu_1 (
    .logic_sel(rom_3_data[3:1]), .a_inv(rom_3_data[7]), .A(RD_A), .B(out_12), .b_inv(rom_3_data[6]),
    .Cflag(CSPR_q[1]), .unused(1'b0), .cin_sel(rom_3_data[5:4]), .engine_sel(rom_3_data[9:8]),
    .write_enable(rom_3_data[0]), .result(out_3), .C(alu_1_v[1]), .Z(alu_1_v[2]), .N(alu_1_v[3]),
    .V(alu_1_v[0]), .write_enable_out(alu_1_write_enable_out));
  // Probe regfile_ra: pin names not known
  // Probe regfile_rb: pin names not known
  // Probe ram_we: pin names not known
  // Probe pc_byte_addr: pin names not known
  // Probe ram_addr: pin names not known
  Adder #(.width(32)) adder_3 (.a(shifter_2_out), .b(32'h8), .out(adder_3_out), .cin(1'b0));  // open: cout
  Comparator #(.width(4)) comparator_7 (.a(rom_2_data[15:12]), .b(4'b1111), .eq(comparator_7_eq));  // open: gt, lt
  Comparator #(.width(4)) comparator_8 (.a(multiplexer_13_out), .b(4'b1111), .eq(comparator_8_eq));  // open: gt, lt
  and CSPR_enable (CSPR_enable_out, condition_pass, not_10_out, rom_2_data[16]);
  // Probe cspr_enable_3: pin names not known
  // Probe alu_c: pin names not known
  // Probe alu_z: pin names not known
  // Probe alu_n: pin names not known
  // Probe alu_v: pin names not known
  // Probe alu_cflag: pin names not known
  or or_15 (or_15_out, bl_taken, branch_taken);
  // Probe pc_plus8: pin names not known
  // Probe rn_is_r15: pin names not known
  // Probe rm_is_r15: pin names not known
  // Probe cspr_1: pin names not known
  Register #(.width(4)) CSPR (.D(alu_1_v), .en(CSPR_enable_out), .clk(clock_1_out), .Q(CSPR_q), .clr(in_1));
  // Probe regfile_rd_a: pin names not known
  // Probe regfile_rd_b: pin names not known
  Multiplexer #(.width(32)) multiplexer_19 (
    .in0(reg16x32_1_1_rd_a), .in1(adder_3_out), .out(RD_A), .sel(comparator_7_eq));
  Multiplexer #(.width(32)) multiplexer_20 (
    .in0(reg16x32_1_1_rd_b), .in1(adder_3_out), .out(out_16), .sel(comparator_8_eq));
  // Probe cspr_2: pin names not known
  // Probe ram_oe: pin names not known
  // Probe cond_n: pin names not known
  // Probe cond_z: pin names not known
  // Probe cond_v: pin names not known
  // Probe on rom_2_data_2
  RAM #(.dataWidth(32), .trigger("falling")) ram_1 (
    .addr(memory_address[9:2]), .we(or_14_out), .oe(1'b1), .clk(clock_1_out), .din(out_16), .dout(out_33));
  // Probe alu_write_enable_out: pin names not known
  condition_checker condition_checker_1 (
    .N(CSPR_q[3]), .Z(CSPR_q[2]), .C(CSPR_q[1]), .cond(rom_2_data_2), .V(CSPR_q[0]), .out_6(condition_pass));
  and and_15 (normal_reg_WE, alu_1_write_enable_out, not_10_out, condition_pass);
  // Probe cspr_enable_1: pin names not known
  // Probe is_b_2: pin names not known
  and and_16 (branch_taken, condition_pass, is_B_out);
  // Probe branch_taken: pin names not known

  // Notes on the sheet:
  //   contents of rom_2 (hex, n*v repeats v):
  //   e3a02000 e3a0e018 e1a0f00e e3a000ee e5820000 eafffffe e3a00055 e5820000 e12fff1e
  //   contents of rom_3 (hex, n*v repeats v):
  //   1 3 151 191 101 121 161 1a1 0 2 150 100 5 7 9 b 201
endmodule

module kogge_stone_1b (
  input  A,
  input  B,
  input  C_in,
  output g,
  output p,
  output sum
);

  and a_and_b (g, A, B);
  xor a_xor_b (p, A, B);
  xor p_xor_cin (sum, p, C_in);
endmodule

module kogge_stone_2b (
  input  A0,
  input  B0,
  input  CIN,
  input  A1,
  input  B1,
  output SUM0,
  output Cout,
  output SUM1
);

  wire bit0_g, bit0_p, bit1_g, bit1_p, pg1_g_out;

  kogge_stone_1b bit0 (.A(A0), .B(B0), .C_in(CIN), .g(bit0_g), .p(bit0_p), .sum(SUM0));
  kogge_stone_1b bit1 (.A(A1), .B(B1), .C_in(pg1_g_out), .g(bit1_g), .p(bit1_p), .sum(SUM1));
  pg_cell pg1 (.G(bit0_g), .P(bit0_p), .G_prev(CIN), .G_out(pg1_g_out));  // open: P_Prev, P_out
  pg_cell pg2 (.G(bit1_g), .P(bit1_p), .G_prev(pg1_g_out), .G_out(Cout));  // open: P_Prev, P_out
endmodule

module pg_cell (
  input  G,
  input  P,
  input  G_prev,
  input  P_Prev,
  output G_out,
  output P_out
);

  wire PandG_prev_out;

  and PandG_prev (PandG_prev_out, P, G_prev);
  and P_and_P_prev (P_out, P, P_Prev);
  or G_or_PandG_prev (G_out, G, PandG_prev_out);
endmodule

module ks_4b (
  input  in_1,
  input  in_2,
  input  in_3,
  input  in_4,
  input  in_5,
  input  in_6,
  input  in_7,
  input  in_8,
  input  in_9,
  output out_10,
  output out_11,
  output out_12,
  output out_13,
  output out_14
);

  wire bit0_g, bit0_p, bit1_g, bit1_p, bit2_g, bit2_p, kogge_stone_1b_1_g, kogge_stone_1b_1_p, s1_0_g_out,
       s1_0_p_out, s1_1_g_out, s1_1_p_out, s1_2_g_out, s1_2_p_out, s1_3_g_out, s1_3_p_out, s2_2_g_out;

  pg_cell s1_3 (
    .G(kogge_stone_1b_1_g), .P(kogge_stone_1b_1_p), .G_prev(bit2_g), .P_Prev(bit2_p), .G_out(s1_3_g_out),
    .P_out(s1_3_p_out));
  pg_cell s2_3 (
    .G(s1_3_g_out), .P(s1_3_p_out), .G_prev(s1_1_g_out), .P_Prev(s1_1_p_out), .G_out(out_14));  // open: P_out
  kogge_stone_1b kogge_stone_1b_1 (
    .A(in_1), .B(in_5), .C_in(s2_2_g_out), .g(kogge_stone_1b_1_g), .p(kogge_stone_1b_1_p), .sum(out_10));
  pg_cell s1_2 (.G(bit2_g), .P(bit2_p), .G_prev(bit1_g), .P_Prev(bit1_p), .G_out(s1_2_g_out), .P_out(s1_2_p_out));
  pg_cell s2_2 (
    .G(s1_2_g_out), .P(s1_2_p_out), .G_prev(s1_0_g_out), .P_Prev(s1_0_p_out), .G_out(s2_2_g_out));  // open: P_out
  kogge_stone_1b bit2 (.A(in_2), .B(in_6), .C_in(s1_1_g_out), .g(bit2_g), .p(bit2_p), .sum(out_11));
  pg_cell s1_1 (.G(bit1_g), .P(bit1_p), .G_prev(bit0_g), .P_Prev(bit0_p), .G_out(s1_1_g_out), .P_out(s1_1_p_out));
  kogge_stone_1b bit1 (.A(in_3), .B(in_7), .C_in(s1_0_g_out), .g(bit1_g), .p(bit1_p), .sum(out_12));
  pg_cell s1_0 (.G(bit0_g), .P(bit0_p), .G_prev(in_9), .G_out(s1_0_g_out), .P_out(s1_0_p_out));  // open: P_Prev
  kogge_stone_1b bit0 (.A(in_4), .B(in_8), .C_in(in_9), .g(bit0_g), .p(bit0_p), .sum(out_13));
endmodule

module ks_32b (
  input  [31:0] A,
  input  [31:0] B,
  input  Cin,
  output SUM31,
  output SUM30,
  output SUM29,
  output SUM28,
  output SUM27,
  output SUM26,
  output SUM25,
  output SUM24,
  output SUM23,
  output SUM22,
  output SUM21,
  output SUM20,
  output SUM19,
  output SUM18,
  output SUM17,
  output SUM16,
  output SUM15,
  output SUM14,
  output SUM13,
  output SUM12,
  output SUM11,
  output SUM10,
  output SUM9,
  output SUM8,
  output SUM7,
  output SUM6,
  output SUM5,
  output SUM4,
  output SUM3,
  output SUM2,
  output sum1,
  output sum0,
  output Cout
);

  wire bit3_g, bit3_p, bit7_g, bit7_p, bit8_g, bit8_p, bit9_g, bit9_p, bit10_g, bit10_p, bit11_g, bit11_p,
       bit12_g, bit12_p, bit13_g, bit13_p, bit14_g, bit14_p, bit15_g, bit15_p, bit16_g, bit16_p, bit17_g,
       bit17_p, bit18_g, bit18_p, bit19_g, bit19_p, bit20_g, bit20_p, bit21_g, bit21_p, bit22_g, bit22_p,
       bit23_g, bit23_p, bit24_g, bit24_p, bit25_g, bit25_p, bit26_g, bit26_p, bit27_g, bit27_p, bit28_g,
       bit28_p, bit29_g, bit29_p, bit30_g, bit30_p, bit31_g, bit31_p, kogge_stone_1b_1_g, kogge_stone_1b_1_p,
       kogge_stone_1b_2_g, kogge_stone_1b_2_p, kogge_stone_1b_3_g, kogge_stone_1b_3_p, kogge_stone_1b_4_g,
       kogge_stone_1b_4_p, kogge_stone_1b_5_g, kogge_stone_1b_5_p, kogge_stone_1b_6_g, kogge_stone_1b_6_p,
       pg_cell_1_g_out, pg_cell_1_p_out, pg_cell_2_g_out, pg_cell_2_p_out, pg_cell_3_g_out, pg_cell_3_p_out,
       pg_cell_5_g_out, pg_cell_5_p_out, pg_cell_6_g_out, pg_cell_6_p_out, pg_cell_7_g_out, pg_cell_7_p_out,
       pg_cell_8_g_out, pg_cell_8_p_out, pg_cell_9_g_out, pg_cell_10_g_out, pg_cell_10_p_out,
       pg_cell_11_g_out, pg_cell_11_p_out, pg_cell_12_g_out, pg_cell_12_p_out, pg_cell_13_g_out,
       pg_cell_13_p_out, pg_cell_14_g_out, pg_cell_15_g_out, pg_cell_15_p_out, pg_cell_16_g_out,
       pg_cell_16_p_out, pg_cell_17_g_out, pg_cell_17_p_out, pg_cell_18_g_out, pg_cell_19_g_out,
       pg_cell_19_p_out, pg_cell_20_g_out, pg_cell_20_p_out, pg_cell_21_g_out, pg_cell_21_p_out,
       pg_cell_22_g_out, pg_cell_22_p_out, pg_cell_23_g_out, pg_cell_24_g_out, pg_cell_24_p_out,
       pg_cell_25_g_out, pg_cell_25_p_out, pg_cell_26_g_out, pg_cell_26_p_out, pg_cell_27_g_out,
       pg_cell_27_p_out, pg_cell_28_g_out, pg_cell_29_g_out, pg_cell_29_p_out, pg_cell_30_g_out,
       pg_cell_30_p_out, pg_cell_31_g_out, pg_cell_31_p_out, pg_cell_32_g_out, pg_cell_32_p_out,
       pg_cell_33_g_out, pg_cell_34_g_out, pg_cell_34_p_out, pg_cell_35_g_out, pg_cell_35_p_out,
       pg_cell_36_g_out, pg_cell_36_p_out, pg_cell_37_g_out, pg_cell_38_g_out, pg_cell_38_p_out,
       pg_cell_39_g_out, pg_cell_39_p_out, pg_cell_40_g_out, pg_cell_40_p_out, pg_cell_41_g_out,
       pg_cell_41_p_out, pg_cell_42_g_out, pg_cell_42_p_out, pg_cell_43_g_out, pg_cell_43_p_out,
       pg_cell_44_g_out, pg_cell_44_p_out, pg_cell_45_g_out, pg_cell_45_p_out, pg_cell_46_g_out,
       pg_cell_46_p_out, pg_cell_47_g_out, pg_cell_47_p_out, pg_cell_48_g_out, pg_cell_48_p_out,
       pg_cell_49_g_out, pg_cell_49_p_out, pg_cell_50_g_out, pg_cell_50_p_out, pg_cell_51_g_out,
       pg_cell_51_p_out, pg_cell_52_g_out, pg_cell_52_p_out, pg_cell_53_g_out, pg_cell_53_p_out,
       pg_cell_54_g_out, pg_cell_54_p_out, pg_cell_55_g_out, pg_cell_55_p_out, pg_cell_56_g_out,
       pg_cell_56_p_out, pg_cell_57_g_out, pg_cell_57_p_out, pg_cell_58_g_out, pg_cell_58_p_out,
       pg_cell_59_g_out, pg_cell_59_p_out, pg_cell_60_g_out, pg_cell_60_p_out, pg_cell_61_g_out,
       pg_cell_61_p_out, pg_cell_62_g_out, pg_cell_62_p_out, pg_cell_63_g_out, pg_cell_63_p_out,
       pg_cell_64_g_out, pg_cell_64_p_out, pg_cell_65_g_out, pg_cell_65_p_out, pg_cell_66_g_out,
       pg_cell_66_p_out, pg_cell_67_g_out, pg_cell_67_p_out, pg_cell_68_g_out, pg_cell_68_p_out,
       pg_cell_69_g_out, pg_cell_69_p_out, pg_cell_70_g_out, pg_cell_70_p_out, pg_cell_71_g_out,
       pg_cell_71_p_out, pg_cell_72_g_out, pg_cell_72_p_out, pg_cell_73_g_out, pg_cell_73_p_out,
       pg_cell_74_g_out, pg_cell_74_p_out, pg_cell_75_g_out, pg_cell_75_p_out, pg_cell_76_g_out,
       pg_cell_76_p_out, pg_cell_77_g_out, pg_cell_77_p_out, pg_cell_78_g_out, pg_cell_78_p_out,
       pg_cell_79_g_out, pg_cell_79_p_out, pg_cell_80_g_out, pg_cell_80_p_out, pg_cell_81_g_out,
       pg_cell_81_p_out, pg_cell_82_g_out, pg_cell_82_p_out, pg_cell_83_g_out, pg_cell_83_p_out,
       pg_cell_84_g_out, pg_cell_84_p_out, pg_cell_85_g_out, pg_cell_85_p_out, pg_cell_86_g_out,
       pg_cell_86_p_out, pg_cell_87_g_out, pg_cell_87_p_out, pg_cell_88_g_out, pg_cell_88_p_out,
       pg_cell_89_g_out, pg_cell_89_p_out, pg_cell_90_g_out, pg_cell_90_p_out, pg_cell_91_g_out,
       pg_cell_91_p_out, pg_cell_92_g_out, pg_cell_92_p_out, pg_cell_93_g_out, pg_cell_93_p_out,
       pg_cell_94_g_out, pg_cell_94_p_out, pg_cell_95_g_out, pg_cell_95_p_out, pg_cell_96_g_out,
       pg_cell_96_p_out, pg_cell_97_g_out, pg_cell_97_p_out, pg_cell_98_g_out, pg_cell_98_p_out,
       pg_cell_99_g_out, pg_cell_99_p_out, pg_cell_100_g_out, pg_cell_100_p_out, pg_cell_101_g_out,
       pg_cell_101_p_out, pg_cell_102_g_out, pg_cell_102_p_out, pg_cell_103_g_out, pg_cell_103_p_out,
       pg_cell_104_g_out, pg_cell_104_p_out, pg_cell_105_g_out, pg_cell_105_p_out, pg_cell_106_g_out,
       pg_cell_106_p_out, pg_cell_107_g_out, pg_cell_107_p_out, pg_cell_108_g_out, pg_cell_108_p_out,
       pg_cell_109_g_out, pg_cell_109_p_out, pg_cell_110_g_out, pg_cell_110_p_out, pg_cell_111_g_out,
       pg_cell_111_p_out, pg_cell_112_g_out, pg_cell_112_p_out, pg_cell_113_g_out, pg_cell_113_p_out,
       pg_cell_114_g_out, pg_cell_114_p_out, s1_7_g_out, s1_7_p_out, s2_7_g_out, s2_7_p_out, s3_7_g_out,
       s3_7_p_out, s3_20_g_out, s3_20_p_out, s3_24_g_out, s3_24_p_out, s3_28_g_out, s3_28_p_out, s3_31_g_out,
       s3_31_p_out, s4_15_g_out, s4_15_p_out, s5_16_g_out, s5_17_g_out, s5_18_g_out, s5_19_g_out,
       s5_20_g_out, s5_21_g_out, s5_22_g_out, s5_23_g_out;

  kogge_stone_1b bit31 (.A(A[31]), .B(B[31]), .C_in(pg_cell_9_g_out), .g(bit31_g), .p(bit31_p), .sum(SUM31));
  pg_cell pg_cell_1 (
    .G(bit31_g), .P(bit31_p), .G_prev(bit30_g), .P_Prev(bit30_p), .G_out(pg_cell_1_g_out),
    .P_out(pg_cell_1_p_out));
  pg_cell pg_cell_2 (
    .G(pg_cell_1_g_out), .P(pg_cell_1_p_out), .G_prev(pg_cell_10_g_out), .P_Prev(pg_cell_10_p_out),
    .G_out(pg_cell_2_g_out), .P_out(pg_cell_2_p_out));
  pg_cell s3_31 (
    .G(pg_cell_2_g_out), .P(pg_cell_2_p_out), .G_prev(pg_cell_20_g_out), .P_Prev(pg_cell_20_p_out),
    .G_out(s3_31_g_out), .P_out(s3_31_p_out));
  pg_cell pg_cell_3 (
    .G(s3_31_g_out), .P(s3_31_p_out), .G_prev(pg_cell_40_g_out), .P_Prev(pg_cell_40_p_out),
    .G_out(pg_cell_3_g_out), .P_out(pg_cell_3_p_out));
  pg_cell pg_cell_4 (
    .G(pg_cell_3_g_out), .P(pg_cell_3_p_out), .G_prev(s4_15_g_out), .P_Prev(s4_15_p_out), .G_out(Cout));  // open: P_out
  kogge_stone_1b bit30 (.A(A[30]), .B(B[30]), .C_in(pg_cell_14_g_out), .g(bit30_g), .p(bit30_p), .sum(SUM30));
  pg_cell pg_cell_5 (
    .G(bit30_g), .P(bit30_p), .G_prev(bit29_g), .P_Prev(bit29_p), .G_out(pg_cell_5_g_out),
    .P_out(pg_cell_5_p_out));
  pg_cell pg_cell_6 (
    .G(pg_cell_5_g_out), .P(pg_cell_5_p_out), .G_prev(pg_cell_15_g_out), .P_Prev(pg_cell_15_p_out),
    .G_out(pg_cell_6_g_out), .P_out(pg_cell_6_p_out));
  pg_cell pg_cell_7 (
    .G(pg_cell_6_g_out), .P(pg_cell_6_p_out), .G_prev(pg_cell_25_g_out), .P_Prev(pg_cell_25_p_out),
    .G_out(pg_cell_7_g_out), .P_out(pg_cell_7_p_out));
  pg_cell pg_cell_8 (
    .G(pg_cell_7_g_out), .P(pg_cell_7_p_out), .G_prev(pg_cell_44_g_out), .P_Prev(pg_cell_44_p_out),
    .G_out(pg_cell_8_g_out), .P_out(pg_cell_8_p_out));
  pg_cell pg_cell_9 (
    .G(pg_cell_8_g_out), .P(pg_cell_8_p_out), .G_prev(pg_cell_75_g_out), .P_Prev(pg_cell_75_p_out),
    .G_out(pg_cell_9_g_out));  // open: P_out
  kogge_stone_1b bit29 (.A(A[29]), .B(B[29]), .C_in(pg_cell_18_g_out), .g(bit29_g), .p(bit29_p), .sum(SUM29));
  pg_cell pg_cell_10 (
    .G(bit29_g), .P(bit29_p), .G_prev(bit28_g), .P_Prev(bit28_p), .G_out(pg_cell_10_g_out),
    .P_out(pg_cell_10_p_out));
  pg_cell pg_cell_11 (
    .G(pg_cell_10_g_out), .P(pg_cell_10_p_out), .G_prev(pg_cell_19_g_out), .P_Prev(pg_cell_19_p_out),
    .G_out(pg_cell_11_g_out), .P_out(pg_cell_11_p_out));
  pg_cell pg_cell_12 (
    .G(pg_cell_11_g_out), .P(pg_cell_11_p_out), .G_prev(pg_cell_25_g_out), .P_Prev(pg_cell_25_p_out),
    .G_out(pg_cell_12_g_out), .P_out(pg_cell_12_p_out));
  pg_cell pg_cell_13 (
    .G(pg_cell_12_g_out), .P(pg_cell_12_p_out), .G_prev(pg_cell_48_g_out), .P_Prev(pg_cell_48_p_out),
    .G_out(pg_cell_13_g_out), .P_out(pg_cell_13_p_out));
  pg_cell pg_cell_14 (
    .G(pg_cell_13_g_out), .P(pg_cell_13_p_out), .G_prev(pg_cell_79_g_out), .P_Prev(pg_cell_79_p_out),
    .G_out(pg_cell_14_g_out));  // open: P_out
  kogge_stone_1b bit28 (.A(A[28]), .B(B[28]), .C_in(pg_cell_23_g_out), .g(bit28_g), .p(bit28_p), .sum(SUM28));
  pg_cell pg_cell_15 (
    .G(bit28_g), .P(bit28_p), .G_prev(bit27_g), .P_Prev(bit27_p), .G_out(pg_cell_15_g_out),
    .P_out(pg_cell_15_p_out));
  pg_cell pg_cell_16 (
    .G(pg_cell_15_g_out), .P(pg_cell_15_p_out), .G_prev(pg_cell_24_g_out), .P_Prev(pg_cell_24_p_out),
    .G_out(pg_cell_16_g_out), .P_out(pg_cell_16_p_out));
  pg_cell s3_28 (
    .G(pg_cell_16_g_out), .P(pg_cell_16_p_out), .G_prev(pg_cell_35_g_out), .P_Prev(pg_cell_35_p_out),
    .G_out(s3_28_g_out), .P_out(s3_28_p_out));
  pg_cell pg_cell_17 (
    .G(s3_28_g_out), .P(s3_28_p_out), .G_prev(s3_20_g_out), .P_Prev(s3_20_p_out), .G_out(pg_cell_17_g_out),
    .P_out(pg_cell_17_p_out));
  pg_cell pg_cell_18 (
    .G(pg_cell_17_g_out), .P(pg_cell_17_p_out), .G_prev(pg_cell_83_g_out), .P_Prev(pg_cell_83_p_out),
    .G_out(pg_cell_18_g_out));  // open: P_out
  kogge_stone_1b bit27 (.A(A[27]), .B(B[27]), .C_in(pg_cell_28_g_out), .g(bit27_g), .p(bit27_p), .sum(SUM27));
  pg_cell pg_cell_19 (
    .G(bit27_g), .P(bit27_p), .G_prev(bit26_g), .P_Prev(bit26_p), .G_out(pg_cell_19_g_out),
    .P_out(pg_cell_19_p_out));
  pg_cell pg_cell_20 (
    .G(pg_cell_19_g_out), .P(pg_cell_19_p_out), .G_prev(pg_cell_29_g_out), .P_Prev(pg_cell_29_p_out),
    .G_out(pg_cell_20_g_out), .P_out(pg_cell_20_p_out));
  pg_cell pg_cell_21 (
    .G(pg_cell_20_g_out), .P(pg_cell_20_p_out), .G_prev(pg_cell_39_g_out), .P_Prev(pg_cell_39_p_out),
    .G_out(pg_cell_21_g_out), .P_out(pg_cell_21_p_out));
  pg_cell pg_cell_22 (
    .G(pg_cell_21_g_out), .P(pg_cell_21_p_out), .G_prev(pg_cell_55_g_out), .P_Prev(pg_cell_55_p_out),
    .G_out(pg_cell_22_g_out), .P_out(pg_cell_22_p_out));
  pg_cell pg_cell_23 (
    .G(pg_cell_22_g_out), .P(pg_cell_22_p_out), .G_prev(pg_cell_87_g_out), .P_Prev(pg_cell_87_p_out),
    .G_out(pg_cell_23_g_out));  // open: P_out
  kogge_stone_1b bit26 (.A(A[26]), .B(B[26]), .C_in(pg_cell_33_g_out), .g(bit26_g), .p(bit26_p), .sum(SUM26));
  pg_cell pg_cell_24 (
    .G(bit26_g), .P(bit26_p), .G_prev(bit25_g), .P_Prev(bit25_p), .G_out(pg_cell_24_g_out),
    .P_out(pg_cell_24_p_out));
  pg_cell pg_cell_25 (
    .G(pg_cell_24_g_out), .P(pg_cell_24_p_out), .G_prev(pg_cell_34_g_out), .P_Prev(pg_cell_34_p_out),
    .G_out(pg_cell_25_g_out), .P_out(pg_cell_25_p_out));
  pg_cell pg_cell_26 (
    .G(pg_cell_25_g_out), .P(pg_cell_25_p_out), .G_prev(pg_cell_43_g_out), .P_Prev(pg_cell_43_p_out),
    .G_out(pg_cell_26_g_out), .P_out(pg_cell_26_p_out));
  pg_cell pg_cell_27 (
    .G(pg_cell_26_g_out), .P(pg_cell_26_p_out), .G_prev(pg_cell_59_g_out), .P_Prev(pg_cell_59_p_out),
    .G_out(pg_cell_27_g_out), .P_out(pg_cell_27_p_out));
  pg_cell pg_cell_28 (
    .G(pg_cell_27_g_out), .P(pg_cell_27_p_out), .G_prev(pg_cell_91_g_out), .P_Prev(pg_cell_91_p_out),
    .G_out(pg_cell_28_g_out));  // open: P_out
  kogge_stone_1b bit25 (.A(A[25]), .B(B[25]), .C_in(pg_cell_37_g_out), .g(bit25_g), .p(bit25_p), .sum(SUM25));
  pg_cell pg_cell_29 (
    .G(bit25_g), .P(bit25_p), .G_prev(bit24_g), .P_Prev(bit24_p), .G_out(pg_cell_29_g_out),
    .P_out(pg_cell_29_p_out));
  pg_cell pg_cell_30 (
    .G(pg_cell_29_g_out), .P(pg_cell_29_p_out), .G_prev(pg_cell_38_g_out), .P_Prev(pg_cell_38_p_out),
    .G_out(pg_cell_30_g_out), .P_out(pg_cell_30_p_out));
  pg_cell pg_cell_31 (
    .G(pg_cell_30_g_out), .P(pg_cell_30_p_out), .G_prev(pg_cell_47_g_out), .P_Prev(pg_cell_47_p_out),
    .G_out(pg_cell_31_g_out), .P_out(pg_cell_31_p_out));
  pg_cell pg_cell_32 (
    .G(pg_cell_31_g_out), .P(pg_cell_31_p_out), .G_prev(pg_cell_63_g_out), .P_Prev(pg_cell_63_p_out),
    .G_out(pg_cell_32_g_out), .P_out(pg_cell_32_p_out));
  pg_cell pg_cell_33 (
    .G(pg_cell_32_g_out), .P(pg_cell_32_p_out), .G_prev(pg_cell_95_g_out), .P_Prev(pg_cell_95_p_out),
    .G_out(pg_cell_33_g_out));  // open: P_out
  kogge_stone_1b bit24 (.A(A[24]), .B(B[24]), .C_in(s5_23_g_out), .g(bit24_g), .p(bit24_p), .sum(SUM24));
  pg_cell pg_cell_34 (
    .G(bit24_g), .P(bit24_p), .G_prev(bit23_g), .P_Prev(bit23_p), .G_out(pg_cell_34_g_out),
    .P_out(pg_cell_34_p_out));
  pg_cell pg_cell_35 (
    .G(pg_cell_34_g_out), .P(pg_cell_34_p_out), .G_prev(pg_cell_42_g_out), .P_Prev(pg_cell_42_p_out),
    .G_out(pg_cell_35_g_out), .P_out(pg_cell_35_p_out));
  pg_cell s3_24 (
    .G(pg_cell_35_g_out), .P(pg_cell_35_p_out), .G_prev(pg_cell_51_g_out), .P_Prev(pg_cell_51_p_out),
    .G_out(s3_24_g_out), .P_out(s3_24_p_out));
  pg_cell pg_cell_36 (
    .G(s3_24_g_out), .P(s3_24_p_out), .G_prev(pg_cell_67_g_out), .P_Prev(pg_cell_67_p_out),
    .G_out(pg_cell_36_g_out), .P_out(pg_cell_36_p_out));
  pg_cell pg_cell_37 (
    .G(pg_cell_36_g_out), .P(pg_cell_36_p_out), .G_prev(pg_cell_99_g_out), .P_Prev(pg_cell_99_p_out),
    .G_out(pg_cell_37_g_out));  // open: P_out
  kogge_stone_1b bit23 (.A(A[23]), .B(B[23]), .C_in(s5_22_g_out), .g(bit23_g), .p(bit23_p), .sum(SUM23));
  pg_cell pg_cell_38 (
    .G(bit23_g), .P(bit23_p), .G_prev(bit22_g), .P_Prev(bit22_p), .G_out(pg_cell_38_g_out),
    .P_out(pg_cell_38_p_out));
  pg_cell pg_cell_39 (
    .G(pg_cell_38_g_out), .P(pg_cell_38_p_out), .G_prev(pg_cell_46_g_out), .P_Prev(pg_cell_46_p_out),
    .G_out(pg_cell_39_g_out), .P_out(pg_cell_39_p_out));
  pg_cell pg_cell_40 (
    .G(pg_cell_39_g_out), .P(pg_cell_39_p_out), .G_prev(pg_cell_54_g_out), .P_Prev(pg_cell_54_p_out),
    .G_out(pg_cell_40_g_out), .P_out(pg_cell_40_p_out));
  pg_cell pg_cell_41 (
    .G(pg_cell_40_g_out), .P(pg_cell_40_p_out), .G_prev(pg_cell_71_g_out), .P_Prev(pg_cell_71_p_out),
    .G_out(pg_cell_41_g_out), .P_out(pg_cell_41_p_out));
  pg_cell s5_23 (
    .G(pg_cell_41_g_out), .P(pg_cell_41_p_out), .G_prev(s3_7_g_out), .P_Prev(s3_7_p_out), .G_out(s5_23_g_out));  // open: P_out
  kogge_stone_1b bit22 (.A(A[22]), .B(B[22]), .C_in(s5_21_g_out), .g(bit22_g), .p(bit22_p), .sum(SUM22));
  pg_cell pg_cell_42 (
    .G(bit22_g), .P(bit22_p), .G_prev(bit21_g), .P_Prev(bit21_p), .G_out(pg_cell_42_g_out),
    .P_out(pg_cell_42_p_out));
  pg_cell pg_cell_43 (
    .G(pg_cell_42_g_out), .P(pg_cell_42_p_out), .G_prev(pg_cell_50_g_out), .P_Prev(pg_cell_50_p_out),
    .G_out(pg_cell_43_g_out), .P_out(pg_cell_43_p_out));
  pg_cell pg_cell_44 (
    .G(pg_cell_43_g_out), .P(pg_cell_43_p_out), .G_prev(pg_cell_58_g_out), .P_Prev(pg_cell_58_p_out),
    .G_out(pg_cell_44_g_out), .P_out(pg_cell_44_p_out));
  pg_cell pg_cell_45 (
    .G(pg_cell_44_g_out), .P(pg_cell_44_p_out), .G_prev(pg_cell_74_g_out), .P_Prev(pg_cell_74_p_out),
    .G_out(pg_cell_45_g_out), .P_out(pg_cell_45_p_out));
  pg_cell s5_22 (
    .G(pg_cell_45_g_out), .P(pg_cell_45_p_out), .G_prev(pg_cell_102_g_out), .P_Prev(pg_cell_102_p_out),
    .G_out(s5_22_g_out));  // open: P_out
  kogge_stone_1b bit21 (.A(A[21]), .B(B[21]), .C_in(s5_20_g_out), .g(bit21_g), .p(bit21_p), .sum(SUM21));
  pg_cell pg_cell_46 (
    .G(bit21_g), .P(bit21_p), .G_prev(bit20_g), .P_Prev(bit20_p), .G_out(pg_cell_46_g_out),
    .P_out(pg_cell_46_p_out));
  pg_cell pg_cell_47 (
    .G(pg_cell_46_g_out), .P(pg_cell_46_p_out), .G_prev(pg_cell_53_g_out), .P_Prev(pg_cell_53_p_out),
    .G_out(pg_cell_47_g_out), .P_out(pg_cell_47_p_out));
  pg_cell pg_cell_48 (
    .G(pg_cell_47_g_out), .P(pg_cell_47_p_out), .G_prev(pg_cell_62_g_out), .P_Prev(pg_cell_62_p_out),
    .G_out(pg_cell_48_g_out), .P_out(pg_cell_48_p_out));
  pg_cell pg_cell_49 (
    .G(pg_cell_48_g_out), .P(pg_cell_48_p_out), .G_prev(pg_cell_78_g_out), .P_Prev(pg_cell_78_p_out),
    .G_out(pg_cell_49_g_out), .P_out(pg_cell_49_p_out));
  pg_cell s5_21 (
    .G(pg_cell_49_g_out), .P(pg_cell_49_p_out), .G_prev(pg_cell_105_g_out), .P_Prev(pg_cell_105_p_out),
    .G_out(s5_21_g_out));  // open: P_out
  kogge_stone_1b bit20 (.A(A[20]), .B(B[20]), .C_in(s5_19_g_out), .g(bit20_g), .p(bit20_p), .sum(SUM20));
  pg_cell pg_cell_50 (
    .G(bit20_g), .P(bit20_p), .G_prev(bit19_g), .P_Prev(bit19_p), .G_out(pg_cell_50_g_out),
    .P_out(pg_cell_50_p_out));
  pg_cell pg_cell_51 (
    .G(pg_cell_50_g_out), .P(pg_cell_50_p_out), .G_prev(pg_cell_57_g_out), .P_Prev(pg_cell_57_p_out),
    .G_out(pg_cell_51_g_out), .P_out(pg_cell_51_p_out));
  pg_cell s3_20 (
    .G(pg_cell_51_g_out), .P(pg_cell_51_p_out), .G_prev(pg_cell_66_g_out), .P_Prev(pg_cell_66_p_out),
    .G_out(s3_20_g_out), .P_out(s3_20_p_out));
  pg_cell pg_cell_52 (
    .G(s3_20_g_out), .P(s3_20_p_out), .G_prev(pg_cell_82_g_out), .P_Prev(pg_cell_82_p_out),
    .G_out(pg_cell_52_g_out), .P_out(pg_cell_52_p_out));
  pg_cell s5_20 (
    .G(pg_cell_52_g_out), .P(pg_cell_52_p_out), .G_prev(pg_cell_108_g_out), .P_Prev(pg_cell_108_p_out),
    .G_out(s5_20_g_out));  // open: P_out
  kogge_stone_1b bit19 (.A(A[19]), .B(B[19]), .C_in(s5_18_g_out), .g(bit19_g), .p(bit19_p), .sum(SUM19));
  pg_cell pg_cell_53 (
    .G(bit19_g), .P(bit19_p), .G_prev(bit18_g), .P_Prev(bit18_p), .G_out(pg_cell_53_g_out),
    .P_out(pg_cell_53_p_out));
  pg_cell pg_cell_54 (
    .G(pg_cell_53_g_out), .P(pg_cell_53_p_out), .G_prev(pg_cell_61_g_out), .P_Prev(pg_cell_61_p_out),
    .G_out(pg_cell_54_g_out), .P_out(pg_cell_54_p_out));
  pg_cell pg_cell_55 (
    .G(pg_cell_54_g_out), .P(pg_cell_54_p_out), .G_prev(pg_cell_70_g_out), .P_Prev(pg_cell_70_p_out),
    .G_out(pg_cell_55_g_out), .P_out(pg_cell_55_p_out));
  pg_cell pg_cell_56 (
    .G(pg_cell_55_g_out), .P(pg_cell_55_p_out), .G_prev(pg_cell_86_g_out), .P_Prev(pg_cell_86_p_out),
    .G_out(pg_cell_56_g_out), .P_out(pg_cell_56_p_out));
  pg_cell s5_19 (
    .G(pg_cell_56_g_out), .P(pg_cell_56_p_out), .G_prev(pg_cell_110_g_out), .P_Prev(pg_cell_110_p_out),
    .G_out(s5_19_g_out));  // open: P_out
  kogge_stone_1b bit18 (.A(A[18]), .B(B[18]), .C_in(s5_17_g_out), .g(bit18_g), .p(bit18_p), .sum(SUM18));
  pg_cell pg_cell_57 (
    .G(bit18_g), .P(bit18_p), .G_prev(bit17_g), .P_Prev(bit17_p), .G_out(pg_cell_57_g_out),
    .P_out(pg_cell_57_p_out));
  pg_cell pg_cell_58 (
    .G(pg_cell_57_g_out), .P(pg_cell_57_p_out), .G_prev(pg_cell_65_g_out), .P_Prev(pg_cell_65_p_out),
    .G_out(pg_cell_58_g_out), .P_out(pg_cell_58_p_out));
  pg_cell pg_cell_59 (
    .G(pg_cell_58_g_out), .P(pg_cell_58_p_out), .G_prev(pg_cell_73_g_out), .P_Prev(pg_cell_73_p_out),
    .G_out(pg_cell_59_g_out), .P_out(pg_cell_59_p_out));
  pg_cell pg_cell_60 (
    .G(pg_cell_59_g_out), .P(pg_cell_59_p_out), .G_prev(pg_cell_90_g_out), .P_Prev(pg_cell_90_p_out),
    .G_out(pg_cell_60_g_out), .P_out(pg_cell_60_p_out));
  pg_cell s5_18 (
    .G(pg_cell_60_g_out), .P(pg_cell_60_p_out), .G_prev(pg_cell_112_g_out), .P_Prev(pg_cell_112_p_out),
    .G_out(s5_18_g_out));  // open: P_out
  kogge_stone_1b bit17 (.A(A[17]), .B(B[17]), .C_in(s5_16_g_out), .g(bit17_g), .p(bit17_p), .sum(SUM17));
  pg_cell pg_cell_61 (
    .G(bit17_g), .P(bit17_p), .G_prev(bit16_g), .P_Prev(bit16_p), .G_out(pg_cell_61_g_out),
    .P_out(pg_cell_61_p_out));
  pg_cell pg_cell_62 (
    .G(pg_cell_61_g_out), .P(pg_cell_61_p_out), .G_prev(pg_cell_69_g_out), .P_Prev(pg_cell_69_p_out),
    .G_out(pg_cell_62_g_out), .P_out(pg_cell_62_p_out));
  pg_cell pg_cell_63 (
    .G(pg_cell_62_g_out), .P(pg_cell_62_p_out), .G_prev(pg_cell_77_g_out), .P_Prev(pg_cell_77_p_out),
    .G_out(pg_cell_63_g_out), .P_out(pg_cell_63_p_out));
  pg_cell pg_cell_64 (
    .G(pg_cell_63_g_out), .P(pg_cell_63_p_out), .G_prev(pg_cell_94_g_out), .P_Prev(pg_cell_94_p_out),
    .G_out(pg_cell_64_g_out), .P_out(pg_cell_64_p_out));
  pg_cell s5_17 (
    .G(pg_cell_64_g_out), .P(pg_cell_64_p_out), .G_prev(pg_cell_113_g_out), .P_Prev(pg_cell_113_p_out),
    .G_out(s5_17_g_out));  // open: P_out
  kogge_stone_1b bit16 (.A(A[16]), .B(B[16]), .C_in(s4_15_g_out), .g(bit16_g), .p(bit16_p), .sum(SUM16));
  pg_cell pg_cell_65 (
    .G(bit16_g), .P(bit16_p), .G_prev(bit15_g), .P_Prev(bit15_p), .G_out(pg_cell_65_g_out),
    .P_out(pg_cell_65_p_out));
  pg_cell pg_cell_66 (
    .G(pg_cell_65_g_out), .P(pg_cell_65_p_out), .G_prev(pg_cell_72_g_out), .P_Prev(pg_cell_72_p_out),
    .G_out(pg_cell_66_g_out), .P_out(pg_cell_66_p_out));
  pg_cell pg_cell_67 (
    .G(pg_cell_66_g_out), .P(pg_cell_66_p_out), .G_prev(pg_cell_81_g_out), .P_Prev(pg_cell_81_p_out),
    .G_out(pg_cell_67_g_out), .P_out(pg_cell_67_p_out));
  pg_cell pg_cell_68 (
    .G(pg_cell_67_g_out), .P(pg_cell_67_p_out), .G_prev(pg_cell_98_g_out), .P_Prev(pg_cell_98_p_out),
    .G_out(pg_cell_68_g_out), .P_out(pg_cell_68_p_out));
  pg_cell s5_16 (
    .G(pg_cell_68_g_out), .P(pg_cell_68_p_out), .G_prev(pg_cell_114_g_out), .P_Prev(pg_cell_114_p_out),
    .G_out(s5_16_g_out));  // open: P_out
  kogge_stone_1b bit15 (.A(A[15]), .B(B[15]), .C_in(pg_cell_75_g_out), .g(bit15_g), .p(bit15_p), .sum(SUM15));
  pg_cell pg_cell_69 (
    .G(bit15_g), .P(bit15_p), .G_prev(bit14_g), .P_Prev(bit14_p), .G_out(pg_cell_69_g_out),
    .P_out(pg_cell_69_p_out));
  pg_cell pg_cell_70 (
    .G(pg_cell_69_g_out), .P(pg_cell_69_p_out), .G_prev(pg_cell_76_g_out), .P_Prev(pg_cell_76_p_out),
    .G_out(pg_cell_70_g_out), .P_out(pg_cell_70_p_out));
  pg_cell pg_cell_71 (
    .G(pg_cell_70_g_out), .P(pg_cell_70_p_out), .G_prev(pg_cell_85_g_out), .P_Prev(pg_cell_85_p_out),
    .G_out(pg_cell_71_g_out), .P_out(pg_cell_71_p_out));
  pg_cell s4_15 (
    .G(pg_cell_71_g_out), .P(pg_cell_71_p_out), .G_prev(s3_7_g_out), .P_Prev(s3_7_p_out),
    .G_out(s4_15_g_out), .P_out(s4_15_p_out));
  kogge_stone_1b bit14 (.A(A[14]), .B(B[14]), .C_in(pg_cell_79_g_out), .g(bit14_g), .p(bit14_p), .sum(SUM14));
  pg_cell pg_cell_72 (
    .G(bit14_g), .P(bit14_p), .G_prev(bit13_g), .P_Prev(bit13_p), .G_out(pg_cell_72_g_out),
    .P_out(pg_cell_72_p_out));
  pg_cell pg_cell_73 (
    .G(pg_cell_72_g_out), .P(pg_cell_72_p_out), .G_prev(pg_cell_80_g_out), .P_Prev(pg_cell_80_p_out),
    .G_out(pg_cell_73_g_out), .P_out(pg_cell_73_p_out));
  pg_cell pg_cell_74 (
    .G(pg_cell_73_g_out), .P(pg_cell_73_p_out), .G_prev(pg_cell_89_g_out), .P_Prev(pg_cell_89_p_out),
    .G_out(pg_cell_74_g_out), .P_out(pg_cell_74_p_out));
  pg_cell pg_cell_75 (
    .G(pg_cell_74_g_out), .P(pg_cell_74_p_out), .G_prev(pg_cell_102_g_out), .P_Prev(pg_cell_102_p_out),
    .G_out(pg_cell_75_g_out), .P_out(pg_cell_75_p_out));
  kogge_stone_1b bit13 (.A(A[13]), .B(B[13]), .C_in(pg_cell_83_g_out), .g(bit13_g), .p(bit13_p), .sum(SUM13));
  pg_cell pg_cell_76 (
    .G(bit13_g), .P(bit13_p), .G_prev(bit12_g), .P_Prev(bit12_p), .G_out(pg_cell_76_g_out),
    .P_out(pg_cell_76_p_out));
  pg_cell pg_cell_77 (
    .G(pg_cell_76_g_out), .P(pg_cell_76_p_out), .G_prev(pg_cell_84_g_out), .P_Prev(pg_cell_84_p_out),
    .G_out(pg_cell_77_g_out), .P_out(pg_cell_77_p_out));
  pg_cell pg_cell_78 (
    .G(pg_cell_77_g_out), .P(pg_cell_77_p_out), .G_prev(pg_cell_93_g_out), .P_Prev(pg_cell_93_p_out),
    .G_out(pg_cell_78_g_out), .P_out(pg_cell_78_p_out));
  pg_cell pg_cell_79 (
    .G(pg_cell_78_g_out), .P(pg_cell_78_p_out), .G_prev(pg_cell_105_g_out), .P_Prev(pg_cell_105_p_out),
    .G_out(pg_cell_79_g_out), .P_out(pg_cell_79_p_out));
  kogge_stone_1b bit12 (.A(A[12]), .B(B[12]), .C_in(pg_cell_87_g_out), .g(bit12_g), .p(bit12_p), .sum(SUM12));
  pg_cell pg_cell_80 (
    .G(bit12_g), .P(bit12_p), .G_prev(bit11_g), .P_Prev(bit11_p), .G_out(pg_cell_80_g_out),
    .P_out(pg_cell_80_p_out));
  pg_cell pg_cell_81 (
    .G(pg_cell_80_g_out), .P(pg_cell_80_p_out), .G_prev(pg_cell_88_g_out), .P_Prev(pg_cell_88_p_out),
    .G_out(pg_cell_81_g_out), .P_out(pg_cell_81_p_out));
  pg_cell pg_cell_82 (
    .G(pg_cell_81_g_out), .P(pg_cell_81_p_out), .G_prev(pg_cell_97_g_out), .P_Prev(pg_cell_97_p_out),
    .G_out(pg_cell_82_g_out), .P_out(pg_cell_82_p_out));
  pg_cell pg_cell_83 (
    .G(pg_cell_82_g_out), .P(pg_cell_82_p_out), .G_prev(pg_cell_108_g_out), .P_Prev(pg_cell_108_p_out),
    .G_out(pg_cell_83_g_out), .P_out(pg_cell_83_p_out));
  kogge_stone_1b bit11 (.A(A[11]), .B(B[11]), .C_in(pg_cell_91_g_out), .g(bit11_g), .p(bit11_p), .sum(SUM11));
  pg_cell pg_cell_84 (
    .G(bit11_g), .P(bit11_p), .G_prev(bit10_g), .P_Prev(bit10_p), .G_out(pg_cell_84_g_out),
    .P_out(pg_cell_84_p_out));
  pg_cell pg_cell_85 (
    .G(pg_cell_84_g_out), .P(pg_cell_84_p_out), .G_prev(pg_cell_92_g_out), .P_Prev(pg_cell_92_p_out),
    .G_out(pg_cell_85_g_out), .P_out(pg_cell_85_p_out));
  pg_cell pg_cell_86 (
    .G(pg_cell_85_g_out), .P(pg_cell_85_p_out), .G_prev(s2_7_g_out), .P_Prev(s2_7_p_out),
    .G_out(pg_cell_86_g_out), .P_out(pg_cell_86_p_out));
  pg_cell pg_cell_87 (
    .G(pg_cell_86_g_out), .P(pg_cell_86_p_out), .G_prev(pg_cell_110_g_out), .P_Prev(pg_cell_110_p_out),
    .G_out(pg_cell_87_g_out), .P_out(pg_cell_87_p_out));
  kogge_stone_1b bit10 (.A(A[10]), .B(B[10]), .C_in(pg_cell_95_g_out), .g(bit10_g), .p(bit10_p), .sum(SUM10));
  pg_cell pg_cell_88 (
    .G(bit10_g), .P(bit10_p), .G_prev(bit9_g), .P_Prev(bit9_p), .G_out(pg_cell_88_g_out),
    .P_out(pg_cell_88_p_out));
  pg_cell pg_cell_89 (
    .G(pg_cell_88_g_out), .P(pg_cell_88_p_out), .G_prev(pg_cell_96_g_out), .P_Prev(pg_cell_96_p_out),
    .G_out(pg_cell_89_g_out), .P_out(pg_cell_89_p_out));
  pg_cell pg_cell_90 (
    .G(pg_cell_89_g_out), .P(pg_cell_89_p_out), .G_prev(pg_cell_101_g_out), .P_Prev(pg_cell_101_p_out),
    .G_out(pg_cell_90_g_out), .P_out(pg_cell_90_p_out));
  pg_cell pg_cell_91 (
    .G(pg_cell_90_g_out), .P(pg_cell_90_p_out), .G_prev(pg_cell_112_g_out), .P_Prev(pg_cell_112_p_out),
    .G_out(pg_cell_91_g_out), .P_out(pg_cell_91_p_out));
  kogge_stone_1b bit9 (.A(A[9]), .B(B[9]), .C_in(pg_cell_99_g_out), .g(bit9_g), .p(bit9_p), .sum(SUM9));
  pg_cell pg_cell_92 (
    .G(bit9_g), .P(bit9_p), .G_prev(bit8_g), .P_Prev(bit8_p), .G_out(pg_cell_92_g_out),
    .P_out(pg_cell_92_p_out));
  pg_cell pg_cell_93 (
    .G(pg_cell_92_g_out), .P(pg_cell_92_p_out), .G_prev(s1_7_g_out), .P_Prev(s1_7_p_out),
    .G_out(pg_cell_93_g_out), .P_out(pg_cell_93_p_out));
  pg_cell pg_cell_94 (
    .G(pg_cell_93_g_out), .P(pg_cell_93_p_out), .G_prev(pg_cell_104_g_out), .P_Prev(pg_cell_104_p_out),
    .G_out(pg_cell_94_g_out), .P_out(pg_cell_94_p_out));
  pg_cell pg_cell_95 (
    .G(pg_cell_94_g_out), .P(pg_cell_94_p_out), .G_prev(pg_cell_113_g_out), .P_Prev(pg_cell_113_p_out),
    .G_out(pg_cell_95_g_out), .P_out(pg_cell_95_p_out));
  kogge_stone_1b bit8 (.A(A[8]), .B(B[8]), .C_in(s3_7_g_out), .g(bit8_g), .p(bit8_p), .sum(SUM8));
  pg_cell pg_cell_96 (
    .G(bit8_g), .P(bit8_p), .G_prev(bit7_g), .P_Prev(bit7_p), .G_out(pg_cell_96_g_out),
    .P_out(pg_cell_96_p_out));
  pg_cell pg_cell_97 (
    .G(pg_cell_96_g_out), .P(pg_cell_96_p_out), .G_prev(pg_cell_100_g_out), .P_Prev(pg_cell_100_p_out),
    .G_out(pg_cell_97_g_out), .P_out(pg_cell_97_p_out));
  pg_cell pg_cell_98 (
    .G(pg_cell_97_g_out), .P(pg_cell_97_p_out), .G_prev(pg_cell_107_g_out), .P_Prev(pg_cell_107_p_out),
    .G_out(pg_cell_98_g_out), .P_out(pg_cell_98_p_out));
  pg_cell pg_cell_99 (
    .G(pg_cell_98_g_out), .P(pg_cell_98_p_out), .G_prev(pg_cell_114_g_out), .P_Prev(pg_cell_114_p_out),
    .G_out(pg_cell_99_g_out), .P_out(pg_cell_99_p_out));
  kogge_stone_1b bit7 (.A(A[7]), .B(B[7]), .C_in(pg_cell_102_g_out), .g(bit7_g), .p(bit7_p), .sum(SUM7));
  pg_cell s1_7 (
    .G(bit7_g), .P(bit7_p), .G_prev(kogge_stone_1b_1_g), .P_Prev(kogge_stone_1b_1_p), .G_out(s1_7_g_out),
    .P_out(s1_7_p_out));
  pg_cell s2_7 (
    .G(s1_7_g_out), .P(s1_7_p_out), .G_prev(pg_cell_103_g_out), .P_Prev(pg_cell_103_p_out),
    .G_out(s2_7_g_out), .P_out(s2_7_p_out));
  pg_cell s3_7 (
    .G(s2_7_g_out), .P(s2_7_p_out), .G_prev(pg_cell_110_g_out), .P_Prev(pg_cell_110_p_out),
    .G_out(s3_7_g_out), .P_out(s3_7_p_out));
  kogge_stone_1b kogge_stone_1b_1 (
    .A(A[6]), .B(B[6]), .C_in(pg_cell_105_g_out), .g(kogge_stone_1b_1_g), .p(kogge_stone_1b_1_p), .sum(SUM6));
  pg_cell pg_cell_100 (
    .G(kogge_stone_1b_1_g), .P(kogge_stone_1b_1_p), .G_prev(kogge_stone_1b_2_g), .P_Prev(kogge_stone_1b_2_p),
    .G_out(pg_cell_100_g_out), .P_out(pg_cell_100_p_out));
  pg_cell pg_cell_101 (
    .G(pg_cell_100_g_out), .P(pg_cell_100_p_out), .G_prev(pg_cell_106_g_out), .P_Prev(pg_cell_106_p_out),
    .G_out(pg_cell_101_g_out), .P_out(pg_cell_101_p_out));
  pg_cell pg_cell_102 (
    .G(pg_cell_101_g_out), .P(pg_cell_101_p_out), .G_prev(pg_cell_112_g_out), .P_Prev(pg_cell_112_p_out),
    .G_out(pg_cell_102_g_out), .P_out(pg_cell_102_p_out));
  kogge_stone_1b kogge_stone_1b_2 (
    .A(A[5]), .B(B[5]), .C_in(pg_cell_108_g_out), .g(kogge_stone_1b_2_g), .p(kogge_stone_1b_2_p), .sum(SUM5));
  pg_cell pg_cell_103 (
    .G(kogge_stone_1b_2_g), .P(kogge_stone_1b_2_p), .G_prev(kogge_stone_1b_3_g), .P_Prev(kogge_stone_1b_3_p),
    .G_out(pg_cell_103_g_out), .P_out(pg_cell_103_p_out));
  pg_cell pg_cell_104 (
    .G(pg_cell_103_g_out), .P(pg_cell_103_p_out), .G_prev(pg_cell_109_g_out), .P_Prev(pg_cell_109_p_out),
    .G_out(pg_cell_104_g_out), .P_out(pg_cell_104_p_out));
  pg_cell pg_cell_105 (
    .G(pg_cell_104_g_out), .P(pg_cell_104_p_out), .G_prev(pg_cell_113_g_out), .P_Prev(pg_cell_113_p_out),
    .G_out(pg_cell_105_g_out), .P_out(pg_cell_105_p_out));
  kogge_stone_1b kogge_stone_1b_3 (
    .A(A[4]), .B(B[4]), .C_in(pg_cell_110_g_out), .g(kogge_stone_1b_3_g), .p(kogge_stone_1b_3_p), .sum(SUM4));
  pg_cell pg_cell_106 (
    .G(kogge_stone_1b_3_g), .P(kogge_stone_1b_3_p), .G_prev(bit3_g), .P_Prev(bit3_p),
    .G_out(pg_cell_106_g_out), .P_out(pg_cell_106_p_out));
  pg_cell pg_cell_107 (
    .G(pg_cell_106_g_out), .P(pg_cell_106_p_out), .G_prev(pg_cell_111_g_out), .P_Prev(pg_cell_111_p_out),
    .G_out(pg_cell_107_g_out), .P_out(pg_cell_107_p_out));
  pg_cell pg_cell_108 (
    .G(pg_cell_107_g_out), .P(pg_cell_107_p_out), .G_prev(pg_cell_114_g_out), .P_Prev(pg_cell_114_p_out),
    .G_out(pg_cell_108_g_out), .P_out(pg_cell_108_p_out));
  kogge_stone_1b bit3 (.A(A[3]), .B(B[3]), .C_in(pg_cell_112_g_out), .g(bit3_g), .p(bit3_p), .sum(SUM3));
  pg_cell pg_cell_109 (
    .G(bit3_g), .P(bit3_p), .G_prev(kogge_stone_1b_4_g), .P_Prev(kogge_stone_1b_4_p),
    .G_out(pg_cell_109_g_out), .P_out(pg_cell_109_p_out));
  pg_cell pg_cell_110 (
    .G(pg_cell_109_g_out), .P(pg_cell_109_p_out), .G_prev(pg_cell_113_g_out), .P_Prev(pg_cell_113_p_out),
    .G_out(pg_cell_110_g_out), .P_out(pg_cell_110_p_out));
  kogge_stone_1b kogge_stone_1b_4 (
    .A(A[2]), .B(B[2]), .C_in(pg_cell_113_g_out), .g(kogge_stone_1b_4_g), .p(kogge_stone_1b_4_p), .sum(SUM2));
  pg_cell pg_cell_111 (
    .G(kogge_stone_1b_4_g), .P(kogge_stone_1b_4_p), .G_prev(kogge_stone_1b_5_g), .P_Prev(kogge_stone_1b_5_p),
    .G_out(pg_cell_111_g_out), .P_out(pg_cell_111_p_out));
  pg_cell pg_cell_112 (
    .G(pg_cell_111_g_out), .P(pg_cell_111_p_out), .G_prev(pg_cell_114_g_out), .P_Prev(pg_cell_114_p_out),
    .G_out(pg_cell_112_g_out), .P_out(pg_cell_112_p_out));
  kogge_stone_1b kogge_stone_1b_5 (
    .A(A[1]), .B(B[1]), .C_in(pg_cell_114_g_out), .g(kogge_stone_1b_5_g), .p(kogge_stone_1b_5_p), .sum(sum1));
  pg_cell pg_cell_113 (
    .G(kogge_stone_1b_5_g), .P(kogge_stone_1b_5_p), .G_prev(pg_cell_114_g_out), .P_Prev(pg_cell_114_p_out),
    .G_out(pg_cell_113_g_out), .P_out(pg_cell_113_p_out));
  kogge_stone_1b kogge_stone_1b_6 (
    .A(A[0]), .B(B[0]), .C_in(Cin), .g(kogge_stone_1b_6_g), .p(kogge_stone_1b_6_p), .sum(sum0));
  pg_cell pg_cell_114 (
    .G(kogge_stone_1b_6_g), .P(kogge_stone_1b_6_p), .G_prev(Cin), .P_Prev(1'b0), .G_out(pg_cell_114_g_out),
    .P_out(pg_cell_114_p_out));
endmodule

module ALU_arithmetic_engine_1 (
  input  a_inversion,
  input  [31:0] A,
  input  [31:0] B,
  input  b_inversion,
  input  Cflag,
  input  unused,
  input  [1:0] Cin_sel,
  output [31:0] Result,
  output Cout
);

  wire multiplexer_1_out;
  wire [31:0] bit_extender_1_out, bit_extender_2_out, xor_1_out, xor_2_out;

  assign bit_extender_1_out = {{31{b_inversion}}, b_inversion};  // Bit_Extender bit_extender_1
  Multiplexer #(.select(2)) multiplexer_1 (
    .in0(1'b0), .in1(1'b1), .in2(Cflag), .in3(unused), .out(multiplexer_1_out), .sel(Cin_sel));
  assign bit_extender_2_out = {{31{a_inversion}}, a_inversion};  // Bit_Extender bit_extender_2
  assign xor_1_out = bit_extender_2_out ^ A;  // XOR_Gate xor_1, 32 bits wide
  assign xor_2_out = B ^ bit_extender_1_out;  // XOR_Gate xor_2, 32 bits wide
  ks_32b ks_32b_1 (
    .A(xor_1_out), .B(xor_2_out), .Cin(multiplexer_1_out), .SUM31(Result[31]), .SUM30(Result[30]),
    .SUM29(Result[29]), .SUM28(Result[28]), .SUM27(Result[27]), .SUM26(Result[26]), .SUM25(Result[25]),
    .SUM24(Result[24]), .SUM23(Result[23]), .SUM22(Result[22]), .SUM21(Result[21]), .SUM20(Result[20]),
    .SUM19(Result[19]), .SUM18(Result[18]), .SUM17(Result[17]), .SUM16(Result[16]), .SUM15(Result[15]),
    .SUM14(Result[14]), .SUM13(Result[13]), .SUM12(Result[12]), .SUM11(Result[11]), .SUM10(Result[10]),
    .SUM9(Result[9]), .SUM8(Result[8]), .SUM7(Result[7]), .SUM6(Result[6]), .SUM5(Result[5]),
    .SUM4(Result[4]), .SUM3(Result[3]), .SUM2(Result[2]), .sum1(Result[1]), .sum0(Result[0]), .Cout(Cout));
endmodule

module ALU (
  input  [2:0] logic_sel,
  input  a_inv,
  input  [31:0] A,
  input  [31:0] B,
  input  b_inv,
  input  Cflag,
  input  unused,
  input  [1:0] cin_sel,
  input  [1:0] engine_sel,
  input  write_enable,
  output [31:0] result,
  output C,
  output Z,
  output N,
  output V,
  output write_enable_out
);

  wire A_eff_out, B_eff_out, or_1_out, xnor_1_out, xor_1_out;
  wire [31:0] alu_arithmetic_engine_1_result, alu_logic_engine_1_result, ks_32b_1_sum0, mul_32_1_carry,
       mul_32_1_sum, undriven, undriven_2, undriven_3;

  mul_32 mul_32_1 (.A(undriven_2), .B(undriven), .sum(mul_32_1_sum), .carry(mul_32_1_carry));
  xor A_eff (A_eff_out, a_inv, A[31]);
  xor B_eff (B_eff_out, b_inv, B[31]);
  ALU_logic_engine alu_logic_engine_1 (.A(A), .B(B), .select_bit(logic_sel), .result(alu_logic_engine_1_result));
  ALU_arithmetic_engine alu_arithmetic_engine_1 (
    .a_inversion(a_inv), .A(A), .B(B), .b_inversion(b_inv), .Cflag(Cflag), .unused(unused),
    .Cin_sel(cin_sel), .Result(alu_arithmetic_engine_1_result), .Cout(C));
  xnor xnor_1 (xnor_1_out, A_eff_out, B_eff_out);
  ks_32b ks_32b_1 (
    .A(mul_32_1_sum), .B(mul_32_1_carry), .SUM31(ks_32b_1_sum0[31]), .SUM30(ks_32b_1_sum0[30]),
    .SUM29(ks_32b_1_sum0[29]), .SUM28(ks_32b_1_sum0[28]), .SUM27(ks_32b_1_sum0[27]),
    .SUM26(ks_32b_1_sum0[26]), .SUM25(ks_32b_1_sum0[25]), .SUM24(ks_32b_1_sum0[24]),
    .SUM23(ks_32b_1_sum0[23]), .SUM22(ks_32b_1_sum0[22]), .SUM21(ks_32b_1_sum0[21]),
    .SUM20(ks_32b_1_sum0[20]), .SUM19(ks_32b_1_sum0[19]), .SUM18(ks_32b_1_sum0[18]),
    .SUM17(ks_32b_1_sum0[17]), .SUM16(ks_32b_1_sum0[16]), .SUM15(ks_32b_1_sum0[15]),
    .SUM14(ks_32b_1_sum0[14]), .SUM13(ks_32b_1_sum0[13]), .SUM12(ks_32b_1_sum0[12]),
    .SUM11(ks_32b_1_sum0[11]), .SUM10(ks_32b_1_sum0[10]), .SUM9(ks_32b_1_sum0[9]), .SUM8(ks_32b_1_sum0[8]),
    .SUM7(ks_32b_1_sum0[7]), .SUM6(ks_32b_1_sum0[6]), .SUM5(ks_32b_1_sum0[5]), .SUM4(ks_32b_1_sum0[4]),
    .SUM3(ks_32b_1_sum0[3]), .SUM2(ks_32b_1_sum0[2]), .sum1(ks_32b_1_sum0[1]), .sum0(ks_32b_1_sum0[0]));  // open: Cin, Cout
  Multiplexer #(.select(2), .width(32)) multiplexer_1 (
    .in0(alu_logic_engine_1_result), .in1(alu_arithmetic_engine_1_result), .in3(undriven_3),
    .out({N, result[30:0]}), .sel(engine_sel));  // open: in2
  xor xor_1 (xor_1_out, N, A_eff_out);
  and and_1 (V, xor_1_out, xnor_1_out);
  or or_1 (or_1_out, result[0], result[1], result[2], result[3], result[4], result[5], result[6], result[7], result[8], result[9], result[10], result[11], result[12], result[13], result[14], result[15], result[16], result[17], result[18], result[19], result[20], result[21], result[22], result[23], result[24], result[25], result[26], result[27], result[28], result[29], result[30], N);
  not not_1 (Z, or_1_out);

  assign result[31] = N;
  assign write_enable_out = write_enable;

  // Notes on the sheet:
  //   A: initial=0x9e3779b9
  //   B: initial=0x7f4a7c15
endmodule

module a_invert (
  input  [31:0] A,
  input  a_inversion,
  input  [31:0] B
);

  wire [31:0] bit_extender_1_out, xor_1_out;

  assign bit_extender_1_out = {{31{a_inversion}}, a_inversion};  // Bit_Extender bit_extender_1
  assign xor_1_out = A ^ bit_extender_1_out;  // XOR_Gate xor_1, 32 bits wide
  ks_32b ks_32b_1 (
    .A(xor_1_out), .B(B), .Cin(a_inversion));  // open: SUM31, SUM30, SUM29, SUM28, SUM27, SUM26, SUM25, SUM24, SUM23, SUM22, SUM21, SUM20, SUM19, SUM18, SUM17, SUM16, SUM15, SUM14, SUM13, SUM12, SUM11, SUM10, SUM9, SUM8, SUM7, SUM6, SUM5, SUM4, SUM3, SUM2, sum1, sum0, Cout
endmodule

module ALU_logic_engine (
  input  [31:0] A,
  input  [31:0] B,
  input  [2:0] select_bit,
  output [31:0] result
);

  wire [31:0] and_1_out, and_2_out, not_1_out, or_1_out, xor_1_out;

  assign not_1_out = ~B;  // NOT_Gate not_1, 32 bits wide
  assign and_1_out = A & B;  // AND_Gate and_1, 32 bits wide
  assign xor_1_out = A ^ B;  // XOR_Gate xor_1, 32 bits wide
  assign or_1_out = A | B;  // OR_Gate or_1, 32 bits wide
  assign and_2_out = A & not_1_out;  // AND_Gate and_2, 32 bits wide
  Multiplexer #(.select(3), .width(32)) multiplexer_1 (
    .in0(and_1_out), .in1(xor_1_out), .in2(or_1_out), .in3(B), .in4(and_2_out), .in5(not_1_out),
    .out(result), .sel(select_bit));  // open: in6, in7
endmodule

module pp_row_32 (
  input  [31:0] Rm,
  input  Rs_bit,
  output [31:0] result
);

  wire [31:0] bit_extender_1_out;

  assign bit_extender_1_out = {{31{Rs_bit}}, Rs_bit};  // Bit_Extender bit_extender_1
  assign result = Rm & bit_extender_1_out;  // AND_Gate and_1, 32 bits wide

  // Notes on the sheet:
  //   Rm: initial=0xdeadbeef
endmodule

module partial_products (
  input  [31:0] Rm,
  input  [31:0] Rs,
  output [31:0] p0,
  output [31:0] p1,
  output [31:0] p2,
  output [31:0] p3,
  output [31:0] p4,
  output [31:0] p5,
  output [31:0] p6,
  output [31:0] p7,
  output [31:0] p8,
  output [31:0] p9,
  output [31:0] p10,
  output [31:0] p11,
  output [31:0] p12,
  output [31:0] p13,
  output [31:0] p14,
  output [31:0] p15,
  output [31:0] p16,
  output [31:0] p17,
  output [31:0] p18,
  output [31:0] p19,
  output [31:0] p20,
  output [31:0] p21,
  output [31:0] p22,
  output [31:0] p23,
  output [31:0] p24,
  output [31:0] p25,
  output [31:0] p26,
  output [31:0] p27,
  output [31:0] p28,
  output [31:0] p29,
  output [31:0] p30,
  output [31:0] p31
);

  wire [31:0] pp_row_32_1_result, pp_row_32_2_result, pp_row_32_3_result, pp_row_32_4_result,
       pp_row_32_5_result, pp_row_32_6_result, pp_row_32_7_result, pp_row_32_8_result, pp_row_32_9_result,
       pp_row_32_10_result, pp_row_32_11_result, pp_row_32_12_result, pp_row_32_13_result,
       pp_row_32_14_result, pp_row_32_15_result, pp_row_32_16_result, pp_row_32_17_result,
       pp_row_32_18_result, pp_row_32_19_result, pp_row_32_20_result, pp_row_32_21_result,
       pp_row_32_22_result, pp_row_32_23_result, pp_row_32_24_result, pp_row_32_25_result,
       pp_row_32_26_result, pp_row_32_27_result, pp_row_32_28_result, pp_row_32_29_result,
       pp_row_32_30_result, pp_row_32_31_result, pp_row_32_32_result;

  pp_row_32 pp_row_32_1 (.Rm(Rm), .Rs_bit(Rs[0]), .result(pp_row_32_1_result));
  pp_row_32 pp_row_32_2 (.Rm(Rm), .Rs_bit(Rs[1]), .result(pp_row_32_2_result));
  pp_row_32 pp_row_32_3 (.Rm(Rm), .Rs_bit(Rs[2]), .result(pp_row_32_3_result));
  pp_row_32 pp_row_32_4 (.Rm(Rm), .Rs_bit(Rs[3]), .result(pp_row_32_4_result));
  pp_row_32 pp_row_32_5 (.Rm(Rm), .Rs_bit(Rs[4]), .result(pp_row_32_5_result));
  pp_row_32 pp_row_32_6 (.Rm(Rm), .Rs_bit(Rs[5]), .result(pp_row_32_6_result));
  pp_row_32 pp_row_32_7 (.Rm(Rm), .Rs_bit(Rs[6]), .result(pp_row_32_7_result));
  pp_row_32 pp_row_32_8 (.Rm(Rm), .Rs_bit(Rs[7]), .result(pp_row_32_8_result));
  pp_row_32 pp_row_32_9 (.Rm(Rm), .Rs_bit(Rs[8]), .result(pp_row_32_9_result));
  pp_row_32 pp_row_32_10 (.Rm(Rm), .Rs_bit(Rs[9]), .result(pp_row_32_10_result));
  pp_row_32 pp_row_32_11 (.Rm(Rm), .Rs_bit(Rs[10]), .result(pp_row_32_11_result));
  pp_row_32 pp_row_32_12 (.Rm(Rm), .Rs_bit(Rs[11]), .result(pp_row_32_12_result));
  pp_row_32 pp_row_32_13 (.Rm(Rm), .Rs_bit(Rs[12]), .result(pp_row_32_13_result));
  pp_row_32 pp_row_32_14 (.Rm(Rm), .Rs_bit(Rs[13]), .result(pp_row_32_14_result));
  pp_row_32 pp_row_32_15 (.Rm(Rm), .Rs_bit(Rs[14]), .result(pp_row_32_15_result));
  pp_row_32 pp_row_32_16 (.Rm(Rm), .Rs_bit(Rs[15]), .result(pp_row_32_16_result));
  pp_row_32 pp_row_32_17 (.Rm(Rm), .Rs_bit(Rs[16]), .result(pp_row_32_17_result));
  pp_row_32 pp_row_32_18 (.Rm(Rm), .Rs_bit(Rs[17]), .result(pp_row_32_18_result));
  pp_row_32 pp_row_32_19 (.Rm(Rm), .Rs_bit(Rs[18]), .result(pp_row_32_19_result));
  pp_row_32 pp_row_32_20 (.Rm(Rm), .Rs_bit(Rs[19]), .result(pp_row_32_20_result));
  pp_row_32 pp_row_32_21 (.Rm(Rm), .Rs_bit(Rs[20]), .result(pp_row_32_21_result));
  pp_row_32 pp_row_32_22 (.Rm(Rm), .Rs_bit(Rs[21]), .result(pp_row_32_22_result));
  pp_row_32 pp_row_32_23 (.Rm(Rm), .Rs_bit(Rs[22]), .result(pp_row_32_23_result));
  pp_row_32 pp_row_32_24 (.Rm(Rm), .Rs_bit(Rs[23]), .result(pp_row_32_24_result));
  pp_row_32 pp_row_32_25 (.Rm(Rm), .Rs_bit(Rs[24]), .result(pp_row_32_25_result));
  pp_row_32 pp_row_32_26 (.Rm(Rm), .Rs_bit(Rs[25]), .result(pp_row_32_26_result));
  pp_row_32 pp_row_32_27 (.Rm(Rm), .Rs_bit(Rs[26]), .result(pp_row_32_27_result));
  pp_row_32 pp_row_32_28 (.Rm(Rm), .Rs_bit(Rs[27]), .result(pp_row_32_28_result));
  pp_row_32 pp_row_32_29 (.Rm(Rm), .Rs_bit(Rs[28]), .result(pp_row_32_29_result));
  pp_row_32 pp_row_32_30 (.Rm(Rm), .Rs_bit(Rs[29]), .result(pp_row_32_30_result));
  pp_row_32 pp_row_32_31 (.Rm(Rm), .Rs_bit(Rs[30]), .result(pp_row_32_31_result));
  pp_row_32 pp_row_32_32 (.Rm(Rm), .Rs_bit(Rs[31]), .result(pp_row_32_32_result));
  Shifter #(.width(32)) shifter_1 (.in(pp_row_32_1_result), .\dist ({5{1'b0}}), .out(p0));
  Shifter #(.width(32)) shifter_2 (.in(pp_row_32_2_result), .\dist (5'b00001), .out(p1));
  Shifter #(.width(32)) shifter_3 (.in(pp_row_32_3_result), .\dist (5'b00010), .out(p2));
  Shifter #(.width(32)) shifter_4 (.in(pp_row_32_4_result), .\dist (5'b00011), .out(p3));
  Shifter #(.width(32)) shifter_5 (.in(pp_row_32_5_result), .\dist (5'b00100), .out(p4));
  Shifter #(.width(32)) shifter_6 (.in(pp_row_32_6_result), .\dist (5'b00101), .out(p5));
  Shifter #(.width(32)) shifter_7 (.in(pp_row_32_7_result), .\dist (5'b00110), .out(p6));
  Shifter #(.width(32)) shifter_8 (.in(pp_row_32_8_result), .\dist (5'b00111), .out(p7));
  Shifter #(.width(32)) shifter_9 (.in(pp_row_32_9_result), .\dist (5'b01000), .out(p8));
  Shifter #(.width(32)) shifter_10 (.in(pp_row_32_10_result), .\dist (5'b01001), .out(p9));
  Shifter #(.width(32)) shifter_11 (.in(pp_row_32_11_result), .\dist (5'b01010), .out(p10));
  Shifter #(.width(32)) shifter_12 (.in(pp_row_32_12_result), .\dist (5'b01011), .out(p11));
  Shifter #(.width(32)) shifter_13 (.in(pp_row_32_13_result), .\dist (5'b01100), .out(p12));
  Shifter #(.width(32)) shifter_14 (.in(pp_row_32_14_result), .\dist (5'b01101), .out(p13));
  Shifter #(.width(32)) shifter_15 (.in(pp_row_32_15_result), .\dist (5'b01110), .out(p14));
  Shifter #(.width(32)) shifter_16 (.in(pp_row_32_16_result), .\dist (5'b01111), .out(p15));
  Shifter #(.width(32)) shifter_17 (.in(pp_row_32_17_result), .\dist (5'b10000), .out(p16));
  Shifter #(.width(32)) shifter_18 (.in(pp_row_32_18_result), .\dist (5'b10001), .out(p17));
  Shifter #(.width(32)) shifter_19 (.in(pp_row_32_19_result), .\dist (5'b10010), .out(p18));
  Shifter #(.width(32)) shifter_20 (.in(pp_row_32_20_result), .\dist (5'b10011), .out(p19));
  Shifter #(.width(32)) shifter_21 (.in(pp_row_32_21_result), .\dist (5'b10100), .out(p20));
  Shifter #(.width(32)) shifter_22 (.in(pp_row_32_22_result), .\dist (5'b10101), .out(p21));
  Shifter #(.width(32)) shifter_23 (.in(pp_row_32_23_result), .\dist (5'b10110), .out(p22));
  Shifter #(.width(32)) shifter_24 (.in(pp_row_32_24_result), .\dist (5'b10111), .out(p23));
  Shifter #(.width(32)) shifter_25 (.in(pp_row_32_25_result), .\dist (5'b11000), .out(p24));
  Shifter #(.width(32)) shifter_26 (.in(pp_row_32_26_result), .\dist (5'b11001), .out(p25));
  Shifter #(.width(32)) shifter_27 (.in(pp_row_32_27_result), .\dist (5'b11010), .out(p26));
  Shifter #(.width(32)) shifter_28 (.in(pp_row_32_28_result), .\dist (5'b11011), .out(p27));
  Shifter #(.width(32)) shifter_29 (.in(pp_row_32_29_result), .\dist (5'b11100), .out(p28));
  Shifter #(.width(32)) shifter_30 (.in(pp_row_32_30_result), .\dist (5'b11101), .out(p29));
  Shifter #(.width(32)) shifter_31 (.in(pp_row_32_31_result), .\dist (5'b11110), .out(p30));
  Shifter #(.width(32)) shifter_32 (.in(pp_row_32_32_result), .\dist ({5{1'b1}}), .out(p31));

  // Notes on the sheet:
  //   Rm: initial=0xdeadbeef
  //   Rs: initial=0xdeadbeef
endmodule

module csa_3to_2 (
  input  [31:0] X,
  input  [31:0] Y,
  input  [31:0] Z,
  output [31:0] sum,
  output [31:0] carry
);

  wire [31:0] maj_out, XandY_out, XandZ_out, xor_1_out, YandZ_out;

  assign XandY_out = X & Y;  // AND_Gate XandY, 32 bits wide
  assign XandZ_out = X & Z;  // AND_Gate XandZ, 32 bits wide
  assign YandZ_out = Y & Z;  // AND_Gate YandZ, 32 bits wide
  assign xor_1_out = X ^ Z;  // XOR_Gate xor_1, 32 bits wide
  assign maj_out = XandY_out | XandZ_out | YandZ_out;  // OR_Gate maj, 32 bits wide
  Shifter #(.width(32)) shifter_1 (.in(maj_out), .\dist (5'b00001), .out(carry));
  assign sum = Y ^ xor_1_out;  // XOR_Gate xor_2, 32 bits wide
endmodule

module mul_32 (
  input  [31:0] A,
  input  [31:0] B,
  output [31:0] sum,
  output [31:0] carry
);

  wire [31:0] cinco_carry, cinco_sum, csa_3to_2_1_carry, csa_3to_2_1_sum, csa_3to_2_2_carry, csa_3to_2_2_sum,
       csa_3to_2_3_carry, csa_3to_2_3_sum, csa_3to_2_4_carry, csa_3to_2_4_sum, csa_3to_2_5_carry,
       csa_3to_2_5_sum, csa_3to_2_6_carry, csa_3to_2_6_sum, csa_3to_2_7_carry, csa_3to_2_7_sum,
       csa_3to_2_8_carry, csa_3to_2_8_sum, csa_3to_2_9_carry, csa_3to_2_9_sum, csa_3to_2_10_carry,
       csa_3to_2_10_sum, csa_3to_2_11_carry, csa_3to_2_11_sum, csa_3to_2_12_carry, csa_3to_2_12_sum,
       csa_3to_2_13_carry, csa_3to_2_13_sum, csa_3to_2_14_carry, csa_3to_2_14_sum, csa_3to_2_15_carry,
       csa_3to_2_15_sum, csa_3to_2_16_carry, csa_3to_2_16_sum, csa_3to_2_17_carry, csa_3to_2_17_sum,
       diecsiete_carry, diecsiete_sum, diez_carry, diez_sum, dos_carry, dos_sum, partial_products_1_p0,
       partial_products_1_p1, partial_products_1_p2, partial_products_1_p3, partial_products_1_p4,
       partial_products_1_p5, partial_products_1_p6, partial_products_1_p7, partial_products_1_p8,
       partial_products_1_p9, partial_products_1_p10, partial_products_1_p11, partial_products_1_p12,
       partial_products_1_p13, partial_products_1_p14, partial_products_1_p15, partial_products_1_p16,
       partial_products_1_p17, partial_products_1_p18, partial_products_1_p19, partial_products_1_p20,
       partial_products_1_p21, partial_products_1_p22, partial_products_1_p23, partial_products_1_p24,
       partial_products_1_p25, partial_products_1_p26, partial_products_1_p27, partial_products_1_p28,
       partial_products_1_p29, partial_products_1_p30, partial_products_1_p31, quince_carry, quince_sum,
       siete_carry, siete_sum, trece_carry, trece_sum, tres_carry, tres_sum, un_carry, un_sum, vente4_carry,
       vente4_sum, vente7_carry, vente7_sum, viente_carry, viente_sum;

  partial_products partial_products_1 (
    .Rm(A), .Rs(B), .p0(partial_products_1_p0), .p1(partial_products_1_p1), .p2(partial_products_1_p2),
    .p3(partial_products_1_p3), .p4(partial_products_1_p4), .p5(partial_products_1_p5),
    .p6(partial_products_1_p6), .p7(partial_products_1_p7), .p8(partial_products_1_p8),
    .p9(partial_products_1_p9), .p10(partial_products_1_p10), .p11(partial_products_1_p11),
    .p12(partial_products_1_p12), .p13(partial_products_1_p13), .p14(partial_products_1_p14),
    .p15(partial_products_1_p15), .p16(partial_products_1_p16), .p17(partial_products_1_p17),
    .p18(partial_products_1_p18), .p19(partial_products_1_p19), .p20(partial_products_1_p20),
    .p21(partial_products_1_p21), .p22(partial_products_1_p22), .p23(partial_products_1_p23),
    .p24(partial_products_1_p24), .p25(partial_products_1_p25), .p26(partial_products_1_p26),
    .p27(partial_products_1_p27), .p28(partial_products_1_p28), .p29(partial_products_1_p29),
    .p30(partial_products_1_p30), .p31(partial_products_1_p31));
  csa_3to_2 un (
    .X(partial_products_1_p0), .Y(partial_products_1_p1), .Z(partial_products_1_p2), .sum(un_sum),
    .carry(un_carry));
  csa_3to_2 dos (.X(un_sum), .Y(un_carry), .Z(partial_products_1_p3), .sum(dos_sum), .carry(dos_carry));
  csa_3to_2 tres (.X(dos_sum), .Y(dos_carry), .Z(partial_products_1_p4), .sum(tres_sum), .carry(tres_carry));
  csa_3to_2 csa_3to_2_1 (
    .X(tres_sum), .Y(tres_carry), .Z(partial_products_1_p5), .sum(csa_3to_2_1_sum), .carry(csa_3to_2_1_carry));
  csa_3to_2 cinco (
    .X(csa_3to_2_1_sum), .Y(csa_3to_2_1_carry), .Z(partial_products_1_p6), .sum(cinco_sum),
    .carry(cinco_carry));
  csa_3to_2 csa_3to_2_2 (
    .X(cinco_sum), .Y(cinco_carry), .Z(partial_products_1_p7), .sum(csa_3to_2_2_sum),
    .carry(csa_3to_2_2_carry));
  csa_3to_2 siete (
    .X(csa_3to_2_2_sum), .Y(csa_3to_2_2_carry), .Z(partial_products_1_p8), .sum(siete_sum),
    .carry(siete_carry));
  csa_3to_2 csa_3to_2_3 (
    .X(siete_sum), .Y(siete_carry), .Z(partial_products_1_p9), .sum(csa_3to_2_3_sum),
    .carry(csa_3to_2_3_carry));
  csa_3to_2 csa_3to_2_4 (
    .X(csa_3to_2_3_sum), .Y(csa_3to_2_3_carry), .Z(partial_products_1_p10), .sum(csa_3to_2_4_sum),
    .carry(csa_3to_2_4_carry));
  csa_3to_2 diez (
    .X(csa_3to_2_4_sum), .Y(csa_3to_2_4_carry), .Z(partial_products_1_p11), .sum(diez_sum), .carry(diez_carry));
  csa_3to_2 csa_3to_2_5 (
    .X(diez_sum), .Y(diez_carry), .Z(partial_products_1_p12), .sum(csa_3to_2_5_sum), .carry(csa_3to_2_5_carry));
  csa_3to_2 csa_3to_2_6 (
    .X(csa_3to_2_5_sum), .Y(csa_3to_2_5_carry), .Z(partial_products_1_p13), .sum(csa_3to_2_6_sum),
    .carry(csa_3to_2_6_carry));
  csa_3to_2 trece (
    .X(csa_3to_2_6_sum), .Y(csa_3to_2_6_carry), .Z(partial_products_1_p14), .sum(trece_sum),
    .carry(trece_carry));
  csa_3to_2 csa_3to_2_7 (
    .X(trece_sum), .Y(trece_carry), .Z(partial_products_1_p15), .sum(csa_3to_2_7_sum),
    .carry(csa_3to_2_7_carry));
  // Probe on quince_sum
  csa_3to_2 quince (
    .X(csa_3to_2_7_sum), .Y(csa_3to_2_7_carry), .Z(partial_products_1_p16), .sum(quince_sum),
    .carry(quince_carry));
  csa_3to_2 csa_3to_2_8 (
    .X(quince_sum), .Y(quince_carry), .Z(partial_products_1_p17), .sum(csa_3to_2_8_sum),
    .carry(csa_3to_2_8_carry));
  csa_3to_2 diecsiete (
    .X(csa_3to_2_8_sum), .Y(csa_3to_2_8_carry), .Z(partial_products_1_p18), .sum(diecsiete_sum),
    .carry(diecsiete_carry));
  csa_3to_2 csa_3to_2_9 (
    .X(diecsiete_sum), .Y(diecsiete_carry), .Z(partial_products_1_p19), .sum(csa_3to_2_9_sum),
    .carry(csa_3to_2_9_carry));
  csa_3to_2 csa_3to_2_10 (
    .X(csa_3to_2_9_sum), .Y(csa_3to_2_9_carry), .Z(partial_products_1_p20), .sum(csa_3to_2_10_sum),
    .carry(csa_3to_2_10_carry));
  csa_3to_2 viente (
    .X(csa_3to_2_10_sum), .Y(csa_3to_2_10_carry), .Z(partial_products_1_p21), .sum(viente_sum),
    .carry(viente_carry));
  csa_3to_2 csa_3to_2_11 (
    .X(viente_sum), .Y(viente_carry), .Z(partial_products_1_p22), .sum(csa_3to_2_11_sum),
    .carry(csa_3to_2_11_carry));
  csa_3to_2 csa_3to_2_12 (
    .X(csa_3to_2_11_sum), .Y(csa_3to_2_11_carry), .Z(partial_products_1_p23), .sum(csa_3to_2_12_sum),
    .carry(csa_3to_2_12_carry));
  csa_3to_2 csa_3to_2_13 (
    .X(csa_3to_2_12_sum), .Y(csa_3to_2_12_carry), .Z(partial_products_1_p24), .sum(csa_3to_2_13_sum),
    .carry(csa_3to_2_13_carry));
  csa_3to_2 vente4 (
    .X(csa_3to_2_13_sum), .Y(csa_3to_2_13_carry), .Z(partial_products_1_p25), .sum(vente4_sum),
    .carry(vente4_carry));
  csa_3to_2 csa_3to_2_14 (
    .X(vente4_sum), .Y(vente4_carry), .Z(partial_products_1_p26), .sum(csa_3to_2_14_sum),
    .carry(csa_3to_2_14_carry));
  csa_3to_2 csa_3to_2_15 (
    .X(csa_3to_2_14_sum), .Y(csa_3to_2_14_carry), .Z(partial_products_1_p27), .sum(csa_3to_2_15_sum),
    .carry(csa_3to_2_15_carry));
  csa_3to_2 vente7 (
    .X(csa_3to_2_15_sum), .Y(csa_3to_2_15_carry), .Z(partial_products_1_p28), .sum(vente7_sum),
    .carry(vente7_carry));
  csa_3to_2 csa_3to_2_16 (
    .X(vente7_sum), .Y(vente7_carry), .Z(partial_products_1_p29), .sum(csa_3to_2_16_sum),
    .carry(csa_3to_2_16_carry));
  csa_3to_2 csa_3to_2_17 (
    .X(csa_3to_2_16_sum), .Y(csa_3to_2_16_carry), .Z(partial_products_1_p30), .sum(csa_3to_2_17_sum),
    .carry(csa_3to_2_17_carry));
  csa_3to_2 csa_3to_2_18 (
    .X(csa_3to_2_17_sum), .Y(csa_3to_2_17_carry), .Z(partial_products_1_p31), .sum(sum), .carry(carry));

  // Notes on the sheet:
  //   A: initial=0xdeadbeef
  //   B: initial=0xdeadbeef
endmodule

module pc_fetch (
  input  CLK,
  input  BRANCH,
  input  hold,
  input  [31:0] IMM,
  input  [31:0] abs_target,
  input  abs_select,
  input  RST,
  output [31:0] pc_plus4,
  output [9:0] pc_out
);

  wire [31:0] adder_2_out, multiplexer_1_out, multiplexer_2_out, multiplexer_3_out, PC_q;

  Register #(.width(32)) PC (
    .D(multiplexer_3_out), .en(1'b1), .clk(CLK), .Q({PC_q[31:12], pc_out, PC_q[1:0]}), .clr(RST));
  Adder #(.width(32)) adder_1 (
    .a({PC_q[31:12], pc_out, PC_q[1:0]}), .b(32'h4), .out(pc_plus4), .cin(1'b0));  // open: cout
  Adder #(.width(32)) adder_2 (
    .a({PC_q[31:12], pc_out, PC_q[1:0]}), .b(IMM), .out(adder_2_out), .cin(1'b0));  // open: cout
  Multiplexer #(.width(32)) multiplexer_1 (
    .in0(adder_2_out), .in1(abs_target), .out(multiplexer_1_out), .sel(abs_select));
  Multiplexer #(.width(32)) multiplexer_2 (
    .in0(pc_plus4), .in1(multiplexer_1_out), .out(multiplexer_2_out), .sel(BRANCH));
  Multiplexer #(.width(32)) multiplexer_3 (
    .in0(multiplexer_2_out), .in1({PC_q[31:12], pc_out, PC_q[1:0]}), .out(multiplexer_3_out), .sel(hold));
endmodule

module reg16x32 (
  input  CLK,
  input  [3:0] WA,
  input  [31:0] WD,
  input  WE,
  input  RST,
  input  [3:0] RA,
  input  [3:0] RB,
  output [31:0] R0_OUTPUT,
  output [31:0] R1_OUTPUT,
  output [31:0] R3_OUTPUT,
  output [31:0] R2_OUPUT,
  output [31:0] R5_OUTPUT,
  output [31:0] R4_OUTPUT,
  output [31:0] RD_A,
  output [31:0] R7_OUTPUT,
  output [31:0] R6_OUTPUT,
  output [31:0] RD_B,
  output [31:0] R8_OUTPUT,
  output [31:0] R9_OUTPUT,
  output [31:0] R11_OUTPUT,
  output [31:0] R10_OUTPUT,
  output [31:0] R13_OUTPUT,
  output [31:0] R12_OUTPUT,
  output [31:0] R15_OUTPUT,
  output [31:0] R14_OUTPUT
);

  wire and_1_out, and_2_out, and_3_out, and_4_out, and_5_out, and_6_out, and_7_out, and_8_out, and_9_out,
       and_10_out, and_11_out, and_12_out, and_13_out, and_14_out, and_15_out, and_16_out, decoder_1_out0,
       decoder_1_out1, decoder_1_out2, decoder_1_out3, decoder_1_out4, decoder_1_out5, decoder_1_out6,
       decoder_1_out7, decoder_1_out8, decoder_1_out9, decoder_1_out10, decoder_1_out11, decoder_1_out12,
       decoder_1_out13, decoder_1_out14, decoder_1_out15;

  Decoder #(.select(4)) decoder_1 (
    .out0(decoder_1_out0), .out1(decoder_1_out1), .out2(decoder_1_out2), .out3(decoder_1_out3),
    .out4(decoder_1_out4), .out5(decoder_1_out5), .out6(decoder_1_out6), .out7(decoder_1_out7),
    .out8(decoder_1_out8), .out9(decoder_1_out9), .out10(decoder_1_out10), .out11(decoder_1_out11),
    .out12(decoder_1_out12), .out13(decoder_1_out13), .out14(decoder_1_out14), .out15(decoder_1_out15),
    .sel(WA), .en(WE));
  and and_1 (and_1_out, decoder_1_out0, WE);
  and and_2 (and_2_out, decoder_1_out1, WE);
  and and_3 (and_3_out, decoder_1_out2, WE);
  and and_4 (and_4_out, decoder_1_out3, WE);
  and and_5 (and_5_out, decoder_1_out4, WE);
  and and_6 (and_6_out, decoder_1_out5, WE);
  and and_7 (and_7_out, decoder_1_out6, WE);
  and and_8 (and_8_out, decoder_1_out7, WE);
  and and_9 (and_9_out, decoder_1_out8, WE);
  and and_10 (and_10_out, decoder_1_out9, WE);
  and and_11 (and_11_out, decoder_1_out10, WE);
  and and_12 (and_12_out, decoder_1_out11, WE);
  and and_13 (and_13_out, decoder_1_out12, WE);
  and and_14 (and_14_out, decoder_1_out13, WE);
  and and_15 (and_15_out, decoder_1_out14, WE);
  and and_16 (and_16_out, decoder_1_out15, WE);
  Register #(.width(32)) R0 (.D(WD), .en(and_1_out), .clk(CLK), .Q(R0_OUTPUT), .clr(RST));
  Register #(.width(32)) R2 (.D(WD), .en(and_3_out), .clk(CLK), .Q(R2_OUPUT), .clr(RST));
  Register #(.width(32)) R4 (.D(WD), .en(and_5_out), .clk(CLK), .Q(R4_OUTPUT), .clr(RST));
  Register #(.width(32)) R6 (.D(WD), .en(and_7_out), .clk(CLK), .Q(R6_OUTPUT), .clr(RST));
  Register #(.width(32)) R8 (.D(WD), .en(and_9_out), .clk(CLK), .Q(R8_OUTPUT), .clr(RST));
  Register #(.width(32)) R10 (.D(WD), .en(and_11_out), .clk(CLK), .Q(R10_OUTPUT), .clr(RST));
  Register #(.width(32)) R12 (.D(WD), .en(and_13_out), .clk(CLK), .Q(R12_OUTPUT), .clr(RST));
  Register #(.width(32)) R14 (.D(WD), .en(and_15_out), .clk(CLK), .Q(R14_OUTPUT), .clr(RST));
  Register #(.width(32)) R1 (.D(WD), .en(and_2_out), .clk(CLK), .Q(R1_OUTPUT), .clr(RST));
  Register #(.width(32)) R3 (.D(WD), .en(and_4_out), .clk(CLK), .Q(R3_OUTPUT), .clr(RST));
  Register #(.width(32)) R5 (.D(WD), .en(and_6_out), .clk(CLK), .Q(R5_OUTPUT), .clr(RST));
  Register #(.width(32)) R7 (.D(WD), .en(and_8_out), .clk(CLK), .Q(R7_OUTPUT), .clr(RST));
  Register #(.width(32)) R9 (.D(WD), .en(and_10_out), .clk(CLK), .Q(R9_OUTPUT), .clr(RST));
  Register #(.width(32)) R11 (.D(WD), .en(and_12_out), .clk(CLK), .Q(R11_OUTPUT), .clr(RST));
  Register #(.width(32)) R13 (.D(WD), .en(and_14_out), .clk(CLK), .Q(R13_OUTPUT), .clr(RST));
  Register #(.width(32)) R15 (.D(WD), .en(and_16_out), .clk(CLK), .Q(R15_OUTPUT), .clr(RST));
  Multiplexer #(.select(4), .width(32)) multiplexer_1 (
    .in0(R0_OUTPUT), .in1(R1_OUTPUT), .in2(R2_OUPUT), .in3(R3_OUTPUT), .in4(R4_OUTPUT), .in5(R5_OUTPUT),
    .in6(R6_OUTPUT), .in7(R7_OUTPUT), .in8(R8_OUTPUT), .in9(R9_OUTPUT), .in10(R10_OUTPUT), .in11(R11_OUTPUT),
    .in12(R12_OUTPUT), .in13(R13_OUTPUT), .in14(R14_OUTPUT), .in15(R15_OUTPUT), .out(RD_A), .sel(RA));
  Multiplexer #(.select(4), .width(32)) multiplexer_2 (
    .in0(R0_OUTPUT), .in1(R1_OUTPUT), .in2(R2_OUPUT), .in3(R3_OUTPUT), .in4(R4_OUTPUT), .in5(R5_OUTPUT),
    .in6(R6_OUTPUT), .in7(R7_OUTPUT), .in8(R8_OUTPUT), .in9(R9_OUTPUT), .in10(R10_OUTPUT), .in11(R11_OUTPUT),
    .in12(R12_OUTPUT), .in13(R13_OUTPUT), .in14(R14_OUTPUT), .in15(R15_OUTPUT), .out(RD_B), .sel(RB));
endmodule

module PE_cell (
  input  [31:0] w_in,
  input  w_load,
  input  CLK,
  input  [31:0] psum_in,
  input  [31:0] a_in,
  output [31:0] psum_out,
  output [31:0] a_out
);

  wire [31:0] ks_32b_1_sum0, mul_32_1_sum, W_reg_q;

  Register #(.width(32)) W_reg (.D(w_in), .en(w_load), .clk(CLK), .Q(W_reg_q));  // open: clr
  Register #(.width(32)) a_reg (.D(a_in), .clk(CLK), .Q(a_out));  // open: en, clr
  mul_32 mul_32_1 (.A(a_in), .B(W_reg_q), .sum(mul_32_1_sum));  // open: carry
  Register #(.width(32)) psum_reg (.D(ks_32b_1_sum0), .clk(CLK), .Q(psum_out));  // open: en, clr
  ks_32b ks_32b_1 (
    .A(psum_in), .B(mul_32_1_sum), .SUM31(ks_32b_1_sum0[31]), .SUM30(ks_32b_1_sum0[30]),
    .SUM29(ks_32b_1_sum0[29]), .SUM28(ks_32b_1_sum0[28]), .SUM27(ks_32b_1_sum0[27]),
    .SUM26(ks_32b_1_sum0[26]), .SUM25(ks_32b_1_sum0[25]), .SUM24(ks_32b_1_sum0[24]),
    .SUM23(ks_32b_1_sum0[23]), .SUM22(ks_32b_1_sum0[22]), .SUM21(ks_32b_1_sum0[21]),
    .SUM20(ks_32b_1_sum0[20]), .SUM19(ks_32b_1_sum0[19]), .SUM18(ks_32b_1_sum0[18]),
    .SUM17(ks_32b_1_sum0[17]), .SUM16(ks_32b_1_sum0[16]), .SUM15(ks_32b_1_sum0[15]),
    .SUM14(ks_32b_1_sum0[14]), .SUM13(ks_32b_1_sum0[13]), .SUM12(ks_32b_1_sum0[12]),
    .SUM11(ks_32b_1_sum0[11]), .SUM10(ks_32b_1_sum0[10]), .SUM9(ks_32b_1_sum0[9]), .SUM8(ks_32b_1_sum0[8]),
    .SUM7(ks_32b_1_sum0[7]), .SUM6(ks_32b_1_sum0[6]), .SUM5(ks_32b_1_sum0[5]), .SUM4(ks_32b_1_sum0[4]),
    .SUM3(ks_32b_1_sum0[3]), .SUM2(ks_32b_1_sum0[2]), .sum1(ks_32b_1_sum0[1]), .sum0(ks_32b_1_sum0[0]));  // open: Cin, Cout
endmodule

module systolic_4x4 (
  input  CLK,
  input  [31:0] w00,
  input  [31:0] w01,
  input  [31:0] w02,
  input  [31:0] w03,
  input  w_load,
  input  [31:0] row0,
  input  [31:0] w10,
  input  [31:0] w11,
  input  [31:0] w12,
  input  [31:0] w13,
  input  [31:0] row1,
  input  [31:0] w20,
  input  [31:0] w21,
  input  [31:0] w22,
  input  [31:0] w23,
  input  [31:0] row2,
  input  [31:0] w30,
  input  [31:0] w31,
  input  [31:0] w32,
  input  [31:0] w33,
  input  [31:0] row3,
  output [31:0] c_col0,
  output [31:0] c_col1,
  output [31:0] c_col2,
  output [31:0] c_col3
);

  wire [31:0] pe_cell_1_a_out, pe_cell_1_psum_out, pe_cell_2_a_out, pe_cell_2_psum_out, pe_cell_3_a_out,
       pe_cell_3_psum_out, pe_cell_4_a_out, pe_cell_5_a_out, pe_cell_5_psum_out, pe_cell_6_a_out,
       pe_cell_6_psum_out, pe_cell_7_a_out, pe_cell_7_psum_out, pe_cell_8_a_out, pe_cell_9_a_out,
       pe_cell_9_psum_out, pe_cell_10_a_out, pe_cell_10_psum_out, pe_cell_11_a_out, pe_cell_11_psum_out,
       pe_cell_12_a_out, pe_cell_13_a_out, pe_cell_13_psum_out, pe_cell_14_a_out, pe_cell_14_psum_out,
       pe_cell_15_a_out, pe_cell_15_psum_out, pe_cell_16_a_out;

  PE_cell pe_cell_1 (
    .w_in(w00), .w_load(w_load), .CLK(CLK), .psum_in({32{1'b0}}), .a_in(row0), .psum_out(pe_cell_1_psum_out),
    .a_out(pe_cell_1_a_out));
  PE_cell pe_cell_2 (
    .w_in(w10), .w_load(w_load), .CLK(CLK), .psum_in(pe_cell_1_psum_out), .a_in(row1),
    .psum_out(pe_cell_2_psum_out), .a_out(pe_cell_2_a_out));
  PE_cell pe_cell_3 (
    .w_in(w20), .w_load(w_load), .CLK(CLK), .psum_in(pe_cell_2_psum_out), .a_in(row2),
    .psum_out(pe_cell_3_psum_out), .a_out(pe_cell_3_a_out));
  PE_cell pe_cell_4 (
    .w_in(w30), .w_load(w_load), .CLK(CLK), .psum_in(pe_cell_3_psum_out), .a_in(row3), .psum_out(c_col0),
    .a_out(pe_cell_4_a_out));
  // Probe on pe_cell_1_psum_out
  // Probe on pe_cell_2_psum_out
  // Probe on pe_cell_3_psum_out
  PE_cell pe_cell_5 (
    .w_in(w01), .w_load(w_load), .CLK(CLK), .psum_in({32{1'b0}}), .a_in(pe_cell_1_a_out),
    .psum_out(pe_cell_5_psum_out), .a_out(pe_cell_5_a_out));
  PE_cell pe_cell_6 (
    .w_in(w11), .w_load(w_load), .CLK(CLK), .psum_in(pe_cell_5_psum_out), .a_in(pe_cell_2_a_out),
    .psum_out(pe_cell_6_psum_out), .a_out(pe_cell_6_a_out));
  PE_cell pe_cell_7 (
    .w_in(w21), .w_load(w_load), .CLK(CLK), .psum_in(pe_cell_6_psum_out), .a_in(pe_cell_3_a_out),
    .psum_out(pe_cell_7_psum_out), .a_out(pe_cell_7_a_out));
  PE_cell pe_cell_8 (
    .w_in(w31), .w_load(w_load), .CLK(CLK), .psum_in(pe_cell_7_psum_out), .a_in(pe_cell_4_a_out),
    .psum_out(c_col1), .a_out(pe_cell_8_a_out));
  // Probe on pe_cell_5_psum_out
  // Probe on pe_cell_6_psum_out
  // Probe on pe_cell_7_psum_out
  PE_cell pe_cell_9 (
    .w_in(w02), .w_load(w_load), .CLK(CLK), .psum_in({32{1'b0}}), .a_in(pe_cell_5_a_out),
    .psum_out(pe_cell_9_psum_out), .a_out(pe_cell_9_a_out));
  PE_cell pe_cell_10 (
    .w_in(w12), .w_load(w_load), .CLK(CLK), .psum_in(pe_cell_9_psum_out), .a_in(pe_cell_6_a_out),
    .psum_out(pe_cell_10_psum_out), .a_out(pe_cell_10_a_out));
  PE_cell pe_cell_11 (
    .w_in(w22), .w_load(w_load), .CLK(CLK), .psum_in(pe_cell_10_psum_out), .a_in(pe_cell_7_a_out),
    .psum_out(pe_cell_11_psum_out), .a_out(pe_cell_11_a_out));
  PE_cell pe_cell_12 (
    .w_in(w32), .w_load(w_load), .CLK(CLK), .psum_in(pe_cell_11_psum_out), .a_in(pe_cell_8_a_out),
    .psum_out(c_col2), .a_out(pe_cell_12_a_out));
  // Probe on pe_cell_9_psum_out
  // Probe on pe_cell_10_psum_out
  // Probe on pe_cell_11_psum_out
  PE_cell pe_cell_13 (
    .w_in(w03), .w_load(w_load), .CLK(CLK), .psum_in({32{1'b0}}), .a_in(pe_cell_9_a_out),
    .psum_out(pe_cell_13_psum_out), .a_out(pe_cell_13_a_out));
  PE_cell pe_cell_14 (
    .w_in(w13), .w_load(w_load), .CLK(CLK), .psum_in(pe_cell_13_psum_out), .a_in(pe_cell_10_a_out),
    .psum_out(pe_cell_14_psum_out), .a_out(pe_cell_14_a_out));
  PE_cell pe_cell_15 (
    .w_in(w23), .w_load(w_load), .CLK(CLK), .psum_in(pe_cell_14_psum_out), .a_in(pe_cell_11_a_out),
    .psum_out(pe_cell_15_psum_out), .a_out(pe_cell_15_a_out));
  PE_cell pe_cell_16 (
    .w_in(w33), .w_load(w_load), .CLK(CLK), .psum_in(pe_cell_15_psum_out), .a_in(pe_cell_12_a_out),
    .psum_out(c_col3), .a_out(pe_cell_16_a_out));
  // Probe on pe_cell_13_psum_out
  // Probe on pe_cell_14_psum_out
  // Probe on pe_cell_15_psum_out
endmodule

module matmul4x4 (
  input  [31:0] w00,
  input  [31:0] w01,
  input  [31:0] w02,
  input  [31:0] w03,
  input  in_5,
  input  [31:0] A0,
  input  [31:0] w10,
  input  [31:0] w11,
  input  [31:0] w12,
  input  [31:0] w13,
  input  [31:0] A1,
  input  [31:0] w20,
  input  [31:0] w21,
  input  [31:0] w22,
  input  [31:0] w23,
  input  [31:0] A2,
  input  [31:0] w30,
  input  [31:0] w31,
  input  [31:0] w32,
  input  [31:0] w33,
  input  [31:0] A3,
  output [31:0] out_22,
  output [31:0] out_23,
  output [31:0] out_24,
  output [31:0] out_25
);

  wire clock_1_out;
  wire [31:0] register_1_q, register_2_q, register_3_q, register_4_q, register_5_q, register_6_q,
       register_7_q, register_8_q, register_10_q, systolic_4x4_1_c_col0, systolic_4x4_1_c_col1,
       systolic_4x4_1_c_col2;

  Clock clock_1 (.out(clock_1_out));
  Register #(.width(32)) register_1 (.D(A2), .clk(clock_1_out), .Q(register_1_q));  // open: en, clr
  Register #(.width(32)) register_2 (.D(A1), .clk(clock_1_out), .Q(register_2_q));  // open: en, clr
  Register #(.width(32)) register_3 (.D(A3), .clk(clock_1_out), .Q(register_3_q));  // open: en, clr
  Register #(.width(32)) register_4 (.D(register_1_q), .clk(clock_1_out), .Q(register_4_q));  // open: en, clr
  Register #(.width(32)) register_5 (.D(register_3_q), .clk(clock_1_out), .Q(register_5_q));  // open: en, clr
  Register #(.width(32)) register_6 (.D(register_5_q), .clk(clock_1_out), .Q(register_6_q));  // open: en, clr
  systolic_4x4 systolic_4x4_1 (
    .CLK(clock_1_out), .w00(w00), .w01(w01), .w02(w02), .w03(w03), .w_load(in_5), .row0(A0), .w10(w10),
    .w11(w11), .w12(w12), .w13(w13), .row1(register_2_q), .w20(w20), .w21(w21), .w22(w22), .w23(w23),
    .row2(register_4_q), .w30(w30), .w31(w31), .w32(w32), .w33(w33), .row3(register_6_q),
    .c_col0(systolic_4x4_1_c_col0), .c_col1(systolic_4x4_1_c_col1), .c_col2(systolic_4x4_1_c_col2),
    .c_col3(out_23));
  Register #(.width(32)) register_7 (.D(systolic_4x4_1_c_col0), .clk(clock_1_out), .Q(register_7_q));  // open: en, clr
  Register #(.width(32)) register_8 (.D(systolic_4x4_1_c_col1), .clk(clock_1_out), .Q(register_8_q));  // open: en, clr
  Register #(.width(32)) register_9 (.D(systolic_4x4_1_c_col2), .clk(clock_1_out), .Q(out_25));  // open: en, clr
  Register #(.width(32)) register_10 (.D(register_7_q), .clk(clock_1_out), .Q(register_10_q));  // open: en, clr
  Register #(.width(32)) register_11 (.D(register_8_q), .clk(clock_1_out), .Q(out_24));  // open: en, clr
  Register #(.width(32)) register_12 (.D(register_10_q), .clk(clock_1_out), .Q(out_22));  // open: en, clr
endmodule

module pp_row_16 (
  input  [15:0] Rm,
  input  Rs_bit,
  output [15:0] result
);

  wire [15:0] bit_extender_1_out;

  assign bit_extender_1_out = {{15{Rs_bit}}, Rs_bit};  // Bit_Extender bit_extender_1
  assign result = Rm & bit_extender_1_out;  // AND_Gate and_1, 16 bits wide

  // Notes on the sheet:
  //   Rm: initial=0xdeadbeef
endmodule

module csa_16 (
  input  [15:0] X,
  input  [15:0] Y,
  input  [15:0] Z,
  output [15:0] sum,
  output [15:0] carry
);

  wire [15:0] maj_out, XandY_out, XandZ_out, xor_1_out, YandZ_out;

  assign XandY_out = X & Y;  // AND_Gate XandY, 16 bits wide
  assign XandZ_out = X & Z;  // AND_Gate XandZ, 16 bits wide
  assign YandZ_out = Y & Z;  // AND_Gate YandZ, 16 bits wide
  assign xor_1_out = X ^ Z;  // XOR_Gate xor_1, 16 bits wide
  assign maj_out = XandY_out | XandZ_out | YandZ_out;  // OR_Gate maj, 16 bits wide
  Shifter #(.width(16)) shifter_1 (.in(maj_out), .\dist (4'b0001), .out(carry));
  assign sum = Y ^ xor_1_out;  // XOR_Gate xor_2, 16 bits wide
endmodule

module pp_8 (
  input  [7:0] Rm,
  input  [7:0] Rs,
  output [15:0] p0,
  output [15:0] p1,
  output [15:0] p2,
  output [15:0] p3,
  output [15:0] p4,
  output [15:0] p5,
  output [15:0] p6,
  output [15:0] p7
);

  wire [15:0] bit_extender_1_out, pp_row_16_1_result, pp_row_16_2_result, pp_row_16_3_result,
       pp_row_16_4_result, pp_row_16_5_result, pp_row_16_6_result, pp_row_16_7_result, pp_row_16_8_result;

  assign bit_extender_1_out = {{8{1'b0}}, Rm};  // Bit_Extender bit_extender_1
  pp_row_16 pp_row_16_1 (.Rm(bit_extender_1_out), .Rs_bit(Rs[0]), .result(pp_row_16_1_result));
  pp_row_16 pp_row_16_2 (.Rm(bit_extender_1_out), .Rs_bit(Rs[1]), .result(pp_row_16_2_result));
  pp_row_16 pp_row_16_3 (.Rm(bit_extender_1_out), .Rs_bit(Rs[2]), .result(pp_row_16_3_result));
  pp_row_16 pp_row_16_4 (.Rm(bit_extender_1_out), .Rs_bit(Rs[3]), .result(pp_row_16_4_result));
  pp_row_16 pp_row_16_5 (.Rm(bit_extender_1_out), .Rs_bit(Rs[4]), .result(pp_row_16_5_result));
  pp_row_16 pp_row_16_6 (.Rm(bit_extender_1_out), .Rs_bit(Rs[5]), .result(pp_row_16_6_result));
  pp_row_16 pp_row_16_7 (.Rm(bit_extender_1_out), .Rs_bit(Rs[6]), .result(pp_row_16_7_result));
  pp_row_16 pp_row_16_8 (.Rm(bit_extender_1_out), .Rs_bit(Rs[7]), .result(pp_row_16_8_result));
  Shifter #(.width(16)) shifter_1 (.in(pp_row_16_1_result), .\dist (4'b0000), .out(p0));
  Shifter #(.width(16)) shifter_2 (.in(pp_row_16_2_result), .\dist (4'b0001), .out(p1));
  Shifter #(.width(16)) shifter_3 (.in(pp_row_16_3_result), .\dist (4'b0010), .out(p2));
  Shifter #(.width(16)) shifter_4 (.in(pp_row_16_4_result), .\dist (4'b0011), .out(p3));
  Shifter #(.width(16)) shifter_5 (.in(pp_row_16_5_result), .\dist (4'b0100), .out(p4));
  Shifter #(.width(16)) shifter_6 (.in(pp_row_16_6_result), .\dist (4'b0101), .out(p5));
  Shifter #(.width(16)) shifter_7 (.in(pp_row_16_7_result), .\dist (4'b0110), .out(p6));
  Shifter #(.width(16)) shifter_8 (.in(pp_row_16_8_result), .\dist (4'b0111), .out(p7));

  // Notes on the sheet:
  //   Rm: initial=0xbe
  //   Rs: initial=0xdeadbeef
endmodule

module mul_8 (
  input  [7:0] in_1,
  input  [7:0] in_2,
  output [31:0] out_3
);

  wire [15:0] csa_16_1_carry, csa_16_1_sum, csa_16_2_carry, csa_16_2_sum, csa_16_3_carry, csa_16_3_sum,
       csa_16_4_carry, csa_16_4_sum, csa_16_5_carry, csa_16_5_sum, csa_16_6_carry, csa_16_6_sum, pp_8_1_p0,
       pp_8_1_p1, pp_8_1_p2, pp_8_1_p3, pp_8_1_p4, pp_8_1_p5, pp_8_1_p6, pp_8_1_p7;
  wire [31:0] bit_extender_1_out, bit_extender_2_out;

  pp_8 pp_8_1 (
    .Rm(in_1), .Rs(in_2), .p0(pp_8_1_p0), .p1(pp_8_1_p1), .p2(pp_8_1_p2), .p3(pp_8_1_p3), .p4(pp_8_1_p4),
    .p5(pp_8_1_p5), .p6(pp_8_1_p6), .p7(pp_8_1_p7));
  csa_16 csa_16_1 (.X(pp_8_1_p0), .Y(pp_8_1_p1), .Z(pp_8_1_p2), .sum(csa_16_1_sum), .carry(csa_16_1_carry));
  csa_16 csa_16_2 (.X(csa_16_1_sum), .Y(csa_16_1_carry), .Z(pp_8_1_p3), .sum(csa_16_2_sum), .carry(csa_16_2_carry));
  csa_16 csa_16_3 (.X(csa_16_2_sum), .Y(csa_16_2_carry), .Z(pp_8_1_p4), .sum(csa_16_3_sum), .carry(csa_16_3_carry));
  csa_16 csa_16_4 (.X(csa_16_3_sum), .Y(csa_16_3_carry), .Z(pp_8_1_p5), .sum(csa_16_4_sum), .carry(csa_16_4_carry));
  csa_16 csa_16_5 (.X(csa_16_4_sum), .Y(csa_16_4_carry), .Z(pp_8_1_p6), .sum(csa_16_5_sum), .carry(csa_16_5_carry));
  csa_16 csa_16_6 (.X(csa_16_5_sum), .Y(csa_16_5_carry), .Z(pp_8_1_p7), .sum(csa_16_6_sum), .carry(csa_16_6_carry));
  assign bit_extender_1_out = {{16{csa_16_6_sum[15]}}, csa_16_6_sum};  // Bit_Extender bit_extender_1
  assign bit_extender_2_out = {{16{csa_16_6_carry[15]}}, csa_16_6_carry};  // Bit_Extender bit_extender_2
  ks_32b ks_32b_1 (
    .A(bit_extender_1_out), .B(bit_extender_2_out), .SUM31(out_3[31]), .SUM30(out_3[30]), .SUM29(out_3[29]),
    .SUM28(out_3[28]), .SUM27(out_3[27]), .SUM26(out_3[26]), .SUM25(out_3[25]), .SUM24(out_3[24]),
    .SUM23(out_3[23]), .SUM22(out_3[22]), .SUM21(out_3[21]), .SUM20(out_3[20]), .SUM19(out_3[19]),
    .SUM18(out_3[18]), .SUM17(out_3[17]), .SUM16(out_3[16]), .SUM15(out_3[15]), .SUM14(out_3[14]),
    .SUM13(out_3[13]), .SUM12(out_3[12]), .SUM11(out_3[11]), .SUM10(out_3[10]), .SUM9(out_3[9]),
    .SUM8(out_3[8]), .SUM7(out_3[7]), .SUM6(out_3[6]), .SUM5(out_3[5]), .SUM4(out_3[4]), .SUM3(out_3[3]),
    .SUM2(out_3[2]), .sum1(out_3[1]), .sum0(out_3[0]));  // open: Cin, Cout

  // Notes on the sheet:
  //   in_1: initial=0xff
  //   in_2: initial=0xff
endmodule
module bs_stage_1 (
  input  [31:0] input_32,
  input  enable,
  input  [1:0] typ_2,
  output [31:0] out_1
);

  wire [31:0] multiplexer_1_out, shifter_1_out, shifter_2_out, shifter_3_out, shifter_4_out;

  Shifter #(.width(32)) shifter_1 (.in(input_32), .\dist (5'b00001), .out(shifter_1_out));
  Shifter #(.shift("lr"), .width(32)) shifter_2 (.in(input_32), .\dist (5'b00001), .out(shifter_2_out));
  Shifter #(.shift("ar"), .width(32)) shifter_3 (.in(input_32), .\dist (5'b00001), .out(shifter_3_out));
  Shifter #(.shift("rr"), .width(32)) shifter_4 (.in(input_32), .\dist (5'b00001), .out(shifter_4_out));
  Multiplexer #(.select(2), .width(32)) multiplexer_1 (
    .in0(shifter_1_out), .in1(shifter_2_out), .in2(shifter_3_out), .in3(shifter_4_out),
    .out(multiplexer_1_out), .sel(typ_2));
  Multiplexer #(.width(32)) multiplexer_2 (.in0(input_32), .in1(multiplexer_1_out), .out(out_1), .sel(enable));

  // Notes on the sheet:
  //   input_32: initial=0x9e3779b8
endmodule

module bs_stage_2 (
  input  [31:0] input_32,
  input  enable,
  input  [1:0] typ_2,
  output [31:0] out_1
);

  wire [31:0] multiplexer_1_out, shifter_1_out, shifter_2_out, shifter_3_out, shifter_4_out;

  Shifter #(.width(32)) shifter_1 (.in(input_32), .\dist (5'b00010), .out(shifter_1_out));
  Shifter #(.shift("lr"), .width(32)) shifter_2 (.in(input_32), .\dist (5'b00010), .out(shifter_2_out));
  Shifter #(.shift("ar"), .width(32)) shifter_3 (.in(input_32), .\dist (5'b00010), .out(shifter_3_out));
  Shifter #(.shift("rr"), .width(32)) shifter_4 (.in(input_32), .\dist (5'b00010), .out(shifter_4_out));
  Multiplexer #(.select(2), .width(32)) multiplexer_1 (
    .in0(shifter_1_out), .in1(shifter_2_out), .in2(shifter_3_out), .in3(shifter_4_out),
    .out(multiplexer_1_out), .sel(typ_2));
  Multiplexer #(.width(32)) multiplexer_2 (.in0(input_32), .in1(multiplexer_1_out), .out(out_1), .sel(enable));

  // Notes on the sheet:
  //   input_32: initial=0x9e3779b8
endmodule

module bs_stage_4 (
  input  [31:0] input_32,
  input  enable,
  input  [1:0] typ_2,
  output [31:0] out_1
);

  wire [31:0] multiplexer_1_out, shifter_1_out, shifter_2_out, shifter_3_out, shifter_4_out;

  Shifter #(.width(32)) shifter_1 (.in(input_32), .\dist (5'b00100), .out(shifter_1_out));
  Shifter #(.shift("lr"), .width(32)) shifter_2 (.in(input_32), .\dist (5'b00100), .out(shifter_2_out));
  Shifter #(.shift("ar"), .width(32)) shifter_3 (.in(input_32), .\dist (5'b00100), .out(shifter_3_out));
  Shifter #(.shift("rr"), .width(32)) shifter_4 (.in(input_32), .\dist (5'b00100), .out(shifter_4_out));
  Multiplexer #(.select(2), .width(32)) multiplexer_1 (
    .in0(shifter_1_out), .in1(shifter_2_out), .in2(shifter_3_out), .in3(shifter_4_out),
    .out(multiplexer_1_out), .sel(typ_2));
  Multiplexer #(.width(32)) multiplexer_2 (.in0(input_32), .in1(multiplexer_1_out), .out(out_1), .sel(enable));

  // Notes on the sheet:
  //   input_32: initial=0x9e3779b8
endmodule

module bs_stage_8 (
  input  [31:0] input_32,
  input  enable,
  input  [1:0] typ_2,
  output [31:0] out_1
);

  wire [31:0] multiplexer_1_out, shifter_1_out, shifter_2_out, shifter_3_out, shifter_4_out;

  Shifter #(.width(32)) shifter_1 (.in(input_32), .\dist (5'b01000), .out(shifter_1_out));
  Shifter #(.shift("lr"), .width(32)) shifter_2 (.in(input_32), .\dist (5'b01000), .out(shifter_2_out));
  Shifter #(.shift("ar"), .width(32)) shifter_3 (.in(input_32), .\dist (5'b01000), .out(shifter_3_out));
  Shifter #(.shift("rr"), .width(32)) shifter_4 (.in(input_32), .\dist (5'b01000), .out(shifter_4_out));
  Multiplexer #(.select(2), .width(32)) multiplexer_1 (
    .in0(shifter_1_out), .in1(shifter_2_out), .in2(shifter_3_out), .in3(shifter_4_out),
    .out(multiplexer_1_out), .sel(typ_2));
  Multiplexer #(.width(32)) multiplexer_2 (.in0(input_32), .in1(multiplexer_1_out), .out(out_1), .sel(enable));

  // Notes on the sheet:
  //   input_32: initial=0x9e3779b8
endmodule

module bs_stage_16 (
  input  [31:0] input_32,
  input  enable,
  input  [1:0] typ_2,
  output [31:0] out_1
);

  wire [31:0] multiplexer_1_out, shifter_1_out, shifter_2_out, shifter_3_out, shifter_4_out;

  Shifter #(.width(32)) shifter_1 (.in(input_32), .\dist (5'b10000), .out(shifter_1_out));
  Shifter #(.shift("lr"), .width(32)) shifter_2 (.in(input_32), .\dist (5'b10000), .out(shifter_2_out));
  Shifter #(.shift("ar"), .width(32)) shifter_3 (.in(input_32), .\dist (5'b10000), .out(shifter_3_out));
  Shifter #(.shift("rr"), .width(32)) shifter_4 (.in(input_32), .\dist (5'b10000), .out(shifter_4_out));
  Multiplexer #(.select(2), .width(32)) multiplexer_1 (
    .in0(shifter_1_out), .in1(shifter_2_out), .in2(shifter_3_out), .in3(shifter_4_out),
    .out(multiplexer_1_out), .sel(typ_2));
  Multiplexer #(.width(32)) multiplexer_2 (.in0(input_32), .in1(multiplexer_1_out), .out(out_1), .sel(enable));

  // Notes on the sheet:
  //   input_32: initial=0x9e3779b8
endmodule

module barrel_32b (
  input  [31:0] input_32b,
  input  [4:0] amnt,
  input  [1:0] typ,
  output [31:0] outp
);

  wire [31:0] bs_stage_1_1_out_1, bs_stage_2_1_out_1, bs_stage_4_1_out_1, bs_stage_8_1_out_1;

  bs_stage_1 bs_stage_1_1 (.input_32(input_32b), .enable(amnt[0]), .typ_2(typ), .out_1(bs_stage_1_1_out_1));
  bs_stage_2 bs_stage_2_1 (.input_32(bs_stage_1_1_out_1), .enable(amnt[1]), .typ_2(typ), .out_1(bs_stage_2_1_out_1));
  bs_stage_4 bs_stage_4_1 (.input_32(bs_stage_2_1_out_1), .enable(amnt[2]), .typ_2(typ), .out_1(bs_stage_4_1_out_1));
  bs_stage_8 bs_stage_8_1 (.input_32(bs_stage_4_1_out_1), .enable(amnt[3]), .typ_2(typ), .out_1(bs_stage_8_1_out_1));
  bs_stage_16 bs_stage_16_1 (.input_32(bs_stage_8_1_out_1), .enable(amnt[4]), .typ_2(typ), .out_1(outp));

  // Notes on the sheet:
  //   input_32b: initial=0x9e3779b9
endmodule

module condition_checker (
  input  N,
  input  Z,
  input  C,
  input  [3:0] cond,
  input  V,
  output out_6
);

  wire and_1_out, and_2_out, not_1_out, not_2_out, not_3_out, not_4_out, not_5_out, or_1_out, or_2_out,
       xor_1_out;

  not not_1 (not_1_out, N);
  not not_2 (not_2_out, Z);
  not not_3 (not_3_out, C);
  not not_4 (not_4_out, V);
  xor xor_1 (xor_1_out, N, V);
  and and_1 (and_1_out, C, not_2_out);
  or or_1 (or_1_out, not_3_out, Z);
  and and_2 (and_2_out, not_2_out, not_5_out);
  or or_2 (or_2_out, Z, xor_1_out);
  not not_5 (not_5_out, xor_1_out);
  Multiplexer #(.select(4)) multiplexer_1 (
    .in0(Z), .in1(not_2_out), .in2(C), .in3(not_3_out), .in4(N), .in5(not_1_out), .in6(V), .in7(not_4_out),
    .in8(and_1_out), .in9(or_1_out), .in10(not_5_out), .in11(xor_1_out), .in12(and_2_out), .in13(or_2_out),
    .in14(1'b1), .in15(1'b0), .out(out_6), .sel(cond));
endmodule

module reg16x32_1 (
  input  CLK,
  input  [3:0] WA,
  input  [31:0] WD,
  input  WE,
  input  RST,
  input  [31:0] WD2,
  input  [3:0] RA,
  input  [3:0] RB,
  input  WE2,
  input  [3:0] WA2,
  output [31:0] R0_OUTPUT,
  output [31:0] R1_OUTPUT,
  output [31:0] R3_OUTPUT,
  output [31:0] R2_OUPUT,
  output [31:0] R5_OUTPUT,
  output [31:0] R4_OUTPUT,
  output [31:0] RD_A,
  output [31:0] R7_OUTPUT,
  output [31:0] R6_OUTPUT,
  output [31:0] RD_B,
  output [31:0] R8_OUTPUT,
  output [31:0] R9_OUTPUT,
  output [31:0] R11_OUTPUT,
  output [31:0] R10_OUTPUT,
  output [31:0] R13_OUTPUT,
  output [31:0] R12_OUTPUT,
  output [31:0] R15_OUTPUT,
  output [31:0] R14_OUTPUT
);

  wire and_1_out, and_2_out, and_3_out, and_4_out, and_5_out, and_6_out, and_7_out, and_8_out, and_9_out,
       and_10_out, and_11_out, and_12_out, and_13_out, and_14_out, and_15_out, and_16_out, decoder_1_out0,
       decoder_1_out1, decoder_1_out2, decoder_1_out3, decoder_1_out4, decoder_1_out5, decoder_1_out6,
       decoder_1_out7, decoder_1_out8, decoder_1_out9, decoder_1_out10, decoder_1_out11, decoder_1_out12,
       decoder_1_out13, decoder_1_out14, decoder_1_out15, decoder_2_out0, decoder_2_out1, decoder_2_out2,
       decoder_2_out3, decoder_2_out4, decoder_2_out5, decoder_2_out6, decoder_2_out7, decoder_2_out8,
       decoder_2_out9, decoder_2_out10, decoder_2_out11, decoder_2_out12, decoder_2_out13, decoder_2_out14,
       decoder_2_out15, or_1_out, or_2_out, or_3_out, or_4_out, or_5_out, or_6_out, or_7_out, or_8_out,
       or_9_out, or_10_out, or_11_out, or_12_out, or_13_out, or_14_out, or_15_out, or_16_out;
  wire [31:0] multiplexer_1_out, multiplexer_2_out, multiplexer_3_out, multiplexer_4_out, multiplexer_5_out,
       multiplexer_6_out, multiplexer_7_out, multiplexer_8_out, multiplexer_9_out, multiplexer_10_out,
       multiplexer_11_out, multiplexer_12_out, multiplexer_13_out, multiplexer_14_out, multiplexer_15_out,
       multiplexer_16_out;

  Decoder #(.select(4)) decoder_1 (
    .out0(decoder_1_out0), .out1(decoder_1_out1), .out2(decoder_1_out2), .out3(decoder_1_out3),
    .out4(decoder_1_out4), .out5(decoder_1_out5), .out6(decoder_1_out6), .out7(decoder_1_out7),
    .out8(decoder_1_out8), .out9(decoder_1_out9), .out10(decoder_1_out10), .out11(decoder_1_out11),
    .out12(decoder_1_out12), .out13(decoder_1_out13), .out14(decoder_1_out14), .out15(decoder_1_out15),
    .sel(WA), .en(WE));
  Decoder #(.select(4)) decoder_2 (
    .out0(decoder_2_out0), .out1(decoder_2_out1), .out2(decoder_2_out2), .out3(decoder_2_out3),
    .out4(decoder_2_out4), .out5(decoder_2_out5), .out6(decoder_2_out6), .out7(decoder_2_out7),
    .out8(decoder_2_out8), .out9(decoder_2_out9), .out10(decoder_2_out10), .out11(decoder_2_out11),
    .out12(decoder_2_out12), .out13(decoder_2_out13), .out14(decoder_2_out14), .out15(decoder_2_out15),
    .sel(WA2), .en(WE2));
  and and_1 (and_1_out, decoder_1_out0, WE);
  and and_2 (and_2_out, decoder_1_out1, WE);
  and and_3 (and_3_out, decoder_1_out2, WE);
  and and_4 (and_4_out, decoder_1_out3, WE);
  and and_5 (and_5_out, decoder_1_out4, WE);
  and and_6 (and_6_out, decoder_1_out5, WE);
  and and_7 (and_7_out, decoder_1_out6, WE);
  and and_8 (and_8_out, decoder_1_out7, WE);
  and and_9 (and_9_out, decoder_1_out8, WE);
  and and_10 (and_10_out, decoder_1_out9, WE);
  and and_11 (and_11_out, decoder_1_out10, WE);
  and and_12 (and_12_out, decoder_1_out11, WE);
  and and_13 (and_13_out, decoder_1_out12, WE);
  and and_14 (and_14_out, decoder_1_out13, WE);
  and and_15 (and_15_out, decoder_1_out14, WE);
  and and_16 (and_16_out, decoder_1_out15, WE);
  or or_1 (or_1_out, and_1_out, decoder_2_out0);
  or or_2 (or_2_out, and_2_out, decoder_2_out1);
  or or_3 (or_3_out, and_3_out, decoder_2_out2);
  or or_4 (or_4_out, and_4_out, decoder_2_out3);
  or or_5 (or_5_out, and_5_out, decoder_2_out4);
  or or_6 (or_6_out, and_6_out, decoder_2_out5);
  or or_7 (or_7_out, and_7_out, decoder_2_out6);
  or or_8 (or_8_out, and_8_out, decoder_2_out7);
  or or_9 (or_9_out, and_13_out, decoder_2_out12);
  or or_10 (or_10_out, and_14_out, decoder_2_out13);
  or or_11 (or_11_out, and_15_out, decoder_2_out14);
  or or_12 (or_12_out, and_16_out, decoder_2_out15);
  or or_13 (or_13_out, and_9_out, decoder_2_out8);
  or or_14 (or_14_out, and_10_out, decoder_2_out9);
  or or_15 (or_15_out, and_11_out, decoder_2_out10);
  or or_16 (or_16_out, and_12_out, decoder_2_out11);
  Multiplexer #(.width(32)) multiplexer_1 (.in0(WD), .in1(WD2), .out(multiplexer_1_out), .sel(decoder_2_out12));
  Multiplexer #(.width(32)) multiplexer_2 (.in0(WD), .in1(WD2), .out(multiplexer_2_out), .sel(decoder_2_out14));
  Multiplexer #(.width(32)) multiplexer_3 (.in0(WD), .in1(WD2), .out(multiplexer_3_out), .sel(decoder_2_out0));
  Multiplexer #(.width(32)) multiplexer_4 (.in0(WD), .in1(WD2), .out(multiplexer_4_out), .sel(decoder_2_out2));
  Multiplexer #(.width(32)) multiplexer_5 (.in0(WD), .in1(WD2), .out(multiplexer_5_out), .sel(decoder_2_out4));
  Multiplexer #(.width(32)) multiplexer_6 (.in0(WD), .in1(WD2), .out(multiplexer_6_out), .sel(decoder_2_out6));
  Multiplexer #(.width(32)) multiplexer_7 (.in0(WD), .in1(WD2), .out(multiplexer_7_out), .sel(decoder_2_out8));
  Multiplexer #(.width(32)) multiplexer_8 (.in0(WD), .in1(WD2), .out(multiplexer_8_out), .sel(decoder_2_out10));
  Register #(.width(32)) R0 (.D(multiplexer_3_out), .en(or_1_out), .clk(CLK), .Q(R0_OUTPUT), .clr(RST));
  Register #(.width(32)) R2 (.D(multiplexer_4_out), .en(or_3_out), .clk(CLK), .Q(R2_OUPUT), .clr(RST));
  Register #(.width(32)) R4 (.D(multiplexer_5_out), .en(or_5_out), .clk(CLK), .Q(R4_OUTPUT), .clr(RST));
  Register #(.width(32)) R6 (.D(multiplexer_6_out), .en(or_7_out), .clk(CLK), .Q(R6_OUTPUT), .clr(RST));
  Register #(.width(32)) R8 (.D(multiplexer_7_out), .en(or_13_out), .clk(CLK), .Q(R8_OUTPUT), .clr(RST));
  Register #(.width(32)) R10 (.D(multiplexer_8_out), .en(or_15_out), .clk(CLK), .Q(R10_OUTPUT), .clr(RST));
  Register #(.width(32)) R12 (.D(multiplexer_1_out), .en(or_9_out), .clk(CLK), .Q(R12_OUTPUT), .clr(RST));
  Register #(.width(32)) R14 (.D(multiplexer_2_out), .en(or_11_out), .clk(CLK), .Q(R14_OUTPUT), .clr(RST));
  Multiplexer #(.width(32)) multiplexer_9 (.in0(WD), .in1(WD2), .out(multiplexer_9_out), .sel(decoder_2_out1));
  Multiplexer #(.width(32)) multiplexer_10 (.in0(WD), .in1(WD2), .out(multiplexer_10_out), .sel(decoder_2_out5));
  Multiplexer #(.width(32)) multiplexer_11 (.in0(WD), .in1(WD2), .out(multiplexer_11_out), .sel(decoder_2_out7));
  Multiplexer #(.width(32)) multiplexer_12 (.in0(WD), .in1(WD2), .out(multiplexer_12_out), .sel(decoder_2_out9));
  Multiplexer #(.width(32)) multiplexer_13 (.in0(WD), .in1(WD2), .out(multiplexer_13_out), .sel(decoder_2_out11));
  Multiplexer #(.width(32)) multiplexer_14 (.in0(WD), .in1(WD2), .out(multiplexer_14_out), .sel(decoder_2_out13));
  Multiplexer #(.width(32)) multiplexer_15 (.in0(WD), .in1(WD2), .out(multiplexer_15_out), .sel(decoder_2_out15));
  Multiplexer #(.width(32)) multiplexer_16 (.in0(WD), .in1(WD2), .out(multiplexer_16_out), .sel(decoder_2_out3));
  Register #(.width(32)) R1 (.D(multiplexer_9_out), .en(or_2_out), .clk(CLK), .Q(R1_OUTPUT), .clr(RST));
  Register #(.width(32)) R3 (.D(multiplexer_16_out), .en(or_4_out), .clk(CLK), .Q(R3_OUTPUT), .clr(RST));
  Register #(.width(32)) R5 (.D(multiplexer_10_out), .en(or_6_out), .clk(CLK), .Q(R5_OUTPUT), .clr(RST));
  Register #(.width(32)) R7 (.D(multiplexer_11_out), .en(or_8_out), .clk(CLK), .Q(R7_OUTPUT), .clr(RST));
  Register #(.width(32)) R9 (.D(multiplexer_12_out), .en(or_14_out), .clk(CLK), .Q(R9_OUTPUT), .clr(RST));
  Register #(.width(32)) R11 (.D(multiplexer_13_out), .en(or_16_out), .clk(CLK), .Q(R11_OUTPUT), .clr(RST));
  Register #(.width(32)) R13 (.D(multiplexer_14_out), .en(or_10_out), .clk(CLK), .Q(R13_OUTPUT), .clr(RST));
  Register #(.width(32)) R15 (.D(multiplexer_15_out), .en(or_12_out), .clk(CLK), .Q(R15_OUTPUT), .clr(RST));
  Multiplexer #(.select(4), .width(32)) multiplexer_17 (
    .in0(R0_OUTPUT), .in1(R1_OUTPUT), .in2(R2_OUPUT), .in3(R3_OUTPUT), .in4(R4_OUTPUT), .in5(R5_OUTPUT),
    .in6(R6_OUTPUT), .in7(R7_OUTPUT), .in8(R8_OUTPUT), .in9(R9_OUTPUT), .in10(R10_OUTPUT), .in11(R11_OUTPUT),
    .in12(R12_OUTPUT), .in13(R13_OUTPUT), .in14(R14_OUTPUT), .in15(R15_OUTPUT), .out(RD_A), .sel(RA));
  Multiplexer #(.select(4), .width(32)) multiplexer_18 (
    .in0(R0_OUTPUT), .in1(R1_OUTPUT), .in2(R2_OUPUT), .in3(R3_OUTPUT), .in4(R4_OUTPUT), .in5(R5_OUTPUT),
    .in6(R6_OUTPUT), .in7(R7_OUTPUT), .in8(R8_OUTPUT), .in9(R9_OUTPUT), .in10(R10_OUTPUT), .in11(R11_OUTPUT),
    .in12(R12_OUTPUT), .in13(R13_OUTPUT), .in14(R14_OUTPUT), .in15(R15_OUTPUT), .out(RD_B), .sel(RB));
endmodule

module block_transfer_control (
  input  clk,
  input  rst,
  input  start,
  input  is_pop,
  input  [15:0] reg_list_in,
  input  [31:0] base_value,
  input  U,
  input  P,
  output hold_pc,
  output active,
  output done,
  output [3:0] reg_idx,
  output reg_selected,
  output [31:0] transfer_address,
  output [31:0] final_address,
  output store_enable,
  output load_enable,
  output phase_reg_q
);

  wire and_1_out, and_2_out, and_3_out, and_4_out, and_6_out, and_7_out, and_8_out, and_10_out, and_11_out,
       and_13_out, and_14_out, comparator_1_eq, comparator_2_eq, idx_adv_out, multiplexer_2_out, not_1_out,
       not_2_out, not_3_out, not_4_out, not_5_out, not_6_out, or_1_out, or_2_out, or_3_out, or_4_out,
       or_6_out, reg_sel_and_toi_2_out, termin_or_idx_adv_out;
  wire [3:0] adder_1_out, adder_2_out, multiplexer_4_out, multiplexer_5_out, multiplexer_6_out,
       multiplexer_9_out;
  wire [15:0] register_1_q;
  wire [31:0] adder_3_out, adder_4_out, multiplexer_1_out, multiplexer_3_out, multiplexer_8_out;

  // Probe p: pin names not known
  // Probe is_pop: pin names not known
  // Probe start: pin names not known
  // Probe rst: pin names not known
  not not_1 (not_1_out, P);
  // Probe clk: pin names not known
  // Probe reg_list_in: pin names not known
  // Probe reg_idx: pin names not known
  // Probe base_value: pin names not known
  or or_1 (or_1_out, reg_selected, start);
  // Probe u: pin names not known
  Register #(.width(16)) register_1 (.D(reg_list_in), .en(and_10_out), .clk(clk), .Q(register_1_q), .clr(rst));
  // Probe register_q: pin names not known
  Multiplexer #(.width(32)) multiplexer_1 (
    .in0(final_address), .in1(multiplexer_8_out), .out(multiplexer_1_out), .sel(reg_sel_and_toi_2_out));
  // Probe not_p: pin names not known
  Register #(.width(1)) ACTIVE_REG (.D(or_6_out), .en(1'b1), .clk(clk), .Q(active), .clr(rst));
  Register #(.width(1)) DONE_REG (.D(and_4_out), .en(1'b1), .clk(clk), .Q(done), .clr(rst));
  Register #(.width(4)) REG_INDEX (.D(multiplexer_9_out), .en(1'b1), .clk(clk), .Q(reg_idx), .clr(rst));
  // Probe to_multiplexer_in0_2: pin names not known
  // Probe to_multiplexer_in1_1: pin names not known
  // Probe to_multiplexer_in2: pin names not known
  // Probe to_multiplexer_in3: pin names not known
  // Probe to_multiplexer_in4: pin names not known
  // Probe to_multiplexer_in5: pin names not known
  // Probe to_multiplexer_in6: pin names not known
  // Probe to_multiplexer_in7: pin names not known
  // Probe to_multiplexer_in8: pin names not known
  // Probe to_multiplexer_in9: pin names not known
  // Probe to_multiplexer_in10: pin names not known
  // Probe to_multiplexer_in11: pin names not known
  // Probe to_multiplexer_in12: pin names not known
  // Probe to_multiplexer_in13: pin names not known
  // Probe to_multiplexer_in14: pin names not known
  // Probe to_multiplexer_in15: pin names not known
  // Probe to_multiplexer_in0_1: pin names not known
  Register #(.width(1)) PHASE_REG (.D(and_13_out), .clk(clk), .Q(phase_reg_q));  // open: en, clr
  Multiplexer #(.select(4)) multiplexer_2 (
    .in0(register_1_q[0]), .in1(register_1_q[1]), .in2(register_1_q[2]), .in3(register_1_q[3]),
    .in4(register_1_q[4]), .in5(register_1_q[5]), .in6(register_1_q[6]), .in7(register_1_q[7]),
    .in8(register_1_q[8]), .in9(register_1_q[9]), .in10(register_1_q[10]), .in11(register_1_q[11]),
    .in12(register_1_q[12]), .in13(register_1_q[13]), .in14(register_1_q[14]), .in15(register_1_q[15]),
    .out(multiplexer_2_out), .sel(reg_idx));
  Multiplexer #(.width(32)) multiplexer_3 (
    .in0(multiplexer_1_out), .in1(base_value), .out(multiplexer_3_out), .sel(and_10_out));
  // Probe address_reg: pin names not known
  // Probe done: pin names not known
  and and_1 (and_1_out, and_11_out, or_3_out);
  // Probe to_not_in: pin names not known
  Adder #(.width(4)) adder_1 (.a(reg_idx), .b(4'b0001), .out(adder_1_out));  // open: cin, cout
  Adder #(.width(4)) adder_2 (.a(reg_idx), .b(4'b1111), .out(adder_2_out));  // open: cin, cout
  // Probe on multiplexer_3_out
  // Probe final_address: pin names not known
  not not_2 (not_2_out, phase_reg_q);
  not not_3 (not_3_out, and_1_out);
  // Probe to_and_in1_3: pin names not known
  // Probe to_and_in0_1: pin names not known
  and and_2 (and_2_out, active, and_11_out);
  Multiplexer #(.width(4)) multiplexer_4 (.in0(4'b1111), .in1(4'b0000), .out(multiplexer_4_out), .sel(U));
  // Probe on multiplexer_2_out
  // Probe reg_selected: pin names not known
  or or_2 (or_2_out, active, done);
  and and_3 (and_3_out, active, not_3_out);
  and and_4 (and_4_out, and_2_out, or_3_out);
  // Probe on adder_1_out
  Multiplexer #(.width(4)) multiplexer_5 (.in0(adder_2_out), .in1(adder_1_out), .out(multiplexer_5_out), .sel(U));
  // Probe on adder_2_out
  Comparator #(.width(4)) comparator_1 (.a(reg_idx), .b(4'b1111), .eq(comparator_1_eq));  // open: gt, lt
  Comparator #(.width(4)) comparator_2 (.a(reg_idx), .b(4'b0000), .eq(comparator_2_eq));  // open: gt, lt
  Register #(.width(32)) address_reg_2 (.D(multiplexer_3_out), .en(or_1_out), .clk(clk), .Q(final_address), .clr(rst));
  // Probe on or_2_out
  not not_4 (not_4_out, is_pop);
  // Probe to_and_in1_4: pin names not known
  // Probe to_and_in1_2: pin names not known
  // Probe phase_reg_2: pin names not known
  // Probe on and_4_out
  // Probe reg_index_1: pin names not known
  Multiplexer #(.width(4)) multiplexer_6 (
    .in0(reg_idx), .in1(multiplexer_5_out), .out(multiplexer_6_out), .sel(idx_adv_out));
  and and_5 (store_enable, reg_selected, not_4_out);
  and and_6 (and_6_out, reg_selected, is_pop);
  or or_3 (or_3_out, not_4_out, phase_reg_q);
  // Probe active_reg_1: pin names not known
  not not_5 (not_5_out, or_2_out);
  // Probe on multiplexer_5_out
  // Probe to_multiplexer_in1_2: pin names not known
  // Probe on comparator_1_eq
  // Probe on comparator_2_eq
  not not_6 (not_6_out, U);
  // Probe to_and_in1_5: pin names not known
  // Probe to_and_in1_1: pin names not known
  Adder #(.width(32)) adder_3 (.a(final_address), .b(32'hfffffffc), .out(adder_3_out), .cin(1'b0));  // open: cout
  Adder #(.width(32)) adder_4 (.a(final_address), .b(32'h4), .out(adder_4_out), .cin(1'b0));  // open: cout
  // Probe to_and_in0_2: pin names not known
  and and_7 (and_7_out, comparator_1_eq, U);
  // Probe to_or_in0: pin names not known
  and and_8 (and_8_out, comparator_2_eq, not_6_out);
  // Probe to_or_in1: pin names not known
  Multiplexer #(.width(32)) multiplexer_7 (
    .in0(multiplexer_8_out), .in1(final_address), .out(transfer_address), .sel(not_1_out));
  // Probe store_enable: pin names not known
  and and_9 (load_enable, and_6_out, phase_reg_q);
  and and_10 (and_10_out, not_5_out, start);
  // Probe on not_5_out
  // Probe on and_3_out
  // Probe on multiplexer_6_out
  // Probe on adder_3_out
  // Probe on adder_4_out
  // Probe phase_reg_q: pin names not known
  or or_4 (or_4_out, and_7_out, and_8_out);
  // Probe to_and_in1_6: pin names not known
  // Probe reg_sel_and_toi: pin names not known
  Multiplexer #(.width(32)) multiplexer_8 (.in0(adder_3_out), .in1(adder_4_out), .out(multiplexer_8_out), .sel(U));
  // Probe active: pin names not known
  and idx_adv (idx_adv_out, and_3_out, or_3_out);
  Multiplexer #(.width(4)) multiplexer_9 (
    .in0(multiplexer_6_out), .in1(multiplexer_4_out), .out(multiplexer_9_out), .sel(and_10_out));
  and and_11 (and_11_out, active, or_4_out);
  and and_12 (reg_selected, active, multiplexer_2_out);
  // Probe on multiplexer_8_out
  and and_13 (and_13_out, active, not_2_out);
  or or_5 (hold_pc, active, and_10_out);
  // Probe hold_pc: pin names not known
  or or_6 (or_6_out, and_10_out, and_3_out);
  // Probe on and_10_out
  // Probe idx_adv_2: pin names not known
  // Probe on and_11_out
  and and_14 (and_14_out, and_11_out, phase_reg_q);
  // Probe termin_or_idx_adv_1: pin names not known
  or termin_or_idx_adv (termin_or_idx_adv_out, and_14_out, idx_adv_out);
  // Probe idx_adv_1: pin names not known
  // Probe termin_or_idx_adv_2: pin names not known
  and reg_sel_and_toi_2 (reg_sel_and_toi_2_out, reg_selected, termin_or_idx_adv_out);
endmodule

module ALU_arithmetic_engine (
  input  a_inversion,
  input  [31:0] A,
  input  [31:0] B,
  input  b_inversion,
  input  Cflag,
  input  unused,
  input  [1:0] Cin_sel,
  output [31:0] Result,
  output Cout
);

  wire multiplexer_1_out;
  wire [31:0] bit_extender_1_out, bit_extender_2_out, xor_1_out, xor_2_out;

  assign bit_extender_1_out = {{31{b_inversion}}, b_inversion};  // Bit_Extender bit_extender_1
  Multiplexer #(.select(2)) multiplexer_1 (
    .in0(1'b0), .in1(1'b1), .in2(Cflag), .in3(unused), .out(multiplexer_1_out), .sel(Cin_sel));
  assign bit_extender_2_out = {{31{a_inversion}}, a_inversion};  // Bit_Extender bit_extender_2
  assign xor_1_out = bit_extender_2_out ^ A;  // XOR_Gate xor_1, 32 bits wide
  assign xor_2_out = B ^ bit_extender_1_out;  // XOR_Gate xor_2, 32 bits wide
  Adder #(.width(32)) adder_1 (.a(xor_1_out), .b(xor_2_out), .out(Result), .cin(multiplexer_1_out), .cout(Cout));
endmodule
