// Logisim project full_adder_1bit.circ as structural Verilog: 1 circuit, main circuit main
module main (
  input  A,
  input  B,
  input  Cin
);

  wire and_a_beff_out, and_Cin_xorabeff_out, b_eff_out, or_andab_andCinxorab_out, xor_a_beff_out,
       xor_abeff_Cin_out;

  xor b_eff (b_eff_out, B, Cin);
  xor xor_a_beff (xor_a_beff_out, A, b_eff_out);
  and and_a_beff (and_a_beff_out, A, b_eff_out);
  and and_Cin_xorabeff (and_Cin_xorabeff_out, xor_a_beff_out, Cin);
  xor xor_abeff_Cin (xor_abeff_Cin_out, xor_a_beff_out, Cin);
  LED led_1 (.in(xor_abeff_Cin_out));
  or or_andab_andCinxorab (or_andab_andCinxorab_out, and_a_beff_out, and_Cin_xorabeff_out);
  LED led_2 (.in(or_andab_andCinxorab_out));
endmodule
