// Logisim project npu_reference.circ as structural Verilog: 2 circuits, main circuit main
module PE_INT8 (
  input  clk,
  input  clear,
  input  enable,
  input  [7:0] activation,
  input  [7:0] weight,
  input  [31:0] psum_in,
  output [31:0] psum_out
);

  wire multiplier_1_p3;
  wire [31:1] adder_1_p3;

  // Bit_Extender #(.in_width(8), .out_width(32), .\type ("sign")) bit_extender_1: pin names not known; wires that end beside it: activation
  // Bit_Extender #(.in_width(8), .out_width(32), .\type ("sign")) bit_extender_2: pin names not known; wires that end beside it: weight
  // Multiplier #(.width(32)) multiplier_1: pin names not known; wires that end beside it: activation, weight, multiplier_1_p3
  // Adder #(.width(32)) adder_1: pin names not known; wires that end beside it: multiplier_1_p3, psum_in, {adder_1_p3, enable}
  Register #(.width(32)) ACC (.D({adder_1_p3, enable}), .en(clear), .clk(clk), .Q(psum_out));  // open: clr
  // Pins of 1 and 32 bits meet at {adder_1_p3, enable}
endmodule

module main (
  input  clear,
  input  enable,
  input  [7:0] activation,
  input  [7:0] weight
);

  wire clk_out, undriven;

  Clock clk (.out(clk_out));
  // PE_INT8 pe_int8_1: pin names not known; wires that end beside it: enable, activation, weight, {32{1'b0}}
  // Probe on undriven
endmodule
