// Logisim project sandbox_32x32_int8.circ as structural Verilog: 45 circuits, main circuit main
module kogge_stone_1b (
  input  A,
  input  B,
  input  C_in,
  output g,
  output p,
  output sum
);

  and a_and_b (g, A, B);
  xor a_xor_b (p, A, B);
  xor p_xor_cin (sum, p, C_in);
endmodule

module kogge_stone_2b (
  input  A0,
  input  B0,
  input  CIN,
  input  A1,
  input  B1,
  output SUM0,
  output Cout,
  output SUM1
);

  wire bit0_g, bit0_p, bit1_g, bit1_p, pg1_g_out;

  kogge_stone_1b bit0 (.A(A0), .B(B0), .C_in(CIN), .g(bit0_g), .p(bit0_p), .sum(SUM0));
  kogge_stone_1b bit1 (.A(A1), .B(B1), .C_in(pg1_g_out), .g(bit1_g), .p(bit1_p), .sum(SUM1));
  pg_cell pg1 (.G(bit0_g), .P(bit0_p), .G_prev(CIN), .G_out(pg1_g_out));  // open: P_Prev, P_out
  pg_cell pg2 (.G(bit1_g), .P(bit1_p), .G_prev(pg1_g_out), .G_out(Cout));  // open: P_Prev, P_out
endmodule

module pg_cell (
  input  G,
  input  P,
  input  G_prev,
  input  P_Prev,
  output G_out,
  output P_out
);

  wire PandG_prev_out;

  and PandG_prev (PandG_prev_out, P, G_prev);
  and P_and_P_prev (P_out, P, P_Prev);
  or G_or_PandG_prev (G_out, G, PandG_prev_out);
endmodule

module ks_4b (
  input  in_1,
  input  in_2,
  input  in_3,
  input  in_4,
  input  in_5,
  input  in_6,
  input  in_7,
  input  in_8,
  input  in_9,
  output out_10,
  output out_11,
  output out_12,
  output out_13,
  output out_14
);

  wire bit0_g, bit0_p, bit1_g, bit1_p, bit2_g, bit2_p, kogge_stone_1b_1_g, kogge_stone_1b_1_p, s1_0_g_out,
       s1_0_p_out, s1_1_g_out, s1_1_p_out, s1_2_g_out, s1_2_p_out, s1_3_g_out, s1_3_p_out, s2_2_g_out;

  pg_cell s1_3 (
    .G(kogge_stone_1b_1_g), .P(kogge_stone_1b_1_p), .G_prev(bit2_g), .P_Prev(bit2_p), .G_out(s1_3_g_out),
    .P_out(s1_3_p_out));
  pg_cell s2_3 (
    .G(s1_3_g_out), .P(s1_3_p_out), .G_prev(s1_1_g_out), .P_Prev(s1_1_p_out), .G_out(out_14));  // open: P_out
  kogge_stone_1b kogge_stone_1b_1 (
    .A(in_1), .B(in_5), .C_in(s2_2_g_out), .g(kogge_stone_1b_1_g), .p(kogge_stone_1b_1_p), .sum(out_10));
  pg_cell s1_2 (.G(bit2_g), .P(bit2_p), .G_prev(bit1_g), .P_Prev(bit1_p), .G_out(s1_2_g_out), .P_out(s1_2_p_out));
  pg_cell s2_2 (
    .G(s1_2_g_out), .P(s1_2_p_out), .G_prev(s1_0_g_out), .P_Prev(s1_0_p_out), .G_out(s2_2_g_out));  // open: P_out
  kogge_stone_1b bit2 (.A(in_2), .B(in_6), .C_in(s1_1_g_out), .g(bit2_g), .p(bit2_p), .sum(out_11));
  pg_cell s1_1 (.G(bit1_g), .P(bit1_p), .G_prev(bit0_g), .P_Prev(bit0_p), .G_out(s1_1_g_out), .P_out(s1_1_p_out));
  kogge_stone_1b bit1 (.A(in_3), .B(in_7), .C_in(s1_0_g_out), .g(bit1_g), .p(bit1_p), .sum(out_12));
  pg_cell s1_0 (.G(bit0_g), .P(bit0_p), .G_prev(in_9), .G_out(s1_0_g_out), .P_out(s1_0_p_out));  // open: P_Prev
  kogge_stone_1b bit0 (.A(in_4), .B(in_8), .C_in(in_9), .g(bit0_g), .p(bit0_p), .sum(out_13));
endmodule

module ks_32b (
  input  [31:0] A,
  input  [31:0] B,
  input  Cin,
  output SUM31,
  output SUM30,
  output SUM29,
  output SUM28,
  output SUM27,
  output SUM26,
  output SUM25,
  output SUM24,
  output SUM23,
  output SUM22,
  output SUM21,
  output SUM20,
  output SUM19,
  output SUM18,
  output SUM17,
  output SUM16,
  output SUM15,
  output SUM14,
  output SUM13,
  output SUM12,
  output SUM11,
  output SUM10,
  output SUM9,
  output SUM8,
  output SUM7,
  output SUM6,
  output SUM5,
  output SUM4,
  output SUM3,
  output SUM2,
  output sum1,
  output sum0,
  output Cout
);

  wire bit3_g, bit3_p, bit7_g, bit7_p, bit8_g, bit8_p, bit9_g, bit9_p, bit10_g, bit10_p, bit11_g, bit11_p,
       bit12_g, bit12_p, bit13_g, bit13_p, bit14_g, bit14_p, bit15_g, bit15_p, bit16_g, bit16_p, bit17_g,
       bit17_p, bit18_g, bit18_p, bit19_g, bit19_p, bit20_g, bit20_p, bit21_g, bit21_p, bit22_g, bit22_p,
       bit23_g, bit23_p, bit24_g, bit24_p, bit25_g, bit25_p, bit26_g, bit26_p, bit27_g, bit27_p, bit28_g,
       bit28_p, bit29_g, bit29_p, bit30_g, bit30_p, bit31_g, bit31_p, kogge_stone_1b_1_g, kogge_stone_1b_1_p,
       kogge_stone_1b_2_g, kogge_stone_1b_2_p, kogge_stone_1b_3_g, kogge_stone_1b_3_p, kogge_stone_1b_4_g,
       kogge_stone_1b_4_p, kogge_stone_1b_5_g, kogge_stone_1b_5_p, kogge_stone_1b_6_g, kogge_stone_1b_6_p,
       pg_cell_1_g_out, pg_cell_1_p_out, pg_cell_2_g_out, pg_cell_2_p_out, pg_cell_3_g_out, pg_cell_3_p_out,
       pg_cell_5_g_out, pg_cell_5_p_out, pg_cell_6_g_out, pg_cell_6_p_out, pg_cell_7_g_out, pg_cell_7_p_out,
       pg_cell_8_g_out, pg_cell_8_p_out, pg_cell_9_g_out, pg_cell_10_g_out, pg_cell_10_p_out,
       pg_cell_11_g_out, pg_cell_11_p_out, pg_cell_12_g_out, pg_cell_12_p_out, pg_cell_13_g_out,
       pg_cell_13_p_out, pg_cell_14_g_out, pg_cell_15_g_out, pg_cell_15_p_out, pg_cell_16_g_out,
       pg_cell_16_p_out, pg_cell_17_g_out, pg_cell_17_p_out, pg_cell_18_g_out, pg_cell_19_g_out,
       pg_cell_19_p_out, pg_cell_20_g_out, pg_cell_20_p_out, pg_cell_21_g_out, pg_cell_21_p_out,
       pg_cell_22_g_out, pg_cell_22_p_out, pg_cell_23_g_out, pg_cell_24_g_out, pg_cell_24_p_out,
       pg_cell_25_g_out, pg_cell_25_p_out, pg_cell_26_g_out, pg_cell_26_p_out, pg_cell_27_g_out,
       pg_cell_27_p_out, pg_cell_28_g_out, pg_cell_29_g_out, pg_cell_29_p_out, pg_cell_30_g_out,
       pg_cell_30_p_out, pg_cell_31_g_out, pg_cell_31_p_out, pg_cell_32_g_out, pg_cell_32_p_out,
       pg_cell_33_g_out, pg_cell_34_g_out, pg_cell_34_p_out, pg_cell_35_g_out, pg_cell_35_p_out,
       pg_cell_36_g_out, pg_cell_36_p_out, pg_cell_37_g_out, pg_cell_38_g_out, pg_cell_38_p_out,
       pg_cell_39_g_out, pg_cell_39_p_out, pg_cell_40_g_out, pg_cell_40_p_out, pg_cell_41_g_out,
       pg_cell_41_p_out, pg_cell_42_g_out, pg_cell_42_p_out, pg_cell_43_g_out, pg_cell_43_p_out,
       pg_cell_44_g_out, pg_cell_44_p_out, pg_cell_45_g_out, pg_cell_45_p_out, pg_cell_46_g_out,
       pg_cell_46_p_out, pg_cell_47_g_out, pg_cell_47_p_out, pg_cell_48_g_out, pg_cell_48_p_out,
       pg_cell_49_g_out, pg_cell_49_p_out, pg_cell_50_g_out, pg_cell_50_p_out, pg_cell_51_g_out,
       pg_cell_51_p_out, pg_cell_52_g_out, pg_cell_52_p_out, pg_cell_53_g_out, pg_cell_53_p_out,
       pg_cell_54_g_out, pg_cell_54_p_out, pg_cell_55_g_out, pg_cell_55_p_out, pg_cell_56_g_out,
       pg_cell_56_p_out, pg_cell_57_g_out, pg_cell_57_p_out, pg_cell_58_g_out, pg_cell_58_p_out,
       pg_cell_59_g_out, pg_cell_59_p_out, pg_cell_60_g_out, pg_cell_60_p_out, pg_cell_61_g_out,
       pg_cell_61_p_out, pg_cell_62_g_out, pg_cell_62_p_out, pg_cell_63_g_out, pg_cell_63_p_out,
       pg_cell_64_g_out, pg_cell_64_p_out, pg_cell_65_g_out, pg_cell_65_p_out, pg_cell_66_g_out,
       pg_cell_66_p_out, pg_cell_67_g_out, pg_cell_67_p_out, pg_cell_68_g_out, pg_cell_68_p_out,
       pg_cell_69_g_out, pg_cell_69_p_out, pg_cell_70_g_out, pg_cell_70_p_out, pg_cell_71_g_out,
       pg_cell_71_p_out, pg_cell_72_g_out, pg_cell_72_p_out, pg_cell_73_g_out, pg_cell_73_p_out,
       pg_cell_74_g_out, pg_cell_74_p_out, pg_cell_75_g_out, pg_cell_75_p_out, pg_cell_76_g_out,
       pg_cell_76_p_out, pg_cell_77_g_out, pg_cell_77_p_out, pg_cell_78_g_out, pg_cell_78_p_out,
       pg_cell_79_g_out, pg_cell_79_p_out, pg_cell_80_g_out, pg_cell_80_p_out, pg_cell_81_g_out,
       pg_cell_81_p_out, pg_cell_82_g_out, pg_cell_82_p_out, pg_cell_83_g_out, pg_cell_83_p_out,
       pg_cell_84_g_out, pg_cell_84_p_out, pg_cell_85_g_out, pg_cell_85_p_out, pg_cell_86_g_out,
       pg_cell_86_p_out, pg_cell_87_g_out, pg_cell_87_p_out, pg_cell_88_g_out, pg_cell_88_p_out,
       pg_cell_89_g_out, pg_cell_89_p_out, pg_cell_90_g_out, pg_cell_90_p_out, pg_cell_91_g_out,
       pg_cell_91_p_out, pg_cell_92_g_out, pg_cell_92_p_out, pg_cell_93_g_out, pg_cell_93_p_out,
       pg_cell_94_g_out, pg_cell_94_p_out, pg_cell_95_g_out, pg_cell_95_p_out, pg_cell_96_g_out,
       pg_cell_96_p_out, pg_cell_97_g_out, pg_cell_97_p_out, pg_cell_98_g_out, pg_cell_98_p_out,
       pg_cell_99_g_out, pg_cell_99_p_out, pg_cell_100_g_out, pg_cell_100_p_out, pg_cell_101_g_out,
       pg_cell_101_p_out, pg_cell_102_g_out, pg_cell_102_p_out, pg_cell_103_g_out, pg_cell_103_p_out,
       pg_cell_104_g_out, pg_cell_104_p_out, pg_cell_105_g_out, pg_cell_105_p_out, pg_cell_106_g_out,
       pg_cell_106_p_out, pg_cell_107_g_out, pg_cell_107_p_out, pg_cell_108_g_out, pg_cell_108_p_out,
       pg_cell_109_g_out, pg_cell_109_p_out, pg_cell_110_g_out, pg_cell_110_p_out, pg_cell_111_g_out,
       pg_cell_111_p_out, pg_cell_112_g_out, pg_cell_112_p_out, pg_cell_113_g_out, pg_cell_113_p_out,
       pg_cell_114_g_out, pg_cell_114_p_out, s1_7_g_out, s1_7_p_out, s2_7_g_out, s2_7_p_out, s3_7_g_out,
       s3_7_p_out, s3_20_g_out, s3_20_p_out, s3_24_g_out, s3_24_p_out, s3_28_g_out, s3_28_p_out, s3_31_g_out,
       s3_31_p_out, s4_15_g_out, s4_15_p_out, s5_16_g_out, s5_17_g_out, s5_18_g_out, s5_19_g_out,
       s5_20_g_out, s5_21_g_out, s5_22_g_out, s5_23_g_out;

  kogge_stone_1b bit31 (.A(A[31]), .B(B[31]), .C_in(pg_cell_9_g_out), .g(bit31_g), .p(bit31_p), .sum(SUM31));
  pg_cell pg_cell_1 (
    .G(bit31_g), .P(bit31_p), .G_prev(bit30_g), .P_Prev(bit30_p), .G_out(pg_cell_1_g_out),
    .P_out(pg_cell_1_p_out));
  pg_cell pg_cell_2 (
    .G(pg_cell_1_g_out), .P(pg_cell_1_p_out), .G_prev(pg_cell_10_g_out), .P_Prev(pg_cell_10_p_out),
    .G_out(pg_cell_2_g_out), .P_out(pg_cell_2_p_out));
  pg_cell s3_31 (
    .G(pg_cell_2_g_out), .P(pg_cell_2_p_out), .G_prev(pg_cell_20_g_out), .P_Prev(pg_cell_20_p_out),
    .G_out(s3_31_g_out), .P_out(s3_31_p_out));
  pg_cell pg_cell_3 (
    .G(s3_31_g_out), .P(s3_31_p_out), .G_prev(pg_cell_40_g_out), .P_Prev(pg_cell_40_p_out),
    .G_out(pg_cell_3_g_out), .P_out(pg_cell_3_p_out));
  pg_cell pg_cell_4 (
    .G(pg_cell_3_g_out), .P(pg_cell_3_p_out), .G_prev(s4_15_g_out), .P_Prev(s4_15_p_out), .G_out(Cout));  // open: P_out
  kogge_stone_1b bit30 (.A(A[30]), .B(B[30]), .C_in(pg_cell_14_g_out), .g(bit30_g), .p(bit30_p), .sum(SUM30));
  pg_cell pg_cell_5 (
    .G(bit30_g), .P(bit30_p), .G_prev(bit29_g), .P_Prev(bit29_p), .G_out(pg_cell_5_g_out),
    .P_out(pg_cell_5_p_out));
  pg_cell pg_cell_6 (
    .G(pg_cell_5_g_out), .P(pg_cell_5_p_out), .G_prev(pg_cell_15_g_out), .P_Prev(pg_cell_15_p_out),
    .G_out(pg_cell_6_g_out), .P_out(pg_cell_6_p_out));
  pg_cell pg_cell_7 (
    .G(pg_cell_6_g_out), .P(pg_cell_6_p_out), .G_prev(pg_cell_25_g_out), .P_Prev(pg_cell_25_p_out),
    .G_out(pg_cell_7_g_out), .P_out(pg_cell_7_p_out));
  pg_cell pg_cell_8 (
    .G(pg_cell_7_g_out), .P(pg_cell_7_p_out), .G_prev(pg_cell_44_g_out), .P_Prev(pg_cell_44_p_out),
    .G_out(pg_cell_8_g_out), .P_out(pg_cell_8_p_out));
  pg_cell pg_cell_9 (
    .G(pg_cell_8_g_out), .P(pg_cell_8_p_out), .G_prev(pg_cell_75_g_out), .P_Prev(pg_cell_75_p_out),
    .G_out(pg_cell_9_g_out));  // open: P_out
  kogge_stone_1b bit29 (.A(A[29]), .B(B[29]), .C_in(pg_cell_18_g_out), .g(bit29_g), .p(bit29_p), .sum(SUM29));
  pg_cell pg_cell_10 (
    .G(bit29_g), .P(bit29_p), .G_prev(bit28_g), .P_Prev(bit28_p), .G_out(pg_cell_10_g_out),
    .P_out(pg_cell_10_p_out));
  pg_cell pg_cell_11 (
    .G(pg_cell_10_g_out), .P(pg_cell_10_p_out), .G_prev(pg_cell_19_g_out), .P_Prev(pg_cell_19_p_out),
    .G_out(pg_cell_11_g_out), .P_out(pg_cell_11_p_out));
  pg_cell pg_cell_12 (
    .G(pg_cell_11_g_out), .P(pg_cell_11_p_out), .G_prev(pg_cell_25_g_out), .P_Prev(pg_cell_25_p_out),
    .G_out(pg_cell_12_g_out), .P_out(pg_cell_12_p_out));
  pg_cell pg_cell_13 (
    .G(pg_cell_12_g_out), .P(pg_cell_12_p_out), .G_prev(pg_cell_48_g_out), .P_Prev(pg_cell_48_p_out),
    .G_out(pg_cell_13_g_out), .P_out(pg_cell_13_p_out));
  pg_cell pg_cell_14 (
    .G(pg_cell_13_g_out), .P(pg_cell_13_p_out), .G_prev(pg_cell_79_g_out), .P_Prev(pg_cell_79_p_out),
    .G_out(pg_cell_14_g_out));  // open: P_out
  kogge_stone_1b bit28 (.A(A[28]), .B(B[28]), .C_in(pg_cell_23_g_out), .g(bit28_g), .p(bit28_p), .sum(SUM28));
  pg_cell pg_cell_15 (
    .G(bit28_g), .P(bit28_p), .G_prev(bit27_g), .P_Prev(bit27_p), .G_out(pg_cell_15_g_out),
    .P_out(pg_cell_15_p_out));
  pg_cell pg_cell_16 (
    .G(pg_cell_15_g_out), .P(pg_cell_15_p_out), .G_prev(pg_cell_24_g_out), .P_Prev(pg_cell_24_p_out),
    .G_out(pg_cell_16_g_out), .P_out(pg_cell_16_p_out));
  pg_cell s3_28 (
    .G(pg_cell_16_g_out), .P(pg_cell_16_p_out), .G_prev(pg_cell_35_g_out), .P_Prev(pg_cell_35_p_out),
    .G_out(s3_28_g_out), .P_out(s3_28_p_out));
  pg_cell pg_cell_17 (
    .G(s3_28_g_out), .P(s3_28_p_out), .G_prev(s3_20_g_out), .P_Prev(s3_20_p_out), .G_out(pg_cell_17_g_out),
    .P_out(pg_cell_17_p_out));
  pg_cell pg_cell_18 (
    .G(pg_cell_17_g_out), .P(pg_cell_17_p_out), .G_prev(pg_cell_83_g_out), .P_Prev(pg_cell_83_p_out),
    .G_out(pg_cell_18_g_out));  // open: P_out
  kogge_stone_1b bit27 (.A(A[27]), .B(B[27]), .C_in(pg_cell_28_g_out), .g(bit27_g), .p(bit27_p), .sum(SUM27));
  pg_cell pg_cell_19 (
    .G(bit27_g), .P(bit27_p), .G_prev(bit26_g), .P_Prev(bit26_p), .G_out(pg_cell_19_g_out),
    .P_out(pg_cell_19_p_out));
  pg_cell pg_cell_20 (
    .G(pg_cell_19_g_out), .P(pg_cell_19_p_out), .G_prev(pg_cell_29_g_out), .P_Prev(pg_cell_29_p_out),
    .G_out(pg_cell_20_g_out), .P_out(pg_cell_20_p_out));
  pg_cell pg_cell_21 (
    .G(pg_cell_20_g_out), .P(pg_cell_20_p_out), .G_prev(pg_cell_39_g_out), .P_Prev(pg_cell_39_p_out),
    .G_out(pg_cell_21_g_out), .P_out(pg_cell_21_p_out));
  pg_cell pg_cell_22 (
    .G(pg_cell_21_g_out), .P(pg_cell_21_p_out), .G_prev(pg_cell_55_g_out), .P_Prev(pg_cell_55_p_out),
    .G_out(pg_cell_22_g_out), .P_out(pg_cell_22_p_out));
  pg_cell pg_cell_23 (
    .G(pg_cell_22_g_out), .P(pg_cell_22_p_out), .G_prev(pg_cell_87_g_out), .P_Prev(pg_cell_87_p_out),
    .G_out(pg_cell_23_g_out));  // open: P_out
  kogge_stone_1b bit26 (.A(A[26]), .B(B[26]), .C_in(pg_cell_33_g_out), .g(bit26_g), .p(bit26_p), .sum(SUM26));
  pg_cell pg_cell_24 (
    .G(bit26_g), .P(bit26_p), .G_prev(bit25_g), .P_Prev(bit25_p), .G_out(pg_cell_24_g_out),
    .P_out(pg_cell_24_p_out));
  pg_cell pg_cell_25 (
    .G(pg_cell_24_g_out), .P(pg_cell_24_p_out), .G_prev(pg_cell_34_g_out), .P_Prev(pg_cell_34_p_out),
    .G_out(pg_cell_25_g_out), .P_out(pg_cell_25_p_out));
  pg_cell pg_cell_26 (
    .G(pg_cell_25_g_out), .P(pg_cell_25_p_out), .G_prev(pg_cell_43_g_out), .P_Prev(pg_cell_43_p_out),
    .G_out(pg_cell_26_g_out), .P_out(pg_cell_26_p_out));
  pg_cell pg_cell_27 (
    .G(pg_cell_26_g_out), .P(pg_cell_26_p_out), .G_prev(pg_cell_59_g_out), .P_Prev(pg_cell_59_p_out),
    .G_out(pg_cell_27_g_out), .P_out(pg_cell_27_p_out));
  pg_cell pg_cell_28 (
    .G(pg_cell_27_g_out), .P(pg_cell_27_p_out), .G_prev(pg_cell_91_g_out), .P_Prev(pg_cell_91_p_out),
    .G_out(pg_cell_28_g_out));  // open: P_out
  kogge_stone_1b bit25 (.A(A[25]), .B(B[25]), .C_in(pg_cell_37_g_out), .g(bit25_g), .p(bit25_p), .sum(SUM25));
  pg_cell pg_cell_29 (
    .G(bit25_g), .P(bit25_p), .G_prev(bit24_g), .P_Prev(bit24_p), .G_out(pg_cell_29_g_out),
    .P_out(pg_cell_29_p_out));
  pg_cell pg_cell_30 (
    .G(pg_cell_29_g_out), .P(pg_cell_29_p_out), .G_prev(pg_cell_38_g_out), .P_Prev(pg_cell_38_p_out),
    .G_out(pg_cell_30_g_out), .P_out(pg_cell_30_p_out));
  pg_cell pg_cell_31 (
    .G(pg_cell_30_g_out), .P(pg_cell_30_p_out), .G_prev(pg_cell_47_g_out), .P_Prev(pg_cell_47_p_out),
    .G_out(pg_cell_31_g_out), .P_out(pg_cell_31_p_out));
  pg_cell pg_cell_32 (
    .G(pg_cell_31_g_out), .P(pg_cell_31_p_out), .G_prev(pg_cell_63_g_out), .P_Prev(pg_cell_63_p_out),
    .G_out(pg_cell_32_g_out), .P_out(pg_cell_32_p_out));
  pg_cell pg_cell_33 (
    .G(pg_cell_32_g_out), .P(pg_cell_32_p_out), .G_prev(pg_cell_95_g_out), .P_Prev(pg_cell_95_p_out),
    .G_out(pg_cell_33_g_out));  // open: P_out
  kogge_stone_1b bit24 (.A(A[24]), .B(B[24]), .C_in(s5_23_g_out), .g(bit24_g), .p(bit24_p), .sum(SUM24));
  pg_cell pg_cell_34 (
    .G(bit24_g), .P(bit24_p), .G_prev(bit23_g), .P_Prev(bit23_p), .G_out(pg_cell_34_g_out),
    .P_out(pg_cell_34_p_out));
  pg_cell pg_cell_35 (
    .G(pg_cell_34_g_out), .P(pg_cell_34_p_out), .G_prev(pg_cell_42_g_out), .P_Prev(pg_cell_42_p_out),
    .G_out(pg_cell_35_g_out), .P_out(pg_cell_35_p_out));
  pg_cell s3_24 (
    .G(pg_cell_35_g_out), .P(pg_cell_35_p_out), .G_prev(pg_cell_51_g_out), .P_Prev(pg_cell_51_p_out),
    .G_out(s3_24_g_out), .P_out(s3_24_p_out));
  pg_cell pg_cell_36 (
    .G(s3_24_g_out), .P(s3_24_p_out), .G_prev(pg_cell_67_g_out), .P_Prev(pg_cell_67_p_out),
    .G_out(pg_cell_36_g_out), .P_out(pg_cell_36_p_out));
  pg_cell pg_cell_37 (
    .G(pg_cell_36_g_out), .P(pg_cell_36_p_out), .G_prev(pg_cell_99_g_out), .P_Prev(pg_cell_99_p_out),
    .G_out(pg_cell_37_g_out));  // open: P_out
  kogge_stone_1b bit23 (.A(A[23]), .B(B[23]), .C_in(s5_22_g_out), .g(bit23_g), .p(bit23_p), .sum(SUM23));
  pg_cell pg_cell_38 (
    .G(bit23_g), .P(bit23_p), .G_prev(bit22_g), .P_Prev(bit22_p), .G_out(pg_cell_38_g_out),
    .P_out(pg_cell_38_p_out));
  pg_cell pg_cell_39 (
    .G(pg_cell_38_g_out), .P(pg_cell_38_p_out), .G_prev(pg_cell_46_g_out), .P_Prev(pg_cell_46_p_out),
    .G_out(pg_cell_39_g_out), .P_out(pg_cell_39_p_out));
  pg_cell pg_cell_40 (
    .G(pg_cell_39_g_out), .P(pg_cell_39_p_out), .G_prev(pg_cell_54_g_out), .P_Prev(pg_cell_54_p_out),
    .G_out(pg_cell_40_g_out), .P_out(pg_cell_40_p_out));
  pg_cell pg_cell_41 (
    .G(pg_cell_40_g_out), .P(pg_cell_40_p_out), .G_prev(pg_cell_71_g_out), .P_Prev(pg_cell_71_p_out),
    .G_out(pg_cell_41_g_out), .P_out(pg_cell_41_p_out));
  pg_cell s5_23 (
    .G(pg_cell_41_g_out), .P(pg_cell_41_p_out), .G_prev(s3_7_g_out), .P_Prev(s3_7_p_out), .G_out(s5_23_g_out));  // open: P_out
  kogge_stone_1b bit22 (.A(A[22]), .B(B[22]), .C_in(s5_21_g_out), .g(bit22_g), .p(bit22_p), .sum(SUM22));
  pg_cell pg_cell_42 (
    .G(bit22_g), .P(bit22_p), .G_prev(bit21_g), .P_Prev(bit21_p), .G_out(pg_cell_42_g_out),
    .P_out(pg_cell_42_p_out));
  pg_cell pg_cell_43 (
    .G(pg_cell_42_g_out), .P(pg_cell_42_p_out), .G_prev(pg_cell_50_g_out), .P_Prev(pg_cell_50_p_out),
    .G_out(pg_cell_43_g_out), .P_out(pg_cell_43_p_out));
  pg_cell pg_cell_44 (
    .G(pg_cell_43_g_out), .P(pg_cell_43_p_out), .G_prev(pg_cell_58_g_out), .P_Prev(pg_cell_58_p_out),
    .G_out(pg_cell_44_g_out), .P_out(pg_cell_44_p_out));
  pg_cell pg_cell_45 (
    .G(pg_cell_44_g_out), .P(pg_cell_44_p_out), .G_prev(pg_cell_74_g_out), .P_Prev(pg_cell_74_p_out),
    .G_out(pg_cell_45_g_out), .P_out(pg_cell_45_p_out));
  pg_cell s5_22 (
    .G(pg_cell_45_g_out), .P(pg_cell_45_p_out), .G_prev(pg_cell_102_g_out), .P_Prev(pg_cell_102_p_out),
    .G_out(s5_22_g_out));  // open: P_out
  kogge_stone_1b bit21 (.A(A[21]), .B(B[21]), .C_in(s5_20_g_out), .g(bit21_g), .p(bit21_p), .sum(SUM21));
  pg_cell pg_cell_46 (
    .G(bit21_g), .P(bit21_p), .G_prev(bit20_g), .P_Prev(bit20_p), .G_out(pg_cell_46_g_out),
    .P_out(pg_cell_46_p_out));
  pg_cell pg_cell_47 (
    .G(pg_cell_46_g_out), .P(pg_cell_46_p_out), .G_prev(pg_cell_53_g_out), .P_Prev(pg_cell_53_p_out),
    .G_out(pg_cell_47_g_out), .P_out(pg_cell_47_p_out));
  pg_cell pg_cell_48 (
    .G(pg_cell_47_g_out), .P(pg_cell_47_p_out), .G_prev(pg_cell_62_g_out), .P_Prev(pg_cell_62_p_out),
    .G_out(pg_cell_48_g_out), .P_out(pg_cell_48_p_out));
  pg_cell pg_cell_49 (
    .G(pg_cell_48_g_out), .P(pg_cell_48_p_out), .G_prev(pg_cell_78_g_out), .P_Prev(pg_cell_78_p_out),
    .G_out(pg_cell_49_g_out), .P_out(pg_cell_49_p_out));
  pg_cell s5_21 (
    .G(pg_cell_49_g_out), .P(pg_cell_49_p_out), .G_prev(pg_cell_105_g_out), .P_Prev(pg_cell_105_p_out),
    .G_out(s5_21_g_out));  // open: P_out
  kogge_stone_1b bit20 (.A(A[20]), .B(B[20]), .C_in(s5_19_g_out), .g(bit20_g), .p(bit20_p), .sum(SUM20));
  pg_cell pg_cell_50 (
    .G(bit20_g), .P(bit20_p), .G_prev(bit19_g), .P_Prev(bit19_p), .G_out(pg_cell_50_g_out),
    .P_out(pg_cell_50_p_out));
  pg_cell pg_cell_51 (
    .G(pg_cell_50_g_out), .P(pg_cell_50_p_out), .G_prev(pg_cell_57_g_out), .P_Prev(pg_cell_57_p_out),
    .G_out(pg_cell_51_g_out), .P_out(pg_cell_51_p_out));
  pg_cell s3_20 (
    .G(pg_cell_51_g_out), .P(pg_cell_51_p_out), .G_prev(pg_cell_66_g_out), .P_Prev(pg_cell_66_p_out),
    .G_out(s3_20_g_out), .P_out(s3_20_p_out));
  pg_cell pg_cell_52 (
    .G(s3_20_g_out), .P(s3_20_p_out), .G_prev(pg_cell_82_g_out), .P_Prev(pg_cell_82_p_out),
    .G_out(pg_cell_52_g_out), .P_out(pg_cell_52_p_out));
  pg_cell s5_20 (
    .G(pg_cell_52_g_out), .P(pg_cell_52_p_out), .G_prev(pg_cell_108_g_out), .P_Prev(pg_cell_108_p_out),
    .G_out(s5_20_g_out));  // open: P_out
  kogge_stone_1b bit19 (.A(A[19]), .B(B[19]), .C_in(s5_18_g_out), .g(bit19_g), .p(bit19_p), .sum(SUM19));
  pg_cell pg_cell_53 (
    .G(bit19_g), .P(bit19_p), .G_prev(bit18_g), .P_Prev(bit18_p), .G_out(pg_cell_53_g_out),
    .P_out(pg_cell_53_p_out));
  pg_cell pg_cell_54 (
    .G(pg_cell_53_g_out), .P(pg_cell_53_p_out), .G_prev(pg_cell_61_g_out), .P_Prev(pg_cell_61_p_out),
    .G_out(pg_cell_54_g_out), .P_out(pg_cell_54_p_out));
  pg_cell pg_cell_55 (
    .G(pg_cell_54_g_out), .P(pg_cell_54_p_out), .G_prev(pg_cell_70_g_out), .P_Prev(pg_cell_70_p_out),
    .G_out(pg_cell_55_g_out), .P_out(pg_cell_55_p_out));
  pg_cell pg_cell_56 (
    .G(pg_cell_55_g_out), .P(pg_cell_55_p_out), .G_prev(pg_cell_86_g_out), .P_Prev(pg_cell_86_p_out),
    .G_out(pg_cell_56_g_out), .P_out(pg_cell_56_p_out));
  pg_cell s5_19 (
    .G(pg_cell_56_g_out), .P(pg_cell_56_p_out), .G_prev(pg_cell_110_g_out), .P_Prev(pg_cell_110_p_out),
    .G_out(s5_19_g_out));  // open: P_out
  kogge_stone_1b bit18 (.A(A[18]), .B(B[18]), .C_in(s5_17_g_out), .g(bit18_g), .p(bit18_p), .sum(SUM18));
  pg_cell pg_cell_57 (
    .G(bit18_g), .P(bit18_p), .G_prev(bit17_g), .P_Prev(bit17_p), .G_out(pg_cell_57_g_out),
    .P_out(pg_cell_57_p_out));
  pg_cell pg_cell_58 (
    .G(pg_cell_57_g_out), .P(pg_cell_57_p_out), .G_prev(pg_cell_65_g_out), .P_Prev(pg_cell_65_p_out),
    .G_out(pg_cell_58_g_out), .P_out(pg_cell_58_p_out));
  pg_cell pg_cell_59 (
    .G(pg_cell_58_g_out), .P(pg_cell_58_p_out), .G_prev(pg_cell_73_g_out), .P_Prev(pg_cell_73_p_out),
    .G_out(pg_cell_59_g_out), .P_out(pg_cell_59_p_out));
  pg_cell pg_cell_60 (
    .G(pg_cell_59_g_out), .P(pg_cell_59_p_out), .G_prev(pg_cell_90_g_out), .P_Prev(pg_cell_90_p_out),
    .G_out(pg_cell_60_g_out), .P_out(pg_cell_60_p_out));
  pg_cell s5_18 (
    .G(pg_cell_60_g_out), .P(pg_cell_60_p_out), .G_prev(pg_cell_112_g_out), .P_Prev(pg_cell_112_p_out),
    .G_out(s5_18_g_out));  // open: P_out
  kogge_stone_1b bit17 (.A(A[17]), .B(B[17]), .C_in(s5_16_g_out), .g(bit17_g), .p(bit17_p), .sum(SUM17));
  pg_cell pg_cell_61 (
    .G(bit17_g), .P(bit17_p), .G_prev(bit16_g), .P_Prev(bit16_p), .G_out(pg_cell_61_g_out),
    .P_out(pg_cell_61_p_out));
  pg_cell pg_cell_62 (
    .G(pg_cell_61_g_out), .P(pg_cell_61_p_out), .G_prev(pg_cell_69_g_out), .P_Prev(pg_cell_69_p_out),
    .G_out(pg_cell_62_g_out), .P_out(pg_cell_62_p_out));
  pg_cell pg_cell_63 (
    .G(pg_cell_62_g_out), .P(pg_cell_62_p_out), .G_prev(pg_cell_77_g_out), .P_Prev(pg_cell_77_p_out),
    .G_out(pg_cell_63_g_out), .P_out(pg_cell_63_p_out));
  pg_cell pg_cell_64 (
    .G(pg_cell_63_g_out), .P(pg_cell_63_p_out), .G_prev(pg_cell_94_g_out), .P_Prev(pg_cell_94_p_out),
    .G_out(pg_cell_64_g_out), .P_out(pg_cell_64_p_out));
  pg_cell s5_17 (
    .G(pg_cell_64_g_out), .P(pg_cell_64_p_out), .G_prev(pg_cell_113_g_out), .P_Prev(pg_cell_113_p_out),
    .G_out(s5_17_g_out));  // open: P_out
  kogge_stone_1b bit16 (.A(A[16]), .B(B[16]), .C_in(s4_15_g_out), .g(bit16_g), .p(bit16_p), .sum(SUM16));
  pg_cell pg_cell_65 (
    .G(bit16_g), .P(bit16_p), .G_prev(bit15_g), .P_Prev(bit15_p), .G_out(pg_cell_65_g_out),
    .P_out(pg_cell_65_p_out));
  pg_cell pg_cell_66 (
    .G(pg_cell_65_g_out), .P(pg_cell_65_p_out), .G_prev(pg_cell_72_g_out), .P_Prev(pg_cell_72_p_out),
    .G_out(pg_cell_66_g_out), .P_out(pg_cell_66_p_out));
  pg_cell pg_cell_67 (
    .G(pg_cell_66_g_out), .P(pg_cell_66_p_out), .G_prev(pg_cell_81_g_out), .P_Prev(pg_cell_81_p_out),
    .G_out(pg_cell_67_g_out), .P_out(pg_cell_67_p_out));
  pg_cell pg_cell_68 (
    .G(pg_cell_67_g_out), .P(pg_cell_67_p_out), .G_prev(pg_cell_98_g_out), .P_Prev(pg_cell_98_p_out),
    .G_out(pg_cell_68_g_out), .P_out(pg_cell_68_p_out));
  pg_cell s5_16 (
    .G(pg_cell_68_g_out), .P(pg_cell_68_p_out), .G_prev(pg_cell_114_g_out), .P_Prev(pg_cell_114_p_out),
    .G_out(s5_16_g_out));  // open: P_out
  kogge_stone_1b bit15 (.A(A[15]), .B(B[15]), .C_in(pg_cell_75_g_out), .g(bit15_g), .p(bit15_p), .sum(SUM15));
  pg_cell pg_cell_69 (
    .G(bit15_g), .P(bit15_p), .G_prev(bit14_g), .P_Prev(bit14_p), .G_out(pg_cell_69_g_out),
    .P_out(pg_cell_69_p_out));
  pg_cell pg_cell_70 (
    .G(pg_cell_69_g_out), .P(pg_cell_69_p_out), .G_prev(pg_cell_76_g_out), .P_Prev(pg_cell_76_p_out),
    .G_out(pg_cell_70_g_out), .P_out(pg_cell_70_p_out));
  pg_cell pg_cell_71 (
    .G(pg_cell_70_g_out), .P(pg_cell_70_p_out), .G_prev(pg_cell_85_g_out), .P_Prev(pg_cell_85_p_out),
    .G_out(pg_cell_71_g_out), .P_out(pg_cell_71_p_out));
  pg_cell s4_15 (
    .G(pg_cell_71_g_out), .P(pg_cell_71_p_out), .G_prev(s3_7_g_out), .P_Prev(s3_7_p_out),
    .G_out(s4_15_g_out), .P_out(s4_15_p_out));
  kogge_stone_1b bit14 (.A(A[14]), .B(B[14]), .C_in(pg_cell_79_g_out), .g(bit14_g), .p(bit14_p), .sum(SUM14));
  pg_cell pg_cell_72 (
    .G(bit14_g), .P(bit14_p), .G_prev(bit13_g), .P_Prev(bit13_p), .G_out(pg_cell_72_g_out),
    .P_out(pg_cell_72_p_out));
  pg_cell pg_cell_73 (
    .G(pg_cell_72_g_out), .P(pg_cell_72_p_out), .G_prev(pg_cell_80_g_out), .P_Prev(pg_cell_80_p_out),
    .G_out(pg_cell_73_g_out), .P_out(pg_cell_73_p_out));
  pg_cell pg_cell_74 (
    .G(pg_cell_73_g_out), .P(pg_cell_73_p_out), .G_prev(pg_cell_89_g_out), .P_Prev(pg_cell_89_p_out),
    .G_out(pg_cell_74_g_out), .P_out(pg_cell_74_p_out));
  pg_cell pg_cell_75 (
    .G(pg_cell_74_g_out), .P(pg_cell_74_p_out), .G_prev(pg_cell_102_g_out), .P_Prev(pg_cell_102_p_out),
    .G_out(pg_cell_75_g_out), .P_out(pg_cell_75_p_out));
  kogge_stone_1b bit13 (.A(A[13]), .B(B[13]), .C_in(pg_cell_83_g_out), .g(bit13_g), .p(bit13_p), .sum(SUM13));
  pg_cell pg_cell_76 (
    .G(bit13_g), .P(bit13_p), .G_prev(bit12_g), .P_Prev(bit12_p), .G_out(pg_cell_76_g_out),
    .P_out(pg_cell_76_p_out));
  pg_cell pg_cell_77 (
    .G(pg_cell_76_g_out), .P(pg_cell_76_p_out), .G_prev(pg_cell_84_g_out), .P_Prev(pg_cell_84_p_out),
    .G_out(pg_cell_77_g_out), .P_out(pg_cell_77_p_out));
  pg_cell pg_cell_78 (
    .G(pg_cell_77_g_out), .P(pg_cell_77_p_out), .G_prev(pg_cell_93_g_out), .P_Prev(pg_cell_93_p_out),
    .G_out(pg_cell_78_g_out), .P_out(pg_cell_78_p_out));
  pg_cell pg_cell_79 (
    .G(pg_cell_78_g_out), .P(pg_cell_78_p_out), .G_prev(pg_cell_105_g_out), .P_Prev(pg_cell_105_p_out),
    .G_out(pg_cell_79_g_out), .P_out(pg_cell_79_p_out));
  kogge_stone_1b bit12 (.A(A[12]), .B(B[12]), .C_in(pg_cell_87_g_out), .g(bit12_g), .p(bit12_p), .sum(SUM12));
  pg_cell pg_cell_80 (
    .G(bit12_g), .P(bit12_p), .G_prev(bit11_g), .P_Prev(bit11_p), .G_out(pg_cell_80_g_out),
    .P_out(pg_cell_80_p_out));
  pg_cell pg_cell_81 (
    .G(pg_cell_80_g_out), .P(pg_cell_80_p_out), .G_prev(pg_cell_88_g_out), .P_Prev(pg_cell_88_p_out),
    .G_out(pg_cell_81_g_out), .P_out(pg_cell_81_p_out));
  pg_cell pg_cell_82 (
    .G(pg_cell_81_g_out), .P(pg_cell_81_p_out), .G_prev(pg_cell_97_g_out), .P_Prev(pg_cell_97_p_out),
    .G_out(pg_cell_82_g_out), .P_out(pg_cell_82_p_out));
  pg_cell pg_cell_83 (
    .G(pg_cell_82_g_out), .P(pg_cell_82_p_out), .G_prev(pg_cell_108_g_out), .P_Prev(pg_cell_108_p_out),
    .G_out(pg_cell_83_g_out), .P_out(pg_cell_83_p_out));
  kogge_stone_1b bit11 (.A(A[11]), .B(B[11]), .C_in(pg_cell_91_g_out), .g(bit11_g), .p(bit11_p), .sum(SUM11));
  pg_cell pg_cell_84 (
    .G(bit11_g), .P(bit11_p), .G_prev(bit10_g), .P_Prev(bit10_p), .G_out(pg_cell_84_g_out),
    .P_out(pg_cell_84_p_out));
  pg_cell pg_cell_85 (
    .G(pg_cell_84_g_out), .P(pg_cell_84_p_out), .G_prev(pg_cell_92_g_out), .P_Prev(pg_cell_92_p_out),
    .G_out(pg_cell_85_g_out), .P_out(pg_cell_85_p_out));
  pg_cell pg_cell_86 (
    .G(pg_cell_85_g_out), .P(pg_cell_85_p_out), .G_prev(s2_7_g_out), .P_Prev(s2_7_p_out),
    .G_out(pg_cell_86_g_out), .P_out(pg_cell_86_p_out));
  pg_cell pg_cell_87 (
    .G(pg_cell_86_g_out), .P(pg_cell_86_p_out), .G_prev(pg_cell_110_g_out), .P_Prev(pg_cell_110_p_out),
    .G_out(pg_cell_87_g_out), .P_out(pg_cell_87_p_out));
  kogge_stone_1b bit10 (.A(A[10]), .B(B[10]), .C_in(pg_cell_95_g_out), .g(bit10_g), .p(bit10_p), .sum(SUM10));
  pg_cell pg_cell_88 (
    .G(bit10_g), .P(bit10_p), .G_prev(bit9_g), .P_Prev(bit9_p), .G_out(pg_cell_88_g_out),
    .P_out(pg_cell_88_p_out));
  pg_cell pg_cell_89 (
    .G(pg_cell_88_g_out), .P(pg_cell_88_p_out), .G_prev(pg_cell_96_g_out), .P_Prev(pg_cell_96_p_out),
    .G_out(pg_cell_89_g_out), .P_out(pg_cell_89_p_out));
  pg_cell pg_cell_90 (
    .G(pg_cell_89_g_out), .P(pg_cell_89_p_out), .G_prev(pg_cell_101_g_out), .P_Prev(pg_cell_101_p_out),
    .G_out(pg_cell_90_g_out), .P_out(pg_cell_90_p_out));
  pg_cell pg_cell_91 (
    .G(pg_cell_90_g_out), .P(pg_cell_90_p_out), .G_prev(pg_cell_112_g_out), .P_Prev(pg_cell_112_p_out),
    .G_out(pg_cell_91_g_out), .P_out(pg_cell_91_p_out));
  kogge_stone_1b bit9 (.A(A[9]), .B(B[9]), .C_in(pg_cell_99_g_out), .g(bit9_g), .p(bit9_p), .sum(SUM9));
  pg_cell pg_cell_92 (
    .G(bit9_g), .P(bit9_p), .G_prev(bit8_g), .P_Prev(bit8_p), .G_out(pg_cell_92_g_out),
    .P_out(pg_cell_92_p_out));
  pg_cell pg_cell_93 (
    .G(pg_cell_92_g_out), .P(pg_cell_92_p_out), .G_prev(s1_7_g_out), .P_Prev(s1_7_p_out),
    .G_out(pg_cell_93_g_out), .P_out(pg_cell_93_p_out));
  pg_cell pg_cell_94 (
    .G(pg_cell_93_g_out), .P(pg_cell_93_p_out), .G_prev(pg_cell_104_g_out), .P_Prev(pg_cell_104_p_out),
    .G_out(pg_cell_94_g_out), .P_out(pg_cell_94_p_out));
  pg_cell pg_cell_95 (
    .G(pg_cell_94_g_out), .P(pg_cell_94_p_out), .G_prev(pg_cell_113_g_out), .P_Prev(pg_cell_113_p_out),
    .G_out(pg_cell_95_g_out), .P_out(pg_cell_95_p_out));
  kogge_stone_1b bit8 (.A(A[8]), .B(B[8]), .C_in(s3_7_g_out), .g(bit8_g), .p(bit8_p), .sum(SUM8));
  pg_cell pg_cell_96 (
    .G(bit8_g), .P(bit8_p), .G_prev(bit7_g), .P_Prev(bit7_p), .G_out(pg_cell_96_g_out),
    .P_out(pg_cell_96_p_out));
  pg_cell pg_cell_97 (
    .G(pg_cell_96_g_out), .P(pg_cell_96_p_out), .G_prev(pg_cell_100_g_out), .P_Prev(pg_cell_100_p_out),
    .G_out(pg_cell_97_g_out), .P_out(pg_cell_97_p_out));
  pg_cell pg_cell_98 (
    .G(pg_cell_97_g_out), .P(pg_cell_97_p_out), .G_prev(pg_cell_107_g_out), .P_Prev(pg_cell_107_p_out),
    .G_out(pg_cell_98_g_out), .P_out(pg_cell_98_p_out));
  pg_cell pg_cell_99 (
    .G(pg_cell_98_g_out), .P(pg_cell_98_p_out), .G_prev(pg_cell_114_g_out), .P_Prev(pg_cell_114_p_out),
    .G_out(pg_cell_99_g_out), .P_out(pg_cell_99_p_out));
  kogge_stone_1b bit7 (.A(A[7]), .B(B[7]), .C_in(pg_cell_102_g_out), .g(bit7_g), .p(bit7_p), .sum(SUM7));
  pg_cell s1_7 (
    .G(bit7_g), .P(bit7_p), .G_prev(kogge_stone_1b_1_g), .P_Prev(kogge_stone_1b_1_p), .G_out(s1_7_g_out),
    .P_out(s1_7_p_out));
  pg_cell s2_7 (
    .G(s1_7_g_out), .P(s1_7_p_out), .G_prev(pg_cell_103_g_out), .P_Prev(pg_cell_103_p_out),
    .G_out(s2_7_g_out), .P_out(s2_7_p_out));
  pg_cell s3_7 (
    .G(s2_7_g_out), .P(s2_7_p_out), .G_prev(pg_cell_110_g_out), .P_Prev(pg_cell_110_p_out),
    .G_out(s3_7_g_out), .P_out(s3_7_p_out));
  kogge_stone_1b kogge_stone_1b_1 (
    .A(A[6]), .B(B[6]), .C_in(pg_cell_105_g_out), .g(kogge_stone_1b_1_g), .p(kogge_stone_1b_1_p), .sum(SUM6));
  pg_cell pg_cell_100 (
    .G(kogge_stone_1b_1_g), .P(kogge_stone_1b_1_p), .G_prev(kogge_stone_1b_2_g), .P_Prev(kogge_stone_1b_2_p),
    .G_out(pg_cell_100_g_out), .P_out(pg_cell_100_p_out));
  pg_cell pg_cell_101 (
    .G(pg_cell_100_g_out), .P(pg_cell_100_p_out), .G_prev(pg_cell_106_g_out), .P_Prev(pg_cell_106_p_out),
    .G_out(pg_cell_101_g_out), .P_out(pg_cell_101_p_out));
  pg_cell pg_cell_102 (
    .G(pg_cell_101_g_out), .P(pg_cell_101_p_out), .G_prev(pg_cell_112_g_out), .P_Prev(pg_cell_112_p_out),
    .G_out(pg_cell_102_g_out), .P_out(pg_cell_102_p_out));
  kogge_stone_1b kogge_stone_1b_2 (
    .A(A[5]), .B(B[5]), .C_in(pg_cell_108_g_out), .g(kogge_stone_1b_2_g), .p(kogge_stone_1b_2_p), .sum(SUM5));
  pg_cell pg_cell_103 (
    .G(kogge_stone_1b_2_g), .P(kogge_stone_1b_2_p), .G_prev(kogge_stone_1b_3_g), .P_Prev(kogge_stone_1b_3_p),
    .G_out(pg_cell_103_g_out), .P_out(pg_cell_103_p_out));
  pg_cell pg_cell_104 (
    .G(pg_cell_103_g_out), .P(pg_cell_103_p_out), .G_prev(pg_cell_109_g_out), .P_Prev(pg_cell_109_p_out),
    .G_out(pg_cell_104_g_out), .P_out(pg_cell_104_p_out));
  pg_cell pg_cell_105 (
    .G(pg_cell_104_g_out), .P(pg_cell_104_p_out), .G_prev(pg_cell_113_g_out), .P_Prev(pg_cell_113_p_out),
    .G_out(pg_cell_105_g_out), .P_out(pg_cell_105_p_out));
  kogge_stone_1b kogge_stone_1b_3 (
    .A(A[4]), .B(B[4]), .C_in(pg_cell_110_g_out), .g(kogge_stone_1b_3_g), .p(kogge_stone_1b_3_p), .sum(SUM4));
  pg_cell pg_cell_106 (
    .G(kogge_stone_1b_3_g), .P(kogge_stone_1b_3_p), .G_prev(bit3_g), .P_Prev(bit3_p),
    .G_out(pg_cell_106_g_out), .P_out(pg_cell_106_p_out));
  pg_cell pg_cell_107 (
    .G(pg_cell_106_g_out), .P(pg_cell_106_p_out), .G_prev(pg_cell_111_g_out), .P_Prev(pg_cell_111_p_out),
    .G_out(pg_cell_107_g_out), .P_out(pg_cell_107_p_out));
  pg_cell pg_cell_108 (
    .G(pg_cell_107_g_out), .P(pg_cell_107_p_out), .G_prev(pg_cell_114_g_out), .P_Prev(pg_cell_114_p_out),
    .G_out(pg_cell_108_g_out), .P_out(pg_cell_108_p_out));
  kogge_stone_1b bit3 (.A(A[3]), .B(B[3]), .C_in(pg_cell_112_g_out), .g(bit3_g), .p(bit3_p), .sum(SUM3));
  pg_cell pg_cell_109 (
    .G(bit3_g), .P(bit3_p), .G_prev(kogge_stone_1b_4_g), .P_Prev(kogge_stone_1b_4_p),
    .G_out(pg_cell_109_g_out), .P_out(pg_cell_109_p_out));
  pg_cell pg_cell_110 (
    .G(pg_cell_109_g_out), .P(pg_cell_109_p_out), .G_prev(pg_cell_113_g_out), .P_Prev(pg_cell_113_p_out),
    .G_out(pg_cell_110_g_out), .P_out(pg_cell_110_p_out));
  kogge_stone_1b kogge_stone_1b_4 (
    .A(A[2]), .B(B[2]), .C_in(pg_cell_113_g_out), .g(kogge_stone_1b_4_g), .p(kogge_stone_1b_4_p), .sum(SUM2));
  pg_cell pg_cell_111 (
    .G(kogge_stone_1b_4_g), .P(kogge_stone_1b_4_p), .G_prev(kogge_stone_1b_5_g), .P_Prev(kogge_stone_1b_5_p),
    .G_out(pg_cell_111_g_out), .P_out(pg_cell_111_p_out));
  pg_cell pg_cell_112 (
    .G(pg_cell_111_g_out), .P(pg_cell_111_p_out), .G_prev(pg_cell_114_g_out), .P_Prev(pg_cell_114_p_out),
    .G_out(pg_cell_112_g_out), .P_out(pg_cell_112_p_out));
  kogge_stone_1b kogge_stone_1b_5 (
    .A(A[1]), .B(B[1]), .C_in(pg_cell_114_g_out), .g(kogge_stone_1b_5_g), .p(kogge_stone_1b_5_p), .sum(sum1));
  pg_cell pg_cell_113 (
    .G(kogge_stone_1b_5_g), .P(kogge_stone_1b_5_p), .G_prev(pg_cell_114_g_out), .P_Prev(pg_cell_114_p_out),
    .G_out(pg_cell_113_g_out), .P_out(pg_cell_113_p_out));
  kogge_stone_1b kogge_stone_1b_6 (
    .A(A[0]), .B(B[0]), .C_in(Cin), .g(kogge_stone_1b_6_g), .p(kogge_stone_1b_6_p), .sum(sum0));
  pg_cell pg_cell_114 (
    .G(kogge_stone_1b_6_g), .P(kogge_stone_1b_6_p), .G_prev(Cin), .P_Prev(1'b0), .G_out(pg_cell_114_g_out),
    .P_out(pg_cell_114_p_out));
endmodule

module ALU_arithmetic_engine_1 (
  input  a_inversion,
  input  [31:0] A,
  input  [31:0] B,
  input  b_inversion,
  input  Cflag,
  input  unused,
  input  [1:0] Cin_sel,
  output [31:0] Result,
  output Cout
);

  wire multiplexer_1_out;
  wire [31:0] bit_extender_1_out, bit_extender_2_out, xor_1_out, xor_2_out;

  assign bit_extender_1_out = {{31{b_inversion}}, b_inversion};  // Bit_Extender bit_extender_1
  Multiplexer #(.select(2)) multiplexer_1 (
    .in0(1'b0), .in1(1'b1), .in2(Cflag), .in3(unused), .out(multiplexer_1_out), .sel(Cin_sel));
  assign bit_extender_2_out = {{31{a_inversion}}, a_inversion};  // Bit_Extender bit_extender_2
  assign xor_1_out = bit_extender_2_out ^ A;  // XOR_Gate xor_1, 32 bits wide
  assign xor_2_out = B ^ bit_extender_1_out;  // XOR_Gate xor_2, 32 bits wide
  ks_32b ks_32b_1 (
    .A(xor_1_out), .B(xor_2_out), .Cin(multiplexer_1_out), .SUM31(Result[31]), .SUM30(Result[30]),
    .SUM29(Result[29]), .SUM28(Result[28]), .SUM27(Result[27]), .SUM26(Result[26]), .SUM25(Result[25]),
    .SUM24(Result[24]), .SUM23(Result[23]), .SUM22(Result[22]), .SUM21(Result[21]), .SUM20(Result[20]),
    .SUM19(Result[19]), .SUM18(Result[18]), .SUM17(Result[17]), .SUM16(Result[16]), .SUM15(Result[15]),
    .SUM14(Result[14]), .SUM13(Result[13]), .SUM12(Result[12]), .SUM11(Result[11]), .SUM10(Result[10]),
    .SUM9(Result[9]), .SUM8(Result[8]), .SUM7(Result[7]), .SUM6(Result[6]), .SUM5(Result[5]),
    .SUM4(Result[4]), .SUM3(Result[3]), .SUM2(Result[2]), .sum1(Result[1]), .sum0(Result[0]), .Cout(Cout));
endmodule

module ALU (
  input  [2:0] logic_sel,
  input  a_inv,
  input  [31:0] A,
  input  [31:0] B,
  input  b_inv,
  input  Cflag,
  input  unused,
  input  [1:0] cin_sel,
  input  [1:0] engine_sel,
  input  write_enable,
  output [31:0] result,
  output C,
  output Z,
  output N,
  output V,
  output write_enable_out
);

  wire A_eff_out, B_eff_out, or_1_out, xnor_1_out, xor_1_out;
  wire [31:0] alu_arithmetic_engine_1_result, alu_logic_engine_1_result, ks_32b_1_sum0, mul_32_1_carry,
       mul_32_1_sum, undriven, undriven_2, undriven_3;

  mul_32 mul_32_1 (.A(undriven_2), .B(undriven), .sum(mul_32_1_sum), .carry(mul_32_1_carry));
  xor A_eff (A_eff_out, a_inv, A[31]);
  xor B_eff (B_eff_out, b_inv, B[31]);
  ALU_logic_engine alu_logic_engine_1 (.A(A), .B(B), .select_bit(logic_sel), .result(alu_logic_engine_1_result));
  ALU_arithmetic_engine alu_arithmetic_engine_1 (
    .a_inversion(a_inv), .A(A), .B(B), .b_inversion(b_inv), .Cflag(Cflag), .unused(unused),
    .Cin_sel(cin_sel), .Result(alu_arithmetic_engine_1_result), .Cout(C));
  xnor xnor_1 (xnor_1_out, A_eff_out, B_eff_out);
  ks_32b ks_32b_1 (
    .A(mul_32_1_sum), .B(mul_32_1_carry), .SUM31(ks_32b_1_sum0[31]), .SUM30(ks_32b_1_sum0[30]),
    .SUM29(ks_32b_1_sum0[29]), .SUM28(ks_32b_1_sum0[28]), .SUM27(ks_32b_1_sum0[27]),
    .SUM26(ks_32b_1_sum0[26]), .SUM25(ks_32b_1_sum0[25]), .SUM24(ks_32b_1_sum0[24]),
    .SUM23(ks_32b_1_sum0[23]), .SUM22(ks_32b_1_sum0[22]), .SUM21(ks_32b_1_sum0[21]),
    .SUM20(ks_32b_1_sum0[20]), .SUM19(ks_32b_1_sum0[19]), .SUM18(ks_32b_1_sum0[18]),
    .SUM17(ks_32b_1_sum0[17]), .SUM16(ks_32b_1_sum0[16]), .SUM15(ks_32b_1_sum0[15]),
    .SUM14(ks_32b_1_sum0[14]), .SUM13(ks_32b_1_sum0[13]), .SUM12(ks_32b_1_sum0[12]),
    .SUM11(ks_32b_1_sum0[11]), .SUM10(ks_32b_1_sum0[10]), .SUM9(ks_32b_1_sum0[9]), .SUM8(ks_32b_1_sum0[8]),
    .SUM7(ks_32b_1_sum0[7]), .SUM6(ks_32b_1_sum0[6]), .SUM5(ks_32b_1_sum0[5]), .SUM4(ks_32b_1_sum0[4]),
    .SUM3(ks_32b_1_sum0[3]), .SUM2(ks_32b_1_sum0[2]), .sum1(ks_32b_1_sum0[1]), .sum0(ks_32b_1_sum0[0]));  // open: Cin, Cout
  Multiplexer #(.select(2), .width(32)) multiplexer_1 (
    .in0(alu_logic_engine_1_result), .in1(alu_arithmetic_engine_1_result), .in3(undriven_3),
    .out({N, result[30:0]}), .sel(engine_sel));  // open: in2
  xor xor_1 (xor_1_out, N, A_eff_out);
  or or_1 (or_1_out, result[0], result[1], result[2], result[3], result[4], result[5], result[6], result[7], result[8], result[9], result[10], result[11], result[12], result[13], result[14], result[15], result[16], result[17], result[18], result[19], result[20], result[21], result[22], result[23], result[24], result[25], result[26], result[27], result[28], result[29], result[30], N);
  and and_1 (V, xor_1_out, xnor_1_out);
  not not_1 (Z, or_1_out);

  assign result[31] = N;
  assign write_enable_out = write_enable;

  // Notes on the sheet:
  //   A: initial=0x9e3779b9
  //   B: initial=0x7f4a7c15
endmodule

module a_invert (
  input  [31:0] A,
  input  a_inversion,
  input  [31:0] B
);

  wire [31:0] bit_extender_1_out, xor_1_out;

  assign bit_extender_1_out = {{31{a_inversion}}, a_inversion};  // Bit_Extender bit_extender_1
  assign xor_1_out = A ^ bit_extender_1_out;  // XOR_Gate xor_1, 32 bits wide
  ks_32b ks_32b_1 (
    .A(xor_1_out), .B(B), .Cin(a_inversion));  // open: SUM31, SUM30, SUM29, SUM28, SUM27, SUM26, SUM25, SUM24, SUM23, SUM22, SUM21, SUM20, SUM19, SUM18, SUM17, SUM16, SUM15, SUM14, SUM13, SUM12, SUM11, SUM10, SUM9, SUM8, SUM7, SUM6, SUM5, SUM4, SUM3, SUM2, sum1, sum0, Cout
endmodule

module ALU_logic_engine (
  input  [31:0] A,
  input  [31:0] B,
  input  [2:0] select_bit,
  output [31:0] result
);

  wire [31:0] and_1_out, and_2_out, not_1_out, or_1_out, xor_1_out;

  assign not_1_out = ~B;  // NOT_Gate not_1, 32 bits wide
  assign and_1_out = A & B;  // AND_Gate and_1, 32 bits wide
  assign xor_1_out = A ^ B;  // XOR_Gate xor_1, 32 bits wide
  assign or_1_out = A | B;  // OR_Gate or_1, 32 bits wide
  assign and_2_out = A & not_1_out;  // AND_Gate and_2, 32 bits wide
  Multiplexer #(.select(3), .width(32)) multiplexer_1 (
    .in0(and_1_out), .in1(xor_1_out), .in2(or_1_out), .in3(B), .in4(and_2_out), .in5(not_1_out),
    .out(result), .sel(select_bit));  // open: in6, in7
endmodule

module pp_row_32 (
  input  [31:0] Rm,
  input  Rs_bit,
  output [31:0] result
);

  wire [31:0] bit_extender_1_out;

  assign bit_extender_1_out = {{31{Rs_bit}}, Rs_bit};  // Bit_Extender bit_extender_1
  assign result = Rm & bit_extender_1_out;  // AND_Gate and_1, 32 bits wide

  // Notes on the sheet:
  //   Rm: initial=0xdeadbeef
endmodule

module partial_products (
  input  [31:0] Rm,
  input  [31:0] Rs,
  output [31:0] p0,
  output [31:0] p1,
  output [31:0] p2,
  output [31:0] p3,
  output [31:0] p4,
  output [31:0] p5,
  output [31:0] p6,
  output [31:0] p7,
  output [31:0] p8,
  output [31:0] p9,
  output [31:0] p10,
  output [31:0] p11,
  output [31:0] p12,
  output [31:0] p13,
  output [31:0] p14,
  output [31:0] p15,
  output [31:0] p16,
  output [31:0] p17,
  output [31:0] p18,
  output [31:0] p19,
  output [31:0] p20,
  output [31:0] p21,
  output [31:0] p22,
  output [31:0] p23,
  output [31:0] p24,
  output [31:0] p25,
  output [31:0] p26,
  output [31:0] p27,
  output [31:0] p28,
  output [31:0] p29,
  output [31:0] p30,
  output [31:0] p31
);

  wire [31:0] pp_row_32_1_result, pp_row_32_2_result, pp_row_32_3_result, pp_row_32_4_result,
       pp_row_32_5_result, pp_row_32_6_result, pp_row_32_7_result, pp_row_32_8_result, pp_row_32_9_result,
       pp_row_32_10_result, pp_row_32_11_result, pp_row_32_12_result, pp_row_32_13_result,
       pp_row_32_14_result, pp_row_32_15_result, pp_row_32_16_result, pp_row_32_17_result,
       pp_row_32_18_result, pp_row_32_19_result, pp_row_32_20_result, pp_row_32_21_result,
       pp_row_32_22_result, pp_row_32_23_result, pp_row_32_24_result, pp_row_32_25_result,
       pp_row_32_26_result, pp_row_32_27_result, pp_row_32_28_result, pp_row_32_29_result,
       pp_row_32_30_result, pp_row_32_31_result, pp_row_32_32_result;

  pp_row_32 pp_row_32_1 (.Rm(Rm), .Rs_bit(Rs[0]), .result(pp_row_32_1_result));
  pp_row_32 pp_row_32_2 (.Rm(Rm), .Rs_bit(Rs[1]), .result(pp_row_32_2_result));
  pp_row_32 pp_row_32_3 (.Rm(Rm), .Rs_bit(Rs[2]), .result(pp_row_32_3_result));
  pp_row_32 pp_row_32_4 (.Rm(Rm), .Rs_bit(Rs[3]), .result(pp_row_32_4_result));
  pp_row_32 pp_row_32_5 (.Rm(Rm), .Rs_bit(Rs[4]), .result(pp_row_32_5_result));
  pp_row_32 pp_row_32_6 (.Rm(Rm), .Rs_bit(Rs[5]), .result(pp_row_32_6_result));
  pp_row_32 pp_row_32_7 (.Rm(Rm), .Rs_bit(Rs[6]), .result(pp_row_32_7_result));
  pp_row_32 pp_row_32_8 (.Rm(Rm), .Rs_bit(Rs[7]), .result(pp_row_32_8_result));
  pp_row_32 pp_row_32_9 (.Rm(Rm), .Rs_bit(Rs[8]), .result(pp_row_32_9_result));
  pp_row_32 pp_row_32_10 (.Rm(Rm), .Rs_bit(Rs[9]), .result(pp_row_32_10_result));
  pp_row_32 pp_row_32_11 (.Rm(Rm), .Rs_bit(Rs[10]), .result(pp_row_32_11_result));
  pp_row_32 pp_row_32_12 (.Rm(Rm), .Rs_bit(Rs[11]), .result(pp_row_32_12_result));
  pp_row_32 pp_row_32_13 (.Rm(Rm), .Rs_bit(Rs[12]), .result(pp_row_32_13_result));
  pp_row_32 pp_row_32_14 (.Rm(Rm), .Rs_bit(Rs[13]), .result(pp_row_32_14_result));
  pp_row_32 pp_row_32_15 (.Rm(Rm), .Rs_bit(Rs[14]), .result(pp_row_32_15_result));
  pp_row_32 pp_row_32_16 (.Rm(Rm), .Rs_bit(Rs[15]), .result(pp_row_32_16_result));
  pp_row_32 pp_row_32_17 (.Rm(Rm), .Rs_bit(Rs[16]), .result(pp_row_32_17_result));
  pp_row_32 pp_row_32_18 (.Rm(Rm), .Rs_bit(Rs[17]), .result(pp_row_32_18_result));
  pp_row_32 pp_row_32_19 (.Rm(Rm), .Rs_bit(Rs[18]), .result(pp_row_32_19_result));
  pp_row_32 pp_row_32_20 (.Rm(Rm), .Rs_bit(Rs[19]), .result(pp_row_32_20_result));
  pp_row_32 pp_row_32_21 (.Rm(Rm), .Rs_bit(Rs[20]), .result(pp_row_32_21_result));
  pp_row_32 pp_row_32_22 (.Rm(Rm), .Rs_bit(Rs[21]), .result(pp_row_32_22_result));
  pp_row_32 pp_row_32_23 (.Rm(Rm), .Rs_bit(Rs[22]), .result(pp_row_32_23_result));
  pp_row_32 pp_row_32_24 (.Rm(Rm), .Rs_bit(Rs[23]), .result(pp_row_32_24_result));
  pp_row_32 pp_row_32_25 (.Rm(Rm), .Rs_bit(Rs[24]), .result(pp_row_32_25_result));
  pp_row_32 pp_row_32_26 (.Rm(Rm), .Rs_bit(Rs[25]), .result(pp_row_32_26_result));
  pp_row_32 pp_row_32_27 (.Rm(Rm), .Rs_bit(Rs[26]), .result(pp_row_32_27_result));
  pp_row_32 pp_row_32_28 (.Rm(Rm), .Rs_bit(Rs[27]), .result(pp_row_32_28_result));
  pp_row_32 pp_row_32_29 (.Rm(Rm), .Rs_bit(Rs[28]), .result(pp_row_32_29_result));
  pp_row_32 pp_row_32_30 (.Rm(Rm), .Rs_bit(Rs[29]), .result(pp_row_32_30_result));
  pp_row_32 pp_row_32_31 (.Rm(Rm), .Rs_bit(Rs[30]), .result(pp_row_32_31_result));
  pp_row_32 pp_row_32_32 (.Rm(Rm), .Rs_bit(Rs[31]), .result(pp_row_32_32_result));
  Shifter #(.width(32)) shifter_1 (.in(pp_row_32_1_result), .\dist ({5{1'b0}}), .out(p0));
  Shifter #(.width(32)) shifter_2 (.in(pp_row_32_2_result), .\dist (5'b00001), .out(p1));
  Shifter #(.width(32)) shifter_3 (.in(pp_row_32_3_result), .\dist (5'b00010), .out(p2));
  Shifter #(.width(32)) shifter_4 (.in(pp_row_32_4_result), .\dist (5'b00011), .out(p3));
  Shifter #(.width(32)) shifter_5 (.in(pp_row_32_5_result), .\dist (5'b00100), .out(p4));
  Shifter #(.width(32)) shifter_6 (.in(pp_row_32_6_result), .\dist (5'b00101), .out(p5));
  Shifter #(.width(32)) shifter_7 (.in(pp_row_32_7_result), .\dist (5'b00110), .out(p6));
  Shifter #(.width(32)) shifter_8 (.in(pp_row_32_8_result), .\dist (5'b00111), .out(p7));
  Shifter #(.width(32)) shifter_9 (.in(pp_row_32_9_result), .\dist (5'b01000), .out(p8));
  Shifter #(.width(32)) shifter_10 (.in(pp_row_32_10_result), .\dist (5'b01001), .out(p9));
  Shifter #(.width(32)) shifter_11 (.in(pp_row_32_11_result), .\dist (5'b01010), .out(p10));
  Shifter #(.width(32)) shifter_12 (.in(pp_row_32_12_result), .\dist (5'b01011), .out(p11));
  Shifter #(.width(32)) shifter_13 (.in(pp_row_32_13_result), .\dist (5'b01100), .out(p12));
  Shifter #(.width(32)) shifter_14 (.in(pp_row_32_14_result), .\dist (5'b01101), .out(p13));
  Shifter #(.width(32)) shifter_15 (.in(pp_row_32_15_result), .\dist (5'b01110), .out(p14));
  Shifter #(.width(32)) shifter_16 (.in(pp_row_32_16_result), .\dist (5'b01111), .out(p15));
  Shifter #(.width(32)) shifter_17 (.in(pp_row_32_17_result), .\dist (5'b10000), .out(p16));
  Shifter #(.width(32)) shifter_18 (.in(pp_row_32_18_result), .\dist (5'b10001), .out(p17));
  Shifter #(.width(32)) shifter_19 (.in(pp_row_32_19_result), .\dist (5'b10010), .out(p18));
  Shifter #(.width(32)) shifter_20 (.in(pp_row_32_20_result), .\dist (5'b10011), .out(p19));
  Shifter #(.width(32)) shifter_21 (.in(pp_row_32_21_result), .\dist (5'b10100), .out(p20));
  Shifter #(.width(32)) shifter_22 (.in(pp_row_32_22_result), .\dist (5'b10101), .out(p21));
  Shifter #(.width(32)) shifter_23 (.in(pp_row_32_23_result), .\dist (5'b10110), .out(p22));
  Shifter #(.width(32)) shifter_24 (.in(pp_row_32_24_result), .\dist (5'b10111), .out(p23));
  Shifter #(.width(32)) shifter_25 (.in(pp_row_32_25_result), .\dist (5'b11000), .out(p24));
  Shifter #(.width(32)) shifter_26 (.in(pp_row_32_26_result), .\dist (5'b11001), .out(p25));
  Shifter #(.width(32)) shifter_27 (.in(pp_row_32_27_result), .\dist (5'b11010), .out(p26));
  Shifter #(.width(32)) shifter_28 (.in(pp_row_32_28_result), .\dist (5'b11011), .out(p27));
  Shifter #(.width(32)) shifter_29 (.in(pp_row_32_29_result), .\dist (5'b11100), .out(p28));
  Shifter #(.width(32)) shifter_30 (.in(pp_row_32_30_result), .\dist (5'b11101), .out(p29));
  Shifter #(.width(32)) shifter_31 (.in(pp_row_32_31_result), .\dist (5'b11110), .out(p30));
  Shifter #(.width(32)) shifter_32 (.in(pp_row_32_32_result), .\dist ({5{1'b1}}), .out(p31));

  // Notes on the sheet:
  //   Rm: initial=0xdeadbeef
  //   Rs: initial=0xdeadbeef
endmodule

module csa_3to_2 (
  input  [31:0] X,
  input  [31:0] Y,
  input  [31:0] Z,
  output [31:0] sum,
  output [31:0] carry
);

  wire [31:0] maj_out, XandY_out, XandZ_out, xor_1_out, YandZ_out;

  assign XandY_out = X & Y;  // AND_Gate XandY, 32 bits wide
  assign XandZ_out = X & Z;  // AND_Gate XandZ, 32 bits wide
  assign YandZ_out = Y & Z;  // AND_Gate YandZ, 32 bits wide
  assign xor_1_out = X ^ Z;  // XOR_Gate xor_1, 32 bits wide
  assign maj_out = XandY_out | XandZ_out | YandZ_out;  // OR_Gate maj, 32 bits wide
  Shifter #(.width(32)) shifter_1 (.in(maj_out), .\dist (5'b00001), .out(carry));
  assign sum = Y ^ xor_1_out;  // XOR_Gate xor_2, 32 bits wide
endmodule

module mul_32 (
  input  [31:0] A,
  input  [31:0] B,
  output [31:0] sum,
  output [31:0] carry
);

  wire [31:0] cinco_carry, cinco_sum, csa_3to_2_1_carry, csa_3to_2_1_sum, csa_3to_2_2_carry, csa_3to_2_2_sum,
       csa_3to_2_3_carry, csa_3to_2_3_sum, csa_3to_2_4_carry, csa_3to_2_4_sum, csa_3to_2_5_carry,
       csa_3to_2_5_sum, csa_3to_2_6_carry, csa_3to_2_6_sum, csa_3to_2_7_carry, csa_3to_2_7_sum,
       csa_3to_2_8_carry, csa_3to_2_8_sum, csa_3to_2_9_carry, csa_3to_2_9_sum, csa_3to_2_10_carry,
       csa_3to_2_10_sum, csa_3to_2_11_carry, csa_3to_2_11_sum, csa_3to_2_12_carry, csa_3to_2_12_sum,
       csa_3to_2_13_carry, csa_3to_2_13_sum, csa_3to_2_14_carry, csa_3to_2_14_sum, csa_3to_2_15_carry,
       csa_3to_2_15_sum, csa_3to_2_16_carry, csa_3to_2_16_sum, csa_3to_2_17_carry, csa_3to_2_17_sum,
       diecsiete_carry, diecsiete_sum, diez_carry, diez_sum, dos_carry, dos_sum, partial_products_1_p0,
       partial_products_1_p1, partial_products_1_p2, partial_products_1_p3, partial_products_1_p4,
       partial_products_1_p5, partial_products_1_p6, partial_products_1_p7, partial_products_1_p8,
       partial_products_1_p9, partial_products_1_p10, partial_products_1_p11, partial_products_1_p12,
       partial_products_1_p13, partial_products_1_p14, partial_products_1_p15, partial_products_1_p16,
       partial_products_1_p17, partial_products_1_p18, partial_products_1_p19, partial_products_1_p20,
       partial_products_1_p21, partial_products_1_p22, partial_products_1_p23, partial_products_1_p24,
       partial_products_1_p25, partial_products_1_p26, partial_products_1_p27, partial_products_1_p28,
       partial_products_1_p29, partial_products_1_p30, partial_products_1_p31, quince_carry, quince_sum,
       siete_carry, siete_sum, trece_carry, trece_sum, tres_carry, tres_sum, un_carry, un_sum, vente4_carry,
       vente4_sum, vente7_carry, vente7_sum, viente_carry, viente_sum;

  partial_products partial_products_1 (
    .Rm(A), .Rs(B), .p0(partial_products_1_p0), .p1(partial_products_1_p1), .p2(partial_products_1_p2),
    .p3(partial_products_1_p3), .p4(partial_products_1_p4), .p5(partial_products_1_p5),
    .p6(partial_products_1_p6), .p7(partial_products_1_p7), .p8(partial_products_1_p8),
    .p9(partial_products_1_p9), .p10(partial_products_1_p10), .p11(partial_products_1_p11),
    .p12(partial_products_1_p12), .p13(partial_products_1_p13), .p14(partial_products_1_p14),
    .p15(partial_products_1_p15), .p16(partial_products_1_p16), .p17(partial_products_1_p17),
    .p18(partial_products_1_p18), .p19(partial_products_1_p19), .p20(partial_products_1_p20),
    .p21(partial_products_1_p21), .p22(partial_products_1_p22), .p23(partial_products_1_p23),
    .p24(partial_products_1_p24), .p25(partial_products_1_p25), .p26(partial_products_1_p26),
    .p27(partial_products_1_p27), .p28(partial_products_1_p28), .p29(partial_products_1_p29),
    .p30(partial_products_1_p30), .p31(partial_products_1_p31));
  csa_3to_2 un (
    .X(partial_products_1_p0), .Y(partial_products_1_p1), .Z(partial_products_1_p2), .sum(un_sum),
    .carry(un_carry));
  csa_3to_2 dos (.X(un_sum), .Y(un_carry), .Z(partial_products_1_p3), .sum(dos_sum), .carry(dos_carry));
  csa_3to_2 tres (.X(dos_sum), .Y(dos_carry), .Z(partial_products_1_p4), .sum(tres_sum), .carry(tres_carry));
  csa_3to_2 csa_3to_2_1 (
    .X(tres_sum), .Y(tres_carry), .Z(partial_products_1_p5), .sum(csa_3to_2_1_sum), .carry(csa_3to_2_1_carry));
  csa_3to_2 cinco (
    .X(csa_3to_2_1_sum), .Y(csa_3to_2_1_carry), .Z(partial_products_1_p6), .sum(cinco_sum),
    .carry(cinco_carry));
  csa_3to_2 csa_3to_2_2 (
    .X(cinco_sum), .Y(cinco_carry), .Z(partial_products_1_p7), .sum(csa_3to_2_2_sum),
    .carry(csa_3to_2_2_carry));
  csa_3to_2 siete (
    .X(csa_3to_2_2_sum), .Y(csa_3to_2_2_carry), .Z(partial_products_1_p8), .sum(siete_sum),
    .carry(siete_carry));
  csa_3to_2 csa_3to_2_3 (
    .X(siete_sum), .Y(siete_carry), .Z(partial_products_1_p9), .sum(csa_3to_2_3_sum),
    .carry(csa_3to_2_3_carry));
  csa_3to_2 csa_3to_2_4 (
    .X(csa_3to_2_3_sum), .Y(csa_3to_2_3_carry), .Z(partial_products_1_p10), .sum(csa_3to_2_4_sum),
    .carry(csa_3to_2_4_carry));
  csa_3to_2 diez (
    .X(csa_3to_2_4_sum), .Y(csa_3to_2_4_carry), .Z(partial_products_1_p11), .sum(diez_sum), .carry(diez_carry));
  csa_3to_2 csa_3to_2_5 (
    .X(diez_sum), .Y(diez_carry), .Z(partial_products_1_p12), .sum(csa_3to_2_5_sum), .carry(csa_3to_2_5_carry));
  csa_3to_2 csa_3to_2_6 (
    .X(csa_3to_2_5_sum), .Y(csa_3to_2_5_carry), .Z(partial_products_1_p13), .sum(csa_3to_2_6_sum),
    .carry(csa_3to_2_6_carry));
  csa_3to_2 trece (
    .X(csa_3to_2_6_sum), .Y(csa_3to_2_6_carry), .Z(partial_products_1_p14), .sum(trece_sum),
    .carry(trece_carry));
  csa_3to_2 csa_3to_2_7 (
    .X(trece_sum), .Y(trece_carry), .Z(partial_products_1_p15), .sum(csa_3to_2_7_sum),
    .carry(csa_3to_2_7_carry));
  // Probe on quince_sum
  csa_3to_2 quince (
    .X(csa_3to_2_7_sum), .Y(csa_3to_2_7_carry), .Z(partial_products_1_p16), .sum(quince_sum),
    .carry(quince_carry));
  csa_3to_2 csa_3to_2_8 (
    .X(quince_sum), .Y(quince_carry), .Z(partial_products_1_p17), .sum(csa_3to_2_8_sum),
    .carry(csa_3to_2_8_carry));
  csa_3to_2 diecsiete (
    .X(csa_3to_2_8_sum), .Y(csa_3to_2_8_carry), .Z(partial_products_1_p18), .sum(diecsiete_sum),
    .carry(diecsiete_carry));
  csa_3to_2 csa_3to_2_9 (
    .X(diecsiete_sum), .Y(diecsiete_carry), .Z(partial_products_1_p19), .sum(csa_3to_2_9_sum),
    .carry(csa_3to_2_9_carry));
  csa_3to_2 csa_3to_2_10 (
    .X(csa_3to_2_9_sum), .Y(csa_3to_2_9_carry), .Z(partial_products_1_p20), .sum(csa_3to_2_10_sum),
    .carry(csa_3to_2_10_carry));
  csa_3to_2 viente (
    .X(csa_3to_2_10_sum), .Y(csa_3to_2_10_carry), .Z(partial_products_1_p21), .sum(viente_sum),
    .carry(viente_carry));
  csa_3to_2 csa_3to_2_11 (
    .X(viente_sum), .Y(viente_carry), .Z(partial_products_1_p22), .sum(csa_3to_2_11_sum),
    .carry(csa_3to_2_11_carry));
  csa_3to_2 csa_3to_2_12 (
    .X(csa_3to_2_11_sum), .Y(csa_3to_2_11_carry), .Z(partial_products_1_p23), .sum(csa_3to_2_12_sum),
    .carry(csa_3to_2_12_carry));
  csa_3to_2 csa_3to_2_13 (
    .X(csa_3to_2_12_sum), .Y(csa_3to_2_12_carry), .Z(partial_products_1_p24), .sum(csa_3to_2_13_sum),
    .carry(csa_3to_2_13_carry));
  csa_3to_2 vente4 (
    .X(csa_3to_2_13_sum), .Y(csa_3to_2_13_carry), .Z(partial_products_1_p25), .sum(vente4_sum),
    .carry(vente4_carry));
  csa_3to_2 csa_3to_2_14 (
    .X(vente4_sum), .Y(vente4_carry), .Z(partial_products_1_p26), .sum(csa_3to_2_14_sum),
    .carry(csa_3to_2_14_carry));
  csa_3to_2 csa_3to_2_15 (
    .X(csa_3to_2_14_sum), .Y(csa_3to_2_14_carry), .Z(partial_products_1_p27), .sum(csa_3to_2_15_sum),
    .carry(csa_3to_2_15_carry));
  csa_3to_2 vente7 (
    .X(csa_3to_2_15_sum), .Y(csa_3to_2_15_carry), .Z(partial_products_1_p28), .sum(vente7_sum),
    .carry(vente7_carry));
  csa_3to_2 csa_3to_2_16 (
    .X(vente7_sum), .Y(vente7_carry), .Z(partial_products_1_p29), .sum(csa_3to_2_16_sum),
    .carry(csa_3to_2_16_carry));
  csa_3to_2 csa_3to_2_17 (
    .X(csa_3to_2_16_sum), .Y(csa_3to_2_16_carry), .Z(partial_products_1_p30), .sum(csa_3to_2_17_sum),
    .carry(csa_3to_2_17_carry));
  csa_3to_2 csa_3to_2_18 (
    .X(csa_3to_2_17_sum), .Y(csa_3to_2_17_carry), .Z(partial_products_1_p31), .sum(sum), .carry(carry));

  // Notes on the sheet:
  //   A: initial=0xdeadbeef
  //   B: initial=0xdeadbeef
endmodule

module pc_fetch (
  input  CLK,
  input  BRANCH,
  input  hold,
  input  [31:0] IMM,
  input  [31:0] abs_target,
  input  abs_select,
  input  RST,
  output [31:0] pc_plus4,
  output [9:0] pc_out
);

  wire [31:0] adder_2_out, multiplexer_1_out, multiplexer_2_out, multiplexer_3_out, PC_q;

  Register #(.width(32)) PC (
    .D(multiplexer_3_out), .en(1'b1), .clk(CLK), .Q({PC_q[31:12], pc_out, PC_q[1:0]}), .clr(RST));
  Adder #(.width(32)) adder_1 (
    .a({PC_q[31:12], pc_out, PC_q[1:0]}), .b(32'h4), .out(pc_plus4), .cin(1'b0));  // open: cout
  Adder #(.width(32)) adder_2 (
    .a({PC_q[31:12], pc_out, PC_q[1:0]}), .b(IMM), .out(adder_2_out), .cin(1'b0));  // open: cout
  Multiplexer #(.width(32)) multiplexer_1 (
    .in0(adder_2_out), .in1(abs_target), .out(multiplexer_1_out), .sel(abs_select));
  Multiplexer #(.width(32)) multiplexer_2 (
    .in0(pc_plus4), .in1(multiplexer_1_out), .out(multiplexer_2_out), .sel(BRANCH));
  Multiplexer #(.width(32)) multiplexer_3 (
    .in0(multiplexer_2_out), .in1({PC_q[31:12], pc_out, PC_q[1:0]}), .out(multiplexer_3_out), .sel(hold));
endmodule

module reg16x32 (
  input  CLK,
  input  [3:0] WA,
  input  [31:0] WD,
  input  WE,
  input  RST,
  input  [3:0] RA,
  input  [3:0] RB,
  output [31:0] R0_OUTPUT,
  output [31:0] R1_OUTPUT,
  output [31:0] R3_OUTPUT,
  output [31:0] R2_OUPUT,
  output [31:0] R5_OUTPUT,
  output [31:0] R4_OUTPUT,
  output [31:0] RD_A,
  output [31:0] R7_OUTPUT,
  output [31:0] R6_OUTPUT,
  output [31:0] RD_B,
  output [31:0] R8_OUTPUT,
  output [31:0] R9_OUTPUT,
  output [31:0] R11_OUTPUT,
  output [31:0] R10_OUTPUT,
  output [31:0] R13_OUTPUT,
  output [31:0] R12_OUTPUT,
  output [31:0] R15_OUTPUT,
  output [31:0] R14_OUTPUT
);

  wire and_1_out, and_2_out, and_3_out, and_4_out, and_5_out, and_6_out, and_7_out, and_8_out, and_9_out,
       and_10_out, and_11_out, and_12_out, and_13_out, and_14_out, and_15_out, and_16_out, decoder_1_out0,
       decoder_1_out1, decoder_1_out2, decoder_1_out3, decoder_1_out4, decoder_1_out5, decoder_1_out6,
       decoder_1_out7, decoder_1_out8, decoder_1_out9, decoder_1_out10, decoder_1_out11, decoder_1_out12,
       decoder_1_out13, decoder_1_out14, decoder_1_out15;

  Decoder #(.select(4)) decoder_1 (
    .out0(decoder_1_out0), .out1(decoder_1_out1), .out2(decoder_1_out2), .out3(decoder_1_out3),
    .out4(decoder_1_out4), .out5(decoder_1_out5), .out6(decoder_1_out6), .out7(decoder_1_out7),
    .out8(decoder_1_out8), .out9(decoder_1_out9), .out10(decoder_1_out10), .out11(decoder_1_out11),
    .out12(decoder_1_out12), .out13(decoder_1_out13), .out14(decoder_1_out14), .out15(decoder_1_out15),
    .sel(WA), .en(WE));
  and and_1 (and_1_out, decoder_1_out0, WE);
  and and_2 (and_2_out, decoder_1_out1, WE);
  and and_3 (and_3_out, decoder_1_out2, WE);
  and and_4 (and_4_out, decoder_1_out3, WE);
  and and_5 (and_5_out, decoder_1_out4, WE);
  and and_6 (and_6_out, decoder_1_out5, WE);
  and and_7 (and_7_out, decoder_1_out6, WE);
  and and_8 (and_8_out, decoder_1_out7, WE);
  and and_9 (and_9_out, decoder_1_out8, WE);
  and and_10 (and_10_out, decoder_1_out9, WE);
  and and_11 (and_11_out, decoder_1_out10, WE);
  and and_12 (and_12_out, decoder_1_out11, WE);
  and and_13 (and_13_out, decoder_1_out12, WE);
  and and_14 (and_14_out, decoder_1_out13, WE);
  and and_15 (and_15_out, decoder_1_out14, WE);
  and and_16 (and_16_out, decoder_1_out15, WE);
  Register #(.width(32)) R0 (.D(WD), .en(and_1_out), .clk(CLK), .Q(R0_OUTPUT), .clr(RST));
  Register #(.width(32)) R2 (.D(WD), .en(and_3_out), .clk(CLK), .Q(R2_OUPUT), .clr(RST));
  Register #(.width(32)) R4 (.D(WD), .en(and_5_out), .clk(CLK), .Q(R4_OUTPUT), .clr(RST));
  Register #(.width(32)) R6 (.D(WD), .en(and_7_out), .clk(CLK), .Q(R6_OUTPUT), .clr(RST));
  Register #(.width(32)) R8 (.D(WD), .en(and_9_out), .clk(CLK), .Q(R8_OUTPUT), .clr(RST));
  Register #(.width(32)) R10 (.D(WD), .en(and_11_out), .clk(CLK), .Q(R10_OUTPUT), .clr(RST));
  Register #(.width(32)) R12 (.D(WD), .en(and_13_out), .clk(CLK), .Q(R12_OUTPUT), .clr(RST));
  Register #(.width(32)) R14 (.D(WD), .en(and_15_out), .clk(CLK), .Q(R14_OUTPUT), .clr(RST));
  Register #(.width(32)) R1 (.D(WD), .en(and_2_out), .clk(CLK), .Q(R1_OUTPUT), .clr(RST));
  Register #(.width(32)) R3 (.D(WD), .en(and_4_out), .clk(CLK), .Q(R3_OUTPUT), .clr(RST));
  Register #(.width(32)) R5 (.D(WD), .en(and_6_out), .clk(CLK), .Q(R5_OUTPUT), .clr(RST));
  Register #(.width(32)) R7 (.D(WD), .en(and_8_out), .clk(CLK), .Q(R7_OUTPUT), .clr(RST));
  Register #(.width(32)) R9 (.D(WD), .en(and_10_out), .clk(CLK), .Q(R9_OUTPUT), .clr(RST));
  Register #(.width(32)) R11 (.D(WD), .en(and_12_out), .clk(CLK), .Q(R11_OUTPUT), .clr(RST));
  Register #(.width(32)) R13 (.D(WD), .en(and_14_out), .clk(CLK), .Q(R13_OUTPUT), .clr(RST));
  Register #(.width(32)) R15 (.D(WD), .en(and_16_out), .clk(CLK), .Q(R15_OUTPUT), .clr(RST));
  Multiplexer #(.select(4), .width(32)) multiplexer_1 (
    .in0(R0_OUTPUT), .in1(R1_OUTPUT), .in2(R2_OUPUT), .in3(R3_OUTPUT), .in4(R4_OUTPUT), .in5(R5_OUTPUT),
    .in6(R6_OUTPUT), .in7(R7_OUTPUT), .in8(R8_OUTPUT), .in9(R9_OUTPUT), .in10(R10_OUTPUT), .in11(R11_OUTPUT),
    .in12(R12_OUTPUT), .in13(R13_OUTPUT), .in14(R14_OUTPUT), .in15(R15_OUTPUT), .out(RD_A), .sel(RA));
  Multiplexer #(.select(4), .width(32)) multiplexer_2 (
    .in0(R0_OUTPUT), .in1(R1_OUTPUT), .in2(R2_OUPUT), .in3(R3_OUTPUT), .in4(R4_OUTPUT), .in5(R5_OUTPUT),
    .in6(R6_OUTPUT), .in7(R7_OUTPUT), .in8(R8_OUTPUT), .in9(R9_OUTPUT), .in10(R10_OUTPUT), .in11(R11_OUTPUT),
    .in12(R12_OUTPUT), .in13(R13_OUTPUT), .in14(R14_OUTPUT), .in15(R15_OUTPUT), .out(RD_B), .sel(RB));
endmodule

module PE_cell_32 (
  input  [31:0] w_in,
  input  w_load,
  input  CLK,
  input  [31:0] psum_in,
  input  [31:0] a_in,
  output [31:0] psum_out,
  output [31:0] a_out
);

  wire [31:0] adder_1_out, multiplier_1_out, W_reg_q;

  Register #(.width(32)) W_reg (.D(w_in), .en(w_load), .clk(CLK), .Q(W_reg_q));  // open: clr
  Multiplier #(.width(32)) multiplier_1 (.a(a_in), .b(W_reg_q), .out(multiplier_1_out));  // open: cin, cout
  Register #(.width(32)) a_reg (.D(a_in), .clk(CLK), .Q(a_out));  // open: en, clr
  Register #(.width(32)) psum_reg (.D(adder_1_out), .clk(CLK), .Q(psum_out));  // open: en, clr
  Adder #(.width(32)) adder_1 (.a(psum_in), .b(multiplier_1_out), .out(adder_1_out));  // open: cin, cout
endmodule

module systolic_4x4 (
  input  CLK,
  input  [31:0] w00,
  input  [31:0] w01,
  input  [31:0] w02,
  input  [31:0] w03,
  input  w_load,
  input  [31:0] p_sum00,
  input  [31:0] p_sum01,
  input  [31:0] p_sum02,
  input  [31:0] p_sum03,
  input  [31:0] row0,
  input  [31:0] w10,
  input  [31:0] w11,
  input  [31:0] w12,
  input  [31:0] w13,
  input  [31:0] row1,
  input  [31:0] w20,
  input  [31:0] w21,
  input  [31:0] w22,
  input  [31:0] w23,
  input  [31:0] row2,
  input  [31:0] w30,
  input  [31:0] w31,
  input  [31:0] w32,
  input  [31:0] w33,
  input  [31:0] row3,
  output [31:0] a_out0,
  output [31:0] a_out1,
  output [31:0] a_out2,
  output [31:0] c_col0,
  output [31:0] c_col1,
  output [31:0] c_col2,
  output [31:0] c_col3,
  output [31:0] a_out3
);

  wire [31:0] pe_cell_32_1_a_out, pe_cell_32_1_psum_out, pe_cell_32_2_a_out, pe_cell_32_2_psum_out,
       pe_cell_32_3_a_out, pe_cell_32_3_psum_out, pe_cell_32_4_a_out, pe_cell_32_5_a_out,
       pe_cell_32_5_psum_out, pe_cell_32_6_a_out, pe_cell_32_6_psum_out, pe_cell_32_7_a_out,
       pe_cell_32_7_psum_out, pe_cell_32_8_a_out, pe_cell_32_9_a_out, pe_cell_32_9_psum_out,
       pe_cell_32_10_a_out, pe_cell_32_10_psum_out, pe_cell_32_11_a_out, pe_cell_32_11_psum_out,
       pe_cell_32_12_a_out, pe_cell_32_13_psum_out, pe_cell_32_14_psum_out, pe_cell_32_15_psum_out;

  PE_cell_32 pe_cell_32_1 (
    .w_in(w00), .w_load(w_load), .CLK(CLK), .psum_in(p_sum00), .a_in(row0), .psum_out(pe_cell_32_1_psum_out),
    .a_out(pe_cell_32_1_a_out));
  PE_cell_32 pe_cell_32_2 (
    .w_in(w10), .w_load(w_load), .CLK(CLK), .psum_in(pe_cell_32_1_psum_out), .a_in(row1),
    .psum_out(pe_cell_32_2_psum_out), .a_out(pe_cell_32_2_a_out));
  PE_cell_32 pe_cell_32_3 (
    .w_in(w20), .w_load(w_load), .CLK(CLK), .psum_in(pe_cell_32_2_psum_out), .a_in(row2),
    .psum_out(pe_cell_32_3_psum_out), .a_out(pe_cell_32_3_a_out));
  PE_cell_32 pe_cell_32_4 (
    .w_in(w30), .w_load(w_load), .CLK(CLK), .psum_in(pe_cell_32_3_psum_out), .a_in(row3), .psum_out(c_col0),
    .a_out(pe_cell_32_4_a_out));
  // Probe on pe_cell_32_1_psum_out
  // Probe on pe_cell_32_2_psum_out
  // Probe on pe_cell_32_3_psum_out
  PE_cell_32 pe_cell_32_5 (
    .w_in(w01), .w_load(w_load), .CLK(CLK), .psum_in(p_sum01), .a_in(pe_cell_32_1_a_out),
    .psum_out(pe_cell_32_5_psum_out), .a_out(pe_cell_32_5_a_out));
  PE_cell_32 pe_cell_32_6 (
    .w_in(w11), .w_load(w_load), .CLK(CLK), .psum_in(pe_cell_32_5_psum_out), .a_in(pe_cell_32_2_a_out),
    .psum_out(pe_cell_32_6_psum_out), .a_out(pe_cell_32_6_a_out));
  PE_cell_32 pe_cell_32_7 (
    .w_in(w21), .w_load(w_load), .CLK(CLK), .psum_in(pe_cell_32_6_psum_out), .a_in(pe_cell_32_3_a_out),
    .psum_out(pe_cell_32_7_psum_out), .a_out(pe_cell_32_7_a_out));
  PE_cell_32 pe_cell_32_8 (
    .w_in(w31), .w_load(w_load), .CLK(CLK), .psum_in(pe_cell_32_7_psum_out), .a_in(pe_cell_32_4_a_out),
    .psum_out(c_col1), .a_out(pe_cell_32_8_a_out));
  // Probe on pe_cell_32_5_psum_out
  // Probe on pe_cell_32_6_psum_out
  // Probe on pe_cell_32_7_psum_out
  PE_cell_32 pe_cell_32_9 (
    .w_in(w02), .w_load(w_load), .CLK(CLK), .psum_in(p_sum02), .a_in(pe_cell_32_5_a_out),
    .psum_out(pe_cell_32_9_psum_out), .a_out(pe_cell_32_9_a_out));
  PE_cell_32 pe_cell_32_10 (
    .w_in(w12), .w_load(w_load), .CLK(CLK), .psum_in(pe_cell_32_9_psum_out), .a_in(pe_cell_32_6_a_out),
    .psum_out(pe_cell_32_10_psum_out), .a_out(pe_cell_32_10_a_out));
  PE_cell_32 pe_cell_32_11 (
    .w_in(w22), .w_load(w_load), .CLK(CLK), .psum_in(pe_cell_32_10_psum_out), .a_in(pe_cell_32_7_a_out),
    .psum_out(pe_cell_32_11_psum_out), .a_out(pe_cell_32_11_a_out));
  PE_cell_32 pe_cell_32_12 (
    .w_in(w32), .w_load(w_load), .CLK(CLK), .psum_in(pe_cell_32_11_psum_out), .a_in(pe_cell_32_8_a_out),
    .psum_out(c_col2), .a_out(pe_cell_32_12_a_out));
  // Probe on pe_cell_32_9_psum_out
  // Probe on pe_cell_32_10_psum_out
  // Probe on pe_cell_32_11_psum_out
  PE_cell_32 pe_cell_32_13 (
    .w_in(w03), .w_load(w_load), .CLK(CLK), .psum_in(p_sum03), .a_in(pe_cell_32_9_a_out),
    .psum_out(pe_cell_32_13_psum_out), .a_out(a_out0));
  PE_cell_32 pe_cell_32_14 (
    .w_in(w13), .w_load(w_load), .CLK(CLK), .psum_in(pe_cell_32_13_psum_out), .a_in(pe_cell_32_10_a_out),
    .psum_out(pe_cell_32_14_psum_out), .a_out(a_out1));
  PE_cell_32 pe_cell_32_15 (
    .w_in(w23), .w_load(w_load), .CLK(CLK), .psum_in(pe_cell_32_14_psum_out), .a_in(pe_cell_32_11_a_out),
    .psum_out(pe_cell_32_15_psum_out), .a_out(a_out2));
  PE_cell_32 pe_cell_32_16 (
    .w_in(w33), .w_load(w_load), .CLK(CLK), .psum_in(pe_cell_32_15_psum_out), .a_in(pe_cell_32_12_a_out),
    .psum_out(c_col3), .a_out(a_out3));
  // Probe on pe_cell_32_13_psum_out
  // Probe on pe_cell_32_14_psum_out
  // Probe on pe_cell_32_15_psum_out
endmodule

module matmul4x4 (
  input  clk,
  input  [31:0] w00,
  input  [31:0] w01,
  input  [31:0] w02,
  input  [31:0] w03,
  input  wload,
  input  [31:0] A0,
  input  [31:0] w10,
  input  [31:0] w11,
  input  [31:0] w12,
  input  [31:0] w13,
  input  [31:0] A1,
  input  [31:0] w20,
  input  [31:0] w21,
  input  [31:0] w22,
  input  [31:0] w23,
  input  [31:0] A2,
  input  [31:0] w30,
  input  [31:0] w31,
  input  [31:0] w32,
  input  [31:0] w33,
  input  [31:0] A3,
  output [31:0] c0,
  output [31:0] c3,
  output [31:0] c1,
  output [31:0] c2
);

  wire [31:0] register_1_q, register_2_q, register_3_q, register_4_q, register_5_q, register_6_q,
       register_7_q, register_8_q, register_10_q, systolic_4x4_1_c_col0, systolic_4x4_1_c_col1,
       systolic_4x4_1_c_col2;

  Register #(.width(32)) register_1 (.D(A2), .clk(clk), .Q(register_1_q));  // open: en, clr
  Register #(.width(32)) register_2 (.D(A1), .clk(clk), .Q(register_2_q));  // open: en, clr
  Register #(.width(32)) register_3 (.D(A3), .clk(clk), .Q(register_3_q));  // open: en, clr
  Register #(.width(32)) register_4 (.D(register_1_q), .clk(clk), .Q(register_4_q));  // open: en, clr
  Register #(.width(32)) register_5 (.D(register_3_q), .clk(clk), .Q(register_5_q));  // open: en, clr
  Register #(.width(32)) register_6 (.D(register_5_q), .clk(clk), .Q(register_6_q));  // open: en, clr
  systolic_4x4 systolic_4x4_1 (
    .CLK(clk), .w00(w00), .w01(w01), .w02(w02), .w03(w03), .w_load(wload), .p_sum00(A0), .p_sum01(w10),
    .p_sum02(w11), .p_sum03(w12), .row0(w13), .w10(register_2_q), .w11(w20), .w12(w21), .w13(w22),
    .row1(w23), .w20(register_4_q), .w21(w30), .w22(w31), .w23(w32), .row2(w33), .w30(register_6_q),
    .c_col0(systolic_4x4_1_c_col0), .c_col1(systolic_4x4_1_c_col1), .c_col2(systolic_4x4_1_c_col2),
    .c_col3(c3));  // open: w31, w32, w33, row3, a_out0, a_out1, a_out2, a_out3
  Register #(.width(32)) register_7 (.D(systolic_4x4_1_c_col0), .clk(clk), .Q(register_7_q));  // open: en, clr
  Register #(.width(32)) register_8 (.D(systolic_4x4_1_c_col1), .clk(clk), .Q(register_8_q));  // open: en, clr
  Register #(.width(32)) register_9 (.D(systolic_4x4_1_c_col2), .clk(clk), .Q(c2));  // open: en, clr
  Register #(.width(32)) register_10 (.D(register_7_q), .clk(clk), .Q(register_10_q));  // open: en, clr
  Register #(.width(32)) register_11 (.D(register_8_q), .clk(clk), .Q(c1));  // open: en, clr
  Register #(.width(32)) register_12 (.D(register_10_q), .clk(clk), .Q(c0));  // open: en, clr
endmodule

module pp_row_16 (
  input  [15:0] Rm,
  input  Rs_bit,
  output [15:0] result
);

  wire [15:0] bit_extender_1_out;

  assign bit_extender_1_out = {{15{Rs_bit}}, Rs_bit};  // Bit_Extender bit_extender_1
  assign result = Rm & bit_extender_1_out;  // AND_Gate and_1, 16 bits wide

  // Notes on the sheet:
  //   Rm: initial=0xdeadbeef
endmodule

module csa_16 (
  input  [15:0] X,
  input  [15:0] Y,
  input  [15:0] Z,
  output [15:0] sum,
  output [15:0] carry
);

  wire [15:0] maj_out, XandY_out, XandZ_out, xor_1_out, YandZ_out;

  assign XandY_out = X & Y;  // AND_Gate XandY, 16 bits wide
  assign XandZ_out = X & Z;  // AND_Gate XandZ, 16 bits wide
  assign YandZ_out = Y & Z;  // AND_Gate YandZ, 16 bits wide
  assign xor_1_out = X ^ Z;  // XOR_Gate xor_1, 16 bits wide
  assign maj_out = XandY_out | XandZ_out | YandZ_out;  // OR_Gate maj, 16 bits wide
  Shifter #(.width(16)) shifter_1 (.in(maj_out), .\dist (4'b0001), .out(carry));
  assign sum = Y ^ xor_1_out;  // XOR_Gate xor_2, 16 bits wide
endmodule

module pp_8 (
  input  [7:0] Rm,
  input  [7:0] Rs,
  output [15:0] p0,
  output [15:0] p1,
  output [15:0] p2,
  output [15:0] p3,
  output [15:0] p4,
  output [15:0] p5,
  output [15:0] p6,
  output [15:0] p7
);

  wire [15:0] bit_extender_1_out, pp_row_16_1_result, pp_row_16_2_result, pp_row_16_3_result,
       pp_row_16_4_result, pp_row_16_5_result, pp_row_16_6_result, pp_row_16_7_result, pp_row_16_8_result;

  assign bit_extender_1_out = {{8{1'b0}}, Rm};  // Bit_Extender bit_extender_1
  pp_row_16 pp_row_16_1 (.Rm(bit_extender_1_out), .Rs_bit(Rs[0]), .result(pp_row_16_1_result));
  pp_row_16 pp_row_16_2 (.Rm(bit_extender_1_out), .Rs_bit(Rs[1]), .result(pp_row_16_2_result));
  pp_row_16 pp_row_16_3 (.Rm(bit_extender_1_out), .Rs_bit(Rs[2]), .result(pp_row_16_3_result));
  pp_row_16 pp_row_16_4 (.Rm(bit_extender_1_out), .Rs_bit(Rs[3]), .result(pp_row_16_4_result));
  pp_row_16 pp_row_16_5 (.Rm(bit_extender_1_out), .Rs_bit(Rs[4]), .result(pp_row_16_5_result));
  pp_row_16 pp_row_16_6 (.Rm(bit_extender_1_out), .Rs_bit(Rs[5]), .result(pp_row_16_6_result));
  pp_row_16 pp_row_16_7 (.Rm(bit_extender_1_out), .Rs_bit(Rs[6]), .result(pp_row_16_7_result));
  pp_row_16 pp_row_16_8 (.Rm(bit_extender_1_out), .Rs_bit(Rs[7]), .result(pp_row_16_8_result));
  Shifter #(.width(16)) shifter_1 (.in(pp_row_16_1_result), .\dist (4'b0000), .out(p0));
  Shifter #(.width(16)) shifter_2 (.in(pp_row_16_2_result), .\dist (4'b0001), .out(p1));
  Shifter #(.width(16)) shifter_3 (.in(pp_row_16_3_result), .\dist (4'b0010), .out(p2));
  Shifter #(.width(16)) shifter_4 (.in(pp_row_16_4_result), .\dist (4'b0011), .out(p3));
  Shifter #(.width(16)) shifter_5 (.in(pp_row_16_5_result), .\dist (4'b0100), .out(p4));
  Shifter #(.width(16)) shifter_6 (.in(pp_row_16_6_result), .\dist (4'b0101), .out(p5));
  Shifter #(.width(16)) shifter_7 (.in(pp_row_16_7_result), .\dist (4'b0110), .out(p6));
  Shifter #(.width(16)) shifter_8 (.in(pp_row_16_8_result), .\dist (4'b0111), .out(p7));

  // Notes on the sheet:
  //   Rm: initial=0xbe
  //   Rs: initial=0xdeadbeef
endmodule

module mul_8 (
  input  [7:0] in_1,
  input  [7:0] in_2,
  output [31:0] out_3
);

  wire [15:0] csa_16_1_carry, csa_16_1_sum, csa_16_2_carry, csa_16_2_sum, csa_16_3_carry, csa_16_3_sum,
       csa_16_4_carry, csa_16_4_sum, csa_16_5_carry, csa_16_5_sum, csa_16_6_carry, csa_16_6_sum, pp_8_1_p0,
       pp_8_1_p1, pp_8_1_p2, pp_8_1_p3, pp_8_1_p4, pp_8_1_p5, pp_8_1_p6, pp_8_1_p7;
  wire [31:0] bit_extender_1_out, bit_extender_2_out;

  pp_8 pp_8_1 (
    .Rm(in_1), .Rs(in_2), .p0(pp_8_1_p0), .p1(pp_8_1_p1), .p2(pp_8_1_p2), .p3(pp_8_1_p3), .p4(pp_8_1_p4),
    .p5(pp_8_1_p5), .p6(pp_8_1_p6), .p7(pp_8_1_p7));
  csa_16 csa_16_1 (.X(pp_8_1_p0), .Y(pp_8_1_p1), .Z(pp_8_1_p2), .sum(csa_16_1_sum), .carry(csa_16_1_carry));
  csa_16 csa_16_2 (.X(csa_16_1_sum), .Y(csa_16_1_carry), .Z(pp_8_1_p3), .sum(csa_16_2_sum), .carry(csa_16_2_carry));
  csa_16 csa_16_3 (.X(csa_16_2_sum), .Y(csa_16_2_carry), .Z(pp_8_1_p4), .sum(csa_16_3_sum), .carry(csa_16_3_carry));
  csa_16 csa_16_4 (.X(csa_16_3_sum), .Y(csa_16_3_carry), .Z(pp_8_1_p5), .sum(csa_16_4_sum), .carry(csa_16_4_carry));
  csa_16 csa_16_5 (.X(csa_16_4_sum), .Y(csa_16_4_carry), .Z(pp_8_1_p6), .sum(csa_16_5_sum), .carry(csa_16_5_carry));
  csa_16 csa_16_6 (.X(csa_16_5_sum), .Y(csa_16_5_carry), .Z(pp_8_1_p7), .sum(csa_16_6_sum), .carry(csa_16_6_carry));
  assign bit_extender_1_out = {{16{csa_16_6_sum[15]}}, csa_16_6_sum};  // Bit_Extender bit_extender_1
  assign bit_extender_2_out = {{16{csa_16_6_carry[15]}}, csa_16_6_carry};  // Bit_Extender bit_extender_2
  ks_32b ks_32b_1 (
    .A(bit_extender_1_out), .B(bit_extender_2_out), .SUM31(out_3[31]), .SUM30(out_3[30]), .SUM29(out_3[29]),
    .SUM28(out_3[28]), .SUM27(out_3[27]), .SUM26(out_3[26]), .SUM25(out_3[25]), .SUM24(out_3[24]),
    .SUM23(out_3[23]), .SUM22(out_3[22]), .SUM21(out_3[21]), .SUM20(out_3[20]), .SUM19(out_3[19]),
    .SUM18(out_3[18]), .SUM17(out_3[17]), .SUM16(out_3[16]), .SUM15(out_3[15]), .SUM14(out_3[14]),
    .SUM13(out_3[13]), .SUM12(out_3[12]), .SUM11(out_3[11]), .SUM10(out_3[10]), .SUM9(out_3[9]),
    .SUM8(out_3[8]), .SUM7(out_3[7]), .SUM6(out_3[6]), .SUM5(out_3[5]), .SUM4(out_3[4]), .SUM3(out_3[3]),
    .SUM2(out_3[2]), .sum1(out_3[1]), .sum0(out_3[0]));  // open: Cin, Cout

  // Notes on the sheet:
  //   in_1: initial=0xff
  //   in_2: initial=0xff
endmodule

module bs_stage_1 (
  input  [31:0] input_32,
  input  enable,
  input  [1:0] typ_2,
  output [31:0] out_1
);

  wire [31:0] multiplexer_1_out, shifter_1_out, shifter_2_out, shifter_3_out, shifter_4_out;

  Shifter #(.width(32)) shifter_1 (.in(input_32), .\dist (5'b00001), .out(shifter_1_out));
  Shifter #(.shift("lr"), .width(32)) shifter_2 (.in(input_32), .\dist (5'b00001), .out(shifter_2_out));
  Shifter #(.shift("ar"), .width(32)) shifter_3 (.in(input_32), .\dist (5'b00001), .out(shifter_3_out));
  Shifter #(.shift("rr"), .width(32)) shifter_4 (.in(input_32), .\dist (5'b00001), .out(shifter_4_out));
  Multiplexer #(.select(2), .width(32)) multiplexer_1 (
    .in0(shifter_1_out), .in1(shifter_2_out), .in2(shifter_3_out), .in3(shifter_4_out),
    .out(multiplexer_1_out), .sel(typ_2));
  Multiplexer #(.width(32)) multiplexer_2 (.in0(input_32), .in1(multiplexer_1_out), .out(out_1), .sel(enable));

  // Notes on the sheet:
  //   input_32: initial=0x9e3779b8
endmodule

module bs_stage_2 (
  input  [31:0] input_32,
  input  enable,
  input  [1:0] typ_2,
  output [31:0] out_1
);

  wire [31:0] multiplexer_1_out, shifter_1_out, shifter_2_out, shifter_3_out, shifter_4_out;

  Shifter #(.width(32)) shifter_1 (.in(input_32), .\dist (5'b00010), .out(shifter_1_out));
  Shifter #(.shift("lr"), .width(32)) shifter_2 (.in(input_32), .\dist (5'b00010), .out(shifter_2_out));
  Shifter #(.shift("ar"), .width(32)) shifter_3 (.in(input_32), .\dist (5'b00010), .out(shifter_3_out));
  Shifter #(.shift("rr"), .width(32)) shifter_4 (.in(input_32), .\dist (5'b00010), .out(shifter_4_out));
  Multiplexer #(.select(2), .width(32)) multiplexer_1 (
    .in0(shifter_1_out), .in1(shifter_2_out), .in2(shifter_3_out), .in3(shifter_4_out),
    .out(multiplexer_1_out), .sel(typ_2));
  Multiplexer #(.width(32)) multiplexer_2 (.in0(input_32), .in1(multiplexer_1_out), .out(out_1), .sel(enable));

  // Notes on the sheet:
  //   input_32: initial=0x9e3779b8
endmodule

module bs_stage_4 (
  input  [31:0] input_32,
  input  enable,
  input  [1:0] typ_2,
  output [31:0] out_1
);

  wire [31:0] multiplexer_1_out, shifter_1_out, shifter_2_out, shifter_3_out, shifter_4_out;

  Shifter #(.width(32)) shifter_1 (.in(input_32), .\dist (5'b00100), .out(shifter_1_out));
  Shifter #(.shift("lr"), .width(32)) shifter_2 (.in(input_32), .\dist (5'b00100), .out(shifter_2_out));
  Shifter #(.shift("ar"), .width(32)) shifter_3 (.in(input_32), .\dist (5'b00100), .out(shifter_3_out));
  Shifter #(.shift("rr"), .width(32)) shifter_4 (.in(input_32), .\dist (5'b00100), .out(shifter_4_out));
  Multiplexer #(.select(2), .width(32)) multiplexer_1 (
    .in0(shifter_1_out), .in1(shifter_2_out), .in2(shifter_3_out), .in3(shifter_4_out),
    .out(multiplexer_1_out), .sel(typ_2));
  Multiplexer #(.width(32)) multiplexer_2 (.in0(input_32), .in1(multiplexer_1_out), .out(out_1), .sel(enable));

  // Notes on the sheet:
  //   input_32: initial=0x9e3779b8
endmodule

module bs_stage_8 (
  input  [31:0] input_32,
  input  enable,
  input  [1:0] typ_2,
  output [31:0] out_1
);

  wire [31:0] multiplexer_1_out, shifter_1_out, shifter_2_out, shifter_3_out, shifter_4_out;

  Shifter #(.width(32)) shifter_1 (.in(input_32), .\dist (5'b01000), .out(shifter_1_out));
  Shifter #(.shift("lr"), .width(32)) shifter_2 (.in(input_32), .\dist (5'b01000), .out(shifter_2_out));
  Shifter #(.shift("ar"), .width(32)) shifter_3 (.in(input_32), .\dist (5'b01000), .out(shifter_3_out));
  Shifter #(.shift("rr"), .width(32)) shifter_4 (.in(input_32), .\dist (5'b01000), .out(shifter_4_out));
  Multiplexer #(.select(2), .width(32)) multiplexer_1 (
    .in0(shifter_1_out), .in1(shifter_2_out), .in2(shifter_3_out), .in3(shifter_4_out),
    .out(multiplexer_1_out), .sel(typ_2));
  Multiplexer #(.width(32)) multiplexer_2 (.in0(input_32), .in1(multiplexer_1_out), .out(out_1), .sel(enable));

  // Notes on the sheet:
  //   input_32: initial=0x9e3779b8
endmodule

module bs_stage_16 (
  input  [31:0] input_32,
  input  enable,
  input  [1:0] typ_2,
  output [31:0] out_1
);

  wire [31:0] multiplexer_1_out, shifter_1_out, shifter_2_out, shifter_3_out, shifter_4_out;

  Shifter #(.width(32)) shifter_1 (.in(input_32), .\dist (5'b10000), .out(shifter_1_out));
  Shifter #(.shift("lr"), .width(32)) shifter_2 (.in(input_32), .\dist (5'b10000), .out(shifter_2_out));
  Shifter #(.shift("ar"), .width(32)) shifter_3 (.in(input_32), .\dist (5'b10000), .out(shifter_3_out));
  Shifter #(.shift("rr"), .width(32)) shifter_4 (.in(input_32), .\dist (5'b10000), .out(shifter_4_out));
  Multiplexer #(.select(2), .width(32)) multiplexer_1 (
    .in0(shifter_1_out), .in1(shifter_2_out), .in2(shifter_3_out), .in3(shifter_4_out),
    .out(multiplexer_1_out), .sel(typ_2));
  Multiplexer #(.width(32)) multiplexer_2 (.in0(input_32), .in1(multiplexer_1_out), .out(out_1), .sel(enable));

  // Notes on the sheet:
  //   input_32: initial=0x9e3779b8
endmodule

module barrel_32b (
  input  [31:0] input_32b,
  input  [4:0] amnt,
  input  [1:0] typ,
  output [31:0] outp
);

  wire [31:0] bs_stage_1_1_out_1, bs_stage_2_1_out_1, bs_stage_4_1_out_1, bs_stage_8_1_out_1;

  bs_stage_1 bs_stage_1_1 (.input_32(input_32b), .enable(amnt[0]), .typ_2(typ), .out_1(bs_stage_1_1_out_1));
  bs_stage_2 bs_stage_2_1 (.input_32(bs_stage_1_1_out_1), .enable(amnt[1]), .typ_2(typ), .out_1(bs_stage_2_1_out_1));
  bs_stage_4 bs_stage_4_1 (.input_32(bs_stage_2_1_out_1), .enable(amnt[2]), .typ_2(typ), .out_1(bs_stage_4_1_out_1));
  bs_stage_8 bs_stage_8_1 (.input_32(bs_stage_4_1_out_1), .enable(amnt[3]), .typ_2(typ), .out_1(bs_stage_8_1_out_1));
  bs_stage_16 bs_stage_16_1 (.input_32(bs_stage_8_1_out_1), .enable(amnt[4]), .typ_2(typ), .out_1(outp));

  // Notes on the sheet:
  //   input_32b: initial=0x9e3779b9
endmodule

module condition_checker (
  input  N,
  input  Z,
  input  C,
  input  [3:0] cond,
  input  V,
  output chk_out
);

  wire and_1_out, and_2_out, not_1_out, not_2_out, not_3_out, not_4_out, not_5_out, or_1_out, or_2_out,
       xor_1_out;

  not not_1 (not_1_out, N);
  not not_2 (not_2_out, Z);
  not not_3 (not_3_out, C);
  not not_4 (not_4_out, V);
  xor xor_1 (xor_1_out, N, V);
  and and_1 (and_1_out, C, not_2_out);
  or or_1 (or_1_out, not_3_out, Z);
  and and_2 (and_2_out, not_2_out, not_5_out);
  or or_2 (or_2_out, Z, xor_1_out);
  not not_5 (not_5_out, xor_1_out);
  Multiplexer #(.select(4)) multiplexer_1 (
    .in0(Z), .in1(not_2_out), .in2(C), .in3(not_3_out), .in4(N), .in5(not_1_out), .in6(V), .in7(not_4_out),
    .in8(and_1_out), .in9(or_1_out), .in10(not_5_out), .in11(xor_1_out), .in12(and_2_out), .in13(or_2_out),
    .in14(1'b1), .in15(1'b0), .out(chk_out), .sel(cond));
endmodule

module reg16x32_1 (
  input  CLK,
  input  [3:0] WA,
  input  [31:0] WD,
  input  WE,
  input  RST,
  input  [31:0] WD2,
  input  [3:0] RA,
  input  [3:0] RB,
  input  WE2,
  input  [3:0] WA2,
  output [31:0] R0_OUTPUT,
  output [31:0] R1_OUTPUT,
  output [31:0] R3_OUTPUT,
  output [31:0] R2_OUPUT,
  output [31:0] R5_OUTPUT,
  output [31:0] R4_OUTPUT,
  output [31:0] RD_A,
  output [31:0] R7_OUTPUT,
  output [31:0] R6_OUTPUT,
  output [31:0] RD_B,
  output [31:0] R8_OUTPUT,
  output [31:0] R9_OUTPUT,
  output [31:0] R11_OUTPUT,
  output [31:0] R10_OUTPUT,
  output [31:0] R13_OUTPUT,
  output [31:0] R12_OUTPUT,
  output [31:0] R15_OUTPUT,
  output [31:0] R14_OUTPUT
);

  wire and_1_out, and_2_out, and_3_out, and_4_out, and_5_out, and_6_out, and_7_out, and_8_out, and_9_out,
       and_10_out, and_11_out, and_12_out, and_13_out, and_14_out, and_15_out, and_16_out, decoder_1_out0,
       decoder_1_out1, decoder_1_out2, decoder_1_out3, decoder_1_out4, decoder_1_out5, decoder_1_out6,
       decoder_1_out7, decoder_1_out8, decoder_1_out9, decoder_1_out10, decoder_1_out11, decoder_1_out12,
       decoder_1_out13, decoder_1_out14, decoder_1_out15, decoder_2_out0, decoder_2_out1, decoder_2_out2,
       decoder_2_out3, decoder_2_out4, decoder_2_out5, decoder_2_out6, decoder_2_out7, decoder_2_out8,
       decoder_2_out9, decoder_2_out10, decoder_2_out11, decoder_2_out12, decoder_2_out13, decoder_2_out14,
       decoder_2_out15, or_1_out, or_2_out, or_3_out, or_4_out, or_5_out, or_6_out, or_7_out, or_8_out,
       or_9_out, or_10_out, or_11_out, or_12_out, or_13_out, or_14_out, or_15_out, or_16_out;
  wire [31:0] multiplexer_1_out, multiplexer_2_out, multiplexer_3_out, multiplexer_4_out, multiplexer_5_out,
       multiplexer_6_out, multiplexer_7_out, multiplexer_8_out, multiplexer_9_out, multiplexer_10_out,
       multiplexer_11_out, multiplexer_12_out, multiplexer_13_out, multiplexer_14_out, multiplexer_15_out,
       multiplexer_16_out;

  Decoder #(.select(4)) decoder_1 (
    .out0(decoder_1_out0), .out1(decoder_1_out1), .out2(decoder_1_out2), .out3(decoder_1_out3),
    .out4(decoder_1_out4), .out5(decoder_1_out5), .out6(decoder_1_out6), .out7(decoder_1_out7),
    .out8(decoder_1_out8), .out9(decoder_1_out9), .out10(decoder_1_out10), .out11(decoder_1_out11),
    .out12(decoder_1_out12), .out13(decoder_1_out13), .out14(decoder_1_out14), .out15(decoder_1_out15),
    .sel(WA), .en(WE));
  Decoder #(.select(4)) decoder_2 (
    .out0(decoder_2_out0), .out1(decoder_2_out1), .out2(decoder_2_out2), .out3(decoder_2_out3),
    .out4(decoder_2_out4), .out5(decoder_2_out5), .out6(decoder_2_out6), .out7(decoder_2_out7),
    .out8(decoder_2_out8), .out9(decoder_2_out9), .out10(decoder_2_out10), .out11(decoder_2_out11),
    .out12(decoder_2_out12), .out13(decoder_2_out13), .out14(decoder_2_out14), .out15(decoder_2_out15),
    .sel(WA2), .en(WE2));
  and and_1 (and_1_out, decoder_1_out0, WE);
  and and_2 (and_2_out, decoder_1_out1, WE);
  and and_3 (and_3_out, decoder_1_out2, WE);
  and and_4 (and_4_out, decoder_1_out3, WE);
  and and_5 (and_5_out, decoder_1_out4, WE);
  and and_6 (and_6_out, decoder_1_out5, WE);
  and and_7 (and_7_out, decoder_1_out6, WE);
  and and_8 (and_8_out, decoder_1_out7, WE);
  and and_9 (and_9_out, decoder_1_out8, WE);
  and and_10 (and_10_out, decoder_1_out9, WE);
  and and_11 (and_11_out, decoder_1_out10, WE);
  and and_12 (and_12_out, decoder_1_out11, WE);
  and and_13 (and_13_out, decoder_1_out12, WE);
  and and_14 (and_14_out, decoder_1_out13, WE);
  and and_15 (and_15_out, decoder_1_out14, WE);
  and and_16 (and_16_out, decoder_1_out15, WE);
  or or_1 (or_1_out, and_1_out, decoder_2_out0);
  or or_2 (or_2_out, and_2_out, decoder_2_out1);
  or or_3 (or_3_out, and_3_out, decoder_2_out2);
  or or_4 (or_4_out, and_4_out, decoder_2_out3);
  or or_5 (or_5_out, and_5_out, decoder_2_out4);
  or or_6 (or_6_out, and_6_out, decoder_2_out5);
  or or_7 (or_7_out, and_7_out, decoder_2_out6);
  or or_8 (or_8_out, and_8_out, decoder_2_out7);
  or or_9 (or_9_out, and_13_out, decoder_2_out12);
  or or_10 (or_10_out, and_14_out, decoder_2_out13);
  or or_11 (or_11_out, and_15_out, decoder_2_out14);
  or or_12 (or_12_out, and_16_out, decoder_2_out15);
  or or_13 (or_13_out, and_9_out, decoder_2_out8);
  or or_14 (or_14_out, and_10_out, decoder_2_out9);
  or or_15 (or_15_out, and_11_out, decoder_2_out10);
  or or_16 (or_16_out, and_12_out, decoder_2_out11);
  Multiplexer #(.width(32)) multiplexer_1 (.in0(WD), .in1(WD2), .out(multiplexer_1_out), .sel(decoder_2_out12));
  Multiplexer #(.width(32)) multiplexer_2 (.in0(WD), .in1(WD2), .out(multiplexer_2_out), .sel(decoder_2_out14));
  Multiplexer #(.width(32)) multiplexer_3 (.in0(WD), .in1(WD2), .out(multiplexer_3_out), .sel(decoder_2_out0));
  Multiplexer #(.width(32)) multiplexer_4 (.in0(WD), .in1(WD2), .out(multiplexer_4_out), .sel(decoder_2_out2));
  Multiplexer #(.width(32)) multiplexer_5 (.in0(WD), .in1(WD2), .out(multiplexer_5_out), .sel(decoder_2_out4));
  Multiplexer #(.width(32)) multiplexer_6 (.in0(WD), .in1(WD2), .out(multiplexer_6_out), .sel(decoder_2_out6));
  Multiplexer #(.width(32)) multiplexer_7 (.in0(WD), .in1(WD2), .out(multiplexer_7_out), .sel(decoder_2_out8));
  Multiplexer #(.width(32)) multiplexer_8 (.in0(WD), .in1(WD2), .out(multiplexer_8_out), .sel(decoder_2_out10));
  Register #(.width(32)) R0 (.D(multiplexer_3_out), .en(or_1_out), .clk(CLK), .Q(R0_OUTPUT), .clr(RST));
  Register #(.width(32)) R2 (.D(multiplexer_4_out), .en(or_3_out), .clk(CLK), .Q(R2_OUPUT), .clr(RST));
  Register #(.width(32)) R4 (.D(multiplexer_5_out), .en(or_5_out), .clk(CLK), .Q(R4_OUTPUT), .clr(RST));
  Register #(.width(32)) R6 (.D(multiplexer_6_out), .en(or_7_out), .clk(CLK), .Q(R6_OUTPUT), .clr(RST));
  Register #(.width(32)) R8 (.D(multiplexer_7_out), .en(or_13_out), .clk(CLK), .Q(R8_OUTPUT), .clr(RST));
  Register #(.width(32)) R10 (.D(multiplexer_8_out), .en(or_15_out), .clk(CLK), .Q(R10_OUTPUT), .clr(RST));
  Register #(.width(32)) R12 (.D(multiplexer_1_out), .en(or_9_out), .clk(CLK), .Q(R12_OUTPUT), .clr(RST));
  Register #(.width(32)) R14 (.D(multiplexer_2_out), .en(or_11_out), .clk(CLK), .Q(R14_OUTPUT), .clr(RST));
  Multiplexer #(.width(32)) multiplexer_9 (.in0(WD), .in1(WD2), .out(multiplexer_9_out), .sel(decoder_2_out1));
  Multiplexer #(.width(32)) multiplexer_10 (.in0(WD), .in1(WD2), .out(multiplexer_10_out), .sel(decoder_2_out5));
  Multiplexer #(.width(32)) multiplexer_11 (.in0(WD), .in1(WD2), .out(multiplexer_11_out), .sel(decoder_2_out7));
  Multiplexer #(.width(32)) multiplexer_12 (.in0(WD), .in1(WD2), .out(multiplexer_12_out), .sel(decoder_2_out9));
  Multiplexer #(.width(32)) multiplexer_13 (.in0(WD), .in1(WD2), .out(multiplexer_13_out), .sel(decoder_2_out11));
  Multiplexer #(.width(32)) multiplexer_14 (.in0(WD), .in1(WD2), .out(multiplexer_14_out), .sel(decoder_2_out13));
  Multiplexer #(.width(32)) multiplexer_15 (.in0(WD), .in1(WD2), .out(multiplexer_15_out), .sel(decoder_2_out15));
  Multiplexer #(.width(32)) multiplexer_16 (.in0(WD), .in1(WD2), .out(multiplexer_16_out), .sel(decoder_2_out3));
  Register #(.width(32)) R1 (.D(multiplexer_9_out), .en(or_2_out), .clk(CLK), .Q(R1_OUTPUT), .clr(RST));
  Register #(.width(32)) R3 (.D(multiplexer_16_out), .en(or_4_out), .clk(CLK), .Q(R3_OUTPUT), .clr(RST));
  Register #(.width(32)) R5 (.D(multiplexer_10_out), .en(or_6_out), .clk(CLK), .Q(R5_OUTPUT), .clr(RST));
  Register #(.width(32)) R7 (.D(multiplexer_11_out), .en(or_8_out), .clk(CLK), .Q(R7_OUTPUT), .clr(RST));
  Register #(.width(32)) R9 (.D(multiplexer_12_out), .en(or_14_out), .clk(CLK), .Q(R9_OUTPUT), .clr(RST));
  Register #(.width(32)) R11 (.D(multiplexer_13_out), .en(or_16_out), .clk(CLK), .Q(R11_OUTPUT), .clr(RST));
  Register #(.width(32)) R13 (.D(multiplexer_14_out), .en(or_10_out), .clk(CLK), .Q(R13_OUTPUT), .clr(RST));
  Register #(.width(32)) R15 (.D(multiplexer_15_out), .en(or_12_out), .clk(CLK), .Q(R15_OUTPUT), .clr(RST));
  Multiplexer #(.select(4), .width(32)) multiplexer_17 (
    .in0(R0_OUTPUT), .in1(R1_OUTPUT), .in2(R2_OUPUT), .in3(R3_OUTPUT), .in4(R4_OUTPUT), .in5(R5_OUTPUT),
    .in6(R6_OUTPUT), .in7(R7_OUTPUT), .in8(R8_OUTPUT), .in9(R9_OUTPUT), .in10(R10_OUTPUT), .in11(R11_OUTPUT),
    .in12(R12_OUTPUT), .in13(R13_OUTPUT), .in14(R14_OUTPUT), .in15(R15_OUTPUT), .out(RD_A), .sel(RA));
  Multiplexer #(.select(4), .width(32)) multiplexer_18 (
    .in0(R0_OUTPUT), .in1(R1_OUTPUT), .in2(R2_OUPUT), .in3(R3_OUTPUT), .in4(R4_OUTPUT), .in5(R5_OUTPUT),
    .in6(R6_OUTPUT), .in7(R7_OUTPUT), .in8(R8_OUTPUT), .in9(R9_OUTPUT), .in10(R10_OUTPUT), .in11(R11_OUTPUT),
    .in12(R12_OUTPUT), .in13(R13_OUTPUT), .in14(R14_OUTPUT), .in15(R15_OUTPUT), .out(RD_B), .sel(RB));
endmodule

module block_transfer_control (
  input  clk,
  input  rst,
  input  start,
  input  is_pop,
  input  [15:0] reg_list_in,
  input  [31:0] base_value,
  input  U,
  input  P,
  output hold_pc,
  output active,
  output done,
  output [3:0] reg_idx,
  output reg_selected,
  output [31:0] transfer_address,
  output [31:0] final_address,
  output store_enable,
  output load_enable,
  output phase_reg_q
);

  wire and_1_out, and_2_out, and_3_out, and_4_out, and_6_out, and_7_out, and_8_out, and_10_out, and_11_out,
       and_13_out, and_14_out, comparator_1_eq, comparator_2_eq, idx_adv_out, multiplexer_2_out, not_1_out,
       not_2_out, not_3_out, not_4_out, not_5_out, not_6_out, or_1_out, or_2_out, or_3_out, or_4_out,
       or_6_out, reg_sel_and_toi_out, termin_or_idx_adv_out;
  wire [3:0] adder_1_out, adder_2_out, multiplexer_4_out, multiplexer_5_out, multiplexer_6_out,
       multiplexer_9_out;
  wire [15:0] register_1_q;
  wire [31:0] adder_3_out, adder_4_out, multiplexer_1_out, multiplexer_3_out, multiplexer_8_out;

  not not_1 (not_1_out, P);
  or or_1 (or_1_out, reg_selected, start);
  Register #(.width(16)) register_1 (.D(reg_list_in), .en(and_10_out), .clk(clk), .Q(register_1_q), .clr(rst));
  Multiplexer #(.width(32)) multiplexer_1 (
    .in0(final_address), .in1(multiplexer_8_out), .out(multiplexer_1_out), .sel(reg_sel_and_toi_out));
  Register #(.width(1)) ACTIVE_REG (.D(or_6_out), .en(1'b1), .clk(clk), .Q(active), .clr(rst));
  Register #(.width(1)) DONE_REG (.D(and_4_out), .en(1'b1), .clk(clk), .Q(done), .clr(rst));
  Register #(.width(4)) REG_INDEX (.D(multiplexer_9_out), .en(1'b1), .clk(clk), .Q(reg_idx), .clr(rst));
  Register #(.width(1)) PHASE_REG (.D(and_13_out), .clk(clk), .Q(phase_reg_q));  // open: en, clr
  Multiplexer #(.select(4)) multiplexer_2 (
    .in0(register_1_q[0]), .in1(register_1_q[1]), .in2(register_1_q[2]), .in3(register_1_q[3]),
    .in4(register_1_q[4]), .in5(register_1_q[5]), .in6(register_1_q[6]), .in7(register_1_q[7]),
    .in8(register_1_q[8]), .in9(register_1_q[9]), .in10(register_1_q[10]), .in11(register_1_q[11]),
    .in12(register_1_q[12]), .in13(register_1_q[13]), .in14(register_1_q[14]), .in15(register_1_q[15]),
    .out(multiplexer_2_out), .sel(reg_idx));
  Multiplexer #(.width(32)) multiplexer_3 (
    .in0(multiplexer_1_out), .in1(base_value), .out(multiplexer_3_out), .sel(and_10_out));
  and and_1 (and_1_out, and_11_out, or_3_out);
  Adder #(.width(4)) adder_1 (.a(reg_idx), .b(4'b0001), .out(adder_1_out));  // open: cin, cout
  Adder #(.width(4)) adder_2 (.a(reg_idx), .b(4'b1111), .out(adder_2_out));  // open: cin, cout
  // Probe on multiplexer_3_out
  not not_2 (not_2_out, phase_reg_q);
  not not_3 (not_3_out, and_1_out);
  and and_2 (and_2_out, active, and_11_out);
  Multiplexer #(.width(4)) multiplexer_4 (.in0(4'b1111), .in1(4'b0000), .out(multiplexer_4_out), .sel(U));
  // Probe on multiplexer_2_out
  or or_2 (or_2_out, active, done);
  and and_3 (and_3_out, active, not_3_out);
  and and_4 (and_4_out, and_2_out, or_3_out);
  // Probe on adder_1_out
  Multiplexer #(.width(4)) multiplexer_5 (.in0(adder_2_out), .in1(adder_1_out), .out(multiplexer_5_out), .sel(U));
  // Probe on adder_2_out
  Comparator #(.width(4)) comparator_1 (.a(reg_idx), .b(4'b1111), .eq(comparator_1_eq));  // open: gt, lt
  Comparator #(.width(4)) comparator_2 (.a(reg_idx), .b(4'b0000), .eq(comparator_2_eq));  // open: gt, lt
  Register #(.width(32)) address_reg (.D(multiplexer_3_out), .en(or_1_out), .clk(clk), .Q(final_address), .clr(rst));
  // Probe on or_2_out
  not not_4 (not_4_out, is_pop);
  // Probe on and_4_out
  Multiplexer #(.width(4)) multiplexer_6 (
    .in0(reg_idx), .in1(multiplexer_5_out), .out(multiplexer_6_out), .sel(idx_adv_out));
  and and_5 (store_enable, reg_selected, not_4_out);
  and and_6 (and_6_out, reg_selected, is_pop);
  or or_3 (or_3_out, not_4_out, phase_reg_q);
  not not_5 (not_5_out, or_2_out);
  // Probe on multiplexer_5_out
  // Probe on comparator_1_eq
  // Probe on comparator_2_eq
  not not_6 (not_6_out, U);
  Adder #(.width(32)) adder_3 (.a(final_address), .b(32'hfffffffc), .out(adder_3_out), .cin(1'b0));  // open: cout
  Adder #(.width(32)) adder_4 (.a(final_address), .b(32'h4), .out(adder_4_out), .cin(1'b0));  // open: cout
  and and_7 (and_7_out, comparator_1_eq, U);
  and and_8 (and_8_out, comparator_2_eq, not_6_out);
  Multiplexer #(.width(32)) multiplexer_7 (
    .in0(multiplexer_8_out), .in1(final_address), .out(transfer_address), .sel(not_1_out));
  and and_9 (load_enable, and_6_out, phase_reg_q);
  and and_10 (and_10_out, not_5_out, start);
  // Probe on not_5_out
  // Probe on and_3_out
  // Probe on multiplexer_6_out
  // Probe on adder_3_out
  // Probe on adder_4_out
  or or_4 (or_4_out, and_7_out, and_8_out);
  Multiplexer #(.width(32)) multiplexer_8 (.in0(adder_3_out), .in1(adder_4_out), .out(multiplexer_8_out), .sel(U));
  and idx_adv (idx_adv_out, and_3_out, or_3_out);
  Multiplexer #(.width(4)) multiplexer_9 (
    .in0(multiplexer_6_out), .in1(multiplexer_4_out), .out(multiplexer_9_out), .sel(and_10_out));
  and and_11 (and_11_out, active, or_4_out);
  and and_12 (reg_selected, active, multiplexer_2_out);
  // Probe on multiplexer_8_out
  and and_13 (and_13_out, active, not_2_out);
  or or_5 (hold_pc, active, and_10_out);
  or or_6 (or_6_out, and_10_out, and_3_out);
  // Probe on and_10_out
  // Probe on and_11_out
  and and_14 (and_14_out, and_11_out, phase_reg_q);
  or termin_or_idx_adv (termin_or_idx_adv_out, and_14_out, idx_adv_out);
  and reg_sel_and_toi (reg_sel_and_toi_out, reg_selected, termin_or_idx_adv_out);
endmodule

module ALU_arithmetic_engine (
  input  a_inversion,
  input  [31:0] A,
  input  [31:0] B,
  input  b_inversion,
  input  Cflag,
  input  unused,
  input  [1:0] Cin_sel,
  output [31:0] Result,
  output Cout
);

  wire multiplexer_1_out;
  wire [31:0] bit_extender_1_out, bit_extender_2_out, xor_1_out, xor_2_out;

  assign bit_extender_1_out = {{31{b_inversion}}, b_inversion};  // Bit_Extender bit_extender_1
  Multiplexer #(.select(2)) multiplexer_1 (
    .in0(1'b0), .in1(1'b1), .in2(Cflag), .in3(unused), .out(multiplexer_1_out), .sel(Cin_sel));
  assign bit_extender_2_out = {{31{a_inversion}}, a_inversion};  // Bit_Extender bit_extender_2
  assign xor_1_out = bit_extender_2_out ^ A;  // XOR_Gate xor_1, 32 bits wide
  assign xor_2_out = B ^ bit_extender_1_out;  // XOR_Gate xor_2, 32 bits wide
  Adder #(.width(32)) adder_1 (.a(xor_1_out), .b(xor_2_out), .out(Result), .cin(multiplexer_1_out), .cout(Cout));
endmodule
module main (
  input  rst,
  output halt
);

  wire ALU_WE, BL_TAKEN, BR_TAKEN, BT_ACTIVE, BT_DONE, CLK, CONDPASS, DATA_RAM_WE, HOLD_PC, IMM_BIT,
       IS_HWXFER, MEM_READ, reg_shift, S_BIT, SBWE, WB_WRITES_PC, WE, WE2;
  wire [1:0] SH_TYP;
  wire [2:0] CLASS;
  wire [3:0] BT_REG_IDX, COND, CPSR, OPCODE, RN, ROT, WA, WA2;
  wire [4:0] SH_AMT;
  wire [7:0] IMM8;
  wire [9:0] ALU_CTRL, PC_WORD;
  wire [15:0] I15_0;
  wire [23:0] BR_IMM24, I27_4;
  wire [31:0] ALU_RES, BR_OFF, BX_TGT, INSTR, LOAD_DATA, MEM_UP_BASE, PC_PLUS4, RD_A, RD_B, rm_val, rs_value,
       WD, WD2;

  Clock u_clk (.out(CLK));
  stage_IF stage_if_1 (
    .clk(CLK), .hold_pc(HOLD_PC), .branch_offset(BR_OFF), .rst(rst), .wb_writes_pc(WB_WRITES_PC),
    .bx_target(BX_TGT), .wb_data(WD), .branch_taken(BR_TAKEN), .bx_taken(halt), .bt_done(BT_DONE),
    .pc_plus4(PC_PLUS4), .pc_word_addr(PC_WORD), .instruction(INSTR));
  stage_ID stage_id_1 (
    .instruction(INSTR), .clk(CLK), .wd(WD), .we(WE), .rst(rst), .wd2(WD2), .we2(WE2),
    .pc_word_addr(PC_WORD), .wa2(WA2), .bt_reg_idx(BT_REG_IDX), .bl_taken(BL_TAKEN), .sbwe(SBWE),
    .bt_active(BT_ACTIVE), .data_ram_we(DATA_RAM_WE), .instr_15_0(I15_0), .branch_imm24(BR_IMM24),
    .instr_27_4(I27_4), .imm8(IMM8), .rs(ROT), .imm_bit(IMM_BIT), .reg_shift(reg_shift), .shift_type(SH_TYP),
    .rn(RN), .shift_amount(SH_AMT), .s_bit(S_BIT), .rd_a(RD_A), .opcode(OPCODE), .class_bits(CLASS), .wa(WA),
    .cond(COND), .rd_b(RD_B), .alu_ctrl(ALU_CTRL), .rs_value(rs_value), .rm_val(rm_val), .IS_HWXFER(IS_HWXFER));  // open: rm, rd, pc_plus8, is_long_mul, is_mult, mul_acc_value
  stage_EX stage_ex_1 (
    .clk(CLK), .rst(rst), .rd_a(RD_A), .rd_b(RD_B), .alu_ctrl(ALU_CTRL), .cond(COND), .class_bits(CLASS),
    .opcode(OPCODE), .imm_bit(IMM_BIT), .imm8(IMM8), .shift_amount(SH_AMT), .rot(ROT),
    .branch_imm24(BR_IMM24), .shift_type(SH_TYP), .s_bit(S_BIT), .instr_27_4(I27_4), .reg_shift(reg_shift),
    .rs_value(rs_value), .alu_result(ALU_RES), .cpsr(CPSR), .alu_we(ALU_WE), .cond_pass(CONDPASS),
    .bl_taken(BL_TAKEN), .branch_taken(BR_TAKEN), .branch_offset(BR_OFF), .bx_target(BX_TGT), .bx_taken(halt));
  stage_MEM stage_mem_1 (
    .clk(CLK), .rst(rst), .rd_a(RD_A), .rd_b(RD_B), .class_bits(CLASS), .opcode(OPCODE), .s_bit(S_BIT),
    .rn(RN), .instr_15_0(I15_0), .cond_pass(CONDPASS), .rm_val(rm_val), .shift_amount(SH_AMT),
    .shift_type(SH_TYP), .is_hwxfer(IS_HWXFER), .wa2(WA2), .mem_read(MEM_READ), .wd2(WD2), .sbwe(SBWE),
    .we2(WE2), .data_ram_we(DATA_RAM_WE), .memory_up_base(MEM_UP_BASE), .hold_pc(HOLD_PC),
    .load_data(LOAD_DATA), .bt_active(BT_ACTIVE), .bt_done(BT_DONE), .bt_reg_idx(BT_REG_IDX));  // open: ldr_reg_we
  stage_WB stage_wb_1 (
    .alu_result(ALU_RES), .alu_we(ALU_WE), .cond_pass(CONDPASS), .bl_taken(BL_TAKEN),
    .branch_taken(BR_TAKEN), .bx_taken(halt), .pc_plus4(PC_PLUS4), .load_data(LOAD_DATA),
    .mem_read(MEM_READ), .memory_up_base(MEM_UP_BASE), .sbwe(SBWE), .data_ram_we(DATA_RAM_WE), .wa(WA),
    .bt_active(BT_ACTIVE), .class_bits(CLASS), .wd(WD), .we(WE), .wb_writes_pc(WB_WRITES_PC));

  // Other names for the same wires on the sheet: BX_TAKEN = halt
endmodule

module stage_IF (
  input  clk,
  input  hold_pc,
  input  [31:0] branch_offset,
  input  rst,
  input  wb_writes_pc,
  input  [31:0] bx_target,
  input  [31:0] wb_data,
  input  branch_taken,
  input  bx_taken,
  input  bt_done,
  output [31:0] pc_plus4,
  output [9:0] pc_word_addr,
  output [31:0] instruction
);

  wire abs_req_out, branch_req_out, not_bt_done_out, pc_apply_out, pc_defer_out, pc_pending_q,
       pending_next_out, redirect_req_out, still_pending_out;
  wire [31:0] multiplexer_1_out, multiplexer_2_out, pc_target_q;

  or redirect_req (redirect_req_out, branch_taken, bx_taken);
  not not_bt_done (not_bt_done_out, bt_done);
  and pc_apply (pc_apply_out, pc_pending_q, bt_done);
  and pc_defer (pc_defer_out, wb_writes_pc, hold_pc);
  or branch_req (branch_req_out, redirect_req_out, pc_apply_out, wb_writes_pc);
  or abs_req (abs_req_out, bx_taken, pc_apply_out, wb_writes_pc);
  pc_fetch pc_fetch_1 (
    .CLK(clk), .BRANCH(branch_req_out), .hold(hold_pc), .IMM(branch_offset), .abs_target(multiplexer_2_out),
    .abs_select(abs_req_out), .RST(rst), .pc_plus4(pc_plus4), .pc_out(pc_word_addr));
  Register #(.width(1)) pc_pending (
    .D(pending_next_out), .en(pending_next_out), .clk(clk), .Q(pc_pending_q), .clr(rst));
  Register #(.width(32)) pc_target (.D(multiplexer_1_out), .en(wb_writes_pc), .clk(clk), .Q(pc_target_q), .clr(rst));
  // Probe on multiplexer_1_out
  Multiplexer #(.width(32)) multiplexer_1 (.in0(bx_target), .in1(wb_data), .out(multiplexer_1_out), .sel(wb_writes_pc));
  and still_pending (still_pending_out, not_bt_done_out, pc_pending_q);
  Multiplexer #(.width(32)) multiplexer_2 (
    .in0(multiplexer_1_out), .in1(pc_target_q), .out(multiplexer_2_out), .sel(pc_apply_out));
  or pending_next (pending_next_out, pc_defer_out, still_pending_out);
  ROM #(.addrWidth(10), .dataWidth(32)) rom_1 (.addr(pc_word_addr), .data(instruction));
  // Probe on multiplexer_2_out
endmodule

module stage_ID (
  input  [31:0] instruction,
  input  clk,
  input  [31:0] wd,
  input  we,
  input  rst,
  input  [31:0] wd2,
  input  we2,
  input  [9:0] pc_word_addr,
  input  [3:0] wa2,
  input  [3:0] bt_reg_idx,
  input  bl_taken,
  input  sbwe,
  input  bt_active,
  input  data_ram_we,
  output [15:0] instr_15_0,
  output [23:0] branch_imm24,
  output [23:0] instr_27_4,
  output [7:0] imm8,
  output [3:0] rs,
  output imm_bit,
  output [3:0] rm,
  output reg_shift,
  output [3:0] rd,
  output [1:0] shift_type,
  output [3:0] rn,
  output [4:0] shift_amount,
  output s_bit,
  output [31:0] rd_a,
  output [3:0] opcode,
  output [2:0] class_bits,
  output [3:0] wa,
  output [31:0] pc_plus8,
  output [3:0] cond,
  output [31:0] rd_b,
  output [9:0] alu_ctrl,
  output [31:0] rs_value,
  output is_long_mul,
  output is_mult,
  output [31:0] mul_acc_value,
  output [31:0] rm_val,
  output IS_HWXFER
);

  wire and_1_out, comparator_1_eq, comparator_2_eq, comparator_3_eq, comparator_4_eq, comparator_5_eq,
       comparator_6_eq, comparator_7_eq, comparator_8_eq, mul_signature_out, not_1_out, not_2_out, not_3_out,
       not_4_out, or_1_out, or_2_out;
  wire [3:0] multiplexer_1_out, multiplexer_2_out, multiplexer_3_out, multiplexer_4_out, multiplexer_5_out;
  wire [31:0] bit_extender_1_out, r0, r1, r2, r3, r4, r5, r6, r7, r8, r9, r10, r11, r12, r13, r14, r15,
       reg16x32_1_1_rd_a, reg16x32_1_1_rd_b, shifter_1_out;

  // Probe on instruction
  // Probe on instruction
  // Probe on instruction
  // Probe on instruction[31:25]
  // Probe on instruction[11:4]
  not not_1 (not_1_out, instruction[20]);
  and and_1 (and_1_out, not_1_out, IS_HWXFER);
  or or_1 (or_1_out, and_1_out, data_ram_we);
  Comparator #(.width(4)) comparator_1 (.a(instruction[19:16]), .b(4'b1111), .eq(comparator_1_eq));  // open: gt, lt
  // Probe on {{12{1'b0}}, instruction[24:21]}
  Multiplexer #(.width(4)) multiplexer_1 (
    .in0(instruction[15:12]), .in1(4'b1110), .out(multiplexer_1_out), .sel(bl_taken));
  Multiplexer #(.width(4)) multiplexer_2 (
    .in0(instruction[3:0]), .in1(instruction[15:12]), .out(multiplexer_2_out), .sel(or_1_out));
  ROM #(.addrWidth(16), .dataWidth(10)) rom_1 (.addr({{12{1'b0}}, instruction[24:21]}), .data(alu_ctrl));
  // Probe on instruction[7:4]
  // Probe on instruction[27:24]
  // Probe on multiplexer_2_out
  not not_2 (not_2_out, instruction[25]);
  // Probe on multiplexer_1_out
  Multiplexer #(.width(4)) multiplexer_3 (
    .in0(multiplexer_2_out), .in1(bt_reg_idx), .out(multiplexer_3_out), .sel(bt_active));
  // Probe on comparator_1_eq
  and and_2 (reg_shift, instruction[4], not_2_out);
  Multiplexer #(.width(4)) multiplexer_4 (
    .in0(multiplexer_1_out), .in1(instruction[19:16]), .out(multiplexer_4_out), .sel(sbwe));
  // Probe on multiplexer_4_out
  Comparator #(.width(4)) comparator_2 (.a(instruction[7:4]), .b(4'b1111), .eq(comparator_2_eq));  // open: gt, lt
  Comparator #(.width(4)) comparator_3 (.a(instruction[7:4]), .b(4'b1101), .eq(comparator_3_eq));  // open: gt, lt
  Comparator #(.width(4)) comparator_4 (.a(instruction[7:4]), .b(4'b1011), .eq(comparator_4_eq));  // open: gt, lt
  Comparator #(.width(4)) comparator_5 (.a(instruction[7:4]), .b(4'b1001), .eq(comparator_5_eq));  // open: gt, lt
  Comparator #(.width(4)) comparator_6 (.a(instruction[27:24]), .b(4'b0000), .eq(comparator_6_eq));  // open: gt, lt
  Comparator #(.width(4)) comparator_7 (.a(multiplexer_3_out), .b(4'b1111), .eq(comparator_7_eq));  // open: gt, lt
  or or_2 (or_2_out, comparator_2_eq, comparator_3_eq, comparator_4_eq);
  Comparator #(.width(3)) comparator_8 (.a(instruction[27:25]), .b(3'b000), .eq(comparator_8_eq));  // open: gt, lt
  Multiplexer #(.width(4)) multiplexer_5 (
    .in0(multiplexer_4_out), .in1(bt_reg_idx), .out(multiplexer_5_out), .sel(bt_active));
  Multiplexer #(.width(4)) multiplexer_6 (.in0(multiplexer_5_out), .in1(instruction[19:16]), .out(wa), .sel(is_mult));
  // Probe on comparator_7_eq
  and and_3 (IS_HWXFER, or_2_out, comparator_8_eq);
  and mul_signature (mul_signature_out, comparator_5_eq, comparator_6_eq);
  // Probe on IS_HWXFER
  not not_3 (not_3_out, instruction[22]);
  not not_4 (not_4_out, instruction[23]);
  and is_mul (is_mult, mul_signature_out, not_3_out, not_4_out);
  reg16x32_1 reg16x32_1_1 (
    .CLK(clk), .WA(wa), .WD(wd), .WE(we), .RST(rst), .WD2(wd2), .RA(instruction[19:16]),
    .RB(multiplexer_3_out), .WE2(we2), .WA2(wa2), .R0_OUTPUT(r0), .R1_OUTPUT(r1), .R3_OUTPUT(r3),
    .R2_OUPUT(r2), .R5_OUTPUT(r5), .R4_OUTPUT(r4), .RD_A(reg16x32_1_1_rd_a), .R7_OUTPUT(r7), .R6_OUTPUT(r6),
    .RD_B(reg16x32_1_1_rd_b), .R8_OUTPUT(r8), .R9_OUTPUT(r9), .R11_OUTPUT(r11), .R10_OUTPUT(r10),
    .R13_OUTPUT(r13), .R12_OUTPUT(r12), .R15_OUTPUT(r15), .R14_OUTPUT(r14));
  and is_mla (is_long_mul, instruction[21], is_mult);
  assign bit_extender_1_out = {{22{1'b0}}, pc_word_addr};  // Bit_Extender bit_extender_1
  Shifter #(.width(32)) shifter_1 (.in(bit_extender_1_out), .\dist (5'b00010), .out(shifter_1_out));
  // Probe on shifter_1_out
  Adder #(.width(32)) adder_1 (.a(shifter_1_out), .b(32'h8), .out(pc_plus8), .cin(1'b0));  // open: cout
  Multiplexer #(.width(32)) multiplexer_7 (.in0(reg16x32_1_1_rd_a), .in1(pc_plus8), .out(rd_a), .sel(comparator_1_eq));
  // Probe on rd_a
  // Probe on rd_b
  Multiplexer #(.width(32)) multiplexer_8 (.in0(reg16x32_1_1_rd_b), .in1(pc_plus8), .out(rd_b), .sel(comparator_7_eq));
  reg_read_mux_16x32 reg_read_mux_16x32_1 (
    .r0(r0), .r1(r1), .r2(r2), .r3(r3), .r4(r4), .r5(r5), .r6(r6), .r7(r7), .r8(r8), .r9(r9), .r10(r10),
    .r11(r11), .r12(r12), .r13(r13), .r14(r14), .r15(r15), .sel(instruction[11:8]), .value(rs_value));
  reg_read_mux_16x32 reg_read_mux_16x32_2 (
    .r0(r0), .r1(r1), .r2(r2), .r3(r3), .r4(r4), .r5(r5), .r6(r6), .r7(r7), .r8(r8), .r9(r9), .r10(r10),
    .r11(r11), .r12(r12), .r13(r13), .r14(r14), .r15(r15), .sel(instruction[15:12]), .value(mul_acc_value));
  reg_read_mux_16x32 reg_read_mux_16x32_3 (
    .r0(r0), .r1(r1), .r2(r2), .r3(r3), .r4(r4), .r5(r5), .r6(r6), .r7(r7), .r8(r8), .r9(r9), .r10(r10),
    .r11(r11), .r12(r12), .r13(r13), .r14(r14), .r15(r15), .sel(instruction[3:0]), .value(rm_val));

  assign branch_imm24 = instruction[23:0];
  assign class_bits = instruction[27:25];
  assign cond = instruction[31:28];
  assign imm8 = instruction[7:0];
  assign imm_bit = instruction[25];
  assign instr_15_0 = instruction[15:0];
  assign instr_27_4 = instruction[27:4];
  assign opcode = instruction[24:21];
  assign rd = instruction[15:12];
  assign rm = instruction[3:0];
  assign rn = instruction[19:16];
  assign rs = instruction[11:8];
  assign s_bit = instruction[20];
  assign shift_amount = instruction[11:7];
  assign shift_type = instruction[6:5];

  // Other names for the same wires on the sheet: sel[3:0] = instruction[11:8]; IS_HW = IS_HWXFER;
  //   IS_MLA = is_long_mul; IS_MUL = is_mult; mav[31:0] = mul_acc_value; rm_value[31:0] = rm_val

  // Notes on the sheet:
  //   contents of rom_1 (hex, n*v repeats v):
  //   1 3 151 191 101 121 161 1a1 0 2 150 100 5 7 9 b 201
endmodule

module stage_EX (
  input  clk,
  input  rst,
  input  [31:0] rd_a,
  input  [31:0] rd_b,
  input  [9:0] alu_ctrl,
  input  [3:0] cond,
  input  [2:0] class_bits,
  input  [3:0] opcode,
  input  imm_bit,
  input  [7:0] imm8,
  input  [4:0] shift_amount,
  input  [3:0] rot,
  input  [23:0] branch_imm24,
  input  [1:0] shift_type,
  input  s_bit,
  input  [23:0] instr_27_4,
  input  reg_shift,
  input  [31:0] rs_value,
  output [31:0] alu_result,
  output [3:0] cpsr,
  output alu_we,
  output cond_pass,
  output bl_taken,
  output branch_taken,
  output [31:0] branch_offset,
  output [31:0] bx_target,
  output bx_taken
);

  wire alu_1_c, alu_1_v, and_1_out, AND_BRCLASS_out, AND_CPSRW_out, AND_ISBL_out, AND_MEMCLASS_out,
       comparator_1_eq, not_1_out, not_2_out, not_3_out, NOT_THUMB_out, OR_NOFLAG2_out, OR_NOFLAG_out,
       rs_ge_32_out;
  wire [1:0] multiplexer_4_out;
  wire [3:0] multiplexer_7_out;
  wire [4:0] multiplexer_1_out, multiplexer_3_out;
  wire [31:0] barrel_32b_1_outp, bit_extender_1_out, bit_extender_2_out, bit_extender_3_out,
       multiplexer_2_out, multiplexer_5_out, multiplexer_6_out, shifter_1_out;

  // Probe on AND_BRCLASS_out
  // Probe on rd_b
  // Probe on class_bits
  // Probe on opcode
  or rs_ge_32 (rs_ge_32_out, rs_value[5], rs_value[6], rs_value[7]);
  not NOT_THUMB (NOT_THUMB_out, rd_b[0]);
  // Probe on alu_ctrl
  // Probe on rs_ge_32_out
  Multiplexer #(.width(5)) multiplexer_1 (
    .in0(shift_amount), .in1(rs_value[4:0]), .out(multiplexer_1_out), .sel(reg_shift));
  assign bit_extender_1_out = {{8{branch_imm24[23]}}, branch_imm24};  // Bit_Extender bit_extender_1
  Multiplexer #(.select(2), .width(32)) multiplexer_2 (
    .in0({32{1'b0}}), .in1({32{1'b0}}), .in2(bit_extender_3_out), .in3(barrel_32b_1_outp),
    .out(multiplexer_2_out), .sel(shift_type));
  Comparator #(.width(24)) comparator_1 (.a(instr_27_4), .b(24'h12fff1), .eq(comparator_1_eq));  // open: gt, lt
  not not_1 (not_1_out, class_bits[1]);
  not not_2 (not_2_out, class_bits[2]);
  // Probe on multiplexer_2_out
  // Probe on comparator_1_eq
  assign bit_extender_2_out = {{24{1'b0}}, imm8};  // Bit_Extender bit_extender_2
  Shifter #(.width(32)) shifter_1 (.in(bit_extender_1_out), .\dist (5'b00010), .out(shifter_1_out));
  and AND_BRCLASS (AND_BRCLASS_out, class_bits[0], not_1_out, class_bits[2]);
  and AND_MEMCLASS (AND_MEMCLASS_out, class_bits[1], not_2_out);
  Adder #(.width(32)) adder_1 (.a(shifter_1_out), .b(32'h8), .out(branch_offset), .cin(1'b0));  // open: cout
  assign bx_target = rd_b & 32'hfffffffc;  // AND_Gate AND_ALIGN, 32 bits wide
  or OR_NOFLAG (OR_NOFLAG_out, comparator_1_eq, AND_BRCLASS_out);
  and AND_BXTAKEN (bx_taken, comparator_1_eq, NOT_THUMB_out, cond_pass);
  // Probe on alu_ctrl[3:1]
  // Probe on alu_ctrl[5:4]
  // Probe on alu_ctrl[9:8]
  // Probe on bit_extender_2_out
  Multiplexer #(.width(5)) multiplexer_3 (
    .in0(multiplexer_1_out), .in1({rot, 1'b0}), .out(multiplexer_3_out), .sel(imm_bit));
  Multiplexer #(.width(2)) multiplexer_4 (.in0(shift_type), .in1(2'b11), .out(multiplexer_4_out), .sel(imm_bit));
  or OR_NOFLAG2 (OR_NOFLAG2_out, OR_NOFLAG_out, AND_MEMCLASS_out);
  and AND_ISBL (AND_ISBL_out, AND_BRCLASS_out, opcode[3]);
  Multiplexer #(.width(32)) multiplexer_5 (
    .in0(rd_b), .in1(bit_extender_2_out), .out(multiplexer_5_out), .sel(imm_bit));
  // Probe on multiplexer_5_out
  // Probe on multiplexer_3_out
  // Probe on multiplexer_4_out
  not not_3 (not_3_out, OR_NOFLAG2_out);
  assign bit_extender_3_out = {{31{multiplexer_5_out[31]}}, multiplexer_5_out[31]};  // Bit_Extender bit_extender_3
  // Probe on not_3_out
  and AND_BTAKEN (branch_taken, cond_pass, AND_BRCLASS_out);
  and AND_BLTAKEN (bl_taken, cond_pass, AND_ISBL_out);
  // Probe on bit_extender_3_out
  and and_1 (and_1_out, rs_ge_32_out, reg_shift);
  and AND_CPSRW (AND_CPSRW_out, cond_pass, not_3_out, s_bit);
  Multiplexer #(.width(32)) multiplexer_6 (
    .in0(barrel_32b_1_outp), .in1(multiplexer_2_out), .out(multiplexer_6_out), .sel(and_1_out));
  barrel_32b barrel_32b_1 (
    .input_32b(multiplexer_5_out), .amnt(multiplexer_3_out), .typ(multiplexer_4_out), .outp(barrel_32b_1_outp));
  // Probe on and_1_out
  ALU alu_1 (
    .logic_sel(alu_ctrl[3:1]), .a_inv(alu_ctrl[7]), .A(rd_a), .B(multiplexer_6_out), .b_inv(alu_ctrl[6]),
    .Cflag(cpsr[1]), .unused(1'b0), .cin_sel(alu_ctrl[5:4]), .engine_sel(alu_ctrl[9:8]),
    .write_enable(alu_ctrl[0]), .result(alu_result), .C(alu_1_c), .Z(multiplexer_7_out[2]),
    .N(multiplexer_7_out[3]), .V(alu_1_v), .write_enable_out(alu_we));
  // Probe on multiplexer_7_out
  Register #(.width(4)) CPSR_reg (.D(multiplexer_7_out), .en(AND_CPSRW_out), .clk(clk), .Q(cpsr), .clr(rst));
  // Probe on cpsr
  Multiplexer #(.select(2)) multiplexer_7 (
    .in0(cpsr[0]), .in1(alu_1_v), .in2(cpsr[0]), .in3(cpsr[0]), .out(multiplexer_7_out[0]),
    .sel(alu_ctrl[9:8]));
  Multiplexer #(.select(2)) multiplexer_8 (
    .in0(cpsr[1]), .in1(alu_1_c), .in2(cpsr[1]), .in3(cpsr[1]), .out(multiplexer_7_out[1]),
    .sel(alu_ctrl[9:8]));
  condition_checker condition_checker_1 (
    .N(cpsr[3]), .Z(cpsr[2]), .C(cpsr[1]), .cond(cond), .V(cpsr[0]), .chk_out(cond_pass));
endmodule

module stage_MEM (
  input  clk,
  input  rst,
  input  [31:0] rd_a,
  input  [31:0] rd_b,
  input  [2:0] class_bits,
  input  [3:0] opcode,
  input  s_bit,
  input  [3:0] rn,
  input  [15:0] instr_15_0,
  input  cond_pass,
  input  [31:0] rm_val,
  input  [4:0] shift_amount,
  input  [1:0] shift_type,
  input  is_hwxfer,
  output [3:0] wa2,
  output mem_read,
  output [31:0] wd2,
  output sbwe,
  output we2,
  output ldr_reg_we,
  output data_ram_we,
  output [31:0] memory_up_base,
  output hold_pc,
  output [31:0] load_data,
  output bt_active,
  output bt_done,
  output [3:0] bt_reg_idx
);

  wire and_1_out, and_2_out, and_3_out, and_4_out, and_5_out, and_9_out, and_10_out, base_writeback_en_out,
       block_transfer_control_1_load_enable, block_transfer_control_1_store_enable, BYTE_ACESS_out,
       combined_out, comparator_1_eq, HW_LOAD_out, m_class, not_1_out, not_2_out, not_3_out, not_4_out,
       not_5_out, not_6_out, not_7_out, not_8_out, OR_START_out, RAM_WE_out, wb_requested_out;
  wire [3:0] multiplexer_10_out, multiplexer_11_out;
  wire [3:1] low_enable_out;
  wire [7:0] multiplexer_12_out;
  wire [15:0] multiplexer_7_out, multiplexer_8_out, multiplexer_13_out;
  wire [31:0] barrel_32b_1_outp, bit_extender_1_out, bit_extender_2_out, bit_extender_3_out,
       bit_extender_4_out, bit_extender_5_out, bit_extender_6_out, bit_extender_7_out,
       block_transfer_control_1_final_address, block_transfer_control_1_transfer_address, DATA_RAM_dout,
       multiplexer_1_out, multiplexer_2_out, multiplexer_3_out, multiplexer_4_out, multiplexer_5_out,
       multiplexer_9_out, multiplexer_14_out, multiplexer_15_out, multiplexer_16_out, multiplexer_17_out,
       PRGM_ROM_data, xor_1_out;

  not not_1 (not_1_out, class_bits[2]);
  // Probe on opcode[0]
  // Probe on opcode[1]
  // Probe on opcode[2]
  // Probe on opcode[3]
  and mem_class (m_class, class_bits[1], not_1_out);
  barrel_32b barrel_32b_1 (.input_32b(rm_val), .amnt(shift_amount), .typ(shift_type), .outp(barrel_32b_1_outp));
  and HW_LOAD (HW_LOAD_out, s_bit, is_hwxfer);
  assign bit_extender_1_out = {{31{not_2_out}}, not_2_out};  // Bit_Extender bit_extender_1
  not not_2 (not_2_out, opcode[2]);
  // Probe on bit_extender_2_out
  assign bit_extender_2_out = {{20{1'b0}}, instr_15_0[11:0]};  // Bit_Extender bit_extender_2
  Comparator #(.width(3)) comparator_1 (.a(class_bits), .b(3'b100), .eq(comparator_1_eq));  // open: gt, lt
  not not_3 (not_3_out, opcode[3]);
  Multiplexer #(.width(32)) multiplexer_1 (
    .in0(bit_extender_2_out), .in1(barrel_32b_1_outp), .out(multiplexer_1_out), .sel(class_bits[0]));
  not not_4 (not_4_out, s_bit);
  and and_1 (and_1_out, comparator_1_eq, cond_pass);
  // Probe on and_2_out
  and and_2 (and_2_out, m_class, s_bit);
  // Probe on and_3_out
  and and_3 (and_3_out, m_class, not_4_out);
  or wb_requested (wb_requested_out, opcode[0], not_3_out);
  assign xor_1_out = multiplexer_3_out ^ bit_extender_1_out;  // XOR_Gate xor_1, 32 bits wide
  // Probe on and_1_out
  or combined (combined_out, and_2_out, HW_LOAD_out);
  and and_4 (and_4_out, and_1_out, s_bit);
  and and_5 (and_5_out, and_1_out, not_5_out);
  not not_5 (not_5_out, s_bit);
  assign bit_extender_3_out = {{24{1'b0}}, {instr_15_0[11:8], instr_15_0[3:0]}};  // Bit_Extender bit_extender_3
  // Probe on and_4_out
  // Probe on and_5_out
  or OR_START (OR_START_out, and_4_out, and_5_out);
  Multiplexer #(.width(32)) multiplexer_2 (
    .in0(rm_val), .in1(bit_extender_3_out), .out(multiplexer_2_out), .sel(opcode[1]));
  Multiplexer #(.width(32)) multiplexer_3 (
    .in0(multiplexer_1_out), .in1(multiplexer_2_out), .out(multiplexer_3_out), .sel(is_hwxfer));
  Adder #(.width(32)) adder_1 (.a(rd_a), .b(xor_1_out), .out(memory_up_base), .cin(not_2_out));  // open: cout
  Multiplexer #(.width(32)) multiplexer_4 (.in0(rd_a), .in1(memory_up_base), .out(multiplexer_4_out), .sel(opcode[3]));
  block_transfer_control block_transfer_control_1 (
    .clk(clk), .rst(rst), .start(OR_START_out), .is_pop(and_4_out), .reg_list_in(instr_15_0),
    .base_value(rd_a), .U(opcode[2]), .P(opcode[3]), .hold_pc(hold_pc), .active(bt_active), .done(bt_done),
    .reg_idx(bt_reg_idx), .transfer_address(block_transfer_control_1_transfer_address),
    .final_address(block_transfer_control_1_final_address),
    .store_enable(block_transfer_control_1_store_enable), .load_enable(block_transfer_control_1_load_enable));  // open: reg_selected, phase_reg_q
  // Probe on multiplexer_4_out
  // Probe on multiplexer_5_out
  Multiplexer #(.width(32)) multiplexer_5 (
    .in0(multiplexer_4_out), .in1(block_transfer_control_1_transfer_address), .out(multiplexer_5_out),
    .sel(bt_active));
  // Probe on multiplexer_5_out
  and and_6 (sbwe, cond_pass, and_3_out, wb_requested_out);
  and and_7 (ldr_reg_we, cond_pass, combined_out);
  and and_8 (data_ram_we, and_3_out, cond_pass);
  and and_9 (and_9_out, cond_pass, and_2_out, wb_requested_out);
  // Probe on and_9_out
  and base_writeback_en (base_writeback_en_out, opcode[0], bt_done);
  // Probe on multiplexer_5_out[9:2]
  not not_6 (not_6_out, multiplexer_5_out[12]);
  // Probe on not_6_out
  or or_1 (mem_read, combined_out, block_transfer_control_1_load_enable);
  or RAM_WE (RAM_WE_out, data_ram_we, and_10_out, block_transfer_control_1_store_enable);
  Multiplexer #(.width(32)) multiplexer_6 (
    .in0(memory_up_base), .in1(block_transfer_control_1_final_address), .out(wd2), .sel(bt_done));
  or or_2 (we2, and_9_out, base_writeback_en_out);
  and and_10 (and_10_out, not_4_out, is_hwxfer);
  not not_7 (not_7_out, and_10_out);
  or high_enable (low_enable_out[3], multiplexer_5_out[1], not_7_out);
  or low_enable (low_enable_out[1], not_7_out, not_8_out);
  not not_8 (not_8_out, multiplexer_5_out[1]);
  // Probe on multiplexer_7_out
  // Probe on multiplexer_8_out
  Multiplexer #(.width(16)) multiplexer_7 (
    .in0(DATA_RAM_dout[31:16]), .in1(rd_b[15:0]), .out(multiplexer_7_out), .sel(multiplexer_5_out[1]));
  Multiplexer #(.width(16)) multiplexer_8 (
    .in0(rd_b[15:0]), .in1(DATA_RAM_dout[15:0]), .out(multiplexer_8_out), .sel(multiplexer_5_out[1]));
  Multiplexer #(.width(32)) multiplexer_9 (
    .in0(rd_b), .in1({multiplexer_7_out, multiplexer_8_out}), .out(multiplexer_9_out), .sel(is_hwxfer));
  RAM #(.byteenables("byteEnables"), .dataWidth(32), .trigger("falling")) DATA_RAM (
    .addr(multiplexer_5_out[9:2]), .we(RAM_WE_out), .oe(1'b1), .clk(clk), .din(multiplexer_15_out),
    .dout(DATA_RAM_dout), .be3(multiplexer_11_out[3]), .be2(multiplexer_11_out[2]),
    .be1(multiplexer_11_out[1]), .be0(multiplexer_11_out[0]));
  ROM #(.addrWidth(10), .dataWidth(32)) PRGM_ROM (.addr(multiplexer_5_out[11:2]), .data(PRGM_ROM_data));
  Multiplexer #(.select(2), .width(4)) multiplexer_10 (
    .in0(4'b0001), .in1(4'b0010), .in2(4'b0100), .in3(4'b1000), .out(multiplexer_10_out),
    .sel(multiplexer_5_out[1:0]));
  Multiplexer #(.width(4)) multiplexer_11 (
    .in0({{2{low_enable_out[3]}}, {2{low_enable_out[1]}}}), .in1(multiplexer_10_out),
    .out(multiplexer_11_out), .sel(BYTE_ACESS_out));
  Multiplexer #(.select(2), .width(8)) multiplexer_12 (
    .in0(multiplexer_16_out[7:0]), .in1(multiplexer_16_out[15:8]), .in2(multiplexer_16_out[23:16]),
    .in3(multiplexer_16_out[31:24]), .out(multiplexer_12_out), .sel(multiplexer_5_out[1:0]));
  Multiplexer #(.width(16)) multiplexer_13 (
    .in0(DATA_RAM_dout[15:0]), .in1(DATA_RAM_dout[31:16]), .out(multiplexer_13_out),
    .sel(multiplexer_5_out[1]));
  and BYTE_ACESS (BYTE_ACESS_out, m_class, opcode[1]);
  assign bit_extender_4_out = {{16{1'b0}}, multiplexer_13_out};  // Bit_Extender bit_extender_4
  assign bit_extender_5_out = {{16{multiplexer_13_out[15]}}, multiplexer_13_out};  // Bit_Extender bit_extender_5
  // Probe on {rd_b[7:0], rd_b[7:0], rd_b[7:0], rd_b[7:0]}
  assign bit_extender_6_out = {{24{multiplexer_12_out[7]}}, multiplexer_12_out};  // Bit_Extender bit_extender_6
  Multiplexer #(.select(2), .width(32)) multiplexer_14 (
    .in0({32{1'b1}}), .in1(bit_extender_4_out), .in2(bit_extender_6_out), .in3(bit_extender_5_out),
    .out(multiplexer_14_out), .sel(shift_type));
  assign bit_extender_7_out = {{24{1'b0}}, multiplexer_12_out};  // Bit_Extender bit_extender_7
  Multiplexer #(.width(32)) multiplexer_15 (
    .in0(multiplexer_9_out), .in1({rd_b[7:0], rd_b[7:0], rd_b[7:0], rd_b[7:0]}), .out(multiplexer_15_out),
    .sel(BYTE_ACESS_out));
  // Probe on multiplexer_16_out
  Multiplexer #(.width(32)) multiplexer_16 (
    .in0(DATA_RAM_dout), .in1(PRGM_ROM_data), .out(multiplexer_16_out), .sel(not_6_out));
  Multiplexer #(.width(32)) multiplexer_17 (
    .in0(multiplexer_16_out), .in1(bit_extender_7_out), .out(multiplexer_17_out), .sel(BYTE_ACESS_out));
  Multiplexer #(.width(32)) multiplexer_18 (
    .in0(multiplexer_17_out), .in1(multiplexer_14_out), .out(load_data), .sel(is_hwxfer));

  assign wa2 = rn;

  // Other names for the same wires on the sheet: b_t = opcode[1]; s_b = s_bit
endmodule

module stage_WB (
  input  [31:0] alu_result,
  input  alu_we,
  input  cond_pass,
  input  bl_taken,
  input  branch_taken,
  input  bx_taken,
  input  [31:0] pc_plus4,
  input  [31:0] load_data,
  input  mem_read,
  input  [31:0] memory_up_base,
  input  sbwe,
  input  data_ram_we,
  input  [3:0] wa,
  input  bt_active,
  input  [2:0] class_bits,
  output [31:0] wd,
  output we,
  output wb_writes_pc
);

  wire and_1_out, and_2_out, comparator_1_eq, comparator_2_eq, not_1_out, or_1_out;
  wire [31:0] multiplexer_1_out, multiplexer_2_out;

  Multiplexer #(.width(32)) multiplexer_1 (.in0(alu_result), .in1(pc_plus4), .out(multiplexer_1_out), .sel(bl_taken));
  // Probe on multiplexer_1_out
  Comparator #(.width(3)) comparator_1 (.a(class_bits), .b(3'b100), .eq(comparator_1_eq));  // open: gt, lt
  Multiplexer #(.width(32)) multiplexer_2 (
    .in0(multiplexer_1_out), .in1(load_data), .out(multiplexer_2_out), .sel(mem_read));
  // Probe on multiplexer_2_out
  Multiplexer #(.width(32)) multiplexer_3 (.in0(multiplexer_2_out), .in1(memory_up_base), .out(wd), .sel(sbwe));
  // Probe on wd
  // Probe on or_1_out
  or or_1 (or_1_out, mem_read, data_ram_we, bl_taken, comparator_1_eq, branch_taken, bx_taken, bt_active);
  not not_1 (not_1_out, or_1_out);
  and and_1 (and_1_out, alu_we, cond_pass, not_1_out);
  and and_2 (and_2_out, cond_pass, mem_read);
  Comparator #(.width(4)) comparator_2 (.a(wa), .b(4'b1111), .eq(comparator_2_eq));  // open: gt, lt
  // Probe on and_1_out
  // Probe on and_2_out
  or or_2 (we, sbwe, bl_taken, and_2_out, and_1_out);
  and and_3 (wb_writes_pc, we, comparator_2_eq);
endmodule

module reg_read_mux_16x32 (
  input  [31:0] r0,
  input  [31:0] r1,
  input  [31:0] r2,
  input  [31:0] r3,
  input  [31:0] r4,
  input  [31:0] r5,
  input  [31:0] r6,
  input  [31:0] r7,
  input  [31:0] r8,
  input  [31:0] r9,
  input  [31:0] r10,
  input  [31:0] r11,
  input  [31:0] r12,
  input  [31:0] r13,
  input  [31:0] r14,
  input  [31:0] r15,
  input  [3:0] sel,
  output [31:0] value
);

  Multiplexer #(.select(4), .width(32)) multiplexer_1 (
    .in0(r0), .in1(r1), .in2(r2), .in3(r3), .in4(r4), .in5(r5), .in6(r6), .in7(r7), .in8(r8), .in9(r9),
    .in10(r10), .in11(r11), .in12(r12), .in13(r13), .in14(r14), .in15(r15), .out(value), .sel(sel));
endmodule

module systolic_8x8 (
  input  clk,
  input  [31:0] w00,
  input  [31:0] w04,
  input  [31:0] w01,
  input  [31:0] w05,
  input  [31:0] w02,
  input  [31:0] w06,
  input  [31:0] w03,
  input  [31:0] w07,
  input  wload,
  input  [31:0] r0,
  input  [31:0] w10,
  input  [31:0] w14,
  input  [31:0] w11,
  input  [31:0] w15,
  input  [31:0] w12,
  input  [31:0] w16,
  input  [31:0] w13,
  input  [31:0] w17,
  input  [31:0] r1,
  input  [31:0] w20,
  input  [31:0] w24,
  input  [31:0] w21,
  input  [31:0] w25,
  input  [31:0] w22,
  input  [31:0] w26,
  input  [31:0] w23,
  input  [31:0] w27,
  input  [31:0] r2,
  input  [31:0] w30,
  input  [31:0] w34,
  input  [31:0] w31,
  input  [31:0] w35,
  input  [31:0] w32,
  input  [31:0] w36,
  input  [31:0] w33,
  input  [31:0] w37,
  input  [31:0] r3,
  input  [31:0] w40,
  input  [31:0] w44,
  input  [31:0] w41,
  input  [31:0] w45,
  input  [31:0] w42,
  input  [31:0] w46,
  input  [31:0] w43,
  input  [31:0] w47,
  input  [31:0] r4,
  input  [31:0] w50,
  input  [31:0] w54,
  input  [31:0] w51,
  input  [31:0] w55,
  input  [31:0] w52,
  input  [31:0] w56,
  input  [31:0] w53,
  input  [31:0] w57,
  input  [31:0] r5,
  input  [31:0] w60,
  input  [31:0] w64,
  input  [31:0] w61,
  input  [31:0] w65,
  input  [31:0] w62,
  input  [31:0] w66,
  input  [31:0] w63,
  input  [31:0] w67,
  input  [31:0] r6,
  input  [31:0] w70,
  input  [31:0] w74,
  input  [31:0] w71,
  input  [31:0] w75,
  input  [31:0] w72,
  input  [31:0] w76,
  input  [31:0] w73,
  input  [31:0] w77,
  input  [31:0] r7,
  output [31:0] a0,
  output [31:0] a1,
  output [31:0] a2,
  output [31:0] a3,
  output [31:0] a4,
  output [31:0] a5,
  output [31:0] a6,
  output [31:0] c0,
  output [31:0] c4,
  output [31:0] c1,
  output [31:0] c5,
  output [31:0] c2,
  output [31:0] c6,
  output [31:0] c3,
  output [31:0] c7,
  output [31:0] a7
);

  wire [31:0] systolic_00_a_out0, systolic_00_a_out1, systolic_00_a_out2, systolic_00_a_out3,
       systolic_00_c_col0, systolic_00_c_col1, systolic_00_c_col2, systolic_00_c_col3, systolic_01_c_col0,
       systolic_01_c_col1, systolic_01_c_col2, systolic_01_c_col3, systolic_10_a_out0, systolic_10_a_out1,
       systolic_10_a_out2, systolic_10_a_out3;

  systolic_4x4 systolic_00 (
    .CLK(clk), .w00(w00), .w01(w01), .w02(w02), .w03(w03), .w_load(wload), .p_sum00({32{1'b0}}),
    .p_sum01({32{1'b0}}), .p_sum02({32{1'b0}}), .p_sum03({32{1'b0}}), .row0(r0), .w10(w10), .w11(w11),
    .w12(w12), .w13(w13), .row1(r1), .w20(w20), .w21(w21), .w22(w22), .w23(w23), .row2(r2), .w30(w30),
    .w31(w31), .w32(w32), .w33(w33), .row3(r3), .a_out0(systolic_00_a_out0), .a_out1(systolic_00_a_out1),
    .a_out2(systolic_00_a_out2), .c_col0(systolic_00_c_col0), .c_col1(systolic_00_c_col1),
    .c_col2(systolic_00_c_col2), .c_col3(systolic_00_c_col3), .a_out3(systolic_00_a_out3));
  systolic_4x4 systolic_10 (
    .CLK(clk), .w00(w40), .w01(w41), .w02(w42), .w03(w43), .w_load(wload), .p_sum00(systolic_00_c_col0),
    .p_sum01(systolic_00_c_col1), .p_sum02(systolic_00_c_col2), .p_sum03(systolic_00_c_col3), .row0(r4),
    .w10(w50), .w11(w51), .w12(w52), .w13(w53), .row1(r5), .w20(w60), .w21(w61), .w22(w62), .w23(w63),
    .row2(r6), .w30(w70), .w31(w71), .w32(w72), .w33(w73), .row3(r7), .a_out0(systolic_10_a_out0),
    .a_out1(systolic_10_a_out1), .a_out2(systolic_10_a_out2), .c_col0(c0), .c_col1(c1), .c_col2(c2),
    .c_col3(c3), .a_out3(systolic_10_a_out3));
  systolic_4x4 systolic_01 (
    .CLK(clk), .w00(w04), .w01(w05), .w02(w06), .w03(w07), .w_load(wload), .p_sum00({32{1'b0}}),
    .p_sum01({32{1'b0}}), .p_sum02({32{1'b0}}), .p_sum03({32{1'b0}}), .row0(systolic_00_a_out0), .w10(w14),
    .w11(w15), .w12(w16), .w13(w17), .row1(systolic_00_a_out1), .w20(w24), .w21(w25), .w22(w26), .w23(w27),
    .row2(systolic_00_a_out2), .w30(w34), .w31(w35), .w32(w36), .w33(w37), .row3(systolic_00_a_out3),
    .a_out0(a0), .a_out1(a1), .a_out2(a2), .c_col0(systolic_01_c_col0), .c_col1(systolic_01_c_col1),
    .c_col2(systolic_01_c_col2), .c_col3(systolic_01_c_col3), .a_out3(a3));
  systolic_4x4 systolic_11 (
    .CLK(clk), .w00(w44), .w01(w45), .w02(w46), .w03(w47), .w_load(wload), .p_sum00(systolic_01_c_col0),
    .p_sum01(systolic_01_c_col1), .p_sum02(systolic_01_c_col2), .p_sum03(systolic_01_c_col3),
    .row0(systolic_10_a_out0), .w10(w54), .w11(w55), .w12(w56), .w13(w57), .row1(systolic_10_a_out1),
    .w20(w64), .w21(w65), .w22(w66), .w23(w67), .row2(systolic_10_a_out2), .w30(w74), .w31(w75), .w32(w76),
    .w33(w77), .row3(systolic_10_a_out3), .a_out0(a4), .a_out1(a5), .a_out2(a6), .c_col0(c4), .c_col1(c5),
    .c_col2(c6), .c_col3(c7), .a_out3(a7));
endmodule

module PE_cell_8 (
  input  [7:0] w_in,
  input  w_load,
  input  CLK,
  input  [31:0] psum_in,
  input  [7:0] a_in,
  output [31:0] psum_out,
  output [7:0] a_out
);

  wire [7:0] W_reg_q;
  wire [15:0] bit_extender_1_out, bit_extender_2_out, multiplier_1_out;
  wire [31:0] adder_1_out, bit_extender_3_out;

  Register W_reg (.D(w_in), .en(w_load), .clk(CLK), .Q(W_reg_q));  // open: clr
  assign bit_extender_1_out = {{8{a_in[7]}}, a_in};  // Bit_Extender bit_extender_1
  assign bit_extender_2_out = {{8{W_reg_q[7]}}, W_reg_q};  // Bit_Extender bit_extender_2
  Register a_reg (.D(a_in), .clk(CLK), .Q(a_out));  // open: en, clr
  Multiplier #(.width(16)) multiplier_1 (
    .a(bit_extender_1_out), .b(bit_extender_2_out), .out(multiplier_1_out));  // open: cin, cout
  assign bit_extender_3_out = {{16{multiplier_1_out[15]}}, multiplier_1_out};  // Bit_Extender bit_extender_3
  Register #(.width(32)) psum_reg (.D(adder_1_out), .clk(CLK), .Q(psum_out));  // open: en, clr
  Adder #(.width(32)) adder_1 (.a(psum_in), .b(bit_extender_3_out), .out(adder_1_out));  // open: cin, cout
endmodule

module systolic_4x4_int8 (
  input  CLK,
  input  [7:0] w00,
  input  [7:0] w01,
  input  [7:0] w02,
  input  [7:0] w03,
  input  w_load,
  input  [31:0] p_sum00,
  input  [31:0] p_sum01,
  input  [31:0] p_sum02,
  input  [31:0] p_sum03,
  input  [7:0] row0,
  input  [7:0] w10,
  input  [7:0] w11,
  input  [7:0] w12,
  input  [7:0] w13,
  input  [7:0] row1,
  input  [7:0] w20,
  input  [7:0] w21,
  input  [7:0] w22,
  input  [7:0] w23,
  input  [7:0] row2,
  input  [7:0] w30,
  input  [7:0] w31,
  input  [7:0] w32,
  input  [7:0] w33,
  input  [7:0] row3,
  output [7:0] a_out0,
  output [7:0] a_out1,
  output [7:0] a_out2,
  output [31:0] c_col0,
  output [31:0] c_col1,
  output [31:0] c_col2,
  output [31:0] c_col3,
  output [7:0] a_out3
);

  wire [7:0] pe_cell_8_1_a_out, pe_cell_8_2_a_out, pe_cell_8_3_a_out, pe_cell_8_4_a_out, pe_cell_8_5_a_out,
       pe_cell_8_6_a_out, pe_cell_8_7_a_out, pe_cell_8_8_a_out, pe_cell_8_9_a_out, pe_cell_8_10_a_out,
       pe_cell_8_11_a_out, pe_cell_8_12_a_out;
  wire [31:0] pe_cell_8_1_psum_out, pe_cell_8_2_psum_out, pe_cell_8_3_psum_out, pe_cell_8_5_psum_out,
       pe_cell_8_6_psum_out, pe_cell_8_7_psum_out, pe_cell_8_9_psum_out, pe_cell_8_10_psum_out,
       pe_cell_8_11_psum_out, pe_cell_8_13_psum_out, pe_cell_8_14_psum_out, pe_cell_8_15_psum_out;

  PE_cell_8 pe_cell_8_1 (
    .w_in(w00), .w_load(w_load), .CLK(CLK), .psum_in(p_sum00), .a_in(row0), .psum_out(pe_cell_8_1_psum_out),
    .a_out(pe_cell_8_1_a_out));
  PE_cell_8 pe_cell_8_2 (
    .w_in(w10), .w_load(w_load), .CLK(CLK), .psum_in(pe_cell_8_1_psum_out), .a_in(row1),
    .psum_out(pe_cell_8_2_psum_out), .a_out(pe_cell_8_2_a_out));
  PE_cell_8 pe_cell_8_3 (
    .w_in(w20), .w_load(w_load), .CLK(CLK), .psum_in(pe_cell_8_2_psum_out), .a_in(row2),
    .psum_out(pe_cell_8_3_psum_out), .a_out(pe_cell_8_3_a_out));
  PE_cell_8 pe_cell_8_4 (
    .w_in(w30), .w_load(w_load), .CLK(CLK), .psum_in(pe_cell_8_3_psum_out), .a_in(row3), .psum_out(c_col0),
    .a_out(pe_cell_8_4_a_out));
  // Probe on pe_cell_8_1_psum_out
  // Probe on pe_cell_8_2_psum_out
  // Probe on pe_cell_8_3_psum_out
  PE_cell_8 pe_cell_8_5 (
    .w_in(w01), .w_load(w_load), .CLK(CLK), .psum_in(p_sum01), .a_in(pe_cell_8_1_a_out),
    .psum_out(pe_cell_8_5_psum_out), .a_out(pe_cell_8_5_a_out));
  PE_cell_8 pe_cell_8_6 (
    .w_in(w11), .w_load(w_load), .CLK(CLK), .psum_in(pe_cell_8_5_psum_out), .a_in(pe_cell_8_2_a_out),
    .psum_out(pe_cell_8_6_psum_out), .a_out(pe_cell_8_6_a_out));
  PE_cell_8 pe_cell_8_7 (
    .w_in(w21), .w_load(w_load), .CLK(CLK), .psum_in(pe_cell_8_6_psum_out), .a_in(pe_cell_8_3_a_out),
    .psum_out(pe_cell_8_7_psum_out), .a_out(pe_cell_8_7_a_out));
  PE_cell_8 pe_cell_8_8 (
    .w_in(w31), .w_load(w_load), .CLK(CLK), .psum_in(pe_cell_8_7_psum_out), .a_in(pe_cell_8_4_a_out),
    .psum_out(c_col1), .a_out(pe_cell_8_8_a_out));
  // Probe on pe_cell_8_5_psum_out
  // Probe on pe_cell_8_6_psum_out
  // Probe on pe_cell_8_7_psum_out
  PE_cell_8 pe_cell_8_9 (
    .w_in(w02), .w_load(w_load), .CLK(CLK), .psum_in(p_sum02), .a_in(pe_cell_8_5_a_out),
    .psum_out(pe_cell_8_9_psum_out), .a_out(pe_cell_8_9_a_out));
  PE_cell_8 pe_cell_8_10 (
    .w_in(w12), .w_load(w_load), .CLK(CLK), .psum_in(pe_cell_8_9_psum_out), .a_in(pe_cell_8_6_a_out),
    .psum_out(pe_cell_8_10_psum_out), .a_out(pe_cell_8_10_a_out));
  PE_cell_8 pe_cell_8_11 (
    .w_in(w22), .w_load(w_load), .CLK(CLK), .psum_in(pe_cell_8_10_psum_out), .a_in(pe_cell_8_7_a_out),
    .psum_out(pe_cell_8_11_psum_out), .a_out(pe_cell_8_11_a_out));
  PE_cell_8 pe_cell_8_12 (
    .w_in(w32), .w_load(w_load), .CLK(CLK), .psum_in(pe_cell_8_11_psum_out), .a_in(pe_cell_8_8_a_out),
    .psum_out(c_col2), .a_out(pe_cell_8_12_a_out));
  // Probe on pe_cell_8_9_psum_out
  // Probe on pe_cell_8_10_psum_out
  // Probe on pe_cell_8_11_psum_out
  PE_cell_8 pe_cell_8_13 (
    .w_in(w03), .w_load(w_load), .CLK(CLK), .psum_in(p_sum03), .a_in(pe_cell_8_9_a_out),
    .psum_out(pe_cell_8_13_psum_out), .a_out(a_out0));
  PE_cell_8 pe_cell_8_14 (
    .w_in(w13), .w_load(w_load), .CLK(CLK), .psum_in(pe_cell_8_13_psum_out), .a_in(pe_cell_8_10_a_out),
    .psum_out(pe_cell_8_14_psum_out), .a_out(a_out1));
  PE_cell_8 pe_cell_8_15 (
    .w_in(w23), .w_load(w_load), .CLK(CLK), .psum_in(pe_cell_8_14_psum_out), .a_in(pe_cell_8_11_a_out),
    .psum_out(pe_cell_8_15_psum_out), .a_out(a_out2));
  PE_cell_8 pe_cell_8_16 (
    .w_in(w33), .w_load(w_load), .CLK(CLK), .psum_in(pe_cell_8_15_psum_out), .a_in(pe_cell_8_12_a_out),
    .psum_out(c_col3), .a_out(a_out3));
  // Probe on pe_cell_8_13_psum_out
  // Probe on pe_cell_8_14_psum_out
  // Probe on pe_cell_8_15_psum_out
endmodule

module systolic_8x8_int8 (
  input  clk,
  input  [7:0] w00,
  input  [7:0] w04,
  input  [7:0] w01,
  input  [7:0] w05,
  input  [7:0] w02,
  input  [7:0] w06,
  input  [7:0] w03,
  input  [7:0] w07,
  input  wload,
  input  [31:0] p_sum00,
  input  [31:0] p_sum04,
  input  [31:0] p_sum01,
  input  [31:0] p_sum05,
  input  [31:0] p_sum02,
  input  [31:0] p_sum06,
  input  [31:0] p_sum03,
  input  [31:0] p_sum07,
  input  [7:0] r0,
  input  [7:0] w10,
  input  [7:0] w14,
  input  [7:0] w11,
  input  [7:0] w15,
  input  [7:0] w12,
  input  [7:0] w16,
  input  [7:0] w13,
  input  [7:0] w17,
  input  [7:0] r1,
  input  [7:0] w20,
  input  [7:0] w24,
  input  [7:0] w21,
  input  [7:0] w25,
  input  [7:0] w22,
  input  [7:0] w26,
  input  [7:0] w23,
  input  [7:0] w27,
  input  [7:0] r2,
  input  [7:0] w30,
  input  [7:0] w34,
  input  [7:0] w31,
  input  [7:0] w35,
  input  [7:0] w32,
  input  [7:0] w36,
  input  [7:0] w33,
  input  [7:0] w37,
  input  [7:0] r3,
  input  [7:0] w40,
  input  [7:0] w44,
  input  [7:0] w41,
  input  [7:0] w45,
  input  [7:0] w42,
  input  [7:0] w46,
  input  [7:0] w43,
  input  [7:0] w47,
  input  [7:0] r4,
  input  [7:0] w50,
  input  [7:0] w54,
  input  [7:0] w51,
  input  [7:0] w55,
  input  [7:0] w52,
  input  [7:0] w56,
  input  [7:0] w53,
  input  [7:0] w57,
  input  [7:0] r5,
  input  [7:0] w60,
  input  [7:0] w64,
  input  [7:0] w61,
  input  [7:0] w65,
  input  [7:0] w62,
  input  [7:0] w66,
  input  [7:0] w63,
  input  [7:0] w67,
  input  [7:0] r6,
  input  [7:0] w70,
  input  [7:0] w74,
  input  [7:0] w71,
  input  [7:0] w75,
  input  [7:0] w72,
  input  [7:0] w76,
  input  [7:0] w73,
  input  [7:0] w77,
  input  [7:0] r7,
  output [7:0] a0,
  output [7:0] a1,
  output [7:0] a2,
  output [7:0] a3,
  output [7:0] a4,
  output [7:0] a5,
  output [7:0] a6,
  output [31:0] c0,
  output [31:0] c4,
  output [31:0] c1,
  output [31:0] c5,
  output [31:0] c2,
  output [31:0] c6,
  output [31:0] c3,
  output [31:0] c7,
  output [7:0] a7
);

  wire [7:0] systolic_4x4_int8_1_a_out0, systolic_4x4_int8_1_a_out1, systolic_4x4_int8_1_a_out2,
       systolic_4x4_int8_1_a_out3, systolic_4x4_int8_2_a_out0, systolic_4x4_int8_2_a_out1,
       systolic_4x4_int8_2_a_out2, systolic_4x4_int8_2_a_out3;
  wire [31:0] systolic_4x4_int8_1_c_col0, systolic_4x4_int8_1_c_col1, systolic_4x4_int8_1_c_col2,
       systolic_4x4_int8_1_c_col3, systolic_4x4_int8_3_c_col0, systolic_4x4_int8_3_c_col1,
       systolic_4x4_int8_3_c_col2, systolic_4x4_int8_3_c_col3;

  systolic_4x4_int8 systolic_4x4_int8_1 (
    .CLK(clk), .w00(w00), .w01(w01), .w02(w02), .w03(w03), .w_load(wload), .p_sum00(p_sum00),
    .p_sum01(p_sum01), .p_sum02(p_sum02), .p_sum03(p_sum03), .row0(r0), .w10(w10), .w11(w11), .w12(w12),
    .w13(w13), .row1(r1), .w20(w20), .w21(w21), .w22(w22), .w23(w23), .row2(r2), .w30(w30), .w31(w31),
    .w32(w32), .w33(w33), .row3(r3), .a_out0(systolic_4x4_int8_1_a_out0),
    .a_out1(systolic_4x4_int8_1_a_out1), .a_out2(systolic_4x4_int8_1_a_out2),
    .c_col0(systolic_4x4_int8_1_c_col0), .c_col1(systolic_4x4_int8_1_c_col1),
    .c_col2(systolic_4x4_int8_1_c_col2), .c_col3(systolic_4x4_int8_1_c_col3),
    .a_out3(systolic_4x4_int8_1_a_out3));
  systolic_4x4_int8 systolic_4x4_int8_2 (
    .CLK(clk), .w00(w40), .w01(w41), .w02(w42), .w03(w43), .w_load(wload),
    .p_sum00(systolic_4x4_int8_1_c_col0), .p_sum01(systolic_4x4_int8_1_c_col1),
    .p_sum02(systolic_4x4_int8_1_c_col2), .p_sum03(systolic_4x4_int8_1_c_col3), .row0(r4), .w10(w50),
    .w11(w51), .w12(w52), .w13(w53), .row1(r5), .w20(w60), .w21(w61), .w22(w62), .w23(w63), .row2(r6),
    .w30(w70), .w31(w71), .w32(w72), .w33(w73), .row3(r7), .a_out0(systolic_4x4_int8_2_a_out0),
    .a_out1(systolic_4x4_int8_2_a_out1), .a_out2(systolic_4x4_int8_2_a_out2), .c_col0(c0), .c_col1(c1),
    .c_col2(c2), .c_col3(c3), .a_out3(systolic_4x4_int8_2_a_out3));
  systolic_4x4_int8 systolic_4x4_int8_3 (
    .CLK(clk), .w00(w04), .w01(w05), .w02(w06), .w03(w07), .w_load(wload), .p_sum00(p_sum04),
    .p_sum01(p_sum05), .p_sum02(p_sum06), .p_sum03(p_sum07), .row0(systolic_4x4_int8_1_a_out0), .w10(w14),
    .w11(w15), .w12(w16), .w13(w17), .row1(systolic_4x4_int8_1_a_out1), .w20(w24), .w21(w25), .w22(w26),
    .w23(w27), .row2(systolic_4x4_int8_1_a_out2), .w30(w34), .w31(w35), .w32(w36), .w33(w37),
    .row3(systolic_4x4_int8_1_a_out3), .a_out0(a0), .a_out1(a1), .a_out2(a2),
    .c_col0(systolic_4x4_int8_3_c_col0), .c_col1(systolic_4x4_int8_3_c_col1),
    .c_col2(systolic_4x4_int8_3_c_col2), .c_col3(systolic_4x4_int8_3_c_col3), .a_out3(a3));
  systolic_4x4_int8 systolic_4x4_int8_4 (
    .CLK(clk), .w00(w44), .w01(w45), .w02(w46), .w03(w47), .w_load(wload),
    .p_sum00(systolic_4x4_int8_3_c_col0), .p_sum01(systolic_4x4_int8_3_c_col1),
    .p_sum02(systolic_4x4_int8_3_c_col2), .p_sum03(systolic_4x4_int8_3_c_col3),
    .row0(systolic_4x4_int8_2_a_out0), .w10(w54), .w11(w55), .w12(w56), .w13(w57),
    .row1(systolic_4x4_int8_2_a_out1), .w20(w64), .w21(w65), .w22(w66), .w23(w67),
    .row2(systolic_4x4_int8_2_a_out2), .w30(w74), .w31(w75), .w32(w76), .w33(w77),
    .row3(systolic_4x4_int8_2_a_out3), .a_out0(a4), .a_out1(a5), .a_out2(a6), .c_col0(c4), .c_col1(c5),
    .c_col2(c6), .c_col3(c7), .a_out3(a7));
endmodule

module PE_cell_FP (
  input  [31:0] w_in,
  input  w_load,
  input  CLK,
  input  [31:0] psum_in,
  input  [31:0] a_in,
  output [31:0] psum_out,
  output [31:0] a_out
);

  wire [31:0] fpadder_1_out, fpmultiplier_1_out, W_reg_q;

  Register #(.width(32)) W_reg (.D(w_in), .en(w_load), .clk(CLK), .Q(W_reg_q));  // open: clr
  FPMultiplier fpmultiplier_1 (.a(a_in), .b(W_reg_q), .out(fpmultiplier_1_out));
  Register #(.width(32)) a_reg (.D(a_in), .clk(CLK), .Q(a_out));  // open: en, clr
  Register #(.width(32)) psum_reg (.D(fpadder_1_out), .clk(CLK), .Q(psum_out));  // open: en, clr
  FPAdder fpadder_1 (.a(psum_in), .b(fpmultiplier_1_out), .out(fpadder_1_out));
endmodule

module systolic_16x16_int8 (
  input  clk,
  input  [7:0] P000,
  input  [7:0] P160,
  input  [7:0] P001,
  input  [7:0] P161,
  input  [7:0] P002,
  input  [7:0] P162,
  input  [7:0] P003,
  input  [7:0] P163,
  input  [7:0] P004,
  input  [7:0] P164,
  input  [7:0] P005,
  input  [7:0] P165,
  input  [7:0] P006,
  input  [7:0] P166,
  input  [7:0] P007,
  input  [7:0] P167,
  input  reset,
  input  [31:0] P008,
  input  [31:0] P168,
  input  [31:0] P009,
  input  [31:0] P169,
  input  [31:0] P010,
  input  [31:0] P170,
  input  [31:0] P011,
  input  [31:0] P171,
  input  [31:0] P012,
  input  [31:0] P172,
  input  [31:0] P013,
  input  [31:0] P173,
  input  [31:0] P014,
  input  [31:0] P174,
  input  [31:0] P015,
  input  [31:0] P175,
  input  [7:0] P016,
  input  [7:0] P017,
  input  [7:0] P176,
  input  [7:0] P018,
  input  [7:0] P177,
  input  [7:0] P019,
  input  [7:0] P178,
  input  [7:0] P020,
  input  [7:0] P179,
  input  [7:0] P021,
  input  [7:0] P180,
  input  [7:0] P022,
  input  [7:0] P181,
  input  [7:0] P023,
  input  [7:0] P182,
  input  [7:0] P024,
  input  [7:0] P183,
  input  [7:0] P025,
  input  [7:0] P026,
  input  [7:0] P184,
  input  [7:0] P027,
  input  [7:0] P185,
  input  [7:0] P028,
  input  [7:0] P186,
  input  [7:0] P029,
  input  [7:0] P187,
  input  [7:0] P030,
  input  [7:0] P188,
  input  [7:0] P031,
  input  [7:0] P189,
  input  [7:0] P032,
  input  [7:0] P190,
  input  [7:0] P033,
  input  [7:0] P191,
  input  [7:0] P034,
  input  [7:0] P035,
  input  [7:0] P192,
  input  [7:0] P036,
  input  [7:0] P193,
  input  [7:0] P037,
  input  [7:0] P194,
  input  [7:0] P038,
  input  [7:0] P195,
  input  [7:0] P039,
  input  [7:0] P196,
  input  [7:0] P040,
  input  [7:0] P197,
  input  [7:0] P041,
  input  [7:0] P198,
  input  [7:0] P042,
  input  [7:0] P199,
  input  [7:0] P043,
  input  [7:0] P044,
  input  [7:0] P200,
  input  [7:0] P045,
  input  [7:0] P201,
  input  [7:0] P046,
  input  [7:0] P202,
  input  [7:0] P047,
  input  [7:0] P203,
  input  [7:0] P048,
  input  [7:0] P204,
  input  [7:0] P049,
  input  [7:0] P205,
  input  [7:0] P050,
  input  [7:0] P206,
  input  [7:0] P051,
  input  [7:0] P207,
  input  [7:0] P052,
  input  [7:0] P053,
  input  [7:0] P208,
  input  [7:0] P054,
  input  [7:0] P209,
  input  [7:0] P055,
  input  [7:0] P210,
  input  [7:0] P056,
  input  [7:0] P211,
  input  [7:0] P057,
  input  [7:0] P212,
  input  [7:0] P058,
  input  [7:0] P213,
  input  [7:0] P059,
  input  [7:0] P214,
  input  [7:0] P060,
  input  [7:0] P215,
  input  [7:0] P061,
  input  [7:0] P062,
  input  [7:0] P216,
  input  [7:0] P063,
  input  [7:0] P217,
  input  [7:0] P064,
  input  [7:0] P218,
  input  [7:0] P065,
  input  [7:0] P219,
  input  [7:0] P066,
  input  [7:0] P220,
  input  [7:0] P067,
  input  [7:0] P221,
  input  [7:0] P068,
  input  [7:0] P222,
  input  [7:0] P069,
  input  [7:0] P223,
  input  [7:0] P070,
  input  [7:0] P071,
  input  [7:0] P224,
  input  [7:0] P072,
  input  [7:0] P225,
  input  [7:0] P073,
  input  [7:0] P226,
  input  [7:0] P074,
  input  [7:0] P227,
  input  [7:0] P075,
  input  [7:0] P228,
  input  [7:0] P076,
  input  [7:0] P229,
  input  [7:0] P077,
  input  [7:0] P230,
  input  [7:0] P078,
  input  [7:0] P231,
  input  [7:0] P079,
  input  [7:0] P080,
  input  [7:0] P232,
  input  [7:0] P081,
  input  [7:0] P233,
  input  [7:0] P082,
  input  [7:0] P234,
  input  [7:0] P083,
  input  [7:0] P235,
  input  [7:0] P084,
  input  [7:0] P236,
  input  [7:0] P085,
  input  [7:0] P237,
  input  [7:0] P086,
  input  [7:0] P238,
  input  [7:0] P087,
  input  [7:0] P239,
  input  [7:0] P088,
  input  [7:0] P089,
  input  [7:0] P240,
  input  [7:0] P090,
  input  [7:0] P241,
  input  [7:0] P091,
  input  [7:0] P242,
  input  [7:0] P092,
  input  [7:0] P243,
  input  [7:0] P093,
  input  [7:0] P244,
  input  [7:0] P094,
  input  [7:0] P245,
  input  [7:0] P095,
  input  [7:0] P246,
  input  [7:0] P096,
  input  [7:0] P247,
  input  [7:0] P097,
  input  [7:0] P098,
  input  [7:0] P248,
  input  [7:0] P099,
  input  [7:0] P249,
  input  [7:0] P100,
  input  [7:0] P250,
  input  [7:0] P101,
  input  [7:0] P251,
  input  [7:0] P102,
  input  [7:0] P252,
  input  [7:0] P103,
  input  [7:0] P253,
  input  [7:0] P104,
  input  [7:0] P254,
  input  [7:0] P105,
  input  [7:0] P255,
  input  [7:0] P106,
  input  [7:0] P107,
  input  [7:0] P256,
  input  [7:0] P108,
  input  [7:0] P257,
  input  [7:0] P109,
  input  [7:0] P258,
  input  [7:0] P110,
  input  [7:0] P259,
  input  [7:0] P111,
  input  [7:0] P260,
  input  [7:0] P112,
  input  [7:0] P261,
  input  [7:0] P113,
  input  [7:0] P262,
  input  [7:0] P114,
  input  [7:0] P263,
  input  [7:0] P115,
  input  [7:0] P116,
  input  [7:0] P264,
  input  [7:0] P117,
  input  [7:0] P265,
  input  [7:0] P118,
  input  [7:0] P266,
  input  [7:0] P119,
  input  [7:0] P267,
  input  [7:0] P120,
  input  [7:0] P268,
  input  [7:0] P121,
  input  [7:0] P269,
  input  [7:0] P122,
  input  [7:0] P270,
  input  [7:0] P123,
  input  [7:0] P271,
  input  [7:0] P124,
  input  [7:0] P125,
  input  [7:0] P272,
  input  [7:0] P126,
  input  [7:0] P273,
  input  [7:0] P127,
  input  [7:0] P274,
  input  [7:0] P128,
  input  [7:0] P275,
  input  [7:0] P129,
  input  [7:0] P276,
  input  [7:0] P130,
  input  [7:0] P277,
  input  [7:0] P131,
  input  [7:0] P278,
  input  [7:0] P132,
  input  [7:0] P279,
  input  [7:0] P133,
  input  [7:0] P134,
  input  [7:0] P280,
  input  [7:0] P135,
  input  [7:0] P281,
  input  [7:0] P136,
  input  [7:0] P282,
  input  [7:0] P137,
  input  [7:0] P283,
  input  [7:0] P138,
  input  [7:0] P284,
  input  [7:0] P139,
  input  [7:0] P285,
  input  [7:0] P140,
  input  [7:0] P286,
  input  [7:0] P141,
  input  [7:0] P287,
  input  [7:0] P142,
  input  [7:0] P143,
  input  [7:0] P288,
  input  [7:0] P144,
  input  [7:0] P289,
  input  [7:0] P145,
  input  [7:0] P290,
  input  [7:0] P146,
  input  [7:0] P291,
  input  [7:0] P147,
  input  [7:0] P292,
  input  [7:0] P148,
  input  [7:0] P293,
  input  [7:0] P149,
  input  [7:0] P294,
  input  [7:0] P150,
  input  [7:0] P295,
  input  [7:0] P151,
  output [7:0] P296,
  output [7:0] P297,
  output [7:0] P298,
  output [7:0] P299,
  output [7:0] P300,
  output [7:0] P301,
  output [7:0] P302,
  output [7:0] P303,
  output [7:0] P304,
  output [7:0] P305,
  output [7:0] P306,
  output [7:0] P307,
  output [7:0] P308,
  output [7:0] P309,
  output [7:0] P310,
  output [31:0] P152,
  output [31:0] P311,
  output [31:0] P153,
  output [31:0] P312,
  output [31:0] P154,
  output [31:0] P313,
  output [31:0] P155,
  output [31:0] P314,
  output [31:0] P156,
  output [31:0] P315,
  output [31:0] P157,
  output [31:0] P316,
  output [31:0] P158,
  output [31:0] P317,
  output [31:0] P159,
  output [31:0] P318,
  output [7:0] P319
);

  wire [7:0] systolic_8x8_int8_1_a0, systolic_8x8_int8_1_a1, systolic_8x8_int8_1_a2, systolic_8x8_int8_1_a3,
       systolic_8x8_int8_1_a4, systolic_8x8_int8_1_a5, systolic_8x8_int8_1_a6, systolic_8x8_int8_1_a7,
       systolic_8x8_int8_2_a0, systolic_8x8_int8_2_a1, systolic_8x8_int8_2_a2, systolic_8x8_int8_2_a3,
       systolic_8x8_int8_2_a4, systolic_8x8_int8_2_a5, systolic_8x8_int8_2_a6, systolic_8x8_int8_2_a7;
  wire [31:0] systolic_8x8_int8_1_c0, systolic_8x8_int8_1_c1, systolic_8x8_int8_1_c2, systolic_8x8_int8_1_c3,
       systolic_8x8_int8_1_c4, systolic_8x8_int8_1_c5, systolic_8x8_int8_1_c6, systolic_8x8_int8_1_c7,
       systolic_8x8_int8_3_c0, systolic_8x8_int8_3_c1, systolic_8x8_int8_3_c2, systolic_8x8_int8_3_c3,
       systolic_8x8_int8_3_c4, systolic_8x8_int8_3_c5, systolic_8x8_int8_3_c6, systolic_8x8_int8_3_c7;

  systolic_8x8_int8 systolic_8x8_int8_1 (
    .clk(clk), .w00(P000), .w04(P001), .w01(P002), .w05(P003), .w02(P004), .w06(P005), .w03(P006),
    .w07(P007), .wload(reset), .p_sum00(P008), .p_sum04(P009), .p_sum01(P010), .p_sum05(P011),
    .p_sum02(P012), .p_sum06(P013), .p_sum03(P014), .p_sum07(P015), .r0(P016), .w10(P017), .w14(P018),
    .w11(P019), .w15(P020), .w12(P021), .w16(P022), .w13(P023), .w17(P024), .r1(P025), .w20(P026),
    .w24(P027), .w21(P028), .w25(P029), .w22(P030), .w26(P031), .w23(P032), .w27(P033), .r2(P034),
    .w30(P035), .w34(P036), .w31(P037), .w35(P038), .w32(P039), .w36(P040), .w33(P041), .w37(P042),
    .r3(P043), .w40(P044), .w44(P045), .w41(P046), .w45(P047), .w42(P048), .w46(P049), .w43(P050),
    .w47(P051), .r4(P052), .w50(P053), .w54(P054), .w51(P055), .w55(P056), .w52(P057), .w56(P058),
    .w53(P059), .w57(P060), .r5(P061), .w60(P062), .w64(P063), .w61(P064), .w65(P065), .w62(P066),
    .w66(P067), .w63(P068), .w67(P069), .r6(P070), .w70(P071), .w74(P072), .w71(P073), .w75(P074),
    .w72(P075), .w76(P076), .w73(P077), .w77(P078), .r7(P079), .a0(systolic_8x8_int8_1_a0),
    .a1(systolic_8x8_int8_1_a1), .a2(systolic_8x8_int8_1_a2), .a3(systolic_8x8_int8_1_a3),
    .a4(systolic_8x8_int8_1_a4), .a5(systolic_8x8_int8_1_a5), .a6(systolic_8x8_int8_1_a6),
    .c0(systolic_8x8_int8_1_c0), .c4(systolic_8x8_int8_1_c4), .c1(systolic_8x8_int8_1_c1),
    .c5(systolic_8x8_int8_1_c5), .c2(systolic_8x8_int8_1_c2), .c6(systolic_8x8_int8_1_c6),
    .c3(systolic_8x8_int8_1_c3), .c7(systolic_8x8_int8_1_c7), .a7(systolic_8x8_int8_1_a7));
  systolic_8x8_int8 systolic_8x8_int8_2 (
    .clk(clk), .w00(P080), .w04(P081), .w01(P082), .w05(P083), .w02(P084), .w06(P085), .w03(P086),
    .w07(P087), .wload(reset), .p_sum00(systolic_8x8_int8_1_c0), .p_sum04(systolic_8x8_int8_1_c4),
    .p_sum01(systolic_8x8_int8_1_c1), .p_sum05(systolic_8x8_int8_1_c5), .p_sum02(systolic_8x8_int8_1_c2),
    .p_sum06(systolic_8x8_int8_1_c6), .p_sum03(systolic_8x8_int8_1_c3), .p_sum07(systolic_8x8_int8_1_c7),
    .r0(P088), .w10(P089), .w14(P090), .w11(P091), .w15(P092), .w12(P093), .w16(P094), .w13(P095),
    .w17(P096), .r1(P097), .w20(P098), .w24(P099), .w21(P100), .w25(P101), .w22(P102), .w26(P103),
    .w23(P104), .w27(P105), .r2(P106), .w30(P107), .w34(P108), .w31(P109), .w35(P110), .w32(P111),
    .w36(P112), .w33(P113), .w37(P114), .r3(P115), .w40(P116), .w44(P117), .w41(P118), .w45(P119),
    .w42(P120), .w46(P121), .w43(P122), .w47(P123), .r4(P124), .w50(P125), .w54(P126), .w51(P127),
    .w55(P128), .w52(P129), .w56(P130), .w53(P131), .w57(P132), .r5(P133), .w60(P134), .w64(P135),
    .w61(P136), .w65(P137), .w62(P138), .w66(P139), .w63(P140), .w67(P141), .r6(P142), .w70(P143),
    .w74(P144), .w71(P145), .w75(P146), .w72(P147), .w76(P148), .w73(P149), .w77(P150), .r7(P151),
    .a0(systolic_8x8_int8_2_a0), .a1(systolic_8x8_int8_2_a1), .a2(systolic_8x8_int8_2_a2),
    .a3(systolic_8x8_int8_2_a3), .a4(systolic_8x8_int8_2_a4), .a5(systolic_8x8_int8_2_a5),
    .a6(systolic_8x8_int8_2_a6), .c0(P152), .c4(P153), .c1(P154), .c5(P155), .c2(P156), .c6(P157), .c3(P158),
    .c7(P159), .a7(systolic_8x8_int8_2_a7));
  systolic_8x8_int8 systolic_8x8_int8_3 (
    .clk(clk), .w00(P160), .w04(P161), .w01(P162), .w05(P163), .w02(P164), .w06(P165), .w03(P166),
    .w07(P167), .wload(reset), .p_sum00(P168), .p_sum04(P169), .p_sum01(P170), .p_sum05(P171),
    .p_sum02(P172), .p_sum06(P173), .p_sum03(P174), .p_sum07(P175), .r0(systolic_8x8_int8_1_a0), .w10(P176),
    .w14(P177), .w11(P178), .w15(P179), .w12(P180), .w16(P181), .w13(P182), .w17(P183),
    .r1(systolic_8x8_int8_1_a1), .w20(P184), .w24(P185), .w21(P186), .w25(P187), .w22(P188), .w26(P189),
    .w23(P190), .w27(P191), .r2(systolic_8x8_int8_1_a2), .w30(P192), .w34(P193), .w31(P194), .w35(P195),
    .w32(P196), .w36(P197), .w33(P198), .w37(P199), .r3(systolic_8x8_int8_1_a3), .w40(P200), .w44(P201),
    .w41(P202), .w45(P203), .w42(P204), .w46(P205), .w43(P206), .w47(P207), .r4(systolic_8x8_int8_1_a4),
    .w50(P208), .w54(P209), .w51(P210), .w55(P211), .w52(P212), .w56(P213), .w53(P214), .w57(P215),
    .r5(systolic_8x8_int8_1_a5), .w60(P216), .w64(P217), .w61(P218), .w65(P219), .w62(P220), .w66(P221),
    .w63(P222), .w67(P223), .r6(systolic_8x8_int8_1_a6), .w70(P224), .w74(P225), .w71(P226), .w75(P227),
    .w72(P228), .w76(P229), .w73(P230), .w77(P231), .r7(systolic_8x8_int8_1_a7), .a0(P296), .a1(P297),
    .a2(P298), .a3(P299), .a4(P300), .a5(P301), .a6(P302), .c0(systolic_8x8_int8_3_c0),
    .c4(systolic_8x8_int8_3_c4), .c1(systolic_8x8_int8_3_c1), .c5(systolic_8x8_int8_3_c5),
    .c2(systolic_8x8_int8_3_c2), .c6(systolic_8x8_int8_3_c6), .c3(systolic_8x8_int8_3_c3),
    .c7(systolic_8x8_int8_3_c7), .a7(P303));
  systolic_8x8_int8 systolic_8x8_int8_4 (
    .clk(clk), .w00(P232), .w04(P233), .w01(P234), .w05(P235), .w02(P236), .w06(P237), .w03(P238),
    .w07(P239), .wload(reset), .p_sum00(systolic_8x8_int8_3_c4), .p_sum04(systolic_8x8_int8_3_c0),
    .p_sum01(systolic_8x8_int8_3_c1), .p_sum05(systolic_8x8_int8_3_c5), .p_sum02(systolic_8x8_int8_3_c2),
    .p_sum06(systolic_8x8_int8_3_c6), .p_sum03(systolic_8x8_int8_3_c3), .p_sum07(systolic_8x8_int8_3_c7),
    .r0(systolic_8x8_int8_2_a0), .w10(P240), .w14(P241), .w11(P242), .w15(P243), .w12(P244), .w16(P245),
    .w13(P246), .w17(P247), .r1(systolic_8x8_int8_2_a1), .w20(P248), .w24(P249), .w21(P250), .w25(P251),
    .w22(P252), .w26(P253), .w23(P254), .w27(P255), .r2(systolic_8x8_int8_2_a2), .w30(P256), .w34(P257),
    .w31(P258), .w35(P259), .w32(P260), .w36(P261), .w33(P262), .w37(P263), .r3(systolic_8x8_int8_2_a3),
    .w40(P264), .w44(P265), .w41(P266), .w45(P267), .w42(P268), .w46(P269), .w43(P270), .w47(P271),
    .r4(systolic_8x8_int8_2_a4), .w50(P272), .w54(P273), .w51(P274), .w55(P275), .w52(P276), .w56(P277),
    .w53(P278), .w57(P279), .r5(systolic_8x8_int8_2_a5), .w60(P280), .w64(P281), .w61(P282), .w65(P283),
    .w62(P284), .w66(P285), .w63(P286), .w67(P287), .r6(systolic_8x8_int8_2_a6), .w70(P288), .w74(P289),
    .w71(P290), .w75(P291), .w72(P292), .w76(P293), .w73(P294), .w77(P295), .r7(systolic_8x8_int8_2_a7),
    .a0(P304), .a1(P305), .a2(P306), .a3(P307), .a4(P308), .a5(P309), .a6(P310), .c0(P311), .c4(P312),
    .c1(P313), .c5(P314), .c2(P315), .c6(P316), .c3(P317), .c7(P318), .a7(P319));
endmodule
